// Logisim project cpu21-riscv-团队项目-井字棋.circ as structural Verilog: 21 circuits, main circuit ◇井字棋游戏
module \井字棋游戏  (
  output RegWrite,
  output MemWrite,
  output [31:0] MDin,
  output [31:0] PC,
  output [31:0] IR,
  output [31:0] RDin
);

  wire AluSrcB, and_1_out, and_2_out, and_3_out, and_5_out, and_6_out, and_7_out, and_8_out, and_9_out,
       and_11_out, and_12_out, and_13_out, and_14_out, and_15_out, and_18_out, and_19_out, and_20_out,
       and_21_out, and_22_out, and_23_out, and_24_out, and_25_out, and_26_out, and_27_out, and_28_out,
       and_29_out, and_30_out, and_31_out, and_32_out, and_52_out, and_56_out, and_57_out, and_61_out,
       and_62_out, and_63_out, beq, bgeu, bne, Branch, CLK, Clr, comparator_1_eq, comparator_2_eq,
       comparator_3_eq, comparator_4_eq, comparator_5_eq, comparator_6_eq, comparator_7_eq, comparator_8_eq,
       comparator_9_eq, d_ff_1_q, d_ff_2_q, d_ff_3_q, d_ff_4_q, d_ff_5_q, d_ff_6_q, d_ff_7_q, d_ff_8_q,
       d_ff_9_q, d_ff_10_q, d_ff_11_q, d_ff_12_q, d_ff_13_q, d_ff_14_q, d_ff_15_q, d_ff_16_q, d_ff_17_q,
       d_ff_18_q, d_ff_19_q, d_ff_20_q, d_ff_21_q, d_ff_22_q, d_ff_23_q, d_ff_24_q, d_ff_25_q,
       decoder_1_out1, decoder_1_out2, decoder_1_out3, decoder_1_out4, decoder_1_out5, decoder_1_out6,
       decoder_1_out7, decoder_1_out8, decoder_1_out9, decoder_1_out10, decoder_1_out11, decoder_1_out12,
       decoder_1_out13, decoder_1_out14, decoder_1_out15, decoder_1_out16, decoder_1_out17, decoder_1_out18,
       decoder_1_out19, decoder_1_out20, decoder_1_out21, decoder_1_out22, decoder_1_out23, decoder_1_out24,
       decoder_1_out25, ecall, en, equal, halt, IE_q, inter, Inter1, Inter2, Inter3, Inter4, Inter5, Inter6,
       Inter7, Inter8, Inter9, Inter10, Inter11, Inter12, Inter13, Inter14, Inter15, Inter16, Inter17,
       Inter18, Inter19, Inter20, Inter21, Inter22, Inter23, Inter24, Inter25, Interr, Interrupt, IR1, IR2,
       IR3, IR4, IR5, IR6, IR7, IR8, IR9, IR10, IR11, IR12, IR13, IR14, IR15, IR16, IR17, IR18, IR19, IR20,
       IR21, IR22, IR23, IR24, IR25, jal, jalr, lhu, MemToReg, MoreAndEqu, not_1_out, not_3_out, not_4_out,
       or_7_out, or_8_out, or_9_out, or_10_out, or_11_out, or_12_out, or_19_out, or_20_out, or_21_out,
       or_22_out, or_23_out, or_29_out, or_30_out, or_31_out, or_32_out, or_33_out, or_39_out, or_40_out,
       or_41_out, or_42_out, or_43_out, or_49_out, or_50_out, or_51_out, or_52_out, or_53_out, or_55_out,
       PCToReg, Ret1, Ret2, Ret3, Ret4, Ret5, Ret6, Ret7, Ret8, Ret9, Ret10, Ret11, Ret12, Ret13, Ret14,
       Ret15, Ret16, Ret17, Ret18, Ret19, Ret20, Ret21, Ret22, Ret23, Ret24, Ret25, RST, S_type, U_type,
       uret, W1, W2, W3, W4, W5, W6, W7, W8, W9, W10, W11, W12, W13, W14, W15, W16, W17, W18, W19, W20, W21,
       W22, W23, W24, W25, \单周期硬布线控制器_1_ecall , \单周期硬布线控制器_1_uret ;
  wire [3:0] AluOP;
  wire [4:0] multiplexer_7_out, multiplexer_8_out, priority_encoder_1_out, \中断号_q ;
  wire [6:0] X, Y;
  wire [11:0] imm12_B;
  wire [15:0] Color, multiplexer_13_out;
  wire [19:0] imm20_J;
  wire [31:0] adder_1_out, adder_2_out, adder_3_out, and_4_out, bit_extender_1_out, bit_extender_2_out,
       bit_extender_3_out, bit_extender_4_out, bit_extender_5_out, EPC, InterAddr, MDout, multiplexer_1_out,
       multiplexer_2_out, multiplexer_4_out, multiplexer_5_out, multiplexer_9_out, multiplexer_11_out,
       multiplexer_12_out, nextPC, PC_4, R1, ram_1_data, Result, RPCin;
  wire [31:1] interrupt_q;
  wire [31:7] \X坐标_q , \Y坐标_q ;
  wire [31:16] Color_q;

  assign bit_extender_1_out = {{12{imm20_J[19]}}, imm20_J};  // Bit_Extender bit_extender_1
  Button \u_重新开始  (.out(RST));
  Button _1 (.out(IR1));
  Button _6 (.out(IR6));
  Button _11 (.out(IR11));
  Button _16 (.out(IR16));
  Button _21 (.out(IR21));
  not not_1 (not_1_out, equal);
  or or_1 (W1, Inter1, d_ff_1_q);
  or or_2 (W6, Inter6, d_ff_2_q);
  or or_3 (W11, Inter11, d_ff_3_q);
  or or_4 (W16, Inter16, d_ff_4_q);
  or or_5 (W21, Inter21, d_ff_5_q);
  LED #(.active("true")) led_1 (.in(W1));
  LED #(.active("true")) led_2 (.in(W6));
  LED #(.active("true")) led_3 (.in(W11));
  LED #(.active("true")) led_4 (.in(W16));
  LED #(.active("true")) led_5 (.in(W21));
  and and_1 (and_1_out, beq, equal);
  and and_2 (and_2_out, not_1_out, bne);
  and and_3 (and_3_out, MoreAndEqu, bgeu);
  Multiplexer #(.select(1), .width(32), .disabled("Z"), .enable("false")) multiplexer_1 (
    .in0(PC_4), .in1(adder_1_out), .out(multiplexer_1_out), .sel(jal));
  Adder #(.width(32)) adder_1 (.a(bit_extender_1_out), .b(PC), .out(adder_1_out));  // open: cin, cout
  assign and_4_out = Result & 32'hfffffffe;  // AND_Gate and_4, 32 bits wide
  assign bit_extender_2_out = {{20{imm12_B[11]}}, imm12_B};  // Bit_Extender bit_extender_2
  D_Flip_Flop #(.trigger("rising"), .Pre_Clr_Positions("LEGACY"), .NegatePresetClear("false"), .enable("true"), .NewFFLayout("false")) d_ff_1 (
    .clk(IR1), .D(1'b1), .Q(d_ff_1_q), .reset(Inter1));  // open: Qn, preset, en
  D_Flip_Flop #(.trigger("rising"), .Pre_Clr_Positions("LEGACY"), .NegatePresetClear("false"), .enable("true"), .NewFFLayout("false")) d_ff_2 (
    .clk(IR6), .D(1'b1), .Q(d_ff_2_q), .reset(Inter6));  // open: Qn, preset, en
  D_Flip_Flop #(.trigger("rising"), .Pre_Clr_Positions("LEGACY"), .NegatePresetClear("false"), .enable("true"), .NewFFLayout("false")) d_ff_3 (
    .clk(IR11), .D(1'b1), .Q(d_ff_3_q), .reset(Inter11));  // open: Qn, preset, en
  D_Flip_Flop #(.trigger("rising"), .Pre_Clr_Positions("LEGACY"), .NegatePresetClear("false"), .enable("true"), .NewFFLayout("false")) d_ff_4 (
    .clk(IR16), .D(1'b1), .Q(d_ff_4_q), .reset(Inter16));  // open: Qn, preset, en
  D_Flip_Flop #(.trigger("rising"), .Pre_Clr_Positions("LEGACY"), .NegatePresetClear("false"), .enable("true"), .NewFFLayout("false")) d_ff_5 (
    .clk(IR21), .D(1'b1), .Q(d_ff_5_q), .reset(Inter21));  // open: Qn, preset, en
  or or_6 (Branch, and_1_out, and_2_out, and_3_out);
  Multiplexer #(.select(1), .width(32), .disabled("Z"), .enable("false")) multiplexer_2 (
    .in0(multiplexer_1_out), .in1(and_4_out), .out(multiplexer_2_out), .sel(jalr));
  Adder #(.width(32)) adder_2 (.a(bit_extender_2_out), .b(PC), .out(adder_2_out));  // open: cin, cout
  or or_7 (or_7_out, d_ff_1_q, Inter1);
  or or_8 (or_8_out, d_ff_2_q, Inter6);
  or or_9 (or_9_out, d_ff_3_q, Inter11);
  or or_10 (or_10_out, d_ff_4_q, Inter16);
  or or_11 (or_11_out, d_ff_5_q, Inter21);
  Button _2 (.out(IR2));
  Button _7 (.out(IR7));
  Button _12 (.out(IR12));
  Button _17 (.out(IR17));
  Button _22 (.out(IR22));
  Multiplexer #(.select(1), .width(32), .disabled("Z"), .enable("false")) multiplexer_3 (
    .in0(multiplexer_2_out), .in1(adder_2_out), .out(nextPC), .sel(Branch));
  and and_5 (and_5_out, or_7_out, ~Ret1);  // AND_Gate
  and and_6 (and_6_out, or_8_out, ~Ret6);  // AND_Gate
  and and_7 (and_7_out, or_9_out, ~Ret11);  // AND_Gate
  and and_8 (and_8_out, or_10_out, ~Ret16);  // AND_Gate
  and and_9 (and_9_out, or_11_out, ~Ret21);  // AND_Gate
  LED #(.active("true")) led_6 (.in(W2));
  LED #(.active("true")) led_7 (.in(W7));
  LED #(.active("true")) led_8 (.in(W12));
  LED #(.active("true")) led_9 (.in(W17));
  LED #(.active("true")) led_10 (.in(W22));
  Multiplexer #(.select(1), .width(32), .disabled("Z"), .enable("false")) multiplexer_4 (
    .in0(nextPC), .in1(InterAddr), .out(multiplexer_4_out), .sel(Interrupt));
  Multiplexer #(.select(1), .width(32), .disabled("Z"), .enable("false")) multiplexer_5 (
    .in0(multiplexer_4_out), .in1(EPC), .out(multiplexer_5_out), .sel(uret));
  Comparator #(.width(32), .mode("twosComplement")) comparator_1 (
    .a(R1), .b(32'ha), .eq(comparator_1_eq));  // open: gt, lt
  D_Flip_Flop #(.trigger("rising"), .Pre_Clr_Positions("LEGACY"), .NegatePresetClear("false"), .enable("true"), .NewFFLayout("false")) u_IR1 (
    .clk(CLK), .D(and_5_out), .Q(Inter1));  // open: Qn, preset, en, reset
  D_Flip_Flop #(.trigger("rising"), .Pre_Clr_Positions("LEGACY"), .NegatePresetClear("false"), .enable("true"), .NewFFLayout("false")) u_IR3 (
    .clk(CLK), .D(and_6_out), .Q(Inter6));  // open: Qn, preset, en, reset
  D_Flip_Flop #(.trigger("rising"), .Pre_Clr_Positions("LEGACY"), .NegatePresetClear("false"), .enable("true"), .NewFFLayout("false")) IR3_2 (
    .clk(CLK), .D(and_7_out), .Q(Inter11));  // open: Qn, preset, en, reset
  D_Flip_Flop #(.trigger("rising"), .Pre_Clr_Positions("LEGACY"), .NegatePresetClear("false"), .enable("true"), .NewFFLayout("false")) IR3_3 (
    .clk(CLK), .D(and_8_out), .Q(Inter16));  // open: Qn, preset, en, reset
  D_Flip_Flop #(.trigger("rising"), .Pre_Clr_Positions("LEGACY"), .NegatePresetClear("false"), .enable("true"), .NewFFLayout("false")) IR3_4 (
    .clk(CLK), .D(and_9_out), .Q(Inter21));  // open: Qn, preset, en, reset
  Button _3 (.out(IR3));
  Button _8 (.out(IR8));
  Button _13 (.out(IR13));
  Button _18 (.out(IR18));
  Button _23 (.out(IR23));
  or or_12 (or_12_out, jal, jalr);
  Adder #(.width(32)) adder_3 (.a({IR[31:12], {12{1'b0}}}), .b(PC), .out(adder_3_out));  // open: cin, cout
  Register #(.width(32), .trigger("rising"), .Select("low")) u_PC (
    .D(multiplexer_5_out), .en(en), .Q(PC), .clk(CLK), .clr(RST));
  and and_10 (halt, comparator_1_eq, ecall);
  not not_2 (en, halt);
  LED #(.active("true")) led_11 (.in(W3));
  LED #(.active("true")) led_12 (.in(W8));
  LED #(.active("true")) led_13 (.in(W13));
  LED #(.active("true")) led_14 (.in(W18));
  LED #(.active("true")) led_15 (.in(W23));
  or or_13 (PCToReg, or_12_out, U_type);
  Multiplexer #(.select(1), .width(32), .disabled("Z"), .enable("false")) multiplexer_6 (
    .in0(PC_4), .in1(adder_3_out), .out(RPCin), .sel(U_type));
  or or_14 (W2, Inter2, d_ff_6_q);
  or or_15 (W7, Inter7, d_ff_7_q);
  or or_16 (W12, Inter12, d_ff_8_q);
  or or_17 (W17, Inter17, d_ff_9_q);
  or or_18 (W22, Inter22, d_ff_10_q);
  // RiscV_Probe riscv_probe_1: pin names not known; wires that end beside it: IR
  Adder #(.width(32)) adder_4 (.a(PC), .b(32'h4), .out(PC_4));  // open: cin, cout
  D_Flip_Flop #(.trigger("rising"), .Pre_Clr_Positions("LEGACY"), .NegatePresetClear("false"), .enable("true"), .NewFFLayout("false")) d_ff_6 (
    .clk(IR2), .D(1'b1), .Q(d_ff_6_q), .reset(Inter2));  // open: Qn, preset, en
  D_Flip_Flop #(.trigger("rising"), .Pre_Clr_Positions("LEGACY"), .NegatePresetClear("false"), .enable("true"), .NewFFLayout("false")) d_ff_7 (
    .clk(IR7), .D(1'b1), .Q(d_ff_7_q), .reset(Inter7));  // open: Qn, preset, en
  D_Flip_Flop #(.trigger("rising"), .Pre_Clr_Positions("LEGACY"), .NegatePresetClear("false"), .enable("true"), .NewFFLayout("false")) d_ff_8 (
    .clk(IR12), .D(1'b1), .Q(d_ff_8_q), .reset(Inter12));  // open: Qn, preset, en
  D_Flip_Flop #(.trigger("rising"), .Pre_Clr_Positions("LEGACY"), .NegatePresetClear("false"), .enable("true"), .NewFFLayout("false")) d_ff_9 (
    .clk(IR17), .D(1'b1), .Q(d_ff_9_q), .reset(Inter17));  // open: Qn, preset, en
  D_Flip_Flop #(.trigger("rising"), .Pre_Clr_Positions("LEGACY"), .NegatePresetClear("false"), .enable("true"), .NewFFLayout("false")) d_ff_10 (
    .clk(IR22), .D(1'b1), .Q(d_ff_10_q), .reset(Inter22));  // open: Qn, preset, en
  Button _4 (.out(IR4));
  Button _9 (.out(IR9));
  Button _14 (.out(IR14));
  Button _19 (.out(IR19));
  Button _24 (.out(IR24));
  ROM #(.addrWidth(20), .dataWidth(32), .Select("high")) rom_1 (.addr(PC[21:2]), .data(IR));
  or or_19 (or_19_out, d_ff_6_q, Inter2);
  or or_20 (or_20_out, d_ff_7_q, Inter7);
  or or_21 (or_21_out, d_ff_8_q, Inter12);
  or or_22 (or_22_out, d_ff_9_q, Inter17);
  or or_23 (or_23_out, d_ff_10_q, Inter22);
  LED #(.active("true")) led_16 (.in(W4));
  LED #(.active("true")) led_17 (.in(W9));
  LED #(.active("true")) led_18 (.in(W14));
  LED #(.active("true")) led_19 (.in(W19));
  LED #(.active("true")) led_20 (.in(W24));
  Comparator #(.width(5), .mode("twosComplement")) comparator_2 (
    .a(IR[24:20]), .b({5{1'b0}}), .eq(comparator_2_eq));  // open: gt, lt
  Comparator #(.width(5), .mode("twosComplement")) comparator_3 (
    .a(IR[24:20]), .b(5'b00010), .eq(comparator_3_eq));  // open: gt, lt
  and and_11 (and_11_out, or_19_out, ~Ret2);  // AND_Gate
  and and_12 (and_12_out, or_20_out, ~Ret7);  // AND_Gate
  and and_13 (and_13_out, or_21_out, ~Ret12);  // AND_Gate
  and and_14 (and_14_out, or_22_out, ~Ret17);  // AND_Gate
  and and_15 (and_15_out, or_23_out, ~Ret22);  // AND_Gate
  Button _5 (.out(IR5));
  Button _10 (.out(IR10));
  Button _15 (.out(IR15));
  Button _20 (.out(IR20));
  Button _25 (.out(IR25));
  and and_16 (ecall, \单周期硬布线控制器_1_ecall , comparator_2_eq);
  and and_17 (uret, \单周期硬布线控制器_1_uret , comparator_3_eq);
  \单周期硬布线控制器  \u_单周期硬布线控制器_1  (
    .Funct({IR[30], IR[25], IR[14:12]}), .OP(IR[6:2]), .ALU_OP(AluOP), .MemToReg(MemToReg),
    .MemWrite(MemWrite), .ALU_SRC(AluSrcB), .RegWrite(RegWrite), .ecall(\单周期硬布线控制器_1_ecall ),
    .S_type(S_type), .Jalr(jalr), .Beq(beq), .JAL(jal), .Bne(bne), .U_type(U_type), .BGEU(bgeu), .LHU(lhu),
    .URET(\单周期硬布线控制器_1_uret ));
  Multiplexer #(.select(1), .width(5), .disabled("Z"), .enable("false")) multiplexer_7 (
    .in0(IR[19:15]), .in1(5'b10001), .out(multiplexer_7_out), .sel(ecall));
  Multiplexer #(.select(1), .width(5), .disabled("Z"), .enable("false")) multiplexer_8 (
    .in0(IR[24:20]), .in1(5'b01010), .out(multiplexer_8_out), .sel(ecall));
  Multiplexer #(.select(1), .width(32), .disabled("Z"), .enable("false")) multiplexer_9 (
    .in0(Result), .in1(MDout), .out(multiplexer_9_out), .sel(MemToReg));
  Shifter #(.width(12), .shift("ll")) shifter_1 (
    .in({IR[31], IR[7], IR[30:25], IR[11:8]}), .\dist (4'b0001), .out(imm12_B));
  Shifter #(.width(20), .shift("ll")) shifter_2 (
    .in({IR[31], IR[19:12], IR[20], IR[30:21]}), .\dist (5'b00001), .out(imm20_J));
  D_Flip_Flop #(.trigger("rising"), .Pre_Clr_Positions("LEGACY"), .NegatePresetClear("false"), .enable("true"), .NewFFLayout("false")) u_IR2 (
    .clk(CLK), .D(and_11_out), .Q(Inter2));  // open: Qn, preset, en, reset
  D_Flip_Flop #(.trigger("rising"), .Pre_Clr_Positions("LEGACY"), .NegatePresetClear("false"), .enable("true"), .NewFFLayout("false")) IR1_2 (
    .clk(CLK), .D(and_12_out), .Q(Inter7));  // open: Qn, preset, en, reset
  D_Flip_Flop #(.trigger("rising"), .Pre_Clr_Positions("LEGACY"), .NegatePresetClear("false"), .enable("true"), .NewFFLayout("false")) IR3_5 (
    .clk(CLK), .D(and_13_out), .Q(Inter12));  // open: Qn, preset, en, reset
  D_Flip_Flop #(.trigger("rising"), .Pre_Clr_Positions("LEGACY"), .NegatePresetClear("false"), .enable("true"), .NewFFLayout("false")) IR3_6 (
    .clk(CLK), .D(and_14_out), .Q(Inter17));  // open: Qn, preset, en, reset
  D_Flip_Flop #(.trigger("rising"), .Pre_Clr_Positions("LEGACY"), .NegatePresetClear("false"), .enable("true"), .NewFFLayout("false")) IR3_7 (
    .clk(CLK), .D(and_15_out), .Q(Inter22));  // open: Qn, preset, en, reset
  LED #(.active("true")) led_21 (.in(W5));
  LED #(.active("true")) led_22 (.in(W10));
  LED #(.active("true")) led_23 (.in(W15));
  LED #(.active("true")) led_24 (.in(W20));
  LED #(.active("true")) led_25 (.in(W25));
  Multiplexer #(.select(1), .width(32), .disabled("Z"), .enable("false")) multiplexer_10 (
    .in0(multiplexer_9_out), .in1(RPCin), .out(RDin), .sel(PCToReg));
  or or_24 (W23, Inter23, d_ff_13_q);
  Regifile regifile_1 (
    .Din(RDin), .Clk(CLK), .R1(R1), .R2(MDin), .WE(RegWrite), .W_num(IR[11:7]), .R1_num(multiplexer_7_out),
    .R2_num(multiplexer_8_out));
  assign bit_extender_3_out = {{20{IR[31]}}, IR[31:20]};  // Bit_Extender bit_extender_3
  assign bit_extender_4_out = {{20{IR[31]}}, {IR[31:25], IR[11:7]}};  // Bit_Extender bit_extender_4
  or or_25 (W3, Inter3, d_ff_14_q);
  or or_26 (W8, Inter8, d_ff_15_q);
  D_Flip_Flop #(.trigger("rising"), .Pre_Clr_Positions("LEGACY"), .NegatePresetClear("false"), .enable("true"), .NewFFLayout("false")) d_ff_11 (
    .clk(IR13), .D(1'b1), .Q(d_ff_11_q), .reset(Inter13));  // open: Qn, preset, en
  or or_27 (W13, Inter13, d_ff_11_q);
  D_Flip_Flop #(.trigger("rising"), .Pre_Clr_Positions("LEGACY"), .NegatePresetClear("false"), .enable("true"), .NewFFLayout("false")) d_ff_12 (
    .clk(IR18), .D(1'b1), .Q(d_ff_12_q), .reset(Inter18));  // open: Qn, preset, en
  or or_28 (W18, Inter18, d_ff_12_q);
  D_Flip_Flop #(.trigger("rising"), .Pre_Clr_Positions("LEGACY"), .NegatePresetClear("false"), .enable("true"), .NewFFLayout("false")) d_ff_13 (
    .clk(IR23), .D(1'b1), .Q(d_ff_13_q), .reset(Inter23));  // open: Qn, preset, en
  Multiplexer #(.select(1), .width(32), .disabled("Z"), .enable("false")) multiplexer_11 (
    .in0(MDin), .in1(multiplexer_12_out), .out(multiplexer_11_out), .sel(AluSrcB));
  Multiplexer #(.select(1), .width(32), .disabled("Z"), .enable("false")) multiplexer_12 (
    .in0(bit_extender_3_out), .in1(bit_extender_4_out), .out(multiplexer_12_out), .sel(S_type));
  D_Flip_Flop #(.trigger("rising"), .Pre_Clr_Positions("LEGACY"), .NegatePresetClear("false"), .enable("true"), .NewFFLayout("false")) d_ff_14 (
    .clk(IR3), .D(1'b1), .Q(d_ff_14_q), .reset(Inter3));  // open: Qn, preset, en
  D_Flip_Flop #(.trigger("rising"), .Pre_Clr_Positions("LEGACY"), .NegatePresetClear("false"), .enable("true"), .NewFFLayout("false")) d_ff_15 (
    .clk(IR8), .D(1'b1), .Q(d_ff_15_q), .reset(Inter8));  // open: Qn, preset, en
  or or_29 (or_29_out, d_ff_13_q, Inter23);
  or or_30 (or_30_out, d_ff_14_q, Inter3);
  or or_31 (or_31_out, d_ff_15_q, Inter8);
  and and_18 (and_18_out, or_31_out, ~Ret8);  // AND_Gate
  or or_32 (or_32_out, d_ff_11_q, Inter13);
  and and_19 (and_19_out, or_32_out, ~Ret13);  // AND_Gate
  or or_33 (or_33_out, d_ff_12_q, Inter18);
  and and_20 (and_20_out, or_33_out, ~Ret18);  // AND_Gate
  and and_21 (and_21_out, or_29_out, ~Ret23);  // AND_Gate
  // LCD_Video lcd_video_1: pin names not known; wires that end beside it: Clr, CLK, ecall, X, Y, {16{1'b1}}
  Clock #(.highDuration(1), .lowDuration(1)) clock_1 (.out(CLK));
  ALU alu_1 (
    .X(R1), .Y(multiplexer_11_out), .AluOP(AluOP), .Equal(equal), .Result(Result), .out_4(MoreAndEqu));  // open: Result_2, out_6
  and and_22 (and_22_out, or_30_out, ~Ret3);  // AND_Gate
  D_Flip_Flop #(.trigger("rising"), .Pre_Clr_Positions("LEGACY"), .NegatePresetClear("false"), .enable("true"), .NewFFLayout("false")) IR2_2 (
    .clk(CLK), .D(and_18_out), .Q(Inter8));  // open: Qn, preset, en, reset
  D_Flip_Flop #(.trigger("rising"), .Pre_Clr_Positions("LEGACY"), .NegatePresetClear("false"), .enable("true"), .NewFFLayout("false")) IR3_8 (
    .clk(CLK), .D(and_19_out), .Q(Inter13));  // open: Qn, preset, en, reset
  D_Flip_Flop #(.trigger("rising"), .Pre_Clr_Positions("LEGACY"), .NegatePresetClear("false"), .enable("true"), .NewFFLayout("false")) IR3_9 (
    .clk(CLK), .D(and_20_out), .Q(Inter18));  // open: Qn, preset, en, reset
  D_Flip_Flop #(.trigger("rising"), .Pre_Clr_Positions("LEGACY"), .NegatePresetClear("false"), .enable("true"), .NewFFLayout("false")) IR3_10 (
    .clk(CLK), .D(and_21_out), .Q(Inter23));  // open: Qn, preset, en, reset
  D_Flip_Flop #(.trigger("rising"), .Pre_Clr_Positions("LEGACY"), .NegatePresetClear("false"), .enable("true"), .NewFFLayout("false")) IR3_11 (
    .clk(CLK), .D(and_22_out), .Q(Inter3));  // open: Qn, preset, en, reset
  or or_34 (W9, Inter9, d_ff_16_q);
  or or_35 (W14, Inter14, d_ff_17_q);
  or or_36 (W19, Inter19, d_ff_18_q);
  or or_37 (W24, Inter24, d_ff_19_q);
  // RiscV_Probe riscv_probe_2: pin names not known; wires that end beside it: IR
  or or_38 (W4, Inter4, d_ff_20_q);
  D_Flip_Flop #(.trigger("rising"), .Pre_Clr_Positions("LEGACY"), .NegatePresetClear("false"), .enable("true"), .NewFFLayout("false")) d_ff_16 (
    .clk(IR9), .D(1'b1), .Q(d_ff_16_q), .reset(Inter9));  // open: Qn, preset, en
  D_Flip_Flop #(.trigger("rising"), .Pre_Clr_Positions("LEGACY"), .NegatePresetClear("false"), .enable("true"), .NewFFLayout("false")) d_ff_17 (
    .clk(IR14), .D(1'b1), .Q(d_ff_17_q), .reset(Inter14));  // open: Qn, preset, en
  D_Flip_Flop #(.trigger("rising"), .Pre_Clr_Positions("LEGACY"), .NegatePresetClear("false"), .enable("true"), .NewFFLayout("false")) d_ff_18 (
    .clk(IR19), .D(1'b1), .Q(d_ff_18_q), .reset(Inter19));  // open: Qn, preset, en
  D_Flip_Flop #(.trigger("rising"), .Pre_Clr_Positions("LEGACY"), .NegatePresetClear("false"), .enable("true"), .NewFFLayout("false")) d_ff_19 (
    .clk(IR24), .D(1'b1), .Q(d_ff_19_q), .reset(Inter24));  // open: Qn, preset, en
  RAM #(.addrWidth(10), .dataWidth(32), .bus("separate"), .Select("high")) ram_1 (
    .addr(Result[11:2]), .din(MDin), .data(ram_1_data), .str(MemWrite), .clk(CLK), .ld(MemToReg), .clr(RST));  // open: sel
  D_Flip_Flop #(.trigger("rising"), .Pre_Clr_Positions("LEGACY"), .NegatePresetClear("false"), .enable("true"), .NewFFLayout("false")) d_ff_20 (
    .clk(IR4), .D(1'b1), .Q(d_ff_20_q), .reset(Inter4));  // open: Qn, preset, en
  or or_39 (or_39_out, d_ff_16_q, Inter9);
  or or_40 (or_40_out, d_ff_17_q, Inter14);
  or or_41 (or_41_out, d_ff_18_q, Inter19);
  or or_42 (or_42_out, d_ff_19_q, Inter24);
  or or_43 (or_43_out, d_ff_20_q, Inter4);
  and and_23 (and_23_out, or_43_out, ~Ret4);  // AND_Gate
  and and_24 (and_24_out, or_39_out, ~Ret9);  // AND_Gate
  and and_25 (and_25_out, or_40_out, ~Ret14);  // AND_Gate
  and and_26 (and_26_out, or_41_out, ~Ret19);  // AND_Gate
  and and_27 (and_27_out, or_42_out, ~Ret24);  // AND_Gate
  Multiplexer #(.select(1), .width(16), .disabled("Z"), .enable("false")) multiplexer_13 (
    .in0(ram_1_data[15:0]), .in1(ram_1_data[31:16]), .out(multiplexer_13_out), .sel(Result[1]));
  assign bit_extender_5_out = {{16{1'b0}}, multiplexer_13_out};  // Bit_Extender bit_extender_5
  D_Flip_Flop #(.trigger("rising"), .Pre_Clr_Positions("LEGACY"), .NegatePresetClear("false"), .enable("true"), .NewFFLayout("false")) IR1_3 (
    .clk(CLK), .D(and_23_out), .Q(Inter4));  // open: Qn, preset, en, reset
  D_Flip_Flop #(.trigger("rising"), .Pre_Clr_Positions("LEGACY"), .NegatePresetClear("false"), .enable("true"), .NewFFLayout("false")) IR3_12 (
    .clk(CLK), .D(and_24_out), .Q(Inter9));  // open: Qn, preset, en, reset
  D_Flip_Flop #(.trigger("rising"), .Pre_Clr_Positions("LEGACY"), .NegatePresetClear("false"), .enable("true"), .NewFFLayout("false")) IR3_13 (
    .clk(CLK), .D(and_25_out), .Q(Inter14));  // open: Qn, preset, en, reset
  D_Flip_Flop #(.trigger("rising"), .Pre_Clr_Positions("LEGACY"), .NegatePresetClear("false"), .enable("true"), .NewFFLayout("false")) IR3_14 (
    .clk(CLK), .D(and_26_out), .Q(Inter19));  // open: Qn, preset, en, reset
  D_Flip_Flop #(.trigger("rising"), .Pre_Clr_Positions("LEGACY"), .NegatePresetClear("false"), .enable("true"), .NewFFLayout("false")) IR3_15 (
    .clk(CLK), .D(and_27_out), .Q(Inter24));  // open: Qn, preset, en, reset
  Multiplexer #(.select(1), .width(32), .disabled("Z"), .enable("false")) multiplexer_14 (
    .in0(ram_1_data), .in1(bit_extender_5_out), .out(MDout), .sel(lhu));
  or or_44 (W5, Inter5, d_ff_21_q);
  or or_45 (W10, Inter10, d_ff_22_q);
  or or_46 (W15, Inter15, d_ff_23_q);
  or or_47 (W20, Inter20, d_ff_24_q);
  or or_48 (W25, Inter25, d_ff_25_q);
  D_Flip_Flop #(.trigger("rising"), .Pre_Clr_Positions("LEGACY"), .NegatePresetClear("false"), .enable("true"), .NewFFLayout("false")) d_ff_21 (
    .clk(IR5), .D(1'b1), .Q(d_ff_21_q), .reset(Inter5));  // open: Qn, preset, en
  D_Flip_Flop #(.trigger("rising"), .Pre_Clr_Positions("LEGACY"), .NegatePresetClear("false"), .enable("true"), .NewFFLayout("false")) d_ff_22 (
    .clk(IR10), .D(1'b1), .Q(d_ff_22_q), .reset(Inter10));  // open: Qn, preset, en
  D_Flip_Flop #(.trigger("rising"), .Pre_Clr_Positions("LEGACY"), .NegatePresetClear("false"), .enable("true"), .NewFFLayout("false")) d_ff_23 (
    .clk(IR15), .D(1'b1), .Q(d_ff_23_q), .reset(Inter15));  // open: Qn, preset, en
  D_Flip_Flop #(.trigger("rising"), .Pre_Clr_Positions("LEGACY"), .NegatePresetClear("false"), .enable("true"), .NewFFLayout("false")) d_ff_24 (
    .clk(IR20), .D(1'b1), .Q(d_ff_24_q), .reset(Inter20));  // open: Qn, preset, en
  D_Flip_Flop #(.trigger("rising"), .Pre_Clr_Positions("LEGACY"), .NegatePresetClear("false"), .enable("true"), .NewFFLayout("false")) d_ff_25 (
    .clk(IR25), .D(1'b1), .Q(d_ff_25_q), .reset(Inter25));  // open: Qn, preset, en
  or or_49 (or_49_out, d_ff_21_q, Inter5);
  or or_50 (or_50_out, d_ff_22_q, Inter10);
  or or_51 (or_51_out, d_ff_23_q, Inter15);
  or or_52 (or_52_out, d_ff_24_q, Inter20);
  and and_28 (and_28_out, or_52_out, ~Ret20);  // AND_Gate
  or or_53 (or_53_out, d_ff_25_q, Inter25);
  and and_29 (and_29_out, or_53_out, ~Ret25);  // AND_Gate
  and and_30 (and_30_out, or_49_out, ~Ret5);  // AND_Gate
  and and_31 (and_31_out, or_50_out, ~Ret10);  // AND_Gate
  and and_32 (and_32_out, or_51_out, ~Ret15);  // AND_Gate
  D_Flip_Flop #(.trigger("rising"), .Pre_Clr_Positions("LEGACY"), .NegatePresetClear("false"), .enable("true"), .NewFFLayout("false")) IR3_16 (
    .clk(CLK), .D(and_28_out), .Q(Inter20));  // open: Qn, preset, en, reset
  D_Flip_Flop #(.trigger("rising"), .Pre_Clr_Positions("LEGACY"), .NegatePresetClear("false"), .enable("true"), .NewFFLayout("false")) IR3_17 (
    .clk(CLK), .D(and_29_out), .Q(Inter25));  // open: Qn, preset, en, reset
  D_Flip_Flop #(.trigger("rising"), .Pre_Clr_Positions("LEGACY"), .NegatePresetClear("false"), .enable("true"), .NewFFLayout("false")) IR2_3 (
    .clk(CLK), .D(and_30_out), .Q(Inter5));  // open: Qn, preset, en, reset
  D_Flip_Flop #(.trigger("rising"), .Pre_Clr_Positions("LEGACY"), .NegatePresetClear("false"), .enable("true"), .NewFFLayout("false")) IR2_4 (
    .clk(CLK), .D(and_31_out), .Q(Inter10));  // open: Qn, preset, en, reset
  D_Flip_Flop #(.trigger("rising"), .Pre_Clr_Positions("LEGACY"), .NegatePresetClear("false"), .enable("true"), .NewFFLayout("false")) IR3_18 (
    .clk(CLK), .D(and_32_out), .Q(Inter15));  // open: Qn, preset, en, reset
  Priority_Encoder #(.select(5), .disabled("Z")) priority_encoder_1 (
    .in0(1'b0), .in1(Inter1), .in2(Inter2), .in3(Inter3), .in4(Inter4), .in5(Inter5), .in6(Inter6),
    .in7(Inter7), .in8(Inter8), .in9(Inter9), .in10(Inter10), .in11(Inter11), .in12(Inter12), .in13(Inter13),
    .in14(Inter14), .in15(Inter15), .in16(Inter16), .in17(Inter17), .in18(Inter18), .in19(Inter19),
    .in20(Inter20), .in21(Inter21), .in22(Inter22), .in23(Inter23), .in24(Inter24), .in25(Inter25),
    .out(priority_encoder_1_out), .gs(Interr));  // open: in26, in27, in28, in29, in30, in31, en_out, en_in
  Register #(.width(5), .trigger("rising"), .Select("low")) \u_中断号  (
    .D(priority_encoder_1_out), .en(Interrupt), .Q(\中断号_q ), .clk(CLK), .clr(RST));
  Multiplexer #(.select(5), .width(32), .disabled("Z"), .enable("false")) multiplexer_15 (
    .in1(32'h2a8), .in2(32'h18dc), .in3(32'h2f10), .in4(32'h4544), .in5(32'h5b78), .in6(32'h71ac),
    .in7(32'h87e0), .in8(32'h9e14), .in9(32'hb448), .in10(32'hca7c), .in11(32'he0b0), .in12(32'hf6e4),
    .in13(32'h10d18), .in14(32'h1234c), .in15(32'h13980), .in16(32'h14fb4), .in17(32'h165e8),
    .in18(32'h17c1c), .in19(32'h19250), .in20(32'h1a884), .in21(32'h1beb8), .in22(32'h1d4ec),
    .in23(32'h1eb20), .in24(32'h20154), .in25(32'h21788), .out(InterAddr), .sel(priority_encoder_1_out));  // open: in0, in26, in27, in28, in29, in30, in31
  Decoder #(.select(5), .tristate("false"), .disabled("Z"), .enable("false")) decoder_1 (
    .out1(decoder_1_out1), .out2(decoder_1_out2), .out3(decoder_1_out3), .out4(decoder_1_out4),
    .out5(decoder_1_out5), .out6(decoder_1_out6), .out7(decoder_1_out7), .out8(decoder_1_out8),
    .out9(decoder_1_out9), .out10(decoder_1_out10), .out11(decoder_1_out11), .out12(decoder_1_out12),
    .out13(decoder_1_out13), .out14(decoder_1_out14), .out15(decoder_1_out15), .out16(decoder_1_out16),
    .out17(decoder_1_out17), .out18(decoder_1_out18), .out19(decoder_1_out19), .out20(decoder_1_out20),
    .out21(decoder_1_out21), .out22(decoder_1_out22), .out23(decoder_1_out23), .out24(decoder_1_out24),
    .out25(decoder_1_out25), .sel(\中断号_q ));  // open: out0, out26, out27, out28, out29, out30, out31
  and and_33 (Ret25, decoder_1_out25, uret);
  and and_34 (Ret1, uret, decoder_1_out1);
  and and_35 (Ret2, decoder_1_out2, uret);
  and and_36 (Ret3, decoder_1_out3, uret);
  and and_37 (Ret10, uret, decoder_1_out10);
  and and_38 (Ret11, decoder_1_out11, uret);
  and and_39 (Ret12, decoder_1_out12, uret);
  and and_40 (Ret19, uret, decoder_1_out19);
  and and_41 (Ret20, decoder_1_out20, uret);
  and and_42 (Ret21, decoder_1_out21, uret);
  and and_43 (Ret4, uret, decoder_1_out4);
  and and_44 (Ret5, uret, decoder_1_out5);
  and and_45 (Ret6, uret, decoder_1_out6);
  and and_46 (Ret13, uret, decoder_1_out13);
  and and_47 (Ret14, decoder_1_out14, uret);
  and and_48 (Ret15, decoder_1_out15, uret);
  and and_49 (Ret22, uret, decoder_1_out22);
  and and_50 (Ret23, decoder_1_out23, uret);
  and and_51 (Ret24, decoder_1_out24, uret);
  Comparator #(.width(5), .mode("unsigned")) comparator_4 (
    .a(IR[11:7]), .b(5'b00001), .eq(comparator_4_eq));  // open: gt, lt
  and and_52 (and_52_out, comparator_4_eq, RegWrite);
  Comparator #(.width(5), .mode("unsigned")) comparator_5 (
    .a(IR[11:7]), .b(5'b00011), .eq(comparator_5_eq));  // open: gt, lt
  Comparator #(.width(5), .mode("unsigned")) comparator_6 (
    .a(IR[11:7]), .b({5{1'b1}}), .eq(comparator_6_eq));  // open: gt, lt
  and and_53 (Ret7, uret, decoder_1_out7);
  and and_54 (Ret8, uret, decoder_1_out8);
  and and_55 (Ret9, uret, decoder_1_out9);
  Register #(.width(32), .trigger("rising"), .Select("low")) \X坐标  (
    .D(RDin), .en(and_52_out), .Q({\X坐标_q , X}), .clk(CLK), .clr(RST));
  Register #(.width(32), .trigger("rising"), .Select("low")) u_Color (
    .D(RDin), .en(and_56_out), .Q({Color_q, Color}), .clk(CLK), .clr(RST));
  and and_56 (and_56_out, comparator_5_eq, RegWrite);
  Register #(.width(32), .trigger("rising"), .Select("low")) u_interrupt (
    .D(RDin), .en(and_57_out), .Q({interrupt_q, inter}), .clk(CLK), .clr(RST));
  and and_57 (and_57_out, comparator_6_eq, RegWrite);
  and and_58 (Ret16, uret, decoder_1_out16);
  and and_59 (Ret17, decoder_1_out17, uret);
  and and_60 (Ret18, decoder_1_out18, uret);
  Comparator #(.width(5), .mode("unsigned")) comparator_7 (
    .a(IR[11:7]), .b(5'b00111), .eq(comparator_7_eq));  // open: gt, lt
  Comparator #(.width(32), .mode("unsigned")) comparator_8 (.a(RDin), .b(32'h1), .eq(comparator_8_eq));  // open: gt, lt
  Comparator #(.width(5), .mode("unsigned")) comparator_9 (
    .a(IR[11:7]), .b(5'b00010), .eq(comparator_9_eq));  // open: gt, lt
  and and_61 (and_61_out, comparator_9_eq, RegWrite);
  Register #(.width(32), .trigger("rising"), .Select("low")) u_EPC (
    .D(nextPC), .en(Interrupt), .Q(EPC), .clk(CLK), .clr(RST));
  and and_62 (and_62_out, comparator_7_eq, RegWrite, comparator_8_eq);
  Register #(.width(32), .trigger("rising"), .Select("low")) \Y坐标  (
    .D(RDin), .en(and_61_out), .Q({\Y坐标_q , Y}), .clk(CLK), .clr(RST));
  or or_54 (Clr, RST, and_62_out);
  Register #(.width(1), .trigger("rising"), .Select("low")) IE (
    .D(Interrupt), .en(or_55_out), .Q(IE_q), .clk(CLK), .clr(RST));
  or or_55 (or_55_out, Interrupt, uret);
  not not_3 (not_3_out, IE_q);
  and and_63 (and_63_out, Interr, not_4_out);
  not not_4 (not_4_out, inter);
  and and_64 (Interrupt, not_3_out, and_63_out);

  // Other names for the same wires on the sheet: imm12_S[11:0] = {IR[31:25], IR[11:7]}; W_num[4:0] = IR[11:7];
  //   imm32_U[31:12] = IR[31:12]; imm12_I[11:0] = IR[31:20]; R2_num[4:0] = IR[24:20]; R2[31:0] = MDin; X0 = Result[1]

  // Notes on the sheet:
  //   游戏界面
  //   Reset 
  //   Reset 
  //   Reset 
  //   Reset 
  //   Reset 
  //   指令存储器
  //   指令字
  //   contents of rom_1 (hex, n*v repeats v):
  //   100f93 400793 7c00813 893 713 93 1808093 300113 110113 73 ff011ce3 170713 fef714e3 713 113 1810113
  //   300093 108093 73 ff009ce3 170713 fef714e3 293 313 393 693 593 613 f93 100713 ae68c63 200713 10e68463
  //   300713 e68863 400713 1ce68463 fe1ff06f 100f93 100393 2800093 2800113 5600713 73 108093 fee09ce3
  //   2300093 3c00113 5b00713 73 108093 fee09ce3 2d00093 2d00113 f00713 73 108093 110113 fff70713 fe0718e3
  //   5100093 2d00113 f00713 73 fff08093 110113 fff70713 fe0718e3 3f00093 2800113 5f00713 73 110113
  //   fee11ce3 a00893 73 100f93 100393 3f00913 3f00993 fef90093 fef98113 2200713 73 108093 110113 fff70713
  //   fe0718e3 1190093 fef98113 2200713 73 fff08093 110113 fff70713 fe0718e3 a00893 73 100f93 100393
  //   3f00913 3f00993 fef90093 898113 1000713 73 fff10113 fff70713 fe071ae3 900713 73 108093 fff10113
  //   fff70713 fe0718e3 1000713 73 108093 fff70713 fe071ae3 900713 73 108093 110113 fff70713 fe0718e3
  //   1000713 73 110113 fff70713 fe071ae3 900713 73 fff08093 110113 fff70713 fe0718e3 1000713 73 fff08093
  //   fff70713 fe071ae3 900713 73 fff08093 fff10113 fff70713 fe0718e3 a00893 73 100f93 100393 3f00913
  //   3f00993 a90093 98113 a00713 73 108093 110113 fff70713 fe0718e3 1100713 73 108093 fff10113 fff70713
  //   fe0718e3 a00893 73 160613 100713 e59463 7440006f 200713 e59463 6e50006f c00913 c00993 ff690093
  //   ff698113 1400713 73 108093 110113 fff70713 fe0718e3 a90093 ff698113 1400713 73 fff08093 110113
  //   fff70713 fe0718e3 100e93 e9e93 1d2e2b3 28793 179713 279813 f77733 1077733 100813 281813 1077733
  //   41070e63 28793 179713 279813 f77733 1077733 100813 381813 1077733 3f070c63 28793 179713 279813
  //   f77733 1077733 100813 481813 1077733 3d070a63 28793 179713 279813 f77733 1077733 100813 781813
  //   1077733 3b070863 28793 179713 279813 f77733 1077733 100813 881813 1077733 39070663 28793 179713
  //   279813 f77733 1077733 100813 981813 1077733 37070463 28793 179713 279813 f77733 1077733 100813
  //   c81813 1077733 35070263 28793 179713 279813 f77733 1077733 100813 d81813 1077733 33070063 28793
  //   179713 279813 f77733 1077733 100813 e81813 1077733 2f070e63 28793 179713 279813 f77733 1077733
  //   100813 1181813 1077733 2d070c63 28793 179713 279813 f77733 1077733 100813 1281813 1077733 2b070a63
  //   28793 179713 279813 f77733 1077733 100813 1381813 1077733 29070863 28793 179713 279813 f77733
  //   1077733 100813 1681813 1077733 27070663 28793 179713 279813 f77733 1077733 100813 1781813 1077733
  //   25070463 28793 179713 279813 f77733 1077733 100813 1881813 1077733 23070263 28793 579713 a79813
  //   f77733 1077733 100813 a81813 1077733 21070063 28793 579713 a79813 f77733 1077733 100813 b81813
  //   1077733 1d070e63 28793 579713 a79813 f77733 1077733 100813 c81813 1077733 1b070c63 28793 579713
  //   a79813 f77733 1077733 100813 d81813 1077733 19070a63 28793 579713 a79813 f77733 1077733 100813
  //   e81813 1077733 17070863 28793 579713 a79813 f77733 1077733 100813 f81813 1077733 15070663 28793
  //   579713 a79813 f77733 1077733 100813 1081813 1077733 13070463 28793 579713 a79813 f77733 1077733
  //   100813 1181813 1077733 11070263 28793 579713 a79813 f77733 1077733 100813 1281813 1077733 f070063
  //   28793 579713 a79813 f77733 1077733 100813 1381813 1077733 b070e63 28793 579713 a79813 f77733 1077733
  //   100813 1481813 1077733 9070c63 28793 579713 a79813 f77733 1077733 100813 1581813 1077733 7070a63
  //   28793 579713 a79813 f77733 1077733 100813 1681813 1077733 5070863 28793 579713 a79813 f77733 1077733
  //   100813 1781813 1077733 3070663 28793 579713 a79813 f77733 1077733 100813 1881813 1077733 1070463
  //   c0006f 100693 200073 28793 679713 c79813 f77733 1077733 100813 c81813 1077733 fd070ce3 28793 679713
  //   c79813 f77733 1077733 100813 d81813 1077733 fb070ae3 28793 679713 c79813 f77733 1077733 100813
  //   e81813 1077733 f90708e3 28793 679713 c79813 f77733 1077733 100813 1181813 1077733 f70706e3 28793
  //   679713 c79813 f77733 1077733 100813 1281813 1077733 f50704e3 28793 679713 c79813 f77733 1077733
  //   100813 1381813 1077733 f30702e3 28793 679713 c79813 f77733 1077733 100813 1681813 1077733 f10700e3
  //   28793 679713 c79813 f77733 1077733 100813 1781813 1077733 ed070ee3 28793 679713 c79813 f77733
  //   1077733 100813 1881813 10777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
  //   rs1
  //   rs2
  //   rd
  //   Reset 
  //   Reset 
  //   Reset 
  //   Reset 
  //   Reset 
  //   Beq
  //   Bgeu
  //   Bne
  //   MemToReg
  //   MemWrite
  //   AluOP
  //   AluSrcB
  //   RegWrite
  //   Reset 
  //   调试界面
  //   Reset 
  //   Reset 
  //   Reset 
  //   Reset 
  //   数据存储器
  //   Reset 
  //   Reset 
  //   Reset 
  //   Reset 
  //   Reset 
  //   Reset 
  //   Reset 
  //   Reset 
  //   Reset 
  //   Reset 
endmodule

// 单周期硬布线控制器
module \单周期硬布线控制器  (
  input  [4:0] OP,
  input  [4:0] Funct,
  output [3:0] ALU_OP,
  output MemToReg,
  output MemWrite,
  output ALU_SRC,
  output RegWrite,
  output ecall,
  output S_type,
  output Beq,
  output Bne,
  output Jalr,
  output JAL,
  output U_type,
  output BGEU,
  output LHU,
  output URET
);

  \运算控制器自动生成  \u_运算控制器自动生成_1  (
    .OP2(OP[0]), .OP3(OP[1]), .OP4(OP[2]), .OP5(OP[3]), .OP6(OP[4]), .F12(Funct[0]), .F13(Funct[1]),
    .F14(Funct[2]), .F25(Funct[3]), .F30(Funct[4]), .S0(ALU_OP[0]), .S1(ALU_OP[1]), .S2(ALU_OP[2]),
    .S3(ALU_OP[3]));
  \控制信号自动生成  \u_控制信号自动生成_1  (
    .OP2(OP[0]), .OP3(OP[1]), .OP4(OP[2]), .OP5(OP[3]), .OP6(OP[4]), .MemToReg(MemToReg), .F12(Funct[0]),
    .F13(Funct[1]), .F14(Funct[2]), .F25(Funct[3]), .F30(Funct[4]), .MemWrite(MemWrite), .ALU_SRC(ALU_SRC),
    .RegWrite(RegWrite), .ecall(ecall), .S_Type(S_type), .BEQ(Beq), .BNE(Bne), .JALR(Jalr), .JAL(JAL),
    .U_Type(U_type), .BGEU(BGEU), .LHU(LHU), .URET(URET));

  // Other names for the same wires on the sheet: OP_CODE[4:0] = OP

  // Notes on the sheet:
  //   运算器控制器，根据指令生成运算器功能选择信号
  //   控制信号生成，产生数据通路需要的其他控制信号
endmodule

module \单周期RISC_V  (
  input  IR1,
  input  IR2,
  input  IR3,
  output RegWrite,
  output MemWrite,
  output [31:0] PC,
  output [31:0] IR,
  output [31:0] RDin,
  output [31:0] MDin,
  output [31:0] LedData
);

  wire AluSrcB, and_1_out, and_2_out, and_3_out, and_4_out, and_5_out, beq, bgeu, bne, Branch, CLK,
       clock_2_out, comparator_1_eq, comparator_2_eq, comparator_2_lt, controlled_buffer_1_out, d_ff_1_q,
       ecall, equal, Go, halt, IR1_t, IR2_t, IR3_t, IRA, IRB, IRC, jal, jalr, lhu, MemToReg, MoreAndEqu,
       nand_1_out, not_1_out, not_2_out, not_3_out, not_4_out, not_5_out, or_3_out, PCToReg, RST, S_type,
       U_type, W1, W2, W3;
  wire [3:0] AluOP;
  wire [4:0] multiplexer_5_out, multiplexer_6_out;
  wire [11:0] imm12_B;
  wire [12:0] CNT_num;
  wire [15:0] multiplexer_11_out, \分支成功数 , \总周期数 ;
  wire [19:0] imm20_J;
  wire [31:0] adder_1_out, adder_2_out, adder_3_out, and_6_out, bit_extender_1_out, bit_extender_2_out,
       bit_extender_3_out, bit_extender_4_out, bit_extender_5_out, MDout, multiplexer_1_out,
       multiplexer_2_out, multiplexer_3_out, multiplexer_7_out, multiplexer_9_out, multiplexer_10_out, PC_4,
       R1, ram_1_data, Result, RPCin;

  Clock #(.highDuration(1), .lowDuration(1)) clock_1 (.out(CLK));
  Button _1 (.out(IRA));
  Button _2 (.out(IRB));
  Button _3 (.out(IRC));
  Button \u_继续运行  (.out(Go));
  LED #(.active("true")) led_1 (.in(W1));
  LED #(.active("true")) led_2 (.in(W2));
  LED #(.active("true")) led_3 (.in(W3));
  // Probe on \分支成功数 
  Hex_Digit_Display hex_digit_display_1 (.value(LedData[31:28]));  // open: dp
  assign bit_extender_1_out = {{12{imm20_J[19]}}, imm20_J};  // Bit_Extender bit_extender_1
  Hex_Digit_Display hex_digit_display_2 (.value(LedData[27:24]));  // open: dp
  Hex_Digit_Display hex_digit_display_3 (.value(LedData[23:20]));  // open: dp
  not not_1 (not_1_out, equal);
  Comparator #(.width(32), .mode("twosComplement")) comparator_1 (
    .a(R1), .b(32'ha), .eq(comparator_1_eq));  // open: gt, lt
  Adder #(.width(32)) adder_1 (.a(bit_extender_1_out), .b(PC), .out(adder_1_out));  // open: cin, cout
  assign bit_extender_2_out = {{20{imm12_B[11]}}, imm12_B};  // Bit_Extender bit_extender_2
  Hex_Digit_Display hex_digit_display_4 (.value(LedData[15:12]));  // open: dp
  Hex_Digit_Display hex_digit_display_5 (.value(LedData[19:16]));  // open: dp
  and and_1 (and_1_out, beq, equal);
  or or_1 (Branch, and_1_out, and_2_out, and_3_out);
  and and_2 (and_2_out, not_1_out, bne);
  and and_3 (and_3_out, MoreAndEqu, bgeu);
  and and_4 (and_4_out, ecall, not_2_out);
  not not_2 (not_2_out, comparator_1_eq);
  and and_5 (and_5_out, comparator_1_eq, ecall);
  not not_3 (not_3_out, Go);
  Multiplexer #(.select(1), .width(32), .disabled("Z"), .enable("false")) multiplexer_1 (
    .in0(PC_4), .in1(adder_1_out), .out(multiplexer_1_out), .sel(jal));
  Multiplexer #(.select(1), .width(32), .disabled("Z"), .enable("false")) multiplexer_2 (
    .in0(multiplexer_1_out), .in1(and_6_out), .out(multiplexer_2_out), .sel(jalr));
  assign and_6_out = Result & 32'hfffffffe;  // AND_Gate and_6, 32 bits wide
  Adder #(.width(32)) adder_2 (.a(bit_extender_2_out), .b(PC), .out(adder_2_out));  // open: cin, cout
  Hex_Digit_Display hex_digit_display_6 (.value(LedData[7:4]));  // open: dp
  Hex_Digit_Display hex_digit_display_7 (.value(LedData[11:8]));  // open: dp
  // Probe on \总周期数 
  Counter #(.width(16), .max('hffff), .ongoal("wrap"), .trigger("rising"), .behavior("new")) counter_1 (
    .count(Branch), .Q(\分支成功数 ), .clk(CLK), .clr(RST));  // open: load, D, carry, preset, down
  Register #(.width(32), .trigger("rising"), .Select("low")) register_1 (
    .D(MDin), .en(and_4_out), .Q(LedData), .clk(CLK), .clr(RST));
  and and_7 (halt, and_5_out, not_3_out);
  Multiplexer #(.select(1), .width(32), .disabled("Z"), .enable("false")) multiplexer_3 (
    .in0(multiplexer_2_out), .in1(adder_2_out), .out(multiplexer_3_out), .sel(Branch));
  not not_4 (not_4_out, halt);
  Hex_Digit_Display hex_digit_display_8 (.value(LedData[3:0]));  // open: dp
  Register #(.width(32), .trigger("rising"), .Select("low")) u_PC (
    .D(multiplexer_3_out), .en(not_4_out), .Q(PC), .clk(CLK), .clr(RST));
  not not_5 (not_5_out, halt);
  or or_2 (IR1_t, IR1, IRA);
  Counter #(.width(16), .max('hffff), .ongoal("wrap"), .trigger("rising"), .behavior("new")) counter_2 (
    .count(not_5_out), .Q(\总周期数 ), .clk(CLK), .clr(RST));  // open: load, D, carry, preset, down
  or or_3 (or_3_out, jal, jalr);
  or or_4 (PCToReg, or_3_out, U_type);
  Multiplexer #(.select(1), .width(32), .disabled("Z"), .enable("false")) multiplexer_4 (
    .in0(PC_4), .in1(adder_3_out), .out(RPCin), .sel(U_type));
  Adder #(.width(32)) adder_3 (.a({IR[31:12], {12{1'b0}}}), .b(PC), .out(adder_3_out));  // open: cin, cout
  // RiscV_Probe riscv_probe_1: pin names not known; wires that end beside it: IR
  Adder #(.width(32)) adder_4 (.a(PC), .b(32'h4), .out(PC_4));  // open: cin, cout
  or or_5 (IR2_t, IR2, IRB);
  ROM #(.addrWidth(10), .dataWidth(32), .Select("high")) rom_1 (.addr(PC[11:2]), .data(IR));
  or or_6 (IR3_t, IR3, IRC);
  \单周期硬布线控制器  \u_单周期硬布线控制器_1  (
    .Funct({IR[30], IR[25], IR[14:12]}), .OP(IR[6:2]), .ALU_OP(AluOP), .MemToReg(MemToReg),
    .MemWrite(MemWrite), .ALU_SRC(AluSrcB), .RegWrite(RegWrite), .ecall(ecall), .S_type(S_type), .Jalr(jalr),
    .Beq(beq), .JAL(jal), .Bne(bne), .U_type(U_type), .BGEU(bgeu), .LHU(lhu));  // open: URET
  Multiplexer #(.select(1), .width(5), .disabled("Z"), .enable("false")) multiplexer_5 (
    .in0(IR[19:15]), .in1(5'b10001), .out(multiplexer_5_out), .sel(ecall));
  Multiplexer #(.select(1), .width(5), .disabled("Z"), .enable("false")) multiplexer_6 (
    .in0(IR[24:20]), .in1(5'b01010), .out(multiplexer_6_out), .sel(ecall));
  Multiplexer #(.select(1), .width(32), .disabled("Z"), .enable("false")) multiplexer_7 (
    .in0(Result), .in1(MDout), .out(multiplexer_7_out), .sel(MemToReg));
  Shifter #(.width(12), .shift("ll")) shifter_1 (
    .in({IR[31], IR[7], IR[30:25], IR[11:8]}), .\dist (4'b0001), .out(imm12_B));
  Shifter #(.width(20), .shift("ll")) shifter_2 (
    .in({IR[31], IR[19:12], IR[20], IR[30:21]}), .\dist (5'b00001), .out(imm20_J));
  Multiplexer #(.select(1), .width(32), .disabled("Z"), .enable("false")) multiplexer_8 (
    .in0(multiplexer_7_out), .in1(RPCin), .out(RDin), .sel(PCToReg));
  Regifile regifile_1 (
    .Din(RDin), .Clk(CLK), .R1(R1), .R2(MDin), .WE(RegWrite), .W_num(IR[11:7]), .R1_num(multiplexer_5_out),
    .R2_num(multiplexer_6_out));
  assign bit_extender_3_out = {{20{IR[31]}}, IR[31:20]};  // Bit_Extender bit_extender_3
  assign bit_extender_4_out = {{20{IR[31]}}, {IR[31:25], IR[11:7]}};  // Bit_Extender bit_extender_4
  Multiplexer #(.select(1), .width(32), .disabled("Z"), .enable("false")) multiplexer_9 (
    .in0(bit_extender_3_out), .in1(bit_extender_4_out), .out(multiplexer_9_out), .sel(S_type));
  Multiplexer #(.select(1), .width(32), .disabled("Z"), .enable("false")) multiplexer_10 (
    .in0(MDin), .in1(multiplexer_9_out), .out(multiplexer_10_out), .sel(AluSrcB));
  ALU alu_1 (
    .X(R1), .Y(multiplexer_10_out), .AluOP(AluOP), .Equal(equal), .Result(Result), .out_4(MoreAndEqu));  // open: Result_2, out_6
  D_Flip_Flop #(.trigger("high"), .Pre_Clr_Positions("LEGACY"), .NegatePresetClear("false"), .enable("true"), .NewFFLayout("false")) d_ff_1 (.Q(d_ff_1_q));  // open: clk, D, Qn, preset, en, reset
  // Probe on 13'hc
  Comparator #(.width(13), .mode("twosComplement")) comparator_2 (
    .a(CNT_num), .b(13'hc), .eq(comparator_2_eq), .lt(comparator_2_lt));  // open: gt
  Clock #(.highDuration(1), .lowDuration(1)) clock_2 (.out(clock_2_out));
  Counter #(.width(13), .max('h1fff), .ongoal("stay"), .trigger("rising"), .behavior("old")) counter_3 (
    .count(comparator_2_lt), .Q(CNT_num), .clk(clock_2_out));  // open: load, D, carry, clr, preset
  nand nand_1 (nand_1_out, d_ff_1_q, comparator_2_eq);
  assign controlled_buffer_1_out = nand_1_out ? clock_2_out : 1'bz;  // Controlled_Buffer controlled_buffer_1
  Pull_Resistor #(.pull(1)) pull_resistor_1 (.node(controlled_buffer_1_out));
  RAM #(.addrWidth(10), .dataWidth(32), .bus("separate"), .Select("high")) ram_1 (
    .addr(Result[11:2]), .din(MDin), .data(ram_1_data), .str(MemWrite), .clk(CLK), .ld(MemToReg), .clr(RST));  // open: sel
  assign bit_extender_5_out = {{16{1'b0}}, multiplexer_11_out};  // Bit_Extender bit_extender_5
  Multiplexer #(.select(1), .width(16), .disabled("Z"), .enable("false")) multiplexer_11 (
    .in0(ram_1_data[15:0]), .in1(ram_1_data[31:16]), .out(multiplexer_11_out), .sel(Result[1]));
  Multiplexer #(.select(1), .width(32), .disabled("Z"), .enable("false")) multiplexer_12 (
    .in0(ram_1_data), .in1(bit_extender_5_out), .out(MDout), .sel(lhu));

  // Other names for the same wires on the sheet: imm12_S[11:0] = {IR[31:25], IR[11:7]}; imm32_U[31:12] = IR[31:12];
  //   imm12_I[11:0] = IR[31:20]; R2[31:0] = MDin; X = Result[1]

  // Notes on the sheet:
  //   中断源
  //   中断等待指示
  //   总复位信号应将除ROM以外所有存储组件全部清零
  //   数码管输出
  //   数码管输出应该用寄存器锁存，否则显示数据只能一闪而过
  //   指令存储器
  //   指令字
  //   contents of rom_1 (hex, n*v repeats v):
  //   100493 100006f 100493 200913 300993 100006f 100493 200913 300993 100006f 100493 200913 300993
  //   100006f 100493 200913 300993 424000ef 100413 100493 1f49493 900533 2200893 73 24d493 48463 fedff06f
  //   900533 2200893 73 100493 249493 900533 2200893 73 48463 fedff06f 100493 1f49493 900533 2200893 73
  //   4034d493 900533 2200893 73 4044d493 900533 2200893 73 4044d493 900533 2200893 73 4044d493 900533
  //   2200893 73 4044d493 900533 2200893 73 4044d493 900533 2200893 73 4044d493 900533 2200893 73 4044d493
  //   900533 2200893 73 100413 1f41993 41f9d993 433 c00913 300b13 140413 f47413 800293 100313 499993
  //   89e9b3 1300533 2200893 73 406282b3 fe0294e3 140413 f00f93 1f47433 1c41413 800293 100313 49d993
  //   89e9b3 1300533 2200893 73 406282b3 fe0294e3 1c45413 406b0b33 b0463 f95ff06f 2b3 fff2c293 829293
  //   ff2e293 500533 2200893 73 fff00413 493 84a023 140413 448493 84a023 140413 448493 84a023 140413
  //   448493 84a023 140413 448493 84a023 140413 448493 84a023 140413 448493 84a023 140413 448493 84a023
  //   140413 448493 84a023 140413 448493 84a023 140413 448493 84a023 140413 448493 84a023 140413 448493
  //   84a023 140413 448493 84a023 140413 448493 84a023 140413 448493 84a023 140413 448493 140413 433
  //   3c00493 42983 4aa03 149a2b3 28663 134a023 1442023 ffc48493 fe9412e3 800533 2200893 73 440413 3c00493
  //   fc9416e3 a00893 73 100293 300313 800493 849493 7648493 1449493 900533 2200893 73 800e13 54d4b3
  //   64d4b3 900533 2200893 73 fffe0e13 fe0e14e3 a00893 73 13 430497 900533 2200893 73 430497 900533
  //   2200893 73 430497 900533 2200893 73 430497 900533 2200893 73 430497 900533 2200893 73 430497 900533
  //   2200893 73 430497 900533 2200893 73 430497 900533 2200893 73 a00893 73 313 1000e13 8400493 849493
  //   8348493 400913 891913 490913 849493 8248493 849493 8148493 891913 490913 891913 490913 932023
  //   12484b3 430313 fffe0e13 fe0e18e3 2000e13 313 35483 900533 2200893 73 230313 fffe0e13 fe0e14e3 a00893
  //   73 f00493 100913 409909b3 900533 2200893 73 fff48493 ff29f6e3 a00893 73 a00893 73 413 140413 800533
  //   2200893 73 240413 800533 2200893 73 340413 800533 2200893 73 440413 800533 2200893 73 540413 800533
  //   2200893 73 640413 800533 2200893 73 740413 800533 2200893 73 840413 800533 2200893 2200893 73 8067
  //   rs1
  //   rs2
  //   rd
  //   Beq
  //   Bgeu
  //   Bne
  //   MemToReg
  //   MemWrite
  //   AluOP
  //   AluSrcB
  //   RegWrite
  //   为方便自动评测，需要输出PC，IR，寄存器堆写如数据RDin
  //   RAM写使能MemWrite、RAM写入数据MDin等信号
  //   控制位
  //   暂停节拍，不能为0
  //   戳工具置1进入计数暂停模式，ctrl+k时钟自动运行到对应节拍暂停
  //   ctrl+k关闭时钟连续运行，将控制位置零，进入单步调试模式调试
  //   用这个时钟源需要去掉电路中的其他时钟源
  //   数据存储器
  //   可计数暂停的时钟源
endmodule

// 运算器控制器
module \运算控制器自动生成  (
  input  OP2,
  input  OP3,
  input  OP4,
  input  OP5,
  input  OP6,
  input  F12,
  input  F13,
  input  F14,
  input  F25,
  input  F30,
  output S0,
  output S1,
  output S2,
  output S3
);

  wire and_1_out, and_2_out, and_3_out, and_4_out, and_5_out, and_6_out, and_7_out, and_8_out, and_9_out,
       and_10_out, and_11_out, and_12_out, and_13_out, and_14_out, and_15_out, and_16_out, and_17_out,
       and_18_out, and_19_out, and_20_out, and_21_out, and_22_out, and_23_out, and_24_out, and_25_out,
       and_26_out, and_27_out, and_28_out, and_29_out, and_30_out, and_31_out, and_32_out, and_33_out,
       and_34_out, and_35_out, and_36_out, and_37_out, and_38_out, and_39_out, and_40_out, and_41_out,
       and_42_out, and_43_out, not_1_out, not_2_out, not_3_out, not_4_out, not_5_out, not_6_out, not_7_out,
       not_8_out, not_9_out, not_10_out, not_11_out, not_12_out, not_13_out, not_14_out, not_15_out,
       not_16_out, not_17_out, not_18_out, not_19_out, not_20_out, not_21_out, not_22_out, not_23_out,
       not_24_out, not_25_out, not_26_out, not_27_out, not_28_out, not_29_out, not_30_out, not_31_out,
       not_32_out, not_33_out, not_34_out, not_35_out, not_36_out, not_37_out, not_38_out, not_39_out,
       not_40_out, not_41_out, not_42_out, not_43_out, not_44_out, not_45_out, not_46_out, not_47_out,
       not_48_out, not_49_out, not_50_out, not_51_out, not_52_out, not_53_out, not_54_out, not_55_out,
       not_56_out, not_57_out, not_58_out, not_59_out, not_60_out, not_61_out, not_62_out, not_63_out,
       not_64_out, not_65_out, not_66_out, not_67_out, not_68_out, not_69_out, not_70_out, not_71_out,
       not_72_out, not_73_out, not_74_out, not_75_out, not_76_out, not_77_out, not_78_out, not_79_out,
       not_80_out, not_81_out, not_82_out, not_83_out, not_84_out, not_85_out, not_86_out, not_87_out,
       not_88_out, not_89_out, not_90_out, not_91_out, not_92_out, not_93_out, not_94_out, not_95_out,
       not_96_out, not_97_out, not_98_out, not_99_out, not_100_out, not_101_out, not_102_out, not_103_out,
       not_104_out, not_105_out, not_106_out, not_107_out, not_108_out, not_109_out, not_110_out,
       not_111_out, not_112_out, not_113_out, not_114_out, not_115_out, not_116_out, not_117_out,
       not_118_out, not_119_out, not_120_out, not_121_out, not_122_out, not_123_out, not_124_out,
       not_125_out, not_126_out, not_127_out, not_128_out, not_129_out, not_130_out, not_131_out,
       not_132_out, not_133_out, not_134_out, not_135_out, not_136_out, not_137_out, not_138_out,
       not_139_out, not_140_out, not_141_out, not_142_out, not_143_out, not_144_out, not_145_out,
       not_146_out, not_147_out, not_148_out, not_149_out, not_150_out, not_151_out, not_152_out,
       not_153_out, not_154_out, not_155_out, not_156_out, not_157_out, not_158_out, not_159_out,
       not_160_out, not_161_out, not_162_out, not_163_out, not_164_out, not_165_out, not_166_out,
       not_167_out, not_168_out, not_169_out, not_170_out, not_171_out, not_172_out, not_173_out,
       not_174_out, not_175_out, not_176_out, not_177_out, not_178_out, not_179_out, not_180_out,
       not_181_out, not_182_out, not_183_out, not_184_out, not_185_out, not_186_out, not_187_out,
       not_188_out, not_189_out, not_190_out, not_191_out, not_192_out, not_193_out, not_194_out,
       not_195_out, not_196_out, not_197_out, not_198_out, not_199_out, not_200_out, not_201_out,
       not_202_out, not_203_out, not_204_out, not_205_out, not_206_out, not_207_out, not_208_out,
       not_209_out, not_210_out, not_211_out, not_212_out, not_213_out, not_214_out, not_215_out,
       not_216_out, not_217_out, not_218_out, not_219_out, not_220_out, not_221_out, not_222_out,
       not_223_out, not_224_out, not_225_out, not_226_out, not_227_out, not_228_out, not_229_out,
       not_230_out, not_231_out, not_232_out, not_233_out, not_234_out, not_235_out, not_236_out,
       not_237_out, not_238_out, not_239_out, not_240_out, not_241_out, not_242_out;

  not not_1 (not_1_out, F30);
  not not_2 (not_2_out, F25);
  not not_3 (not_3_out, F14);
  not not_4 (not_4_out, F13);
  not not_5 (not_5_out, F12);
  not not_6 (not_6_out, OP6);
  not not_7 (not_7_out, OP3);
  not not_8 (not_8_out, OP2);
  not not_9 (not_9_out, F30);
  not not_10 (not_10_out, F25);
  not not_11 (not_11_out, OP6);
  not not_12 (not_12_out, OP3);
  not not_13 (not_13_out, OP2);
  not not_14 (not_14_out, F30);
  not not_15 (not_15_out, F25);
  not not_16 (not_16_out, F14);
  not not_17 (not_17_out, F12);
  not not_18 (not_18_out, OP6);
  not not_19 (not_19_out, OP3);
  not not_20 (not_20_out, OP2);
  not not_21 (not_21_out, F14);
  not not_22 (not_22_out, F13);
  not not_23 (not_23_out, F12);
  not not_24 (not_24_out, OP6);
  not not_25 (not_25_out, OP5);
  not not_26 (not_26_out, OP3);
  not not_27 (not_27_out, OP2);
  not not_28 (not_28_out, OP6);
  not not_29 (not_29_out, OP5);
  not not_30 (not_30_out, OP3);
  not not_31 (not_31_out, OP2);
  not not_32 (not_32_out, F13);
  not not_33 (not_33_out, F12);
  not not_34 (not_34_out, OP6);
  not not_35 (not_35_out, OP5);
  not not_36 (not_36_out, OP3);
  not not_37 (not_37_out, OP2);
  not not_38 (not_38_out, F14);
  not not_39 (not_39_out, F12);
  not not_40 (not_40_out, OP6);
  not not_41 (not_41_out, OP5);
  not not_42 (not_42_out, OP3);
  not not_43 (not_43_out, OP2);
  not not_44 (not_44_out, F25);
  not not_45 (not_45_out, F13);
  not not_46 (not_46_out, OP6);
  not not_47 (not_47_out, OP5);
  not not_48 (not_48_out, OP3);
  not not_49 (not_49_out, OP2);
  not not_50 (not_50_out, F14);
  not not_51 (not_51_out, F12);
  not not_52 (not_52_out, OP6);
  not not_53 (not_53_out, OP5);
  not not_54 (not_54_out, OP4);
  not not_55 (not_55_out, OP3);
  not not_56 (not_56_out, OP2);
  not not_57 (not_57_out, F14);
  not not_58 (not_58_out, F12);
  not not_59 (not_59_out, OP6);
  not not_60 (not_60_out, OP4);
  not not_61 (not_61_out, OP3);
  not not_62 (not_62_out, OP2);
  not not_63 (not_63_out, F14);
  not not_64 (not_64_out, F13);
  not not_65 (not_65_out, F12);
  not not_66 (not_66_out, OP4);
  not not_67 (not_67_out, OP3);
  not not_68 (not_68_out, OP2);
  not not_69 (not_69_out, F14);
  not not_70 (not_70_out, F13);
  not not_71 (not_71_out, OP4);
  not not_72 (not_72_out, OP3);
  not not_73 (not_73_out, OP2);
  not not_74 (not_74_out, OP4);
  not not_75 (not_75_out, F14);
  not not_76 (not_76_out, F13);
  not not_77 (not_77_out, F12);
  not not_78 (not_78_out, OP4);
  not not_79 (not_79_out, OP3);
  not not_80 (not_80_out, F13);
  not not_81 (not_81_out, OP6);
  not not_82 (not_82_out, OP5);
  not not_83 (not_83_out, OP4);
  not not_84 (not_84_out, OP3);
  not not_85 (not_85_out, OP2);
  not not_86 (not_86_out, F25);
  not not_87 (not_87_out, F14);
  not not_88 (not_88_out, F13);
  not not_89 (not_89_out, F12);
  not not_90 (not_90_out, OP6);
  not not_91 (not_91_out, OP3);
  not not_92 (not_92_out, OP2);
  not not_93 (not_93_out, F30);
  not not_94 (not_94_out, F25);
  not not_95 (not_95_out, OP6);
  not not_96 (not_96_out, OP3);
  not not_97 (not_97_out, OP2);
  not not_98 (not_98_out, F30);
  not not_99 (not_99_out, F25);
  not not_100 (not_100_out, F14);
  not not_101 (not_101_out, F12);
  not not_102 (not_102_out, OP6);
  not not_103 (not_103_out, OP3);
  not not_104 (not_104_out, OP2);
  not not_105 (not_105_out, OP6);
  not not_106 (not_106_out, OP5);
  not not_107 (not_107_out, OP3);
  not not_108 (not_108_out, OP2);
  not not_109 (not_109_out, F14);
  not not_110 (not_110_out, F12);
  not not_111 (not_111_out, OP6);
  not not_112 (not_112_out, OP5);
  not not_113 (not_113_out, OP3);
  not not_114 (not_114_out, OP2);
  not not_115 (not_115_out, F30);
  not not_116 (not_116_out, F25);
  not not_117 (not_117_out, F13);
  not not_118 (not_118_out, OP6);
  not not_119 (not_119_out, OP5);
  not not_120 (not_120_out, OP3);
  not not_121 (not_121_out, OP2);
  not not_122 (not_122_out, F30);
  not not_123 (not_123_out, F25);
  not not_124 (not_124_out, F13);
  not not_125 (not_125_out, OP6);
  not not_126 (not_126_out, OP3);
  not not_127 (not_127_out, OP2);
  not not_128 (not_128_out, F30);
  not not_129 (not_129_out, F25);
  not not_130 (not_130_out, F14);
  not not_131 (not_131_out, F13);
  not not_132 (not_132_out, F12);
  not not_133 (not_133_out, OP6);
  not not_134 (not_134_out, OP3);
  not not_135 (not_135_out, OP2);
  not not_136 (not_136_out, F25);
  not not_137 (not_137_out, F14);
  not not_138 (not_138_out, F13);
  not not_139 (not_139_out, F12);
  not not_140 (not_140_out, OP6);
  not not_141 (not_141_out, OP3);
  not not_142 (not_142_out, OP2);
  not not_143 (not_143_out, F30);
  not not_144 (not_144_out, F25);
  not not_145 (not_145_out, OP6);
  not not_146 (not_146_out, OP3);
  not not_147 (not_147_out, OP2);
  not not_148 (not_148_out, F30);
  not not_149 (not_149_out, F25);
  not not_150 (not_150_out, F14);
  not not_151 (not_151_out, OP6);
  not not_152 (not_152_out, OP3);
  not not_153 (not_153_out, OP2);
  not not_154 (not_154_out, F14);
  not not_155 (not_155_out, F13);
  not not_156 (not_156_out, F12);
  not not_157 (not_157_out, OP6);
  not not_158 (not_158_out, OP5);
  not not_159 (not_159_out, OP3);
  not not_160 (not_160_out, OP2);
  not not_161 (not_161_out, OP6);
  not not_162 (not_162_out, OP5);
  not not_163 (not_163_out, OP3);
  not not_164 (not_164_out, OP2);
  not not_165 (not_165_out, F14);
  not not_166 (not_166_out, F12);
  not not_167 (not_167_out, OP6);
  not not_168 (not_168_out, OP5);
  not not_169 (not_169_out, OP4);
  not not_170 (not_170_out, OP3);
  not not_171 (not_171_out, OP2);
  not not_172 (not_172_out, F14);
  not not_173 (not_173_out, F12);
  not not_174 (not_174_out, OP6);
  not not_175 (not_175_out, OP4);
  not not_176 (not_176_out, OP3);
  not not_177 (not_177_out, OP2);
  not not_178 (not_178_out, F14);
  not not_179 (not_179_out, F13);
  not not_180 (not_180_out, F12);
  not not_181 (not_181_out, OP4);
  not not_182 (not_182_out, OP3);
  not not_183 (not_183_out, OP2);
  not not_184 (not_184_out, F14);
  not not_185 (not_185_out, F13);
  not not_186 (not_186_out, OP4);
  not not_187 (not_187_out, OP3);
  not not_188 (not_188_out, OP2);
  not not_189 (not_189_out, OP4);
  not not_190 (not_190_out, F14);
  not not_191 (not_191_out, F13);
  not not_192 (not_192_out, F12);
  not not_193 (not_193_out, OP4);
  not not_194 (not_194_out, OP3);
  not not_195 (not_195_out, F13);
  not not_196 (not_196_out, OP6);
  not not_197 (not_197_out, OP5);
  not not_198 (not_198_out, OP4);
  not not_199 (not_199_out, OP3);
  not not_200 (not_200_out, OP2);
  not not_201 (not_201_out, OP4);
  not not_202 (not_202_out, OP3);
  not not_203 (not_203_out, OP2);
  not not_204 (not_204_out, F30);
  not not_205 (not_205_out, F25);
  not not_206 (not_206_out, F12);
  not not_207 (not_207_out, OP6);
  not not_208 (not_208_out, OP3);
  not not_209 (not_209_out, OP2);
  not not_210 (not_210_out, F30);
  not not_211 (not_211_out, F25);
  not not_212 (not_212_out, F14);
  not not_213 (not_213_out, F12);
  not not_214 (not_214_out, OP6);
  not not_215 (not_215_out, OP3);
  not not_216 (not_216_out, OP2);
  not not_217 (not_217_out, F30);
  not not_218 (not_218_out, F25);
  not not_219 (not_219_out, F14);
  not not_220 (not_220_out, OP6);
  not not_221 (not_221_out, OP3);
  not not_222 (not_222_out, OP2);
  not not_223 (not_223_out, F12);
  not not_224 (not_224_out, OP6);
  not not_225 (not_225_out, OP5);
  not not_226 (not_226_out, OP3);
  not not_227 (not_227_out, OP2);
  not not_228 (not_228_out, F13);
  not not_229 (not_229_out, F12);
  not not_230 (not_230_out, OP6);
  not not_231 (not_231_out, OP5);
  not not_232 (not_232_out, OP3);
  not not_233 (not_233_out, OP2);
  not not_234 (not_234_out, F14);
  not not_235 (not_235_out, F12);
  not not_236 (not_236_out, OP6);
  not not_237 (not_237_out, OP5);
  not not_238 (not_238_out, OP3);
  not not_239 (not_239_out, OP2);
  not not_240 (not_240_out, OP4);
  not not_241 (not_241_out, OP3);
  not not_242 (not_242_out, OP2);
  and and_1 (and_1_out, not_1_out, not_2_out, not_3_out, not_4_out, not_5_out, not_6_out, OP5, OP4, not_7_out, not_8_out);
  and and_2 (and_2_out, not_9_out, not_10_out, F14, F13, F12, not_11_out, OP5, OP4, not_12_out, not_13_out);
  and and_3 (and_3_out, not_14_out, not_15_out, not_16_out, F13, not_17_out, not_18_out, OP5, OP4, not_19_out, not_20_out);
  and and_4 (and_4_out, not_21_out, not_22_out, not_23_out, not_24_out, not_25_out, OP4, not_26_out, not_27_out);
  and and_5 (and_5_out, F14, F13, F12, not_28_out, not_29_out, OP4, not_30_out, not_31_out);
  and and_6 (and_6_out, F14, not_32_out, not_33_out, not_34_out, not_35_out, OP4, not_36_out, not_37_out);
  and and_7 (and_7_out, not_38_out, F13, not_39_out, not_40_out, not_41_out, OP4, not_42_out, not_43_out);
  and and_8 (and_8_out, F30, not_44_out, F14, not_45_out, F12, not_46_out, not_47_out, OP4, not_48_out, not_49_out);
  and and_9 (and_9_out, not_50_out, F13, not_51_out, not_52_out, not_53_out, not_54_out, not_55_out, not_56_out);
  and and_10 (and_10_out, not_57_out, F13, not_58_out, not_59_out, OP5, not_60_out, not_61_out, not_62_out);
  and and_11 (and_11_out, not_63_out, not_64_out, not_65_out, OP6, OP5, not_66_out, not_67_out, not_68_out);
  and and_12 (and_12_out, not_69_out, not_70_out, F12, OP6, OP5, not_71_out, not_72_out, not_73_out);
  and and_13 (and_13_out, OP6, OP5, not_74_out, OP3, OP2);
  and and_14 (and_14_out, not_75_out, not_76_out, not_77_out, OP6, OP5, not_78_out, not_79_out, OP2);
  and and_15 (and_15_out, F14, not_80_out, F12, not_81_out, not_82_out, not_83_out, not_84_out, not_85_out);
  and and_16 (and_16_out, F30, not_86_out, not_87_out, not_88_out, not_89_out, not_90_out, OP5, OP4, not_91_out, not_92_out);
  and and_17 (and_17_out, not_93_out, not_94_out, F14, F13, F12, not_95_out, OP5, OP4, not_96_out, not_97_out);
  and and_18 (and_18_out, not_98_out, not_99_out, not_100_out, F13, not_101_out, not_102_out, OP5, OP4, not_103_out, not_104_out);
  and and_19 (and_19_out, F14, F13, F12, not_105_out, not_106_out, OP4, not_107_out, not_108_out);
  and and_20 (and_20_out, not_109_out, F13, not_110_out, not_111_out, not_112_out, OP4, not_113_out, not_114_out);
  and and_21 (and_21_out, not_115_out, not_116_out, F14, not_117_out, F12, not_118_out, not_119_out, OP4, not_120_out, not_121_out);
  and and_22 (and_22_out, not_122_out, not_123_out, F14, not_124_out, F12, not_125_out, OP5, OP4, not_126_out, not_127_out);
  and and_23 (and_23_out, not_128_out, not_129_out, not_130_out, not_131_out, not_132_out, not_133_out, OP5, OP4, not_134_out, not_135_out);
  and and_24 (and_24_out, F30, not_136_out, not_137_out, not_138_out, not_139_out, not_140_out, OP5, OP4, not_141_out, not_142_out);
  and and_25 (and_25_out, not_143_out, not_144_out, F14, F13, F12, not_145_out, OP5, OP4, not_146_out, not_147_out);
  and and_26 (and_26_out, not_148_out, not_149_out, not_150_out, F13, F12, not_151_out, OP5, OP4, not_152_out, not_153_out);
  and and_27 (and_27_out, not_154_out, not_155_out, not_156_out, not_157_out, not_158_out, OP4, not_159_out, not_160_out);
  and and_28 (and_28_out, F14, F13, F12, not_161_out, not_162_out, OP4, not_163_out, not_164_out);
  and and_29 (and_29_out, not_165_out, F13, not_166_out, not_167_out, not_168_out, not_169_out, not_170_out, not_171_out);
  and and_30 (and_30_out, not_172_out, F13, not_173_out, not_174_out, OP5, not_175_out, not_176_out, not_177_out);
  and and_31 (and_31_out, not_178_out, not_179_out, not_180_out, OP6, OP5, not_181_out, not_182_out, not_183_out);
  and and_32 (and_32_out, not_184_out, not_185_out, F12, OP6, OP5, not_186_out, not_187_out, not_188_out);
  and and_33 (and_33_out, OP6, OP5, not_189_out, OP3, OP2);
  and and_34 (and_34_out, not_190_out, not_191_out, not_192_out, OP6, OP5, not_193_out, not_194_out, OP2);
  and and_35 (and_35_out, F14, not_195_out, F12, not_196_out, not_197_out, not_198_out, not_199_out, not_200_out);
  and and_36 (and_36_out, F14, F13, F12, OP6, OP5, not_201_out, not_202_out, not_203_out);
  and and_37 (and_37_out, not_204_out, not_205_out, F14, F13, not_206_out, not_207_out, OP5, OP4, not_208_out, not_209_out);
  and and_38 (and_38_out, not_210_out, not_211_out, not_212_out, F13, not_213_out, not_214_out, OP5, OP4, not_215_out, not_216_out);
  and and_39 (and_39_out, not_217_out, not_218_out, not_219_out, F13, F12, not_220_out, OP5, OP4, not_221_out, not_222_out);
  and and_40 (and_40_out, F14, F13, not_223_out, not_224_out, not_225_out, OP4, not_226_out, not_227_out);
  and and_41 (and_41_out, F14, not_228_out, not_229_out, not_230_out, not_231_out, OP4, not_232_out, not_233_out);
  and and_42 (and_42_out, not_234_out, F13, not_235_out, not_236_out, not_237_out, OP4, not_238_out, not_239_out);
  and and_43 (and_43_out, F14, F13, F12, OP6, OP5, not_240_out, not_241_out, not_242_out);
  or or_1 (S0, and_1_out, and_2_out, and_3_out, and_4_out, and_5_out, and_6_out, and_7_out, and_8_out, and_9_out, and_10_out, and_11_out, and_12_out, and_13_out, and_14_out, and_15_out);
  or or_2 (S1, and_16_out, and_17_out, and_18_out, and_19_out, and_20_out, and_21_out, and_22_out);
  or or_3 (S2, and_23_out, and_24_out, and_25_out, and_26_out, and_27_out, and_28_out, and_29_out, and_30_out, and_31_out, and_32_out, and_33_out, and_34_out, and_35_out, and_36_out);
  or or_4 (S3, and_37_out, and_38_out, and_39_out, and_40_out, and_41_out, and_42_out, and_43_out);
endmodule

// 控制信号生成
module \控制信号自动生成  (
  input  OP2,
  input  OP3,
  input  OP4,
  input  OP5,
  input  OP6,
  input  F12,
  input  F13,
  input  F14,
  input  F25,
  input  F30,
  output MemToReg,
  output MemWrite,
  output ALU_SRC,
  output RegWrite,
  output ecall,
  output S_Type,
  output BEQ,
  output BNE,
  output JALR,
  output JAL,
  output U_Type,
  output BGEU,
  output LHU,
  output URET
);

  wire and_1_out, and_2_out, and_4_out, and_5_out, and_6_out, and_7_out, and_8_out, and_9_out, and_10_out,
       and_11_out, and_12_out, and_13_out, and_14_out, and_15_out, and_16_out, and_17_out, and_18_out,
       and_19_out, and_20_out, and_21_out, and_22_out, not_1_out, not_2_out, not_3_out, not_4_out, not_5_out,
       not_6_out, not_7_out, not_8_out, not_9_out, not_10_out, not_11_out, not_12_out, not_13_out,
       not_14_out, not_15_out, not_16_out, not_17_out, not_18_out, not_19_out, not_20_out, not_21_out,
       not_22_out, not_23_out, not_24_out, not_25_out, not_26_out, not_27_out, not_28_out, not_29_out,
       not_30_out, not_31_out, not_32_out, not_33_out, not_34_out, not_35_out, not_36_out, not_37_out,
       not_38_out, not_39_out, not_40_out, not_41_out, not_42_out, not_43_out, not_44_out, not_45_out,
       not_46_out, not_47_out, not_48_out, not_49_out, not_50_out, not_51_out, not_52_out, not_53_out,
       not_54_out, not_55_out, not_56_out, not_57_out, not_58_out, not_59_out, not_60_out, not_61_out,
       not_62_out, not_63_out, not_64_out, not_65_out, not_66_out, not_67_out, not_68_out, not_69_out,
       not_70_out, not_71_out, not_72_out, not_73_out, not_74_out, not_75_out, not_76_out, not_77_out,
       not_78_out, not_79_out, not_80_out, not_81_out, not_82_out, not_83_out, not_84_out, not_85_out,
       not_86_out, not_87_out, not_88_out, not_89_out, not_90_out, not_91_out, not_92_out, not_93_out,
       not_94_out, not_95_out, not_96_out, not_97_out, not_98_out, not_99_out, not_100_out, not_101_out,
       not_102_out, not_103_out, not_104_out, not_105_out, not_106_out, not_107_out, not_108_out,
       not_109_out, not_110_out, not_111_out, not_112_out, not_113_out, not_114_out, not_115_out,
       not_116_out, not_117_out, not_118_out, not_119_out, not_120_out, not_121_out, not_122_out,
       not_123_out, not_124_out, not_125_out, not_126_out, not_127_out, not_128_out, not_129_out,
       not_130_out, not_131_out, not_132_out, not_133_out, not_134_out, not_135_out, not_136_out,
       not_137_out, not_138_out, not_139_out, not_140_out, not_141_out, not_142_out, not_143_out,
       not_144_out, not_145_out, not_146_out, not_147_out, not_148_out, not_149_out, not_150_out,
       not_151_out, not_152_out, not_153_out, not_154_out, not_155_out, not_156_out, not_157_out,
       not_158_out, not_159_out, not_160_out;

  not not_1 (not_1_out, OP2);
  not not_2 (not_2_out, OP3);
  not not_3 (not_3_out, OP4);
  not not_4 (not_4_out, OP5);
  not not_5 (not_5_out, OP6);
  not not_6 (not_6_out, F12);
  not not_7 (not_7_out, F14);
  not not_8 (not_8_out, OP2);
  not not_9 (not_9_out, OP3);
  not not_10 (not_10_out, OP4);
  not not_11 (not_11_out, OP5);
  not not_12 (not_12_out, OP6);
  not not_13 (not_13_out, F13);
  not not_14 (not_14_out, OP2);
  not not_15 (not_15_out, OP3);
  not not_16 (not_16_out, OP4);
  not not_17 (not_17_out, OP6);
  not not_18 (not_18_out, F12);
  not not_19 (not_19_out, F14);
  not not_20 (not_20_out, OP2);
  not not_21 (not_21_out, OP3);
  not not_22 (not_22_out, OP4);
  not not_23 (not_23_out, OP6);
  not not_24 (not_24_out, F12);
  not not_25 (not_25_out, F14);
  not not_26 (not_26_out, OP2);
  not not_27 (not_27_out, OP3);
  not not_28 (not_28_out, OP4);
  not not_29 (not_29_out, OP5);
  not not_30 (not_30_out, OP6);
  not not_31 (not_31_out, F13);
  not not_32 (not_32_out, OP2);
  not not_33 (not_33_out, OP3);
  not not_34 (not_34_out, OP5);
  not not_35 (not_35_out, OP6);
  not not_36 (not_36_out, F12);
  not not_37 (not_37_out, OP2);
  not not_38 (not_38_out, OP3);
  not not_39 (not_39_out, OP5);
  not not_40 (not_40_out, OP6);
  not not_41 (not_41_out, F13);
  not not_42 (not_42_out, F25);
  not not_43 (not_43_out, F30);
  not not_44 (not_44_out, OP2);
  not not_45 (not_45_out, OP3);
  not not_46 (not_46_out, OP5);
  not not_47 (not_47_out, OP6);
  not not_48 (not_48_out, F25);
  not not_49 (not_49_out, OP2);
  not not_50 (not_50_out, OP3);
  not not_51 (not_51_out, OP5);
  not not_52 (not_52_out, OP6);
  not not_53 (not_53_out, OP3);
  not not_54 (not_54_out, OP4);
  not not_55 (not_55_out, F12);
  not not_56 (not_56_out, F13);
  not not_57 (not_57_out, F14);
  not not_58 (not_58_out, OP2);
  not not_59 (not_59_out, OP3);
  not not_60 (not_60_out, OP5);
  not not_61 (not_61_out, OP6);
  not not_62 (not_62_out, F12);
  not not_63 (not_63_out, F14);
  not not_64 (not_64_out, OP2);
  not not_65 (not_65_out, OP3);
  not not_66 (not_66_out, OP4);
  not not_67 (not_67_out, OP5);
  not not_68 (not_68_out, OP6);
  not not_69 (not_69_out, F13);
  not not_70 (not_70_out, OP2);
  not not_71 (not_71_out, OP3);
  not not_72 (not_72_out, OP6);
  not not_73 (not_73_out, F12);
  not not_74 (not_74_out, F13);
  not not_75 (not_75_out, F14);
  not not_76 (not_76_out, F25);
  not not_77 (not_77_out, OP3);
  not not_78 (not_78_out, OP5);
  not not_79 (not_79_out, OP6);
  not not_80 (not_80_out, F12);
  not not_81 (not_81_out, OP3);
  not not_82 (not_82_out, OP5);
  not not_83 (not_83_out, OP6);
  not not_84 (not_84_out, F13);
  not not_85 (not_85_out, F25);
  not not_86 (not_86_out, F30);
  not not_87 (not_87_out, OP3);
  not not_88 (not_88_out, OP5);
  not not_89 (not_89_out, OP6);
  not not_90 (not_90_out, F25);
  not not_91 (not_91_out, OP3);
  not not_92 (not_92_out, OP5);
  not not_93 (not_93_out, OP6);
  not not_94 (not_94_out, OP2);
  not not_95 (not_95_out, OP3);
  not not_96 (not_96_out, OP6);
  not not_97 (not_97_out, F25);
  not not_98 (not_98_out, F30);
  not not_99 (not_99_out, OP2);
  not not_100 (not_100_out, OP3);
  not not_101 (not_101_out, OP6);
  not not_102 (not_102_out, F25);
  not not_103 (not_103_out, F30);
  not not_104 (not_104_out, OP4);
  not not_105 (not_105_out, F12);
  not not_106 (not_106_out, F13);
  not not_107 (not_107_out, F14);
  not not_108 (not_108_out, OP3);
  not not_109 (not_109_out, OP5);
  not not_110 (not_110_out, OP6);
  not not_111 (not_111_out, OP4);
  not not_112 (not_112_out, OP2);
  not not_113 (not_113_out, OP3);
  not not_114 (not_114_out, F12);
  not not_115 (not_115_out, F13);
  not not_116 (not_116_out, F14);
  not not_117 (not_117_out, F25);
  not not_118 (not_118_out, F30);
  not not_119 (not_119_out, OP2);
  not not_120 (not_120_out, OP3);
  not not_121 (not_121_out, OP4);
  not not_122 (not_122_out, OP6);
  not not_123 (not_123_out, F12);
  not not_124 (not_124_out, F14);
  not not_125 (not_125_out, OP2);
  not not_126 (not_126_out, OP3);
  not not_127 (not_127_out, OP4);
  not not_128 (not_128_out, F12);
  not not_129 (not_129_out, F13);
  not not_130 (not_130_out, F14);
  not not_131 (not_131_out, OP2);
  not not_132 (not_132_out, OP3);
  not not_133 (not_133_out, OP4);
  not not_134 (not_134_out, F13);
  not not_135 (not_135_out, F14);
  not not_136 (not_136_out, OP3);
  not not_137 (not_137_out, OP4);
  not not_138 (not_138_out, F12);
  not not_139 (not_139_out, F13);
  not not_140 (not_140_out, F14);
  not not_141 (not_141_out, OP4);
  not not_142 (not_142_out, OP3);
  not not_143 (not_143_out, OP5);
  not not_144 (not_144_out, OP6);
  not not_145 (not_145_out, OP2);
  not not_146 (not_146_out, OP3);
  not not_147 (not_147_out, OP4);
  not not_148 (not_148_out, OP2);
  not not_149 (not_149_out, OP3);
  not not_150 (not_150_out, OP4);
  not not_151 (not_151_out, OP5);
  not not_152 (not_152_out, OP6);
  not not_153 (not_153_out, F13);
  not not_154 (not_154_out, F30);
  not not_155 (not_155_out, F25);
  not not_156 (not_156_out, F14);
  not not_157 (not_157_out, F13);
  not not_158 (not_158_out, F12);
  not not_159 (not_159_out, OP3);
  not not_160 (not_160_out, OP2);
  and and_1 (and_1_out, not_1_out, not_2_out, not_3_out, not_4_out, not_5_out, not_6_out, F13, not_7_out);
  and and_2 (and_2_out, not_8_out, not_9_out, not_10_out, not_11_out, not_12_out, F12, not_13_out, F14);
  and and_3 (MemWrite, not_14_out, not_15_out, not_16_out, OP5, not_17_out, not_18_out, F13, not_19_out);
  and and_4 (and_4_out, not_20_out, not_21_out, not_22_out, not_23_out, not_24_out, F13, not_25_out);
  and and_5 (and_5_out, not_26_out, not_27_out, not_28_out, not_29_out, not_30_out, F12, not_31_out, F14);
  and and_6 (and_6_out, not_32_out, not_33_out, OP4, not_34_out, not_35_out, not_36_out);
  and and_7 (and_7_out, not_37_out, not_38_out, OP4, not_39_out, not_40_out, not_41_out, not_42_out, not_43_out);
  and and_8 (and_8_out, not_44_out, not_45_out, OP4, not_46_out, not_47_out, F14, not_48_out);
  and and_9 (and_9_out, not_49_out, not_50_out, OP4, not_51_out, not_52_out, F13, F14);
  and and_10 (and_10_out, OP2, not_53_out, not_54_out, OP5, OP6, not_55_out, not_56_out, not_57_out);
  and and_11 (and_11_out, not_58_out, not_59_out, not_60_out, not_61_out, not_62_out, F13, not_63_out);
  and and_12 (and_12_out, not_64_out, not_65_out, not_66_out, not_67_out, not_68_out, F12, not_69_out, F14);
  and and_13 (and_13_out, not_70_out, not_71_out, OP4, not_72_out, not_73_out, not_74_out, not_75_out, not_76_out);
  and and_14 (and_14_out, not_77_out, OP4, not_78_out, not_79_out, not_80_out);
  and and_15 (and_15_out, not_81_out, OP4, not_82_out, not_83_out, not_84_out, not_85_out, not_86_out);
  and and_16 (and_16_out, not_87_out, OP4, not_88_out, not_89_out, F14, not_90_out);
  and and_17 (and_17_out, not_91_out, OP4, not_92_out, not_93_out, F13, F14);
  and and_18 (and_18_out, not_94_out, not_95_out, OP4, not_96_out, F12, F14, not_97_out, not_98_out);
  and and_19 (and_19_out, not_99_out, not_100_out, OP4, OP5, not_101_out, F13, not_102_out, not_103_out);
  and and_20 (and_20_out, OP2, not_104_out, OP5, OP6, not_105_out, not_106_out, not_107_out);
  and and_21 (and_21_out, OP2, not_108_out, OP4, not_109_out, not_110_out);
  and and_22 (and_22_out, OP2, OP3, not_111_out, OP5, OP6);
  and and_23 (ecall, not_112_out, not_113_out, OP4, OP5, OP6, not_114_out, not_115_out, not_116_out, not_117_out, not_118_out);
  and and_24 (S_Type, not_119_out, not_120_out, not_121_out, OP5, not_122_out, not_123_out, F13, not_124_out);
  and and_25 (BEQ, not_125_out, not_126_out, not_127_out, OP5, OP6, not_128_out, not_129_out, not_130_out);
  and and_26 (BNE, not_131_out, not_132_out, not_133_out, OP5, OP6, F12, not_134_out, not_135_out);
  and and_27 (JALR, OP2, not_136_out, not_137_out, OP5, OP6, not_138_out, not_139_out, not_140_out);
  and and_28 (JAL, OP2, OP3, not_141_out, OP5, OP6);
  and and_29 (U_Type, OP2, not_142_out, OP4, not_143_out, not_144_out);
  and and_30 (BGEU, not_145_out, not_146_out, not_147_out, OP5, OP6, F12, F13, F14);
  and and_31 (LHU, not_148_out, not_149_out, not_150_out, not_151_out, not_152_out, F12, not_153_out, F14);
  and and_32 (URET, not_154_out, not_155_out, not_156_out, not_157_out, not_158_out, OP6, OP5, OP4, not_159_out, not_160_out);
  or or_1 (MemToReg, and_1_out, and_2_out);
  or or_2 (ALU_SRC, and_4_out, and_5_out, and_6_out, and_7_out, and_8_out, and_9_out, and_10_out);
  or or_3 (RegWrite, and_11_out, and_12_out, and_13_out, and_14_out, and_15_out, and_16_out, and_17_out, and_18_out, and_19_out, and_20_out, and_21_out, and_22_out);
endmodule

// ALU
module ALU (
  input  [31:0] X,
  input  [31:0] Y,
  input  [3:0] AluOP,
  output out_4,
  output Equal,
  output out_6,
  output [31:0] Result,
  output [31:0] Result_2
);

  wire [0:0] comparator_1_lt, comparator_2_lt;
  wire [31:0] adder_1_out, AND_out, divider_1_out, divider_1_rem, multiplier_1_cout, multiplier_1_out,
       NOR_out, OR_out, shifter_1_out, shifter_2_out, shifter_3_out, subtractor_1_out, XOR_out;

  assign AND_out = X & Y;  // AND_Gate AND, 32 bits wide
  assign OR_out = X | Y;  // OR_Gate OR, 32 bits wide
  Shifter #(.width(32), .shift("ll")) shifter_1 (.in(X), .\dist (Y[4:0]), .out(shifter_1_out));
  Shifter #(.width(32), .shift("ar")) shifter_2 (.in(X), .\dist (Y[4:0]), .out(shifter_2_out));
  Shifter #(.width(32), .shift("lr")) shifter_3 (.in(X), .\dist (Y[4:0]), .out(shifter_3_out));
  Multiplier #(.width(32)) multiplier_1 (.a(X), .b(Y), .out(multiplier_1_out), .cout(multiplier_1_cout));  // open: cin
  Divider #(.width(32)) divider_1 (.a(X), .b(Y), .out(divider_1_out), .rem(divider_1_rem));  // open: upper
  Adder #(.width(32)) adder_1 (.a(X), .b(Y), .out(adder_1_out));  // open: cin, cout
  Subtractor #(.width(32)) subtractor_1 (.a(X), .b(Y), .out(subtractor_1_out));  // open: bin, bout
  assign XOR_out = X ^ Y;  // XOR_Gate XOR, 32 bits wide
  assign NOR_out = ~(X | Y);  // NOR_Gate NOR, 32 bits wide
  Comparator #(.width(32), .mode("twosComplement")) comparator_1 (
    .a(X), .b(Y), .eq(Equal), .lt(comparator_1_lt[0]));  // open: gt
  Comparator #(.width(32), .mode("unsigned")) comparator_2 (.a(X), .b(Y), .lt(comparator_2_lt[0]));  // open: gt, eq
  Multiplexer #(.select(4), .width(32), .disabled("Z"), .enable("false")) multiplexer_1 (
    .in0(shifter_1_out), .in1(shifter_2_out), .in2(shifter_3_out), .in3(multiplier_1_out),
    .in4(divider_1_out), .in5(adder_1_out), .in6(subtractor_1_out), .in7(AND_out), .in8(OR_out),
    .in9(XOR_out), .in10(NOR_out), .in11({{31{1'b0}}, comparator_1_lt[0]}),
    .in12({{31{1'b0}}, comparator_2_lt[0]}), .in13({32{1'b0}}), .in14({32{1'b0}}), .in15({32{1'b0}}),
    .out(Result), .sel(AluOP));
  Multiplexer #(.select(4), .width(32), .disabled("Z"), .enable("false")) multiplexer_2 (
    .in0({32{1'b0}}), .in1({32{1'b0}}), .in2({32{1'b0}}), .in3(multiplier_1_cout), .in4(divider_1_rem),
    .in5({32{1'b0}}), .in6({32{1'b0}}), .in7({32{1'b0}}), .in8({32{1'b0}}), .in9({32{1'b0}}),
    .in10({32{1'b0}}), .in11({32{1'b0}}), .in12({32{1'b0}}), .in13({32{1'b0}}), .in14({32{1'b0}}),
    .in15({32{1'b0}}), .out(Result_2), .sel(AluOP));
  Multiplexer #(.select(4), .width(1), .disabled("Z"), .enable("false")) multiplexer_3 (
    .in0(1'b0), .in1(1'b0), .in2(1'b0), .in3(1'b0), .in4(1'b0), .in5(1'b0), .in6(1'b0), .in7(1'b0),
    .in8(1'b0), .in9(1'b0), .in10(1'b0), .in11(comparator_1_lt[0]), .in12(comparator_2_lt[0]), .in13(1'b0),
    .in14(1'b0), .in15(1'b0), .out(out_6), .sel(AluOP));
  not not_1 (out_4, out_6);

  // Other names for the same wires on the sheet: Result2[31:0] = Result_2; S[3:0] = AluOP; tunnel = out_6;
  //   tunnel_t = out_4

  // Notes on the sheet:
  //   不要改变此引脚区域内容，也不要改变ALU封装形式
  //   输入引脚
  //   输出引脚
endmodule

module Regifile (
  input  [31:0] Din,
  input  Clk,
  input  WE,
  input  [4:0] R1_num,
  input  [4:0] W_num,
  input  [4:0] R2_num,
  output [31:0] R1,
  output [31:0] R2
);

  // RegisterFile registerfile_1: pin names not known; wires that end beside it: Din, Clk, WE, W_num, R1_num, R2_num, R1, R2
endmodule

module \理想流水线  (
  output RegWrite,
  output MemWrite,
  output [31:0] IF_PC,
  output [31:0] ID_PC,
  output [31:0] EX_PC,
  output [31:0] M_PC,
  output [31:0] WB_PC,
  output [31:0] RDin,
  output [31:0] MDin,
  output [31:0] LedData
);

  wire CLK, clock_1_out, clock_2_out, comparator_1_eq, comparator_1_lt, d_ff_1_q, Go, IR1, IR2, IR3,
       nand_1_out, RST, W1, W2, W3;
  wire [12:0] CNT_num;
  wire [15:0] \LoadUse次数 , \总周期数 , \插入气泡数 , \无条件分支数 , \条件分支成功数 ;
  wire [31:0] EX_IR, ID_IR, IF_IR, MEM_IR, WB_IR;

  Button \u_总复位  (.out(RST));
  Button _1 (.out(IR1));
  Button _2 (.out(IR2));
  Button _3 (.out(IR3));
  // Probe on \总周期数 
  // Probe on \总周期数 
  Button \u_继续运行  (.out(Go));
  LED #(.active("true")) led_1 (.in(W1));
  LED #(.active("true")) led_2 (.in(W2));
  LED #(.active("true")) led_3 (.in(W3));
  Hex_Digit_Display hex_digit_display_1 (.value(LedData[31:28]));  // open: dp
  // Probe on IF_PC[19:0]
  // RiscV_Probe riscv_probe_1: pin names not known; wires that end beside it: IF_IR
  Hex_Digit_Display hex_digit_display_2 (.value(LedData[23:20]));  // open: dp
  Hex_Digit_Display hex_digit_display_3 (.value(LedData[27:24]));  // open: dp
  // Probe on ID_PC[19:0]
  // RiscV_Probe riscv_probe_2: pin names not known; wires that end beside it: ID_IR
  Hex_Digit_Display hex_digit_display_4 (.value(LedData[15:12]));  // open: dp
  Hex_Digit_Display hex_digit_display_5 (.value(LedData[19:16]));  // open: dp
  Hex_Digit_Display hex_digit_display_6 (.value(LedData[7:4]));  // open: dp
  Hex_Digit_Display hex_digit_display_7 (.value(LedData[11:8]));  // open: dp
  Clock #(.highDuration(1), .lowDuration(1)) clock_1 (.out(clock_1_out));
  // Probe on EX_PC[19:0]
  // RiscV_Probe riscv_probe_3: pin names not known; wires that end beside it: clock_1_out, EX_IR, CLK
  Hex_Digit_Display hex_digit_display_8 (.value(LedData[3:0]));  // open: dp
  // Probe on \总周期数 
  // Probe on M_PC[19:0]
  // RiscV_Probe riscv_probe_4: pin names not known; wires that end beside it: MEM_IR
  // Probe on \总周期数 
  // Probe on \无条件分支数 
  // Probe on \条件分支成功数 
  // Probe on \插入气泡数 
  // Probe on \LoadUse次数 
  // Probe on IF_PC[11:0]
  // Probe on WB_PC[19:0]
  // RiscV_Probe riscv_probe_5: pin names not known; wires that end beside it: WB_IR
  // Probe on EX_PC[11:0]
  // Probe on ID_PC[11:0]
  // Probe on M_PC[11:0]
  D_Flip_Flop #(.trigger("high"), .Pre_Clr_Positions("LEGACY"), .NegatePresetClear("false"), .enable("true"), .NewFFLayout("false")) d_ff_1 (.Q(d_ff_1_q));  // open: clk, D, Qn, preset, en, reset
  // Probe on 13'hc
  // Probe on WB_PC[11:0]
  Comparator #(.width(13), .mode("twosComplement")) comparator_1 (
    .a(CNT_num), .b(13'hc), .eq(comparator_1_eq), .lt(comparator_1_lt));  // open: gt
  Clock #(.highDuration(1), .lowDuration(1)) clock_2 (.out(clock_2_out));
  nand nand_1 (nand_1_out, d_ff_1_q, comparator_1_eq);
  Counter #(.width(13), .max('h1fff), .ongoal("stay"), .trigger("rising"), .behavior("old")) counter_1 (
    .count(comparator_1_lt), .Q(CNT_num), .clk(clock_2_out));  // open: load, D, carry, clr, preset
  assign CLK = nand_1_out ? clock_2_out : 1'bz;  // Controlled_Buffer controlled_buffer_1
  Pull_Resistor #(.pull(1)) pull_resistor_1 (.node(CLK));

  // Other names for the same wires on the sheet: MEM_PC[31:0] = M_PC

  // Notes on the sheet:
  //   中断源
  //   时空图监测，可删除
  //   中断等待指示
  //   数码管输出
  //   控制位
  //   流水调试日志用
  //   暂停节拍，不能为0
  //   戳工具置1进入计数暂停模式，ctrl+k时钟自动运行到对应节拍暂停
  //   ctrl+k关闭时钟连续运行，将控制位置零，进入单步调试模式调试
  //   用这个时钟源需要去掉电路中的其他时钟源
  //   可计数暂停的时钟源
  //   为方便自动评测，需要输出流水线各段保存的PC值，注意是PC不是PC+4，另外ID段寄存器写入信息，Mem段内存写入信息也要输出
endmodule
module \流水线_EX段分支  (
  output RegWrite,
  output MemWrite,
  output [31:0] IF_PC,
  output [31:0] ID_PC,
  output [31:0] EX_PC,
  output [31:0] M_PC,
  output [31:0] WB_PC,
  output [31:0] RDin,
  output [31:0] MDin,
  output [31:0] LedData
);

  wire and_2_out, and_3_out, and_4_out, and_5_out, and_6_out, Branch, CLK, clock_2_out, comparator_1_eq,
       comparator_1_lt, comparator_2_eq, controlled_buffer_1_out, d_ff_1_q, ecall, en, equal,
       ex_mem_1_haltout, ex_mem_1_jalout, ex_mem_1_jalrout, ex_mem_1_lhuout, ex_mem_1_regwriteout,
       ex_mem_1_u_tpyeout, Go, halt, id_ex_1_alusrcbout, id_ex_1_beqout, id_ex_1_bgeuout, id_ex_1_bneout,
       id_ex_1_ecallout, id_ex_1_lhuout, id_ex_1_memtoregout, id_ex_1_memwriteout, id_ex_1_regwriteout,
       id_ex_1_s_tpyeout, id_ex_1_u_tpyeout, IR1, IR2, IR3, Jal, Jalr, mem_wb_1_haltout, mem_wb_1_jalout,
       mem_wb_1_jalrout, mem_wb_1_lhuout, mem_wb_1_memtoregout, mem_wb_1_u_tpyeout, mem_wb_1_xout, MemToReg,
       MoreAndEqu, nand_1_out, not_1_out, not_2_out, not_3_out, not_4_out, or_1_out, or_2_out, or_3_out,
       or_5_out, RST, W1, W2, W3, \单周期硬布线控制器_1_alu_src , \单周期硬布线控制器_1_beq , \单周期硬布线控制器_1_bgeu ,
       \单周期硬布线控制器_1_bne , \单周期硬布线控制器_1_jal , \单周期硬布线控制器_1_jalr , \单周期硬布线控制器_1_lhu , \单周期硬布线控制器_1_memtoreg ,
       \单周期硬布线控制器_1_memwrite , \单周期硬布线控制器_1_regwrite , \单周期硬布线控制器_1_s_type , \单周期硬布线控制器_1_u_type ;
  wire [3:0] id_ex_1_aluopout, \单周期硬布线控制器_1_alu_op ;
  wire [4:0] ex_mem_1_w_out, id_ex_1_w_out, ID_Funct, multiplexer_4_out, multiplexer_5_out, W_num;
  wire [11:0] shifter_1_out;
  wire [12:0] CNT_num;
  wire [15:0] adder_4_out, \LoadUse次数 , multiplexer_8_out, \总周期数 , \插入气泡数 , \无条件分支数 , \条件分支成功数 ;
  wire [19:0] shifter_2_out;
  wire [31:0] adder_1_out, adder_2_out, adder_3_out, adder_5_out, and_1_out, bit_extender_1_out,
       bit_extender_2_out, bit_extender_3_out, bit_extender_4_out, bit_extender_5_out, EX_IR,
       ex_mem_1_imm_u_out, ex_mem_1_resultout, id_ex_1_imm_i_out, id_ex_1_imm_s_out, id_ex_1_imm_u_out,
       id_ex_1_r1out, id_ex_1_r2out, ID_IR, IF_IR, imm_B, imm_J, Jalr_Addr, MEM_IR, mem_wb_1_aluresultout,
       mem_wb_1_imm_u_out, mem_wb_1_rmdataout, multiplexer_1_out, multiplexer_2_out, multiplexer_3_out,
       multiplexer_6_out, multiplexer_7_out, multiplexer_9_out, multiplexer_10_out, multiplexer_11_out, R1,
       R2, ram_1_data, WB_IR, WB_PC_4;

  Button \u_总复位  (.out(RST));
  Button _1 (.out(IR1));
  Button _2 (.out(IR2));
  Button _3 (.out(IR3));
  // Probe on \总周期数 
  // Probe on \总周期数 
  Button \u_继续运行  (.out(Go));
  LED #(.active("true")) led_1 (.in(W1));
  LED #(.active("true")) led_2 (.in(W2));
  LED #(.active("true")) led_3 (.in(W3));
  Hex_Digit_Display hex_digit_display_1 (.value(LedData[31:28]));  // open: dp
  // Probe on IF_PC[19:0]
  // RiscV_Probe riscv_probe_1: pin names not known; wires that end beside it: IF_IR
  Hex_Digit_Display hex_digit_display_2 (.value(LedData[27:24]));  // open: dp
  Hex_Digit_Display hex_digit_display_3 (.value(LedData[23:20]));  // open: dp
  // Probe on ID_PC[19:0]
  // RiscV_Probe riscv_probe_2: pin names not known; wires that end beside it: {ID_IR[31], ID_Funct[4], ID_IR[29:26], ID_Funct[3], ID_IR[24:15], ID_Funct[2:0], ID_IR[11:0]}
  Adder #(.width(32)) adder_1 (.a(imm_J), .b(EX_PC), .out(adder_1_out));  // open: cin, cout
  assign and_1_out = Jalr_Addr & 32'hfffffffe;  // AND_Gate and_1, 32 bits wide
  Hex_Digit_Display hex_digit_display_4 (.value(LedData[15:12]));  // open: dp
  Hex_Digit_Display hex_digit_display_5 (.value(LedData[19:16]));  // open: dp
  Multiplexer #(.select(1), .width(32), .disabled("Z"), .enable("false")) multiplexer_1 (
    .in0(adder_3_out), .in1(adder_1_out), .out(multiplexer_1_out), .sel(Jal));
  Multiplexer #(.select(1), .width(32), .disabled("Z"), .enable("false")) multiplexer_2 (
    .in0(multiplexer_1_out), .in1(and_1_out), .out(multiplexer_2_out), .sel(Jalr));
  Adder #(.width(32)) adder_2 (.a(imm_B), .b(EX_PC), .out(adder_2_out));  // open: cin, cout
  Hex_Digit_Display hex_digit_display_6 (.value(LedData[7:4]));  // open: dp
  Hex_Digit_Display hex_digit_display_7 (.value(LedData[11:8]));  // open: dp
  Clock #(.highDuration(1), .lowDuration(1)) clock_1 (.out(CLK));
  // Probe on EX_PC[19:0]
  // RiscV_Probe riscv_probe_3: pin names not known; wires that end beside it: EX_IR
  Multiplexer #(.select(1), .width(32), .disabled("Z"), .enable("false")) multiplexer_3 (
    .in0(multiplexer_2_out), .in1(adder_2_out), .out(multiplexer_3_out), .sel(Branch));
  not not_1 (not_1_out, halt);
  Hex_Digit_Display hex_digit_display_8 (.value(LedData[3:0]));  // open: dp
  Register #(.width(32), .trigger("rising"), .Select("low")) PC (
    .D(multiplexer_3_out), .en(not_1_out), .Q(IF_PC), .clk(CLK), .clr(RST));
  // Probe on \总周期数 
  // Probe on M_PC[19:0]
  // RiscV_Probe riscv_probe_4: pin names not known; wires that end beside it: MEM_IR
  // Probe on \总周期数 
  // Probe on \无条件分支数 
  // Probe on \条件分支成功数 
  // Probe on \插入气泡数 
  // Probe on \LoadUse次数 
  Adder #(.width(32)) adder_3 (.a(IF_PC), .b(32'h4), .out(adder_3_out));  // open: cin, cout
  // Probe on IF_PC[11:0]
  // Probe on WB_PC[19:0]
  // RiscV_Probe riscv_probe_5: pin names not known; wires that end beside it: WB_IR
  ROM #(.addrWidth(10), .dataWidth(32), .Select("high")) rom_1 (.addr(IF_PC[11:2]), .data(IF_IR));
  // Probe on ID_PC[11:0]
  // Probe on EX_PC[11:0]
  IF_ID if_id_1 (
    .PCin(IF_PC), .IRin(IF_IR), .PCout(ID_PC),
    .IRout({ID_IR[31], ID_Funct[4], ID_IR[29:26], ID_Funct[3], ID_IR[24:15], ID_Funct[2:0], ID_IR[11:0]}),
    .RST(or_2_out), .EN_H(en), .CLK(CLK));
  // Probe on M_PC[11:0]
  D_Flip_Flop #(.trigger("high"), .Pre_Clr_Positions("LEGACY"), .NegatePresetClear("false"), .enable("true"), .NewFFLayout("false")) d_ff_1 (.Q(d_ff_1_q));  // open: clk, D, Qn, preset, en, reset
  // Probe on 13'hc
  // Probe on WB_PC[11:0]
  Comparator #(.width(13), .mode("twosComplement")) comparator_1 (
    .a(CNT_num), .b(13'hc), .eq(comparator_1_eq), .lt(comparator_1_lt));  // open: gt
  Clock #(.highDuration(1), .lowDuration(1)) clock_2 (.out(clock_2_out));
  assign bit_extender_1_out = {{20{ID_IR[31]}}, {ID_IR[31], ID_Funct[4], ID_IR[29:26], ID_Funct[3], ID_IR[24:20]}};  // Bit_Extender bit_extender_1
  assign bit_extender_2_out = {{20{ID_IR[31]}}, {ID_IR[31], ID_Funct[4], ID_IR[29:26], ID_Funct[3], ID_IR[11:7]}};  // Bit_Extender bit_extender_2
  nand nand_1 (nand_1_out, d_ff_1_q, comparator_1_eq);
  Counter #(.width(13), .max('h1fff), .ongoal("stay"), .trigger("rising"), .behavior("old")) counter_1 (
    .count(comparator_1_lt), .Q(CNT_num), .clk(clock_2_out));  // open: load, D, carry, clr, preset
  \单周期硬布线控制器  \u_单周期硬布线控制器_1  (
    .Funct(ID_Funct), .OP(ID_IR[6:2]), .ALU_OP(\单周期硬布线控制器_1_alu_op ), .MemToReg(\单周期硬布线控制器_1_memtoreg ),
    .MemWrite(\单周期硬布线控制器_1_memwrite ), .ALU_SRC(\单周期硬布线控制器_1_alu_src ), .RegWrite(\单周期硬布线控制器_1_regwrite ),
    .ecall(ecall), .S_type(\单周期硬布线控制器_1_s_type ), .Jalr(\单周期硬布线控制器_1_jalr ), .Beq(\单周期硬布线控制器_1_beq ),
    .JAL(\单周期硬布线控制器_1_jal ), .Bne(\单周期硬布线控制器_1_bne ), .U_type(\单周期硬布线控制器_1_u_type ),
    .BGEU(\单周期硬布线控制器_1_bgeu ), .LHU(\单周期硬布线控制器_1_lhu ));  // open: URET
  Multiplexer #(.select(1), .width(5), .disabled("Z"), .enable("false")) multiplexer_4 (
    .in0(ID_IR[19:15]), .in1(5'b10001), .out(multiplexer_4_out), .sel(ecall));
  Multiplexer #(.select(1), .width(5), .disabled("Z"), .enable("false")) multiplexer_5 (
    .in0(ID_IR[24:20]), .in1(5'b01010), .out(multiplexer_5_out), .sel(ecall));
  Shifter #(.width(12), .shift("ll")) shifter_1 (
    .in({ID_IR[31], ID_IR[7], ID_Funct[4], ID_IR[29:26], ID_Funct[3], ID_IR[11:8]}), .\dist (4'b0001),
    .out(shifter_1_out));
  Shifter #(.width(20), .shift("ll")) shifter_2 (
    .in({ID_IR[31], ID_IR[19:15], ID_Funct[2:0], ID_IR[20], ID_Funct[4], ID_IR[29:26], ID_Funct[3], ID_IR[24:21]}),
    .\dist (5'b00001), .out(shifter_2_out));
  assign controlled_buffer_1_out = nand_1_out ? clock_2_out : 1'bz;  // Controlled_Buffer controlled_buffer_1
  assign bit_extender_3_out = {{20{shifter_1_out[11]}}, shifter_1_out};  // Bit_Extender bit_extender_3
  assign bit_extender_4_out = {{12{shifter_2_out[19]}}, shifter_2_out};  // Bit_Extender bit_extender_4
  Pull_Resistor #(.pull(1)) pull_resistor_1 (.node(controlled_buffer_1_out));
  Regifile regifile_1 (
    .Din(RDin), .Clk(CLK), .R1(R1), .R2(R2), .WE(RegWrite), .W_num(W_num), .R1_num(multiplexer_4_out),
    .R2_num(multiplexer_5_out));
  not not_2 (not_2_out, halt);
  Counter #(.width(16), .max('hffff), .ongoal("wrap"), .trigger("rising"), .behavior("new")) counter_2 (
    .count(not_2_out), .Q(\总周期数 ), .clk(CLK), .clr(RST));  // open: load, D, carry, preset, down
  Comparator #(.width(32), .mode("twosComplement")) comparator_2 (
    .a(R1), .b(32'ha), .eq(comparator_2_eq));  // open: gt, lt
  not not_3 (not_3_out, comparator_2_eq);
  or or_1 (or_1_out, Branch, Jal, Jalr);
  and and_2 (and_2_out, ecall, not_3_out);
  and and_3 (and_3_out, comparator_2_eq, ecall);
  Register #(.width(32), .trigger("rising"), .Select("low")) register_1 (
    .D(R2), .en(and_2_out), .Q(LedData), .clk(CLK), .clr(RST));
  Counter #(.width(16), .max('hffff), .ongoal("wrap"), .trigger("rising"), .behavior("new")) counter_3 (
    .count(Branch), .Q(\条件分支成功数 ), .clk(CLK), .clr(RST));  // open: load, D, carry, preset, down
  or or_2 (or_2_out, RST, or_1_out);
  ID_EX id_ex_1 (
    .PCin(ID_PC), .PCout(EX_PC),
    .IRin({ID_IR[31], ID_Funct[4], ID_IR[29:26], ID_Funct[3], ID_IR[24:15], ID_Funct[2:0], ID_IR[11:0]}),
    .IRout(EX_IR), .RST(or_2_out), .EN_H(en), .CLK(CLK), .Imm_I_in(bit_extender_1_out),
    .Imm_I_out(id_ex_1_imm_i_out), .Imm_S_in(bit_extender_2_out), .Imm_S_out(id_ex_1_imm_s_out),
    .Imm_B_in(bit_extender_3_out), .Imm_B_out(imm_B), .Imm_J_in(bit_extender_4_out), .Imm_J_out(imm_J),
    .Imm_U_in({ID_IR[31], ID_Funct[4], ID_IR[29:26], ID_Funct[3], ID_IR[24:15], ID_Funct[2:0], {12{1'b0}}}),
    .Imm_U_out(id_ex_1_imm_u_out), .R1in(R1), .R1out(id_ex_1_r1out), .R2in(R2), .R2out(id_ex_1_r2out),
    .Lhuin(\单周期硬布线控制器_1_lhu ), .Lhuout(id_ex_1_lhuout), .Jalrin(\单周期硬布线控制器_1_jalr ), .Jalrout(Jalr),
    .Jalout(Jal), .Jalin(\单周期硬布线控制器_1_jal ), .Beqin(\单周期硬布线控制器_1_beq ), .Beqout(id_ex_1_beqout),
    .Bgeuin(\单周期硬布线控制器_1_bgeu ), .Bgeuout(id_ex_1_bgeuout), .Bnein(\单周期硬布线控制器_1_bne ),
    .Bneout(id_ex_1_bneout), .MemToRegin(\单周期硬布线控制器_1_memtoreg ), .MemToRegout(id_ex_1_memtoregout),
    .MemWritein(\单周期硬布线控制器_1_memwrite ), .MemWriteout(id_ex_1_memwriteout),
    .AluSrcBin(\单周期硬布线控制器_1_alu_src ), .AluSrcBout(id_ex_1_alusrcbout), .RegWritein(\单周期硬布线控制器_1_regwrite ),
    .RegWriteout(id_ex_1_regwriteout), .U_Typein(\单周期硬布线控制器_1_u_type ), .U_Tpyeout(id_ex_1_u_tpyeout),
    .AluOpin(\单周期硬布线控制器_1_alu_op ), .AluOpout(id_ex_1_aluopout), .S_Typein(\单周期硬布线控制器_1_s_type ),
    .S_Tpyeout(id_ex_1_s_tpyeout), .Ecallin(and_3_out), .Ecallout(id_ex_1_ecallout), .W_in(ID_IR[11:7]),
    .W_out(id_ex_1_w_out));  // open: R1Forwardin, R1Forwardout, R2Forwardin, R2Forwardout
  Multiplexer #(.select(1), .width(32), .disabled("Z"), .enable("false")) multiplexer_6 (
    .in0(id_ex_1_imm_i_out), .in1(id_ex_1_imm_s_out), .out(multiplexer_6_out), .sel(id_ex_1_s_tpyeout));
  or or_3 (or_3_out, Jal, Jalr);
  Multiplexer #(.select(1), .width(32), .disabled("Z"), .enable("false")) multiplexer_7 (
    .in0(id_ex_1_r2out), .in1(multiplexer_6_out), .out(multiplexer_7_out), .sel(id_ex_1_alusrcbout));
  Counter #(.width(16), .max('hffff), .ongoal("wrap"), .trigger("rising"), .behavior("new")) counter_4 (
    .count(or_3_out), .Q(\无条件分支数 ), .clk(CLK), .clr(RST));  // open: load, D, carry, preset, down
  and and_4 (and_4_out, id_ex_1_beqout, equal);
  not not_4 (not_4_out, equal);
  and and_5 (and_5_out, not_4_out, id_ex_1_bneout);
  and and_6 (and_6_out, MoreAndEqu, id_ex_1_bgeuout);
  ALU alu_1 (
    .X(id_ex_1_r1out), .Y(multiplexer_7_out), .AluOP(id_ex_1_aluopout), .Equal(equal), .Result(Jalr_Addr),
    .out_4(MoreAndEqu));  // open: Result_2, out_6
  or or_4 (Branch, and_4_out, and_5_out, and_6_out);
  EX_MEM ex_mem_1 (
    .PCin(EX_PC), .Lhuin(id_ex_1_lhuout), .PCout(M_PC), .Lhuout(ex_mem_1_lhuout), .Jalrin(Jalr),
    .Jalrout(ex_mem_1_jalrout), .IRin(EX_IR), .IRout(MEM_IR), .Jalin(Jal), .Jalout(ex_mem_1_jalout),
    .MemToRegin(id_ex_1_memtoregout), .MemToRegout(MemToReg), .MemWritein(id_ex_1_memwriteout),
    .MemWriteout(MemWrite), .Imm_U_in(id_ex_1_imm_u_out), .Imm_U_out(ex_mem_1_imm_u_out),
    .Resultin(Jalr_Addr), .Resultout(ex_mem_1_resultout), .RegWritein(id_ex_1_regwriteout),
    .RegWriteout(ex_mem_1_regwriteout), .U_Typein(id_ex_1_u_tpyeout), .U_Tpyeout(ex_mem_1_u_tpyeout),
    .Haltin(id_ex_1_ecallout), .Haltout(ex_mem_1_haltout), .W_in(id_ex_1_w_out), .W_out(ex_mem_1_w_out),
    .RST(RST), .EN_H(en), .CLK(CLK), .WMdatain(id_ex_1_r2out), .WMdataout(MDin));
  Adder #(.width(16)) adder_4 (.a(\无条件分支数 ), .b(\条件分支成功数 ), .out(adder_4_out));  // open: cin, cout
  Shifter #(.width(16), .shift("ll")) shifter_3 (.in(adder_4_out), .\dist (4'b0001), .out(\插入气泡数 ));
  RAM #(.addrWidth(10), .dataWidth(32), .bus("separate"), .Select("high")) ram_1 (
    .addr(ex_mem_1_resultout[11:2]), .din(MDin), .data(ram_1_data), .str(MemWrite), .clk(CLK), .ld(MemToReg),
    .clr(RST));  // open: sel
  MEM_WB mem_wb_1 (
    .Lhuin(ex_mem_1_lhuout), .PCin(M_PC), .Jalrin(ex_mem_1_jalrout), .Jalin(ex_mem_1_jalout), .IRin(MEM_IR),
    .MemToRegin(MemToReg), .Imm_U_in(ex_mem_1_imm_u_out), .RegWritein(ex_mem_1_regwriteout),
    .AluResultin(ex_mem_1_resultout), .U_Typein(ex_mem_1_u_tpyeout), .RMdatain(ram_1_data),
    .Haltin(ex_mem_1_haltout), .W_in(ex_mem_1_w_out), .Lhuout(mem_wb_1_lhuout), .PCout(WB_PC),
    .Jalrout(mem_wb_1_jalrout), .Jalout(mem_wb_1_jalout), .IRout(WB_IR), .MemToRegout(mem_wb_1_memtoregout),
    .Imm_U_out(mem_wb_1_imm_u_out), .RegWriteout(RegWrite), .AluResultout(mem_wb_1_aluresultout),
    .U_Tpyeout(mem_wb_1_u_tpyeout), .RMdataout(mem_wb_1_rmdataout), .Haltout(mem_wb_1_haltout),
    .W_out(W_num), .RST(RST), .EN_H(en), .CLK(CLK), .Xin(ex_mem_1_resultout[1]), .Xout(mem_wb_1_xout));
  Multiplexer #(.select(1), .width(16), .disabled("Z"), .enable("false")) multiplexer_8 (
    .in0(mem_wb_1_rmdataout[15:0]), .in1(mem_wb_1_rmdataout[31:16]), .out(multiplexer_8_out),
    .sel(mem_wb_1_xout));
  Adder #(.width(32)) adder_5 (.a(WB_PC), .b(mem_wb_1_imm_u_out), .out(adder_5_out));  // open: cin, cout
  and and_7 (halt, mem_wb_1_haltout, ~Go);  // AND_Gate
  not not_5 (en, halt);
  Adder #(.width(32)) adder_6 (.a(32'h4), .b(WB_PC), .out(WB_PC_4));  // open: cin, cout
  or or_5 (or_5_out, mem_wb_1_jalrout, mem_wb_1_jalout, mem_wb_1_u_tpyeout);
  assign bit_extender_5_out = {{16{1'b0}}, multiplexer_8_out};  // Bit_Extender bit_extender_5
  Multiplexer #(.select(1), .width(32), .disabled("Z"), .enable("false")) multiplexer_9 (
    .in0(mem_wb_1_rmdataout), .in1(bit_extender_5_out), .out(multiplexer_9_out), .sel(mem_wb_1_lhuout));
  Multiplexer #(.select(1), .width(32), .disabled("Z"), .enable("false")) multiplexer_10 (
    .in0(WB_PC_4), .in1(adder_5_out), .out(multiplexer_10_out), .sel(mem_wb_1_u_tpyeout));
  Multiplexer #(.select(1), .width(32), .disabled("Z"), .enable("false")) multiplexer_11 (
    .in0(mem_wb_1_aluresultout), .in1(multiplexer_9_out), .out(multiplexer_11_out), .sel(mem_wb_1_memtoregout));
  Multiplexer #(.select(1), .width(32), .disabled("Z"), .enable("false")) multiplexer_12 (
    .in0(multiplexer_11_out), .in1(multiplexer_10_out), .out(RDin), .sel(or_5_out));

  // Other names for the same wires on the sheet: RD_num[4:0] = ID_IR[11:7]; ID_IR (some bits) = ID_Funct;
  //   ID_OP[4:0] = ID_IR[6:2]; MEM_PC[31:0] = M_PC; WriteBackData[31:0] = RDin

  // Notes on the sheet:
  //   中断源
  //   时空图监测，可删除
  //   中断等待指示
  //   数码管输出
  //   指令存储器
  //   指令字
  //   contents of rom_1 (hex, n*v repeats v):
  //   100493 100006f 100493 200913 300993 100006f 100493 200913 300993 100006f 100493 200913 300993
  //   100006f 100493 200913 300993 424000ef 100413 100493 1f49493 900533 2200893 73 24d493 48463 fedff06f
  //   900533 2200893 73 100493 249493 900533 2200893 73 48463 fedff06f 100493 1f49493 900533 2200893 73
  //   4034d493 900533 2200893 73 4044d493 900533 2200893 73 4044d493 900533 2200893 73 4044d493 900533
  //   2200893 73 4044d493 900533 2200893 73 4044d493 900533 2200893 73 4044d493 900533 2200893 73 4044d493
  //   900533 2200893 73 100413 1f41993 41f9d993 433 c00913 300b13 140413 f47413 800293 100313 499993
  //   89e9b3 1300533 2200893 73 406282b3 fe0294e3 140413 f00f93 1f47433 1c41413 800293 100313 49d993
  //   89e9b3 1300533 2200893 73 406282b3 fe0294e3 1c45413 406b0b33 b0463 f95ff06f 2b3 fff2c293 829293
  //   ff2e293 500533 2200893 73 fff00413 493 84a023 140413 448493 84a023 140413 448493 84a023 140413
  //   448493 84a023 140413 448493 84a023 140413 448493 84a023 140413 448493 84a023 140413 448493 84a023
  //   140413 448493 84a023 140413 448493 84a023 140413 448493 84a023 140413 448493 84a023 140413 448493
  //   84a023 140413 448493 84a023 140413 448493 84a023 140413 448493 84a023 140413 448493 140413 433
  //   3c00493 42983 4aa03 149a2b3 28663 134a023 1442023 ffc48493 fe9412e3 800533 2200893 73 440413 3c00493
  //   fc9416e3 a00893 73 100293 300313 800493 849493 7648493 1449493 900533 2200893 73 800e13 54d4b3
  //   64d4b3 900533 2200893 73 fffe0e13 fe0e14e3 a00893 73 13 430497 900533 2200893 73 430497 900533
  //   2200893 73 430497 900533 2200893 73 430497 900533 2200893 73 430497 900533 2200893 73 430497 900533
  //   2200893 73 430497 900533 2200893 73 430497 900533 2200893 73 a00893 73 313 1000e13 8400493 849493
  //   8348493 400913 891913 490913 849493 8248493 849493 8148493 891913 490913 891913 490913 932023
  //   12484b3 430313 fffe0e13 fe0e18e3 2000e13 313 35483 900533 2200893 73 230313 fffe0e13 fe0e14e3 a00893
  //   73 f00493 100913 409909b3 900533 2200893 73 fff48493 ff29f6e3 a00893 73 a00893 73 413 140413 800533
  //   2200893 73 240413 800533 2200893 73 340413 800533 2200893 73 440413 800533 2200893 73 540413 800533
  //   2200893 73 640413 800533 2200893 73 740413 800533 2200893 73 840413 800533 2200893 2200893 73 8067
  //   控制位
  //   流水调试日志用
  //   暂停节拍，不能为0
  //   rs1
  //   rs2
  //   rd
  //   戳工具置1进入计数暂停模式，ctrl+k时钟自动运行到对应节拍暂停
  //   ctrl+k关闭时钟连续运行，将控制位置零，进入单步调试模式调试
  //   Beq
  //   Bgeu
  //   Bne
  //   MemToReg
  //   MemWrite
  //   AluOP
  //   AluSrcB
  //   RegWrite
  //   U_Type
  //   S_Type
  //   可计数暂停的时钟源
  //   为方便自动评测，需要输出流水线各段保存的PC值，注意是PC不是PC+4，另外ID段寄存器写入信息，Mem段内存写入信息也要输出
  //   数据存储器
endmodule

// 寄存器有效信号判断
module \寄存器有效信号判断自动生成  (
  input  OP2,
  input  OP3,
  input  OP4,
  input  OP5,
  input  OP6,
  input  F12,
  input  F13,
  input  F14,
  input  F25,
  input  F30,
  output R1,
  output R2
);

  wire and_1_out, and_2_out, and_3_out, and_4_out, and_5_out, and_6_out, and_7_out, and_8_out, and_9_out,
       and_10_out, and_11_out, and_12_out, and_13_out, and_14_out, and_15_out, and_16_out, and_17_out,
       and_18_out, and_19_out, and_20_out, and_21_out, and_22_out, and_23_out, and_24_out, and_25_out,
       and_26_out, and_27_out, and_28_out, and_29_out, and_30_out, and_31_out, and_32_out, and_33_out,
       and_34_out, and_35_out, not_1_out, not_2_out, not_3_out, not_4_out, not_5_out, not_6_out, not_7_out,
       not_8_out, not_9_out, not_10_out, not_11_out, not_12_out, not_13_out, not_14_out, not_15_out,
       not_16_out, not_17_out, not_18_out, not_19_out, not_20_out, not_21_out, not_22_out, not_23_out,
       not_24_out, not_25_out, not_26_out, not_27_out, not_28_out, not_29_out, not_30_out, not_31_out,
       not_32_out, not_33_out, not_34_out, not_35_out, not_36_out, not_37_out, not_38_out, not_39_out,
       not_40_out, not_41_out, not_42_out, not_43_out, not_44_out, not_45_out, not_46_out, not_47_out,
       not_48_out, not_49_out, not_50_out, not_51_out, not_52_out, not_53_out, not_54_out, not_55_out,
       not_56_out, not_57_out, not_58_out, not_59_out, not_60_out, not_61_out, not_62_out, not_63_out,
       not_64_out, not_65_out, not_66_out, not_67_out, not_68_out, not_69_out, not_70_out, not_71_out,
       not_72_out, not_73_out, not_74_out, not_75_out, not_76_out, not_77_out, not_78_out, not_79_out,
       not_80_out, not_81_out, not_82_out, not_83_out, not_84_out, not_85_out, not_86_out, not_87_out,
       not_88_out, not_89_out, not_90_out, not_91_out, not_92_out, not_93_out, not_94_out, not_95_out,
       not_96_out, not_97_out, not_98_out, not_99_out, not_100_out, not_101_out, not_102_out, not_103_out,
       not_104_out, not_105_out, not_106_out, not_107_out, not_108_out, not_109_out, not_110_out,
       not_111_out, not_112_out, not_113_out, not_114_out, not_115_out, not_116_out, not_117_out,
       not_118_out, not_119_out, not_120_out, not_121_out, not_122_out, not_123_out, not_124_out,
       not_125_out, not_126_out, not_127_out, not_128_out, not_129_out, not_130_out, not_131_out,
       not_132_out, not_133_out, not_134_out, not_135_out, not_136_out, not_137_out, not_138_out,
       not_139_out, not_140_out, not_141_out, not_142_out, not_143_out, not_144_out, not_145_out,
       not_146_out, not_147_out, not_148_out, not_149_out, not_150_out, not_151_out, not_152_out,
       not_153_out, not_154_out, not_155_out, not_156_out, not_157_out, not_158_out, not_159_out,
       not_160_out, not_161_out, not_162_out, not_163_out, not_164_out, not_165_out, not_166_out,
       not_167_out, not_168_out, not_169_out, not_170_out, not_171_out, not_172_out, not_173_out,
       not_174_out, not_175_out, not_176_out, not_177_out, not_178_out, not_179_out, not_180_out,
       not_181_out, not_182_out, not_183_out, not_184_out, not_185_out, not_186_out, not_187_out,
       not_188_out, not_189_out, not_190_out, not_191_out, not_192_out, not_193_out, not_194_out,
       not_195_out, not_196_out, not_197_out, not_198_out, not_199_out, not_200_out, not_201_out,
       not_202_out, not_203_out, not_204_out, not_205_out, not_206_out, not_207_out, not_208_out,
       not_209_out, not_210_out, not_211_out;

  not not_1 (not_1_out, F30);
  not not_2 (not_2_out, F25);
  not not_3 (not_3_out, F14);
  not not_4 (not_4_out, F13);
  not not_5 (not_5_out, F12);
  not not_6 (not_6_out, OP6);
  not not_7 (not_7_out, OP3);
  not not_8 (not_8_out, OP2);
  not not_9 (not_9_out, F25);
  not not_10 (not_10_out, F14);
  not not_11 (not_11_out, F13);
  not not_12 (not_12_out, F12);
  not not_13 (not_13_out, OP6);
  not not_14 (not_14_out, OP3);
  not not_15 (not_15_out, OP2);
  not not_16 (not_16_out, F30);
  not not_17 (not_17_out, F25);
  not not_18 (not_18_out, OP6);
  not not_19 (not_19_out, OP3);
  not not_20 (not_20_out, OP2);
  not not_21 (not_21_out, F30);
  not not_22 (not_22_out, F25);
  not not_23 (not_23_out, F12);
  not not_24 (not_24_out, OP6);
  not not_25 (not_25_out, OP3);
  not not_26 (not_26_out, OP2);
  not not_27 (not_27_out, F30);
  not not_28 (not_28_out, F25);
  not not_29 (not_29_out, F14);
  not not_30 (not_30_out, F12);
  not not_31 (not_31_out, OP6);
  not not_32 (not_32_out, OP3);
  not not_33 (not_33_out, OP2);
  not not_34 (not_34_out, F30);
  not not_35 (not_35_out, F25);
  not not_36 (not_36_out, F14);
  not not_37 (not_37_out, OP6);
  not not_38 (not_38_out, OP3);
  not not_39 (not_39_out, OP2);
  not not_40 (not_40_out, F14);
  not not_41 (not_41_out, F13);
  not not_42 (not_42_out, F12);
  not not_43 (not_43_out, OP6);
  not not_44 (not_44_out, OP5);
  not not_45 (not_45_out, OP3);
  not not_46 (not_46_out, OP2);
  not not_47 (not_47_out, OP6);
  not not_48 (not_48_out, OP5);
  not not_49 (not_49_out, OP3);
  not not_50 (not_50_out, OP2);
  not not_51 (not_51_out, F12);
  not not_52 (not_52_out, OP6);
  not not_53 (not_53_out, OP5);
  not not_54 (not_54_out, OP3);
  not not_55 (not_55_out, OP2);
  not not_56 (not_56_out, F13);
  not not_57 (not_57_out, F12);
  not not_58 (not_58_out, OP6);
  not not_59 (not_59_out, OP5);
  not not_60 (not_60_out, OP3);
  not not_61 (not_61_out, OP2);
  not not_62 (not_62_out, F14);
  not not_63 (not_63_out, F12);
  not not_64 (not_64_out, OP6);
  not not_65 (not_65_out, OP5);
  not not_66 (not_66_out, OP3);
  not not_67 (not_67_out, OP2);
  not not_68 (not_68_out, F30);
  not not_69 (not_69_out, F25);
  not not_70 (not_70_out, F14);
  not not_71 (not_71_out, F13);
  not not_72 (not_72_out, OP6);
  not not_73 (not_73_out, OP5);
  not not_74 (not_74_out, OP3);
  not not_75 (not_75_out, OP2);
  not not_76 (not_76_out, F30);
  not not_77 (not_77_out, F25);
  not not_78 (not_78_out, F13);
  not not_79 (not_79_out, OP6);
  not not_80 (not_80_out, OP5);
  not not_81 (not_81_out, OP3);
  not not_82 (not_82_out, OP2);
  not not_83 (not_83_out, F25);
  not not_84 (not_84_out, F13);
  not not_85 (not_85_out, OP6);
  not not_86 (not_86_out, OP5);
  not not_87 (not_87_out, OP3);
  not not_88 (not_88_out, OP2);
  not not_89 (not_89_out, F14);
  not not_90 (not_90_out, F12);
  not not_91 (not_91_out, OP6);
  not not_92 (not_92_out, OP5);
  not not_93 (not_93_out, OP4);
  not not_94 (not_94_out, OP3);
  not not_95 (not_95_out, OP2);
  not not_96 (not_96_out, F14);
  not not_97 (not_97_out, F12);
  not not_98 (not_98_out, OP6);
  not not_99 (not_99_out, OP4);
  not not_100 (not_100_out, OP3);
  not not_101 (not_101_out, OP2);
  not not_102 (not_102_out, F30);
  not not_103 (not_103_out, F25);
  not not_104 (not_104_out, F14);
  not not_105 (not_105_out, F13);
  not not_106 (not_106_out, F12);
  not not_107 (not_107_out, OP3);
  not not_108 (not_108_out, OP2);
  not not_109 (not_109_out, F14);
  not not_110 (not_110_out, F13);
  not not_111 (not_111_out, F12);
  not not_112 (not_112_out, OP4);
  not not_113 (not_113_out, OP3);
  not not_114 (not_114_out, OP2);
  not not_115 (not_115_out, F14);
  not not_116 (not_116_out, F13);
  not not_117 (not_117_out, OP4);
  not not_118 (not_118_out, OP3);
  not not_119 (not_119_out, OP2);
  not not_120 (not_120_out, F14);
  not not_121 (not_121_out, F13);
  not not_122 (not_122_out, F12);
  not not_123 (not_123_out, OP4);
  not not_124 (not_124_out, OP3);
  not not_125 (not_125_out, F30);
  not not_126 (not_126_out, F25);
  not not_127 (not_127_out, F13);
  not not_128 (not_128_out, OP6);
  not not_129 (not_129_out, OP3);
  not not_130 (not_130_out, OP2);
  not not_131 (not_131_out, F13);
  not not_132 (not_132_out, OP6);
  not not_133 (not_133_out, OP5);
  not not_134 (not_134_out, OP4);
  not not_135 (not_135_out, OP3);
  not not_136 (not_136_out, OP2);
  not not_137 (not_137_out, OP4);
  not not_138 (not_138_out, OP3);
  not not_139 (not_139_out, OP2);
  not not_140 (not_140_out, F30);
  not not_141 (not_141_out, F25);
  not not_142 (not_142_out, F14);
  not not_143 (not_143_out, F13);
  not not_144 (not_144_out, F12);
  not not_145 (not_145_out, OP6);
  not not_146 (not_146_out, OP3);
  not not_147 (not_147_out, OP2);
  not not_148 (not_148_out, F25);
  not not_149 (not_149_out, F14);
  not not_150 (not_150_out, F13);
  not not_151 (not_151_out, F12);
  not not_152 (not_152_out, OP6);
  not not_153 (not_153_out, OP3);
  not not_154 (not_154_out, OP2);
  not not_155 (not_155_out, F30);
  not not_156 (not_156_out, F25);
  not not_157 (not_157_out, OP6);
  not not_158 (not_158_out, OP3);
  not not_159 (not_159_out, OP2);
  not not_160 (not_160_out, F30);
  not not_161 (not_161_out, F25);
  not not_162 (not_162_out, F12);
  not not_163 (not_163_out, OP6);
  not not_164 (not_164_out, OP3);
  not not_165 (not_165_out, OP2);
  not not_166 (not_166_out, F30);
  not not_167 (not_167_out, F25);
  not not_168 (not_168_out, F14);
  not not_169 (not_169_out, F12);
  not not_170 (not_170_out, OP6);
  not not_171 (not_171_out, OP3);
  not not_172 (not_172_out, OP2);
  not not_173 (not_173_out, F30);
  not not_174 (not_174_out, F25);
  not not_175 (not_175_out, F14);
  not not_176 (not_176_out, OP6);
  not not_177 (not_177_out, OP3);
  not not_178 (not_178_out, OP2);
  not not_179 (not_179_out, F14);
  not not_180 (not_180_out, F12);
  not not_181 (not_181_out, OP6);
  not not_182 (not_182_out, OP4);
  not not_183 (not_183_out, OP3);
  not not_184 (not_184_out, OP2);
  not not_185 (not_185_out, F30);
  not not_186 (not_186_out, F25);
  not not_187 (not_187_out, F14);
  not not_188 (not_188_out, F13);
  not not_189 (not_189_out, F12);
  not not_190 (not_190_out, OP3);
  not not_191 (not_191_out, OP2);
  not not_192 (not_192_out, F14);
  not not_193 (not_193_out, F13);
  not not_194 (not_194_out, F12);
  not not_195 (not_195_out, OP4);
  not not_196 (not_196_out, OP3);
  not not_197 (not_197_out, OP2);
  not not_198 (not_198_out, F14);
  not not_199 (not_199_out, F13);
  not not_200 (not_200_out, OP4);
  not not_201 (not_201_out, OP3);
  not not_202 (not_202_out, OP2);
  not not_203 (not_203_out, F30);
  not not_204 (not_204_out, F25);
  not not_205 (not_205_out, F13);
  not not_206 (not_206_out, OP6);
  not not_207 (not_207_out, OP3);
  not not_208 (not_208_out, OP2);
  not not_209 (not_209_out, OP4);
  not not_210 (not_210_out, OP3);
  not not_211 (not_211_out, OP2);
  and and_1 (and_1_out, not_1_out, not_2_out, not_3_out, not_4_out, not_5_out, not_6_out, OP5, OP4, not_7_out, not_8_out);
  and and_2 (and_2_out, F30, not_9_out, not_10_out, not_11_out, not_12_out, not_13_out, OP5, OP4, not_14_out, not_15_out);
  and and_3 (and_3_out, not_16_out, not_17_out, F14, F13, F12, not_18_out, OP5, OP4, not_19_out, not_20_out);
  and and_4 (and_4_out, not_21_out, not_22_out, F14, F13, not_23_out, not_24_out, OP5, OP4, not_25_out, not_26_out);
  and and_5 (and_5_out, not_27_out, not_28_out, not_29_out, F13, not_30_out, not_31_out, OP5, OP4, not_32_out, not_33_out);
  and and_6 (and_6_out, not_34_out, not_35_out, not_36_out, F13, F12, not_37_out, OP5, OP4, not_38_out, not_39_out);
  and and_7 (and_7_out, not_40_out, not_41_out, not_42_out, not_43_out, not_44_out, OP4, not_45_out, not_46_out);
  and and_8 (and_8_out, F14, F13, F12, not_47_out, not_48_out, OP4, not_49_out, not_50_out);
  and and_9 (and_9_out, F14, F13, not_51_out, not_52_out, not_53_out, OP4, not_54_out, not_55_out);
  and and_10 (and_10_out, F14, not_56_out, not_57_out, not_58_out, not_59_out, OP4, not_60_out, not_61_out);
  and and_11 (and_11_out, not_62_out, F13, not_63_out, not_64_out, not_65_out, OP4, not_66_out, not_67_out);
  and and_12 (and_12_out, not_68_out, not_69_out, not_70_out, not_71_out, F12, not_72_out, not_73_out, OP4, not_74_out, not_75_out);
  and and_13 (and_13_out, not_76_out, not_77_out, F14, not_78_out, F12, not_79_out, not_80_out, OP4, not_81_out, not_82_out);
  and and_14 (and_14_out, F30, not_83_out, F14, not_84_out, F12, not_85_out, not_86_out, OP4, not_87_out, not_88_out);
  and and_15 (and_15_out, not_89_out, F13, not_90_out, not_91_out, not_92_out, not_93_out, not_94_out, not_95_out);
  and and_16 (and_16_out, not_96_out, F13, not_97_out, not_98_out, OP5, not_99_out, not_100_out, not_101_out);
  and and_17 (and_17_out, not_102_out, not_103_out, not_104_out, not_105_out, not_106_out, OP6, OP5, OP4, not_107_out, not_108_out);
  and and_18 (and_18_out, not_109_out, not_110_out, not_111_out, OP6, OP5, not_112_out, not_113_out, not_114_out);
  and and_19 (and_19_out, not_115_out, not_116_out, F12, OP6, OP5, not_117_out, not_118_out, not_119_out);
  and and_20 (and_20_out, not_120_out, not_121_out, not_122_out, OP6, OP5, not_123_out, not_124_out, OP2);
  and and_21 (and_21_out, not_125_out, not_126_out, F14, not_127_out, F12, not_128_out, OP5, OP4, not_129_out, not_130_out);
  and and_22 (and_22_out, F14, not_131_out, F12, not_132_out, not_133_out, not_134_out, not_135_out, not_136_out);
  and and_23 (and_23_out, F14, F13, F12, OP6, OP5, not_137_out, not_138_out, not_139_out);
  and and_24 (and_24_out, not_140_out, not_141_out, not_142_out, not_143_out, not_144_out, not_145_out, OP5, OP4, not_146_out, not_147_out);
  and and_25 (and_25_out, F30, not_148_out, not_149_out, not_150_out, not_151_out, not_152_out, OP5, OP4, not_153_out, not_154_out);
  and and_26 (and_26_out, not_155_out, not_156_out, F14, F13, F12, not_157_out, OP5, OP4, not_158_out, not_159_out);
  and and_27 (and_27_out, not_160_out, not_161_out, F14, F13, not_162_out, not_163_out, OP5, OP4, not_164_out, not_165_out);
  and and_28 (and_28_out, not_166_out, not_167_out, not_168_out, F13, not_169_out, not_170_out, OP5, OP4, not_171_out, not_172_out);
  and and_29 (and_29_out, not_173_out, not_174_out, not_175_out, F13, F12, not_176_out, OP5, OP4, not_177_out, not_178_out);
  and and_30 (and_30_out, not_179_out, F13, not_180_out, not_181_out, OP5, not_182_out, not_183_out, not_184_out);
  and and_31 (and_31_out, not_185_out, not_186_out, not_187_out, not_188_out, not_189_out, OP6, OP5, OP4, not_190_out, not_191_out);
  and and_32 (and_32_out, not_192_out, not_193_out, not_194_out, OP6, OP5, not_195_out, not_196_out, not_197_out);
  and and_33 (and_33_out, not_198_out, not_199_out, F12, OP6, OP5, not_200_out, not_201_out, not_202_out);
  and and_34 (and_34_out, not_203_out, not_204_out, F14, not_205_out, F12, not_206_out, OP5, OP4, not_207_out, not_208_out);
  and and_35 (and_35_out, F14, F13, F12, OP6, OP5, not_209_out, not_210_out, not_211_out);
  or or_1 (R2, and_24_out, and_25_out, and_26_out, and_27_out, and_28_out, and_29_out, and_30_out, and_31_out, and_32_out, and_33_out, and_34_out, and_35_out);
  or or_2 (R1, and_1_out, and_2_out, and_3_out, and_4_out, and_5_out, and_6_out, and_7_out, and_8_out, and_9_out, and_10_out, and_11_out, and_12_out, and_13_out, and_14_out, and_15_out, and_16_out, and_17_out, and_18_out, and_19_out, and_20_out, and_21_out, and_22_out, and_23_out);
endmodule

// 数据冲突处理逻辑-气泡
module \数据冲突处理逻辑_气泡  (
  input  [4:0] ID_R1_num,
  input  [4:0] EX_W_num,
  input  EX_RegWrite,
  input  [4:0] ID_R2_num,
  input  [4:0] MEM_W_num,
  input  MEM_RegWrite,
  input  [4:0] OP,
  input  [4:0] Funct,
  output \数据相关 
);

  wire and_1_out, and_2_out, and_3_out, and_4_out, and_5_out, and_6_out, comparator_1_eq, comparator_2_eq,
       comparator_3_eq, comparator_4_eq, comparator_5_eq, comparator_6_eq, comparator_7_eq, comparator_8_eq,
       or_1_out, or_2_out, \寄存器有效信号判断自动生成_1_r1 , \寄存器有效信号判断自动生成_1_r2 ;

  \寄存器有效信号判断自动生成  \u_寄存器有效信号判断自动生成_1  (
    .OP2(OP[0]), .OP3(OP[1]), .OP4(OP[2]), .OP5(OP[3]), .OP6(OP[4]), .F12(Funct[0]), .F13(Funct[1]),
    .F14(Funct[2]), .F25(Funct[3]), .F30(Funct[4]), .R1(\寄存器有效信号判断自动生成_1_r1 ), .R2(\寄存器有效信号判断自动生成_1_r2 ));
  Comparator #(.width(5), .mode("twosComplement")) comparator_1 (
    .a(ID_R1_num), .b(EX_W_num), .eq(comparator_1_eq));  // open: gt, lt
  Comparator #(.width(5), .mode("twosComplement")) comparator_2 (
    .a(EX_W_num), .b({5{1'b0}}), .eq(comparator_2_eq));  // open: gt, lt
  Comparator #(.width(5), .mode("twosComplement")) comparator_3 (
    .a(ID_R2_num), .b(EX_W_num), .eq(comparator_3_eq));  // open: gt, lt
  Comparator #(.width(5), .mode("twosComplement")) comparator_4 (
    .a(EX_W_num), .b({5{1'b0}}), .eq(comparator_4_eq));  // open: gt, lt
  and and_1 (and_1_out, comparator_1_eq, EX_RegWrite, ~comparator_2_eq);  // AND_Gate
  and and_2 (and_2_out, comparator_3_eq, EX_RegWrite, ~comparator_4_eq);  // AND_Gate
  Comparator #(.width(5), .mode("twosComplement")) comparator_5 (
    .a(ID_R1_num), .b(MEM_W_num), .eq(comparator_5_eq));  // open: gt, lt
  Comparator #(.width(5), .mode("twosComplement")) comparator_6 (
    .a(MEM_W_num), .b({5{1'b0}}), .eq(comparator_6_eq));  // open: gt, lt
  Comparator #(.width(5), .mode("twosComplement")) comparator_7 (
    .a(ID_R2_num), .b(MEM_W_num), .eq(comparator_7_eq));  // open: gt, lt
  Comparator #(.width(5), .mode("twosComplement")) comparator_8 (
    .a(MEM_W_num), .b({5{1'b0}}), .eq(comparator_8_eq));  // open: gt, lt
  and and_3 (and_3_out, comparator_5_eq, MEM_RegWrite, ~comparator_6_eq);  // AND_Gate
  and and_4 (and_4_out, comparator_7_eq, MEM_RegWrite, ~comparator_8_eq);  // AND_Gate
  or or_1 (or_1_out, and_3_out, and_1_out);
  or or_2 (or_2_out, and_2_out, and_4_out);
  and and_5 (and_5_out, or_1_out, \寄存器有效信号判断自动生成_1_r1 );
  and and_6 (and_6_out, \寄存器有效信号判断自动生成_1_r2 , or_2_out);
  or or_3 (\数据相关 , and_5_out, and_6_out);
endmodule

// 数据冲突处理逻辑-重定向
module \数据冲突处理逻辑_重定向  (
  input  [4:0] ID_R1_num,
  input  [4:0] EX_W_num,
  input  EX_RegWrite,
  input  [4:0] EX_OP,
  input  [4:0] ID_R2_num,
  input  [4:0] MEM_W_num,
  input  MEM_RegWrite,
  input  [4:0] ID_OP,
  input  [4:0] ID_Funct,
  output \数据相关 ,
  output [1:0] R1Forward,
  output Load_Use,
  output [1:0] R2Forward
);

  wire and_3_out, and_4_out, and_5_out, and_6_out, and_9_out, and_10_out, and_11_out, and_12_out,
       comparator_1_eq, comparator_2_eq, comparator_3_eq, comparator_4_eq, comparator_5_eq, comparator_6_eq,
       comparator_7_eq, comparator_8_eq, comparator_9_eq, comparator_10_eq, \EX_R1冲突 , \EX_R2冲突 , \MEM_R1冲突 ,
       \MEM_R2冲突 , or_1_out, or_2_out, or_4_out, or_5_out, \R1使用 , \R2使用 ;

  \寄存器有效信号判断自动生成  \u_寄存器有效信号判断自动生成_1  (
    .OP2(ID_OP[0]), .OP3(ID_OP[1]), .OP4(ID_OP[2]), .OP5(ID_OP[3]), .OP6(ID_OP[4]), .F12(ID_Funct[0]),
    .F13(ID_Funct[1]), .F14(ID_Funct[2]), .F25(ID_Funct[3]), .F30(ID_Funct[4]), .R1(\R1使用 ), .R2(\R2使用 ));
  Comparator #(.width(5), .mode("twosComplement")) comparator_1 (
    .a(ID_R1_num), .b(EX_W_num), .eq(comparator_1_eq));  // open: gt, lt
  Comparator #(.width(5), .mode("twosComplement")) comparator_2 (
    .a(EX_W_num), .b({5{1'b0}}), .eq(comparator_2_eq));  // open: gt, lt
  Comparator #(.width(5), .mode("twosComplement")) comparator_3 (
    .a(ID_R2_num), .b(EX_W_num), .eq(comparator_3_eq));  // open: gt, lt
  Comparator #(.width(5), .mode("twosComplement")) comparator_4 (
    .a(EX_W_num), .b({5{1'b0}}), .eq(comparator_4_eq));  // open: gt, lt
  and and_1 (\EX_R1冲突 , comparator_1_eq, EX_RegWrite, ~comparator_2_eq);  // AND_Gate
  and and_2 (\EX_R2冲突 , comparator_3_eq, EX_RegWrite, ~comparator_4_eq);  // AND_Gate
  and and_3 (and_3_out, \R1使用 , \MEM_R1冲突 );
  and and_4 (and_4_out, \R1使用 , \EX_R1冲突 );
  and and_5 (and_5_out, \R2使用 , \MEM_R2冲突 );
  and and_6 (and_6_out, \R2使用 , \EX_R2冲突 );
  Priority_Encoder #(.select(2), .disabled("Z")) priority_encoder_1 (
    .in0(1'b1), .in1(and_3_out), .in2(and_4_out), .out(R1Forward));  // open: in3, gs, en_out, en_in
  Priority_Encoder #(.select(2), .disabled("Z")) priority_encoder_2 (
    .in0(1'b1), .in1(and_5_out), .in2(and_6_out), .out(R2Forward));  // open: in3, gs, en_out, en_in
  Comparator #(.width(5), .mode("twosComplement")) comparator_5 (
    .a(ID_R1_num), .b(MEM_W_num), .eq(comparator_5_eq));  // open: gt, lt
  Comparator #(.width(5), .mode("twosComplement")) comparator_6 (
    .a(MEM_W_num), .b({5{1'b0}}), .eq(comparator_6_eq));  // open: gt, lt
  Comparator #(.width(5), .mode("twosComplement")) comparator_7 (
    .a(ID_R2_num), .b(MEM_W_num), .eq(comparator_7_eq));  // open: gt, lt
  Comparator #(.width(5), .mode("twosComplement")) comparator_8 (
    .a(MEM_W_num), .b({5{1'b0}}), .eq(comparator_8_eq));  // open: gt, lt
  and and_7 (\MEM_R1冲突 , comparator_5_eq, MEM_RegWrite, ~comparator_6_eq);  // AND_Gate
  and and_8 (\MEM_R2冲突 , comparator_7_eq, MEM_RegWrite, ~comparator_8_eq);  // AND_Gate
  or or_1 (or_1_out, \MEM_R1冲突 , \EX_R1冲突 );
  or or_2 (or_2_out, \EX_R2冲突 , \MEM_R2冲突 );
  and and_9 (and_9_out, or_1_out, \R1使用 );
  and and_10 (and_10_out, \R2使用 , or_2_out);
  and and_11 (and_11_out, \R1使用 , \EX_R1冲突 );
  and and_12 (and_12_out, \EX_R2冲突 , \R2使用 );
  Comparator #(.width(5), .mode("twosComplement")) comparator_9 (
    .a(EX_OP), .b({5{1'b0}}), .eq(comparator_9_eq));  // open: gt, lt
  Comparator #(.width(5), .mode("twosComplement")) comparator_10 (
    .a(EX_OP), .b(5'b00101), .eq(comparator_10_eq));  // open: gt, lt
  or or_3 (\数据相关 , and_9_out, and_10_out);
  or or_4 (or_4_out, and_11_out, and_12_out);
  or or_5 (or_5_out, comparator_9_eq, comparator_10_eq);
  and and_13 (Load_Use, or_4_out, or_5_out);

  // Notes on the sheet:
  //   lw、lhu
  //   auipc
endmodule

module \气泡流水线  (
  output RegWrite,
  output MemWrite,
  output [31:0] IF_PC,
  output [31:0] ID_PC,
  output [31:0] EX_PC,
  output [31:0] M_PC,
  output [31:0] WB_PC,
  output [31:0] RDin,
  output [31:0] MDin,
  output [31:0] LedData
);

  wire and_2_out, and_3_out, and_4_out, and_5_out, and_6_out, and_7_out, and_8_out, and_9_out, Branch, CLK,
       clock_2_out, comparator_1_eq, comparator_1_lt, comparator_2_eq, controlled_buffer_1_out, d_ff_1_q, en,
       equal, ex_mem_1_haltout, ex_mem_1_jalout, ex_mem_1_jalrout, ex_mem_1_lhuout, ex_mem_1_u_tpyeout,
       EX_RegWrite_num, Go, halt, ID_ecall, id_ex_1_alusrcbout, id_ex_1_beqout, id_ex_1_bgeuout,
       id_ex_1_bneout, id_ex_1_ecallout, id_ex_1_lhuout, id_ex_1_memtoregout, id_ex_1_memwriteout,
       id_ex_1_s_tpyeout, id_ex_1_u_tpyeout, IR1, IR2, IR3, Jal, Jalr, MEM_RegWrite_num, mem_wb_1_haltout,
       mem_wb_1_jalout, mem_wb_1_jalrout, mem_wb_1_lhuout, mem_wb_1_memtoregout, mem_wb_1_u_tpyeout,
       mem_wb_1_xout, MemToReg, MoreAndEqu, nand_1_out, not_1_out, not_2_out, not_3_out, not_4_out,
       not_5_out, not_6_out, not_7_out, not_8_out, or_1_out, or_2_out, or_3_out, or_4_out, or_6_out, RST, W1,
       W2, W3, \单周期硬布线控制器_1_alu_src , \单周期硬布线控制器_1_beq , \单周期硬布线控制器_1_bgeu , \单周期硬布线控制器_1_bne ,
       \单周期硬布线控制器_1_jal , \单周期硬布线控制器_1_jalr , \单周期硬布线控制器_1_lhu , \单周期硬布线控制器_1_memtoreg ,
       \单周期硬布线控制器_1_memwrite , \单周期硬布线控制器_1_regwrite , \单周期硬布线控制器_1_s_type , \单周期硬布线控制器_1_u_type , \数据相关 ;
  wire [3:0] id_ex_1_aluopout, \单周期硬布线控制器_1_alu_op ;
  wire [4:0] EX_W_num, ID_Funct, ID_R1_num, ID_R2_num, MEM_W_num, W_num;
  wire [11:0] shifter_1_out;
  wire [12:0] CNT_num;
  wire [15:0] \LoadUse次数 , multiplexer_8_out, \总周期数 , \插入气泡数 , \无条件分支数 , \条件分支成功数 ;
  wire [19:0] shifter_2_out;
  wire [31:0] adder_1_out, adder_2_out, adder_3_out, adder_4_out, and_1_out, bit_extender_1_out,
       bit_extender_2_out, bit_extender_3_out, bit_extender_4_out, bit_extender_5_out, EX_IR,
       ex_mem_1_imm_u_out, ex_mem_1_resultout, id_ex_1_imm_i_out, id_ex_1_imm_s_out, id_ex_1_imm_u_out,
       id_ex_1_r1out, id_ex_1_r2out, ID_IR, IF_IR, imm_B, imm_J, Jalr_Addr, MEM_IR, mem_wb_1_aluresultout,
       mem_wb_1_imm_u_out, mem_wb_1_rmdataout, multiplexer_1_out, multiplexer_2_out, multiplexer_3_out,
       multiplexer_6_out, multiplexer_7_out, multiplexer_9_out, multiplexer_10_out, multiplexer_11_out, R1,
       R2, ram_1_data, WB_IR, WB_PC_4;

  Button \u_总复位  (.out(RST));
  Button _1 (.out(IR1));
  Button _2 (.out(IR2));
  Button _3 (.out(IR3));
  // Probe on \总周期数 
  // Probe on \总周期数 
  Button \u_继续运行  (.out(Go));
  LED #(.active("true")) led_1 (.in(W1));
  LED #(.active("true")) led_2 (.in(W2));
  LED #(.active("true")) led_3 (.in(W3));
  Hex_Digit_Display hex_digit_display_1 (.value(LedData[31:28]));  // open: dp
  // Probe on IF_PC[19:0]
  // RiscV_Probe riscv_probe_1: pin names not known; wires that end beside it: IF_IR
  Hex_Digit_Display hex_digit_display_2 (.value(LedData[27:24]));  // open: dp
  Hex_Digit_Display hex_digit_display_3 (.value(LedData[23:20]));  // open: dp
  // Probe on ID_PC[19:0]
  // RiscV_Probe riscv_probe_2: pin names not known; wires that end beside it: {ID_IR[31], ID_Funct[4], ID_IR[29:26], ID_Funct[3], ID_IR[24:15], ID_Funct[2:0], ID_IR[11:0]}
  Multiplexer #(.select(1), .width(32), .disabled("Z"), .enable("false")) multiplexer_1 (
    .in0(adder_3_out), .in1(adder_1_out), .out(multiplexer_1_out), .sel(Jal));
  Adder #(.width(32)) adder_1 (.a(imm_J), .b(EX_PC), .out(adder_1_out));  // open: cin, cout
  assign and_1_out = Jalr_Addr & 32'hfffffffe;  // AND_Gate and_1, 32 bits wide
  Hex_Digit_Display hex_digit_display_4 (.value(LedData[19:16]));  // open: dp
  Hex_Digit_Display hex_digit_display_5 (.value(LedData[15:12]));  // open: dp
  \数据冲突处理逻辑_气泡  \u_数据冲突处理逻辑_气泡_1  (
    .ID_R1_num(ID_R1_num), .EX_W_num(EX_W_num), .EX_RegWrite(EX_RegWrite_num), .ID_R2_num(ID_R2_num),
    .MEM_W_num(MEM_W_num), .MEM_RegWrite(MEM_RegWrite_num), .OP(ID_IR[6:2]), .Funct(ID_Funct), .\数据相关 (\数据相关 ));
  Multiplexer #(.select(1), .width(32), .disabled("Z"), .enable("false")) multiplexer_2 (
    .in0(multiplexer_1_out), .in1(and_1_out), .out(multiplexer_2_out), .sel(Jalr));
  Adder #(.width(32)) adder_2 (.a(imm_B), .b(EX_PC), .out(adder_2_out));  // open: cin, cout
  Hex_Digit_Display hex_digit_display_6 (.value(LedData[11:8]));  // open: dp
  Hex_Digit_Display hex_digit_display_7 (.value(LedData[7:4]));  // open: dp
  Clock #(.highDuration(1), .lowDuration(1)) clock_1 (.out(CLK));
  // Probe on EX_PC[19:0]
  // RiscV_Probe riscv_probe_3: pin names not known; wires that end beside it: EX_IR
  Multiplexer #(.select(1), .width(32), .disabled("Z"), .enable("false")) multiplexer_3 (
    .in0(multiplexer_2_out), .in1(adder_2_out), .out(multiplexer_3_out), .sel(Branch));
  and and_2 (and_2_out, not_1_out, not_2_out);
  not not_1 (not_1_out, \数据相关 );
  not not_2 (not_2_out, halt);
  Hex_Digit_Display hex_digit_display_8 (.value(LedData[3:0]));  // open: dp
  Register #(.width(32), .trigger("rising"), .Select("low")) PC (
    .D(multiplexer_3_out), .en(and_2_out), .Q(IF_PC), .clk(CLK), .clr(RST));
  // Probe on \总周期数 
  // Probe on M_PC[19:0]
  // RiscV_Probe riscv_probe_4: pin names not known; wires that end beside it: MEM_IR
  // Probe on \总周期数 
  // Probe on \无条件分支数 
  // Probe on \条件分支成功数 
  // Probe on \插入气泡数 
  // Probe on \LoadUse次数 
  Adder #(.width(32)) adder_3 (.a(IF_PC), .b(32'h4), .out(adder_3_out));  // open: cin, cout
  // Probe on IF_PC[11:0]
  // Probe on WB_PC[19:0]
  // RiscV_Probe riscv_probe_5: pin names not known; wires that end beside it: WB_IR
  or or_1 (or_1_out, Branch, Jal, Jalr);
  ROM #(.addrWidth(10), .dataWidth(32), .Select("high")) rom_1 (.addr(IF_PC[11:2]), .data(IF_IR));
  not not_3 (not_3_out, \数据相关 );
  // Probe on EX_PC[11:0]
  // Probe on ID_PC[11:0]
  or or_2 (or_2_out, RST, or_1_out);
  IF_ID if_id_1 (
    .PCin(IF_PC), .IRin(IF_IR), .PCout(ID_PC),
    .IRout({ID_IR[31], ID_Funct[4], ID_IR[29:26], ID_Funct[3], ID_IR[24:15], ID_Funct[2:0], ID_IR[11:0]}),
    .RST(or_2_out), .EN_H(and_3_out), .CLK(CLK));
  and and_3 (and_3_out, not_3_out, en);
  // Probe on M_PC[11:0]
  D_Flip_Flop #(.trigger("high"), .Pre_Clr_Positions("LEGACY"), .NegatePresetClear("false"), .enable("true"), .NewFFLayout("false")) d_ff_1 (.Q(d_ff_1_q));  // open: clk, D, Qn, preset, en, reset
  // Probe on 13'hc
  // Probe on WB_PC[11:0]
  Comparator #(.width(13), .mode("twosComplement")) comparator_1 (
    .a(CNT_num), .b(13'hc), .eq(comparator_1_eq), .lt(comparator_1_lt));  // open: gt
  Clock #(.highDuration(1), .lowDuration(1)) clock_2 (.out(clock_2_out));
  \单周期硬布线控制器  \u_单周期硬布线控制器_1  (
    .Funct(ID_Funct), .OP(ID_IR[6:2]), .ALU_OP(\单周期硬布线控制器_1_alu_op ), .MemToReg(\单周期硬布线控制器_1_memtoreg ),
    .MemWrite(\单周期硬布线控制器_1_memwrite ), .ALU_SRC(\单周期硬布线控制器_1_alu_src ), .RegWrite(\单周期硬布线控制器_1_regwrite ),
    .ecall(ID_ecall), .S_type(\单周期硬布线控制器_1_s_type ), .Jalr(\单周期硬布线控制器_1_jalr ), .Beq(\单周期硬布线控制器_1_beq ),
    .JAL(\单周期硬布线控制器_1_jal ), .Bne(\单周期硬布线控制器_1_bne ), .U_type(\单周期硬布线控制器_1_u_type ),
    .BGEU(\单周期硬布线控制器_1_bgeu ), .LHU(\单周期硬布线控制器_1_lhu ));  // open: URET
  Multiplexer #(.select(1), .width(5), .disabled("Z"), .enable("false")) multiplexer_4 (
    .in0(ID_IR[24:20]), .in1(5'b01010), .out(ID_R2_num), .sel(ID_ecall));
  assign bit_extender_1_out = {{20{ID_IR[31]}}, {ID_IR[31], ID_Funct[4], ID_IR[29:26], ID_Funct[3], ID_IR[24:20]}};  // Bit_Extender bit_extender_1
  assign bit_extender_2_out = {{20{ID_IR[31]}}, {ID_IR[31], ID_Funct[4], ID_IR[29:26], ID_Funct[3], ID_IR[11:7]}};  // Bit_Extender bit_extender_2
  nand nand_1 (nand_1_out, d_ff_1_q, comparator_1_eq);
  Counter #(.width(13), .max('h1fff), .ongoal("stay"), .trigger("rising"), .behavior("old")) counter_1 (
    .count(comparator_1_lt), .Q(CNT_num), .clk(clock_2_out));  // open: load, D, carry, clr, preset
  Multiplexer #(.select(1), .width(5), .disabled("Z"), .enable("false")) multiplexer_5 (
    .in0(ID_IR[19:15]), .in1(5'b10001), .out(ID_R1_num), .sel(ID_ecall));
  Shifter #(.width(12), .shift("ll")) shifter_1 (
    .in({ID_IR[31], ID_IR[7], ID_Funct[4], ID_IR[29:26], ID_Funct[3], ID_IR[11:8]}), .\dist (4'b0001),
    .out(shifter_1_out));
  Shifter #(.width(20), .shift("ll")) shifter_2 (
    .in({ID_IR[31], ID_IR[19:15], ID_Funct[2:0], ID_IR[20], ID_Funct[4], ID_IR[29:26], ID_Funct[3], ID_IR[24:21]}),
    .\dist (5'b00001), .out(shifter_2_out));
  assign controlled_buffer_1_out = nand_1_out ? clock_2_out : 1'bz;  // Controlled_Buffer controlled_buffer_1
  assign bit_extender_3_out = {{20{shifter_1_out[11]}}, shifter_1_out};  // Bit_Extender bit_extender_3
  assign bit_extender_4_out = {{12{shifter_2_out[19]}}, shifter_2_out};  // Bit_Extender bit_extender_4
  Pull_Resistor #(.pull(1)) pull_resistor_1 (.node(controlled_buffer_1_out));
  not not_4 (not_4_out, CLK);
  Regifile regifile_1 (
    .Din(RDin), .Clk(not_4_out), .R1(R1), .R2(R2), .WE(RegWrite), .W_num(W_num), .R1_num(ID_R1_num),
    .R2_num(ID_R2_num));
  not not_5 (not_5_out, halt);
  Counter #(.width(16), .max('hffff), .ongoal("wrap"), .trigger("rising"), .behavior("new")) counter_2 (
    .count(not_5_out), .Q(\总周期数 ), .clk(CLK), .clr(RST));  // open: load, D, carry, preset, down
  Comparator #(.width(32), .mode("twosComplement")) comparator_2 (
    .a(R1), .b(32'ha), .eq(comparator_2_eq));  // open: gt, lt
  not not_6 (not_6_out, comparator_2_eq);
  and and_4 (and_4_out, ID_ecall, not_6_out);
  and and_5 (and_5_out, comparator_2_eq, ID_ecall);
  Register #(.width(32), .trigger("rising"), .Select("low")) register_1 (
    .D(R2), .en(and_4_out), .Q(LedData), .clk(CLK), .clr(RST));
  Counter #(.width(16), .max('hffff), .ongoal("wrap"), .trigger("rising"), .behavior("new")) counter_3 (
    .count(Branch), .Q(\条件分支成功数 ), .clk(CLK), .clr(RST));  // open: load, D, carry, preset, down
  or or_3 (or_3_out, or_2_out, \数据相关 );
  ID_EX id_ex_1 (
    .PCin(ID_PC), .PCout(EX_PC),
    .IRin({ID_IR[31], ID_Funct[4], ID_IR[29:26], ID_Funct[3], ID_IR[24:15], ID_Funct[2:0], ID_IR[11:0]}),
    .IRout(EX_IR), .RST(or_3_out), .EN_H(en), .CLK(CLK), .Imm_I_in(bit_extender_1_out),
    .Imm_I_out(id_ex_1_imm_i_out), .Imm_S_in(bit_extender_2_out), .Imm_S_out(id_ex_1_imm_s_out),
    .Imm_B_in(bit_extender_3_out), .Imm_B_out(imm_B), .Imm_J_in(bit_extender_4_out), .Imm_J_out(imm_J),
    .Imm_U_in({ID_IR[31], ID_Funct[4], ID_IR[29:26], ID_Funct[3], ID_IR[24:15], ID_Funct[2:0], {12{1'b0}}}),
    .Imm_U_out(id_ex_1_imm_u_out), .R1in(R1), .R1out(id_ex_1_r1out), .R2in(R2), .R2out(id_ex_1_r2out),
    .Lhuin(\单周期硬布线控制器_1_lhu ), .Lhuout(id_ex_1_lhuout), .Jalrin(\单周期硬布线控制器_1_jalr ), .Jalrout(Jalr),
    .Jalout(Jal), .Jalin(\单周期硬布线控制器_1_jal ), .Beqin(\单周期硬布线控制器_1_beq ), .Beqout(id_ex_1_beqout),
    .Bgeuin(\单周期硬布线控制器_1_bgeu ), .Bgeuout(id_ex_1_bgeuout), .Bnein(\单周期硬布线控制器_1_bne ),
    .Bneout(id_ex_1_bneout), .MemToRegin(\单周期硬布线控制器_1_memtoreg ), .MemToRegout(id_ex_1_memtoregout),
    .MemWritein(\单周期硬布线控制器_1_memwrite ), .MemWriteout(id_ex_1_memwriteout),
    .AluSrcBin(\单周期硬布线控制器_1_alu_src ), .AluSrcBout(id_ex_1_alusrcbout), .RegWritein(\单周期硬布线控制器_1_regwrite ),
    .RegWriteout(EX_RegWrite_num), .U_Typein(\单周期硬布线控制器_1_u_type ), .U_Tpyeout(id_ex_1_u_tpyeout),
    .AluOpin(\单周期硬布线控制器_1_alu_op ), .AluOpout(id_ex_1_aluopout), .S_Typein(\单周期硬布线控制器_1_s_type ),
    .S_Tpyeout(id_ex_1_s_tpyeout), .Ecallin(and_5_out), .Ecallout(id_ex_1_ecallout), .W_in(ID_IR[11:7]),
    .W_out(EX_W_num));  // open: R1Forwardin, R1Forwardout, R2Forwardin, R2Forwardout
  Multiplexer #(.select(1), .width(32), .disabled("Z"), .enable("false")) multiplexer_6 (
    .in0(id_ex_1_imm_i_out), .in1(id_ex_1_imm_s_out), .out(multiplexer_6_out), .sel(id_ex_1_s_tpyeout));
  not not_7 (not_7_out, equal);
  Multiplexer #(.select(1), .width(32), .disabled("Z"), .enable("false")) multiplexer_7 (
    .in0(id_ex_1_r2out), .in1(multiplexer_6_out), .out(multiplexer_7_out), .sel(id_ex_1_alusrcbout));
  or or_4 (or_4_out, Jal, Jalr);
  Counter #(.width(16), .max('hffff), .ongoal("wrap"), .trigger("rising"), .behavior("new")) counter_4 (
    .count(or_4_out), .Q(\无条件分支数 ), .clk(CLK), .clr(RST));  // open: load, D, carry, preset, down
  and and_6 (and_6_out, id_ex_1_beqout, equal);
  and and_7 (and_7_out, not_7_out, id_ex_1_bneout);
  and and_8 (and_8_out, MoreAndEqu, id_ex_1_bgeuout);
  ALU alu_1 (
    .X(id_ex_1_r1out), .Y(multiplexer_7_out), .AluOP(id_ex_1_aluopout), .Equal(equal), .Result(Jalr_Addr),
    .out_4(MoreAndEqu));  // open: Result_2, out_6
  or or_5 (Branch, and_6_out, and_7_out, and_8_out);
  not not_8 (not_8_out, halt);
  EX_MEM ex_mem_1 (
    .PCin(EX_PC), .Lhuin(id_ex_1_lhuout), .PCout(M_PC), .Lhuout(ex_mem_1_lhuout), .Jalrin(Jalr),
    .Jalrout(ex_mem_1_jalrout), .IRin(EX_IR), .IRout(MEM_IR), .Jalin(Jal), .Jalout(ex_mem_1_jalout),
    .MemToRegin(id_ex_1_memtoregout), .MemToRegout(MemToReg), .MemWritein(id_ex_1_memwriteout),
    .MemWriteout(MemWrite), .Imm_U_in(id_ex_1_imm_u_out), .Imm_U_out(ex_mem_1_imm_u_out),
    .Resultin(Jalr_Addr), .Resultout(ex_mem_1_resultout), .RegWritein(EX_RegWrite_num),
    .RegWriteout(MEM_RegWrite_num), .U_Typein(id_ex_1_u_tpyeout), .U_Tpyeout(ex_mem_1_u_tpyeout),
    .Haltin(id_ex_1_ecallout), .Haltout(ex_mem_1_haltout), .W_in(EX_W_num), .W_out(MEM_W_num), .RST(RST),
    .EN_H(en), .CLK(CLK), .WMdatain(id_ex_1_r2out), .WMdataout(MDin));
  and and_9 (and_9_out, not_8_out, \数据相关 );
  Counter #(.width(16), .max('hffff), .ongoal("wrap"), .trigger("rising"), .behavior("new")) counter_5 (
    .count(and_9_out), .Q(\插入气泡数 ), .clk(CLK), .clr(RST));  // open: load, D, carry, preset, down
  RAM #(.addrWidth(10), .dataWidth(32), .bus("separate"), .Select("high")) ram_1 (
    .addr(ex_mem_1_resultout[11:2]), .din(MDin), .data(ram_1_data), .str(MemWrite), .clk(CLK), .ld(MemToReg),
    .clr(RST));  // open: sel
  MEM_WB mem_wb_1 (
    .Lhuin(ex_mem_1_lhuout), .PCin(M_PC), .Jalrin(ex_mem_1_jalrout), .Jalin(ex_mem_1_jalout), .IRin(MEM_IR),
    .MemToRegin(MemToReg), .Imm_U_in(ex_mem_1_imm_u_out), .RegWritein(MEM_RegWrite_num),
    .AluResultin(ex_mem_1_resultout), .U_Typein(ex_mem_1_u_tpyeout), .RMdatain(ram_1_data),
    .Haltin(ex_mem_1_haltout), .W_in(MEM_W_num), .Lhuout(mem_wb_1_lhuout), .PCout(WB_PC),
    .Jalrout(mem_wb_1_jalrout), .Jalout(mem_wb_1_jalout), .IRout(WB_IR), .MemToRegout(mem_wb_1_memtoregout),
    .Imm_U_out(mem_wb_1_imm_u_out), .RegWriteout(RegWrite), .AluResultout(mem_wb_1_aluresultout),
    .U_Tpyeout(mem_wb_1_u_tpyeout), .RMdataout(mem_wb_1_rmdataout), .Haltout(mem_wb_1_haltout),
    .W_out(W_num), .RST(RST), .EN_H(en), .CLK(CLK), .Xin(ex_mem_1_resultout[1]), .Xout(mem_wb_1_xout));
  Multiplexer #(.select(1), .width(16), .disabled("Z"), .enable("false")) multiplexer_8 (
    .in0(mem_wb_1_rmdataout[15:0]), .in1(mem_wb_1_rmdataout[31:16]), .out(multiplexer_8_out),
    .sel(mem_wb_1_xout));
  Adder #(.width(32)) adder_4 (.a(WB_PC), .b(mem_wb_1_imm_u_out), .out(adder_4_out));  // open: cin, cout
  and and_10 (halt, mem_wb_1_haltout, ~Go);  // AND_Gate
  not not_9 (en, halt);
  Adder #(.width(32)) adder_5 (.a(32'h4), .b(WB_PC), .out(WB_PC_4));  // open: cin, cout
  or or_6 (or_6_out, mem_wb_1_jalrout, mem_wb_1_jalout, mem_wb_1_u_tpyeout);
  assign bit_extender_5_out = {{16{1'b0}}, multiplexer_8_out};  // Bit_Extender bit_extender_5
  Multiplexer #(.select(1), .width(32), .disabled("Z"), .enable("false")) multiplexer_9 (
    .in0(mem_wb_1_rmdataout), .in1(bit_extender_5_out), .out(multiplexer_9_out), .sel(mem_wb_1_lhuout));
  Multiplexer #(.select(1), .width(32), .disabled("Z"), .enable("false")) multiplexer_10 (
    .in0(WB_PC_4), .in1(adder_4_out), .out(multiplexer_10_out), .sel(mem_wb_1_u_tpyeout));
  Multiplexer #(.select(1), .width(32), .disabled("Z"), .enable("false")) multiplexer_11 (
    .in0(mem_wb_1_aluresultout), .in1(multiplexer_9_out), .out(multiplexer_11_out), .sel(mem_wb_1_memtoregout));
  Multiplexer #(.select(1), .width(32), .disabled("Z"), .enable("false")) multiplexer_12 (
    .in0(multiplexer_11_out), .in1(multiplexer_10_out), .out(RDin), .sel(or_6_out));

  // Other names for the same wires on the sheet: ID_RD_num[4:0] = ID_IR[11:7]; ID_IR (some bits) = ID_Funct;
  //   ID_OP[4:0] = ID_IR[6:2]; MEM_PC[31:0] = M_PC; WriteBackData[31:0] = RDin

  // Notes on the sheet:
  //   中断源
  //   时空图监测，可删除
  //   中断等待指示
  //   数码管输出
  //   指令存储器
  //   指令字
  //   contents of rom_1 (hex, n*v repeats v):
  //   100493 100006f 100493 200913 300993 100006f 100493 200913 300993 100006f 100493 200913 300993
  //   100006f 100493 200913 300993 424000ef 100413 100493 1f49493 900533 2200893 73 24d493 48463 fedff06f
  //   900533 2200893 73 100493 249493 900533 2200893 73 48463 fedff06f 100493 1f49493 900533 2200893 73
  //   4034d493 900533 2200893 73 4044d493 900533 2200893 73 4044d493 900533 2200893 73 4044d493 900533
  //   2200893 73 4044d493 900533 2200893 73 4044d493 900533 2200893 73 4044d493 900533 2200893 73 4044d493
  //   900533 2200893 73 100413 1f41993 41f9d993 433 c00913 300b13 140413 f47413 800293 100313 499993
  //   89e9b3 1300533 2200893 73 406282b3 fe0294e3 140413 f00f93 1f47433 1c41413 800293 100313 49d993
  //   89e9b3 1300533 2200893 73 406282b3 fe0294e3 1c45413 406b0b33 b0463 f95ff06f 2b3 fff2c293 829293
  //   ff2e293 500533 2200893 73 fff00413 493 84a023 140413 448493 84a023 140413 448493 84a023 140413
  //   448493 84a023 140413 448493 84a023 140413 448493 84a023 140413 448493 84a023 140413 448493 84a023
  //   140413 448493 84a023 140413 448493 84a023 140413 448493 84a023 140413 448493 84a023 140413 448493
  //   84a023 140413 448493 84a023 140413 448493 84a023 140413 448493 84a023 140413 448493 140413 433
  //   3c00493 42983 4aa03 149a2b3 28663 134a023 1442023 ffc48493 fe9412e3 800533 2200893 73 440413 3c00493
  //   fc9416e3 a00893 73 100293 300313 800493 849493 7648493 1449493 900533 2200893 73 800e13 54d4b3
  //   64d4b3 900533 2200893 73 fffe0e13 fe0e14e3 a00893 73 13 430497 900533 2200893 73 430497 900533
  //   2200893 73 430497 900533 2200893 73 430497 900533 2200893 73 430497 900533 2200893 73 430497 900533
  //   2200893 73 430497 900533 2200893 73 430497 900533 2200893 73 a00893 73 313 1000e13 8400493 849493
  //   8348493 400913 891913 490913 849493 8248493 849493 8148493 891913 490913 891913 490913 932023
  //   12484b3 430313 fffe0e13 fe0e18e3 2000e13 313 35483 900533 2200893 73 230313 fffe0e13 fe0e14e3 a00893
  //   73 f00493 100913 409909b3 900533 2200893 73 fff48493 ff29f6e3 a00893 73 a00893 73 413 140413 800533
  //   2200893 73 240413 800533 2200893 73 340413 800533 2200893 73 440413 800533 2200893 73 540413 800533
  //   2200893 73 640413 800533 2200893 73 740413 800533 2200893 73 840413 800533 2200893 2200893 73 8067
  //   控制位
  //   流水调试日志用
  //   暂停节拍，不能为0
  //   rs1
  //   rs2
  //   rd
  //   戳工具置1进入计数暂停模式，ctrl+k时钟自动运行到对应节拍暂停
  //   ctrl+k关闭时钟连续运行，将控制位置零，进入单步调试模式调试
  //   Beq
  //   Bgeu
  //   Bne
  //   MemToReg
  //   MemWrite
  //   AluOP
  //   AluSrcB
  //   RegWrite
  //   U_Type
  //   S_Type
  //   可计数暂停的时钟源
  //   为方便自动评测，需要输出流水线各段保存的PC值，注意是PC不是PC+4，另外ID段寄存器写入信息，Mem段内存写入信息也要输出
  //   数据存储器
endmodule

module \重定向流水线  (
  output RegWrite,
  output MemWrite,
  output [31:0] IF_PC,
  output [31:0] ID_PC,
  output [31:0] EX_PC,
  output [31:0] M_PC,
  output [31:0] WB_PC,
  output [31:0] RDin,
  output [31:0] MDin,
  output [31:0] LedData
);

  wire and_2_out, and_3_out, and_4_out, and_5_out, and_6_out, and_7_out, and_8_out, and_9_out, Branch, CLK,
       clock_2_out, comparator_1_eq, comparator_1_lt, comparator_2_eq, controlled_buffer_1_out, d_ff_1_q, en,
       equal, EX_ecall, ex_mem_1_haltout, ex_mem_1_jalout, ex_mem_1_jalrout, ex_mem_1_lhuout,
       ex_mem_1_u_tpyeout, EX_RegWrite_num, Go, halt, ID_ecall, id_ex_1_alusrcbout, id_ex_1_beqout,
       id_ex_1_bgeuout, id_ex_1_bneout, id_ex_1_lhuout, id_ex_1_memtoregout, id_ex_1_memwriteout,
       id_ex_1_s_tpyeout, id_ex_1_u_tpyeout, IR1, IR2, IR3, Jal, Jalr, Load_Use, MEM_RegWrite_num,
       mem_wb_1_haltout, mem_wb_1_jalout, mem_wb_1_jalrout, mem_wb_1_lhuout, mem_wb_1_memtoregout,
       mem_wb_1_u_tpyeout, mem_wb_1_xout, MemToReg, MoreAndEqu, nand_1_out, not_1_out, not_2_out, not_3_out,
       not_4_out, not_5_out, not_6_out, not_7_out, not_8_out, or_1_out, or_2_out, or_3_out, or_4_out,
       or_6_out, RST, W1, W2, W3, \单周期硬布线控制器_1_alu_src , \单周期硬布线控制器_1_beq , \单周期硬布线控制器_1_bgeu ,
       \单周期硬布线控制器_1_bne , \单周期硬布线控制器_1_jal , \单周期硬布线控制器_1_jalr , \单周期硬布线控制器_1_lhu , \单周期硬布线控制器_1_memtoreg ,
       \单周期硬布线控制器_1_memwrite , \单周期硬布线控制器_1_regwrite , \单周期硬布线控制器_1_s_type , \单周期硬布线控制器_1_u_type , \数据相关 ;
  wire [1:0] id_ex_1_r1forwardout, id_ex_1_r2forwardout, R1Forward, R2Forward;
  wire [3:0] id_ex_1_aluopout, \单周期硬布线控制器_1_alu_op ;
  wire [4:0] EX_W_num, ID_Funct, ID_R1_num, ID_R2_num, MEM_W_num, W_num;
  wire [11:0] shifter_1_out;
  wire [12:0] CNT_num;
  wire [15:0] adder_4_out, \LoadUse次数 , multiplexer_10_out, shifter_3_out, \总周期数 , \插入气泡数 , \无条件分支数 ,
       \条件分支成功数 ;
  wire [19:0] shifter_2_out;
  wire [31:0] adder_1_out, adder_2_out, adder_3_out, adder_7_out, and_1_out, bit_extender_1_out,
       bit_extender_2_out, bit_extender_3_out, bit_extender_4_out, bit_extender_5_out, EX_IR,
       ex_mem_1_imm_u_out, EX_R1, EX_R2, id_ex_1_imm_i_out, id_ex_1_imm_s_out, id_ex_1_imm_u_out,
       id_ex_1_r1out, id_ex_1_r2out, ID_IR, ID_R1, ID_R2, IF_IR, imm_B, imm_J, Jalr_Addr, MEM_IR,
       mem_wb_1_aluresultout, mem_wb_1_imm_u_out, mem_wb_1_rmdataout, multiplexer_1_out, multiplexer_2_out,
       multiplexer_3_out, multiplexer_8_out, multiplexer_9_out, multiplexer_11_out, multiplexer_12_out,
       multiplexer_13_out, ram_1_data, RT, WB_IR, WB_PC_4;

  Button \u_总复位  (.out(RST));
  Button _1 (.out(IR1));
  Button _2 (.out(IR2));
  Button _3 (.out(IR3));
  // Probe on \总周期数 
  // Probe on \总周期数 
  Button \u_继续运行  (.out(Go));
  LED #(.active("true")) led_1 (.in(W1));
  LED #(.active("true")) led_2 (.in(W2));
  LED #(.active("true")) led_3 (.in(W3));
  Hex_Digit_Display hex_digit_display_1 (.value(LedData[31:28]));  // open: dp
  // Probe on IF_PC[19:0]
  // RiscV_Probe riscv_probe_1: pin names not known; wires that end beside it: IF_IR
  Hex_Digit_Display hex_digit_display_2 (.value(LedData[23:20]));  // open: dp
  Hex_Digit_Display hex_digit_display_3 (.value(LedData[27:24]));  // open: dp
  // Probe on ID_PC[19:0]
  // RiscV_Probe riscv_probe_2: pin names not known; wires that end beside it: {ID_IR[31], ID_Funct[4], ID_IR[29:26], ID_Funct[3], ID_IR[24:15], ID_Funct[2:0], ID_IR[11:0]}
  Multiplexer #(.select(1), .width(32), .disabled("Z"), .enable("false")) multiplexer_1 (
    .in0(adder_3_out), .in1(adder_1_out), .out(multiplexer_1_out), .sel(Jal));
  Adder #(.width(32)) adder_1 (.a(imm_J), .b(EX_PC), .out(adder_1_out));  // open: cin, cout
  assign and_1_out = Jalr_Addr & 32'hfffffffe;  // AND_Gate and_1, 32 bits wide
  Hex_Digit_Display hex_digit_display_4 (.value(LedData[19:16]));  // open: dp
  Hex_Digit_Display hex_digit_display_5 (.value(LedData[15:12]));  // open: dp
  \数据冲突处理逻辑_重定向  \u_数据冲突处理逻辑_重定向_1  (
    .ID_R1_num(ID_R1_num), .EX_W_num(EX_W_num), .EX_RegWrite(EX_RegWrite_num), .EX_OP(EX_IR[6:2]),
    .ID_R2_num(ID_R2_num), .MEM_W_num(MEM_W_num), .MEM_RegWrite(MEM_RegWrite_num), .ID_OP(ID_IR[6:2]),
    .ID_Funct(ID_Funct), .\数据相关 (\数据相关 ), .R1Forward(R1Forward), .Load_Use(Load_Use), .R2Forward(R2Forward));
  Multiplexer #(.select(1), .width(32), .disabled("Z"), .enable("false")) multiplexer_2 (
    .in0(multiplexer_1_out), .in1(and_1_out), .out(multiplexer_2_out), .sel(Jalr));
  Adder #(.width(32)) adder_2 (.a(imm_B), .b(EX_PC), .out(adder_2_out));  // open: cin, cout
  Hex_Digit_Display hex_digit_display_6 (.value(LedData[11:8]));  // open: dp
  Hex_Digit_Display hex_digit_display_7 (.value(LedData[7:4]));  // open: dp
  Clock #(.highDuration(1), .lowDuration(1)) clock_1 (.out(CLK));
  // Probe on EX_PC[19:0]
  // RiscV_Probe riscv_probe_3: pin names not known; wires that end beside it: EX_IR
  Multiplexer #(.select(1), .width(32), .disabled("Z"), .enable("false")) multiplexer_3 (
    .in0(multiplexer_2_out), .in1(adder_2_out), .out(multiplexer_3_out), .sel(Branch));
  and and_2 (and_2_out, not_2_out, not_1_out);
  not not_1 (not_1_out, halt);
  not not_2 (not_2_out, Load_Use);
  Hex_Digit_Display hex_digit_display_8 (.value(LedData[3:0]));  // open: dp
  Register #(.width(32), .trigger("rising"), .Select("low")) PC (
    .D(multiplexer_3_out), .en(and_2_out), .Q(IF_PC), .clk(CLK), .clr(RST));
  // Probe on \总周期数 
  // Probe on M_PC[19:0]
  // RiscV_Probe riscv_probe_4: pin names not known; wires that end beside it: MEM_IR
  // Probe on \总周期数 
  // Probe on \无条件分支数 
  // Probe on \条件分支成功数 
  // Probe on \插入气泡数 
  // Probe on \LoadUse次数 
  ROM #(.addrWidth(10), .dataWidth(32), .Select("high")) rom_1 (.addr(IF_PC[11:2]), .data(IF_IR));
  Adder #(.width(32)) adder_3 (.a(IF_PC), .b(32'h4), .out(adder_3_out));  // open: cin, cout
  // Probe on IF_PC[11:0]
  // Probe on WB_PC[19:0]
  // RiscV_Probe riscv_probe_5: pin names not known; wires that end beside it: WB_IR
  or or_1 (or_1_out, Branch, Jal, Jalr);
  not not_3 (not_3_out, Load_Use);
  and and_3 (and_3_out, not_3_out, en);
  // Probe on ID_PC[11:0]
  // Probe on EX_PC[11:0]
  or or_2 (or_2_out, RST, or_1_out);
  IF_ID if_id_1 (
    .PCin(IF_PC), .IRin(IF_IR), .PCout(ID_PC),
    .IRout({ID_IR[31], ID_Funct[4], ID_IR[29:26], ID_Funct[3], ID_IR[24:15], ID_Funct[2:0], ID_IR[11:0]}),
    .RST(or_2_out), .EN_H(and_3_out), .CLK(CLK));
  // Probe on M_PC[11:0]
  D_Flip_Flop #(.trigger("high"), .Pre_Clr_Positions("LEGACY"), .NegatePresetClear("false"), .enable("true"), .NewFFLayout("false")) d_ff_1 (.Q(d_ff_1_q));  // open: clk, D, Qn, preset, en, reset
  // Probe on 13'hc
  // Probe on WB_PC[11:0]
  Comparator #(.width(13), .mode("twosComplement")) comparator_1 (
    .a(CNT_num), .b(13'hc), .eq(comparator_1_eq), .lt(comparator_1_lt));  // open: gt
  Clock #(.highDuration(1), .lowDuration(1)) clock_2 (.out(clock_2_out));
  \单周期硬布线控制器  \u_单周期硬布线控制器_1  (
    .Funct(ID_Funct), .OP(ID_IR[6:2]), .ALU_OP(\单周期硬布线控制器_1_alu_op ), .MemToReg(\单周期硬布线控制器_1_memtoreg ),
    .MemWrite(\单周期硬布线控制器_1_memwrite ), .ALU_SRC(\单周期硬布线控制器_1_alu_src ), .RegWrite(\单周期硬布线控制器_1_regwrite ),
    .ecall(ID_ecall), .S_type(\单周期硬布线控制器_1_s_type ), .Jalr(\单周期硬布线控制器_1_jalr ), .Beq(\单周期硬布线控制器_1_beq ),
    .JAL(\单周期硬布线控制器_1_jal ), .Bne(\单周期硬布线控制器_1_bne ), .U_type(\单周期硬布线控制器_1_u_type ),
    .BGEU(\单周期硬布线控制器_1_bgeu ), .LHU(\单周期硬布线控制器_1_lhu ));  // open: URET
  Multiplexer #(.select(1), .width(5), .disabled("Z"), .enable("false")) multiplexer_4 (
    .in0(ID_IR[24:20]), .in1(5'b01010), .out(ID_R2_num), .sel(ID_ecall));
  assign bit_extender_1_out = {{20{ID_IR[31]}}, {ID_IR[31], ID_Funct[4], ID_IR[29:26], ID_Funct[3], ID_IR[24:20]}};  // Bit_Extender bit_extender_1
  assign bit_extender_2_out = {{20{ID_IR[31]}}, {ID_IR[31], ID_Funct[4], ID_IR[29:26], ID_Funct[3], ID_IR[11:7]}};  // Bit_Extender bit_extender_2
  nand nand_1 (nand_1_out, d_ff_1_q, comparator_1_eq);
  Counter #(.width(13), .max('h1fff), .ongoal("stay"), .trigger("rising"), .behavior("old")) counter_1 (
    .count(comparator_1_lt), .Q(CNT_num), .clk(clock_2_out));  // open: load, D, carry, clr, preset
  Multiplexer #(.select(1), .width(5), .disabled("Z"), .enable("false")) multiplexer_5 (
    .in0(ID_IR[19:15]), .in1(5'b10001), .out(ID_R1_num), .sel(ID_ecall));
  Shifter #(.width(12), .shift("ll")) shifter_1 (
    .in({ID_IR[31], ID_IR[7], ID_Funct[4], ID_IR[29:26], ID_Funct[3], ID_IR[11:8]}), .\dist (4'b0001),
    .out(shifter_1_out));
  Shifter #(.width(20), .shift("ll")) shifter_2 (
    .in({ID_IR[31], ID_IR[19:15], ID_Funct[2:0], ID_IR[20], ID_Funct[4], ID_IR[29:26], ID_Funct[3], ID_IR[24:21]}),
    .\dist (5'b00001), .out(shifter_2_out));
  assign controlled_buffer_1_out = nand_1_out ? clock_2_out : 1'bz;  // Controlled_Buffer controlled_buffer_1
  assign bit_extender_3_out = {{20{shifter_1_out[11]}}, shifter_1_out};  // Bit_Extender bit_extender_3
  assign bit_extender_4_out = {{12{shifter_2_out[19]}}, shifter_2_out};  // Bit_Extender bit_extender_4
  Pull_Resistor #(.pull(1)) pull_resistor_1 (.node(controlled_buffer_1_out));
  not not_4 (not_4_out, CLK);
  Regifile regifile_1 (
    .Din(RDin), .Clk(not_4_out), .R1(ID_R1), .R2(ID_R2), .WE(RegWrite), .W_num(W_num), .R1_num(ID_R1_num),
    .R2_num(ID_R2_num));
  not not_5 (not_5_out, halt);
  Counter #(.width(16), .max('hffff), .ongoal("wrap"), .trigger("rising"), .behavior("new")) counter_2 (
    .count(not_5_out), .Q(\总周期数 ), .clk(CLK), .clr(RST));  // open: load, D, carry, preset, down
  Counter #(.width(16), .max('hffff), .ongoal("wrap"), .trigger("rising"), .behavior("new")) counter_3 (
    .count(Branch), .Q(\条件分支成功数 ), .clk(CLK), .clr(RST));  // open: load, D, carry, preset, down
  or or_3 (or_3_out, or_2_out, Load_Use);
  ID_EX id_ex_1 (
    .PCin(ID_PC), .PCout(EX_PC),
    .IRin({ID_IR[31], ID_Funct[4], ID_IR[29:26], ID_Funct[3], ID_IR[24:15], ID_Funct[2:0], ID_IR[11:0]}),
    .IRout(EX_IR), .RST(or_3_out), .EN_H(en), .CLK(CLK), .Imm_I_in(bit_extender_1_out),
    .Imm_I_out(id_ex_1_imm_i_out), .Imm_S_in(bit_extender_2_out), .Imm_S_out(id_ex_1_imm_s_out),
    .Imm_B_in(bit_extender_3_out), .Imm_B_out(imm_B), .Imm_J_in(bit_extender_4_out), .Imm_J_out(imm_J),
    .Imm_U_in({ID_IR[31], ID_Funct[4], ID_IR[29:26], ID_Funct[3], ID_IR[24:15], ID_Funct[2:0], {12{1'b0}}}),
    .Imm_U_out(id_ex_1_imm_u_out), .R1in(ID_R1), .R1out(id_ex_1_r1out), .R2in(ID_R2), .R2out(id_ex_1_r2out),
    .Lhuin(\单周期硬布线控制器_1_lhu ), .Lhuout(id_ex_1_lhuout), .Jalrin(\单周期硬布线控制器_1_jalr ), .Jalrout(Jalr),
    .Jalout(Jal), .Jalin(\单周期硬布线控制器_1_jal ), .Beqin(\单周期硬布线控制器_1_beq ), .Beqout(id_ex_1_beqout),
    .Bgeuin(\单周期硬布线控制器_1_bgeu ), .Bgeuout(id_ex_1_bgeuout), .Bnein(\单周期硬布线控制器_1_bne ),
    .Bneout(id_ex_1_bneout), .MemToRegin(\单周期硬布线控制器_1_memtoreg ), .MemToRegout(id_ex_1_memtoregout),
    .MemWritein(\单周期硬布线控制器_1_memwrite ), .MemWriteout(id_ex_1_memwriteout),
    .AluSrcBin(\单周期硬布线控制器_1_alu_src ), .AluSrcBout(id_ex_1_alusrcbout), .RegWritein(\单周期硬布线控制器_1_regwrite ),
    .RegWriteout(EX_RegWrite_num), .U_Typein(\单周期硬布线控制器_1_u_type ), .U_Tpyeout(id_ex_1_u_tpyeout),
    .AluOpin(\单周期硬布线控制器_1_alu_op ), .AluOpout(id_ex_1_aluopout), .S_Typein(\单周期硬布线控制器_1_s_type ),
    .S_Tpyeout(id_ex_1_s_tpyeout), .Ecallin(ID_ecall), .Ecallout(EX_ecall), .W_in(ID_IR[11:7]),
    .W_out(EX_W_num), .R1Forwardin(R1Forward), .R1Forwardout(id_ex_1_r1forwardout), .R2Forwardin(R2Forward),
    .R2Forwardout(id_ex_1_r2forwardout));
  Multiplexer #(.select(2), .width(32), .disabled("Z"), .enable("false")) multiplexer_6 (
    .in0(id_ex_1_r1out), .in1(RDin), .in2(RT), .out(EX_R1), .sel(id_ex_1_r1forwardout));  // open: in3
  Multiplexer #(.select(2), .width(32), .disabled("Z"), .enable("false")) multiplexer_7 (
    .in0(id_ex_1_r2out), .in1(RDin), .in2(RT), .out(EX_R2), .sel(id_ex_1_r2forwardout));  // open: in3
  Multiplexer #(.select(1), .width(32), .disabled("Z"), .enable("false")) multiplexer_8 (
    .in0(id_ex_1_imm_i_out), .in1(id_ex_1_imm_s_out), .out(multiplexer_8_out), .sel(id_ex_1_s_tpyeout));
  not not_6 (not_6_out, equal);
  Multiplexer #(.select(1), .width(32), .disabled("Z"), .enable("false")) multiplexer_9 (
    .in0(EX_R2), .in1(multiplexer_8_out), .out(multiplexer_9_out), .sel(id_ex_1_alusrcbout));
  Comparator #(.width(32), .mode("twosComplement")) comparator_2 (
    .a(EX_R1), .b(32'ha), .eq(comparator_2_eq));  // open: gt, lt
  not not_7 (not_7_out, comparator_2_eq);
  or or_4 (or_4_out, Jal, Jalr);
  Counter #(.width(16), .max('hffff), .ongoal("wrap"), .trigger("rising"), .behavior("new")) counter_4 (
    .count(or_4_out), .Q(\无条件分支数 ), .clk(CLK), .clr(RST));  // open: load, D, carry, preset, down
  and and_4 (and_4_out, id_ex_1_beqout, equal);
  and and_5 (and_5_out, not_6_out, id_ex_1_bneout);
  and and_6 (and_6_out, MoreAndEqu, id_ex_1_bgeuout);
  ALU alu_1 (
    .X(EX_R1), .Y(multiplexer_9_out), .AluOP(id_ex_1_aluopout), .Equal(equal), .Result(Jalr_Addr),
    .out_4(MoreAndEqu));  // open: Result_2, out_6
  and and_7 (and_7_out, EX_ecall, not_7_out);
  and and_8 (and_8_out, comparator_2_eq, EX_ecall);
  or or_5 (Branch, and_4_out, and_5_out, and_6_out);
  Register #(.width(32), .trigger("rising"), .Select("low")) register_1 (
    .D(EX_R2), .en(and_7_out), .Q(LedData), .clk(CLK), .clr(RST));
  EX_MEM ex_mem_1 (
    .PCin(EX_PC), .Lhuin(id_ex_1_lhuout), .PCout(M_PC), .Lhuout(ex_mem_1_lhuout), .Jalrin(Jalr),
    .Jalrout(ex_mem_1_jalrout), .IRin(EX_IR), .IRout(MEM_IR), .Jalin(Jal), .Jalout(ex_mem_1_jalout),
    .MemToRegin(id_ex_1_memtoregout), .MemToRegout(MemToReg), .MemWritein(id_ex_1_memwriteout),
    .MemWriteout(MemWrite), .Imm_U_in(id_ex_1_imm_u_out), .Imm_U_out(ex_mem_1_imm_u_out),
    .Resultin(Jalr_Addr), .Resultout(RT), .RegWritein(EX_RegWrite_num), .RegWriteout(MEM_RegWrite_num),
    .U_Typein(id_ex_1_u_tpyeout), .U_Tpyeout(ex_mem_1_u_tpyeout), .Haltin(and_8_out),
    .Haltout(ex_mem_1_haltout), .W_in(EX_W_num), .W_out(MEM_W_num), .RST(RST), .EN_H(en), .CLK(CLK),
    .WMdatain(EX_R2), .WMdataout(MDin));
  Adder #(.width(16)) adder_4 (.a(\条件分支成功数 ), .b(\无条件分支数 ), .out(adder_4_out));  // open: cin, cout
  not not_8 (not_8_out, halt);
  and and_9 (and_9_out, not_8_out, Load_Use);
  Shifter #(.width(16), .shift("ll")) shifter_3 (.in(adder_4_out), .\dist (4'b0001), .out(shifter_3_out));
  Counter #(.width(16), .max('hffff), .ongoal("wrap"), .trigger("rising"), .behavior("new")) counter_5 (
    .count(and_9_out), .Q(\LoadUse次数 ), .clk(CLK), .clr(RST));  // open: load, D, carry, preset, down
  Adder #(.width(16)) adder_5 (.a(shifter_3_out), .b(\LoadUse次数 ), .out(\插入气泡数 ));  // open: cin, cout
  RAM #(.addrWidth(10), .dataWidth(32), .bus("separate"), .Select("high")) ram_1 (
    .addr(RT[11:2]), .din(MDin), .data(ram_1_data), .str(MemWrite), .clk(CLK), .ld(MemToReg), .clr(RST));  // open: sel
  MEM_WB mem_wb_1 (
    .Lhuin(ex_mem_1_lhuout), .PCin(M_PC), .Jalrin(ex_mem_1_jalrout), .Jalin(ex_mem_1_jalout), .IRin(MEM_IR),
    .MemToRegin(MemToReg), .Imm_U_in(ex_mem_1_imm_u_out), .RegWritein(MEM_RegWrite_num), .AluResultin(RT),
    .U_Typein(ex_mem_1_u_tpyeout), .RMdatain(ram_1_data), .Haltin(ex_mem_1_haltout), .W_in(MEM_W_num),
    .Lhuout(mem_wb_1_lhuout), .PCout(WB_PC), .Jalrout(mem_wb_1_jalrout), .Jalout(mem_wb_1_jalout),
    .IRout(WB_IR), .MemToRegout(mem_wb_1_memtoregout), .Imm_U_out(mem_wb_1_imm_u_out),
    .RegWriteout(RegWrite), .AluResultout(mem_wb_1_aluresultout), .U_Tpyeout(mem_wb_1_u_tpyeout),
    .RMdataout(mem_wb_1_rmdataout), .Haltout(mem_wb_1_haltout), .W_out(W_num), .RST(RST), .EN_H(en),
    .CLK(CLK), .Xin(RT[1]), .Xout(mem_wb_1_xout));
  Adder #(.width(32)) adder_6 (.a(32'h4), .b(WB_PC), .out(WB_PC_4));  // open: cin, cout
  Multiplexer #(.select(1), .width(16), .disabled("Z"), .enable("false")) multiplexer_10 (
    .in0(mem_wb_1_rmdataout[15:0]), .in1(mem_wb_1_rmdataout[31:16]), .out(multiplexer_10_out),
    .sel(mem_wb_1_xout));
  Adder #(.width(32)) adder_7 (.a(WB_PC), .b(mem_wb_1_imm_u_out), .out(adder_7_out));  // open: cin, cout
  and and_10 (halt, mem_wb_1_haltout, ~Go);  // AND_Gate
  not not_9 (en, halt);
  or or_6 (or_6_out, mem_wb_1_jalrout, mem_wb_1_jalout, mem_wb_1_u_tpyeout);
  assign bit_extender_5_out = {{16{1'b0}}, multiplexer_10_out};  // Bit_Extender bit_extender_5
  Multiplexer #(.select(1), .width(32), .disabled("Z"), .enable("false")) multiplexer_11 (
    .in0(WB_PC_4), .in1(adder_7_out), .out(multiplexer_11_out), .sel(mem_wb_1_u_tpyeout));
  Multiplexer #(.select(1), .width(32), .disabled("Z"), .enable("false")) multiplexer_12 (
    .in0(mem_wb_1_rmdataout), .in1(bit_extender_5_out), .out(multiplexer_12_out), .sel(mem_wb_1_lhuout));
  Multiplexer #(.select(1), .width(32), .disabled("Z"), .enable("false")) multiplexer_13 (
    .in0(mem_wb_1_aluresultout), .in1(multiplexer_12_out), .out(multiplexer_13_out),
    .sel(mem_wb_1_memtoregout));
  Multiplexer #(.select(1), .width(32), .disabled("Z"), .enable("false")) multiplexer_14 (
    .in0(multiplexer_13_out), .in1(multiplexer_11_out), .out(RDin), .sel(or_6_out));

  // Other names for the same wires on the sheet: ID_RD_num[4:0] = ID_IR[11:7]; ID_IR (some bits) = ID_Funct;
  //   ID_OP[4:0] = ID_IR[6:2]; MEM_PC[31:0] = M_PC; WD[31:0] = RDin; WriteBackData[31:0] = RDin

  // Notes on the sheet:
  //   中断源
  //   时空图监测，可删除
  //   中断等待指示
  //   数码管输出
  //   指令存储器
  //   contents of rom_1 (hex, n*v repeats v):
  //   100493 100006f 100493 200913 300993 100006f 100493 200913 300993 100006f 100493 200913 300993
  //   100006f 100493 200913 300993 424000ef 100413 100493 1f49493 900533 2200893 73 24d493 48463 fedff06f
  //   900533 2200893 73 100493 249493 900533 2200893 73 48463 fedff06f 100493 1f49493 900533 2200893 73
  //   4034d493 900533 2200893 73 4044d493 900533 2200893 73 4044d493 900533 2200893 73 4044d493 900533
  //   2200893 73 4044d493 900533 2200893 73 4044d493 900533 2200893 73 4044d493 900533 2200893 73 4044d493
  //   900533 2200893 73 100413 1f41993 41f9d993 433 c00913 300b13 140413 f47413 800293 100313 499993
  //   89e9b3 1300533 2200893 73 406282b3 fe0294e3 140413 f00f93 1f47433 1c41413 800293 100313 49d993
  //   89e9b3 1300533 2200893 73 406282b3 fe0294e3 1c45413 406b0b33 b0463 f95ff06f 2b3 fff2c293 829293
  //   ff2e293 500533 2200893 73 fff00413 493 84a023 140413 448493 84a023 140413 448493 84a023 140413
  //   448493 84a023 140413 448493 84a023 140413 448493 84a023 140413 448493 84a023 140413 448493 84a023
  //   140413 448493 84a023 140413 448493 84a023 140413 448493 84a023 140413 448493 84a023 140413 448493
  //   84a023 140413 448493 84a023 140413 448493 84a023 140413 448493 84a023 140413 448493 140413 433
  //   3c00493 42983 4aa03 149a2b3 28663 134a023 1442023 ffc48493 fe9412e3 800533 2200893 73 440413 3c00493
  //   fc9416e3 a00893 73 100293 300313 800493 849493 7648493 1449493 900533 2200893 73 800e13 54d4b3
  //   64d4b3 900533 2200893 73 fffe0e13 fe0e14e3 a00893 73 13 430497 900533 2200893 73 430497 900533
  //   2200893 73 430497 900533 2200893 73 430497 900533 2200893 73 430497 900533 2200893 73 430497 900533
  //   2200893 73 430497 900533 2200893 73 430497 900533 2200893 73 a00893 73 313 1000e13 8400493 849493
  //   8348493 400913 891913 490913 849493 8248493 849493 8148493 891913 490913 891913 490913 932023
  //   12484b3 430313 fffe0e13 fe0e18e3 2000e13 313 35483 900533 2200893 73 230313 fffe0e13 fe0e14e3 a00893
  //   73 f00493 100913 409909b3 900533 2200893 73 fff48493 ff29f6e3 a00893 73 a00893 73 413 140413 800533
  //   2200893 73 240413 800533 2200893 73 340413 800533 2200893 73 440413 800533 2200893 73 540413 800533
  //   2200893 73 640413 800533 2200893 73 740413 800533 2200893 73 840413 800533 2200893 2200893 73 8067
  //   指令字
  //   控制位
  //   流水调试日志用
  //   暂停节拍，不能为0
  //   rs1
  //   rs2
  //   rd
  //   戳工具置1进入计数暂停模式，ctrl+k时钟自动运行到对应节拍暂停
  //   ctrl+k关闭时钟连续运行，将控制位置零，进入单步调试模式调试
  //   Beq
  //   Bgeu
  //   Bne
  //   MemToReg
  //   MemWrite
  //   AluOP
  //   AluSrcB
  //   RegWrite
  //   U_Type
  //   S_Type
  //   可计数暂停的时钟源
  //   为方便自动评测，需要输出流水线各段保存的PC值，注意是PC不是PC+4，另外ID段寄存器写入信息，Mem段内存写入信息也要输出
  //   数据存储器
endmodule

module \中断按键参考电路  (
  input  \同步清零信号 ,
  output \与中断屏蔽位与 
);

  wire \_1号中断_out , and_1_out, clock_1_out, d_ff_1_q, or_1_out, or_2_out;

  Clock #(.highDuration(1), .lowDuration(1)) clock_1 (.out(clock_1_out));
  Button \_1号中断  (.out(\_1号中断_out ));
  LED #(.active("true")) \_1号中断等待指示灯  (.in(or_1_out));
  or or_1 (or_1_out, \与中断屏蔽位与 , d_ff_1_q);
  D_Flip_Flop #(.trigger("rising"), .Pre_Clr_Positions("LEGACY"), .NegatePresetClear("false"), .enable("true"), .NewFFLayout("false")) d_ff_1 (
    .clk(\_1号中断_out ), .D(1'b1), .Q(d_ff_1_q), .reset(\与中断屏蔽位与 ));  // open: Qn, preset, en
  or or_2 (or_2_out, d_ff_1_q, \与中断屏蔽位与 );
  and and_1 (and_1_out, or_2_out, ~\同步清零信号 );  // AND_Gate
  D_Flip_Flop #(.trigger("rising"), .Pre_Clr_Positions("LEGACY"), .NegatePresetClear("false"), .enable("true"), .NewFFLayout("false")) IR1 (
    .clk(clock_1_out), .D(and_1_out), .Q(\与中断屏蔽位与 ));  // open: Qn, preset, en, reset

  // Notes on the sheet:
  //   中断信号采样参考电路
  //   Reset 
endmodule

module \单周期_多级中断  (
  input  IR1,
  input  IR2,
  input  IR3,
  output RegWrite,
  output MemWrite,
  output [31:0] PC,
  output [31:0] IR,
  output [31:0] RDin,
  output [31:0] MDin,
  output [31:0] LedData
);

  wire CLK, comparator_1_eq, comparator_2_eq, comparator_3_eq, comparator_4_eq, comparator_5_eq, Go, IR1_t,
       IR2_t, IR3_t, IRA, IRB, IRC, or_1_out, or_2_out, W1, W2, W3;
  wire [15:0] \总周期数 ;

  Clock #(.highDuration(1), .lowDuration(1)) clock_1 (.out(CLK));
  Button _1 ();  // open: out
  Button _2 ();  // open: out
  Button _3 ();  // open: out
  Button \u_继续运行  (.out(Go));
  LED #(.active("true")) led_1 (.in(W1));
  LED #(.active("true")) led_2 (.in(W2));
  LED #(.active("true")) led_3 (.in(W3));
  Hex_Digit_Display hex_digit_display_1 (.value(LedData[31:28]));  // open: dp
  Comparator #(.width(16), .mode("twosComplement")) comparator_1 (
    .a(\总周期数 ), .b(16'h7), .eq(comparator_1_eq));  // open: gt, lt
  Comparator #(.width(16), .mode("twosComplement")) comparator_2 (
    .a(\总周期数 ), .b(16'h241), .eq(comparator_2_eq));  // open: gt, lt
  Hex_Digit_Display hex_digit_display_2 (.value(LedData[23:20]));  // open: dp
  Hex_Digit_Display hex_digit_display_3 (.value(LedData[27:24]));  // open: dp
  Comparator #(.width(16), .mode("twosComplement")) comparator_3 (
    .a(16'h258), .b(\总周期数 ), .eq(comparator_3_eq));  // open: gt, lt
  or or_1 (or_1_out, comparator_3_eq, comparator_4_eq);
  Comparator #(.width(16), .mode("twosComplement")) comparator_4 (
    .a(\总周期数 ), .b(16'h1), .eq(comparator_4_eq));  // open: gt, lt
  Comparator #(.width(16), .mode("twosComplement")) comparator_5 (
    .a(\总周期数 ), .b(16'h4), .eq(comparator_5_eq));  // open: gt, lt
  or or_2 (or_2_out, comparator_1_eq, comparator_2_eq);
  Hex_Digit_Display hex_digit_display_4 (.value(LedData[15:12]));  // open: dp
  Hex_Digit_Display hex_digit_display_5 (.value(LedData[19:16]));  // open: dp
  Pull_Resistor #(.pull(0)) pull_resistor_1 (.node(IRA));
  assign IRA = or_1_out ? ~CLK : 1'bz;  // Controlled_Inverter controlled_inverter_1
  Pull_Resistor #(.pull(0)) pull_resistor_2 (.node(IRB));
  assign IRB = comparator_5_eq ? ~CLK : 1'bz;  // Controlled_Inverter controlled_inverter_2
  Pull_Resistor #(.pull(0)) pull_resistor_3 (.node(IRC));
  assign IRC = or_2_out ? ~CLK : 1'bz;  // Controlled_Inverter controlled_inverter_3
  Hex_Digit_Display hex_digit_display_6 (.value(LedData[7:4]));  // open: dp
  Hex_Digit_Display hex_digit_display_7 (.value(LedData[11:8]));  // open: dp
  // Probe on \总周期数 
  Hex_Digit_Display hex_digit_display_8 (.value(LedData[3:0]));  // open: dp
  or or_3 (IR1_t, IR1, IRA);
  or or_4 (IR2_t, IR2, IRB);
  or or_5 (IR3_t, IR3, IRC);

  // Notes on the sheet:
  //   中断源
  //   中断等待指示
  //   总复位信号应将除ROM以外所有存储组件全部清零
  //   多级中断测试信号模拟器
  //   数码管输出
  //   数码管输出应该用寄存器锁存，否则显示数据只能一闪而过
  //   为方便自动评测，需要输出PC，IR，寄存器堆写如数据RDin
  //   RAM写使能MemWrite、RAM写入数据MDin等信号
endmodule

module \封装正确性测试  (
);

  wire IR1, IR2, IR3, MemW, RegW;
  wire [31:0] EX_PC, ID_PC, IF_PC, IR, LED, MDin, MDinr, MEM_PC, PC, RDin, RDinr, WB_PC;

  \单周期RISC_V  \u_单周期risc_v_1  (
    .IR1(IR1), .IR2(IR2), .IR3(IR3), .RegWrite(RegW), .MemWrite(MemW), .PC(PC), .IR(IR), .RDin(RDin),
    .MDin(MDin), .LedData(LED));
  \气泡流水线  \u_气泡流水线_1  (
    .RegWrite(RegW), .MemWrite(MemW), .IF_PC(IF_PC), .ID_PC(ID_PC), .EX_PC(EX_PC), .M_PC(MEM_PC),
    .WB_PC(WB_PC), .RDin(RDinr), .MDin(MDinr), .LedData(LED));
  \井字棋游戏  \u_井字棋游戏_1  (.RegWrite(RegW), .MemWrite(MemW), .MDin(PC), .PC(IR), .IR(RDin), .RDin(MDin));
  \理想流水线  \u_理想流水线_1  (
    .RegWrite(RegW), .MemWrite(MemW), .IF_PC(IF_PC), .ID_PC(ID_PC), .EX_PC(EX_PC), .M_PC(MEM_PC),
    .WB_PC(WB_PC), .RDin(RDinr), .MDin(MDinr), .LedData(LED));
  \重定向流水线  \u_重定向流水线_1  (
    .RegWrite(RegW), .MemWrite(MemW), .IF_PC(IF_PC), .ID_PC(ID_PC), .EX_PC(EX_PC), .M_PC(MEM_PC),
    .WB_PC(WB_PC), .RDin(RDinr), .MDin(MDinr), .LedData(LED));
  \单周期_多级中断  \u_单周期_多级中断_1  (
    .IR1(IR1), .IR2(IR2), .IR3(IR3), .RegWrite(RegW), .MemWrite(MemW), .PC(PC), .IR(IR), .RDin(RDin),
    .MDin(MDin), .LedData(LED));

  // Notes on the sheet:
  //   单周期封装测试
  //   气泡流水封装测试
  //   单周期+单级中断封装测试
  //   请检查上面封装有无位宽不匹配，引脚标签是否和连接的标签相对应，否则无法在educoder平台上正确测试
  //   理想流水封装测试
  //   重定向流水封装测试
  //   单周期+多级中断封装测试
endmodule

// IF/ID
module IF_ID (
  input  [31:0] PCin,
  input  [31:0] IRin,
  input  RST,
  input  EN_H,
  input  CLK,
  output [31:0] PCout,
  output [31:0] IRout
);

  wire [31:0] multiplexer_1_out, multiplexer_2_out;

  Multiplexer #(.select(1), .width(32), .disabled("Z"), .enable("false")) multiplexer_1 (
    .in0(PCin), .in1({32{1'b0}}), .out(multiplexer_1_out), .sel(RST));
  Multiplexer #(.select(1), .width(32), .disabled("Z"), .enable("false")) multiplexer_2 (
    .in0(IRin), .in1({32{1'b0}}), .out(multiplexer_2_out), .sel(RST));
  Register #(.width(32), .trigger("rising"), .Select("low")) register_1 (
    .D(multiplexer_1_out), .en(EN_H), .Q(PCout), .clk(CLK));  // open: clr
  Register #(.width(32), .trigger("rising"), .Select("low")) register_2 (
    .D(multiplexer_2_out), .en(EN_H), .Q(IRout), .clk(CLK));  // open: clr
endmodule

// ID/EX
module ID_EX (
  input  [31:0] PCin,
  input  Lhuin,
  input  Jalrin,
  input  [31:0] IRin,
  input  Jalin,
  input  Beqin,
  input  [31:0] Imm_I_in,
  input  Bgeuin,
  input  [31:0] Imm_S_in,
  input  Bnein,
  input  [31:0] Imm_B_in,
  input  MemToRegin,
  input  MemWritein,
  input  [31:0] Imm_J_in,
  input  [3:0] AluOpin,
  input  [31:0] Imm_U_in,
  input  AluSrcBin,
  input  [31:0] R1in,
  input  RegWritein,
  input  U_Typein,
  input  [31:0] R2in,
  input  S_Typein,
  input  Ecallin,
  input  [4:0] W_in,
  input  [1:0] R1Forwardin,
  input  [1:0] R2Forwardin,
  input  RST,
  input  EN_H,
  input  CLK,
  output [31:0] PCout,
  output Lhuout,
  output Jalrout,
  output [31:0] IRout,
  output Jalout,
  output Beqout,
  output [31:0] Imm_I_out,
  output Bgeuout,
  output [31:0] Imm_S_out,
  output Bneout,
  output [31:0] Imm_B_out,
  output MemToRegout,
  output MemWriteout,
  output [31:0] Imm_J_out,
  output [3:0] AluOpout,
  output [31:0] Imm_U_out,
  output AluSrcBout,
  output [31:0] R1out,
  output RegWriteout,
  output U_Tpyeout,
  output [31:0] R2out,
  output S_Tpyeout,
  output Ecallout,
  output [4:0] W_out,
  output [1:0] R1Forwardout,
  output [1:0] R2Forwardout
);

  wire multiplexer_10_out, multiplexer_11_out, multiplexer_12_out, multiplexer_13_out, multiplexer_14_out,
       multiplexer_15_out, multiplexer_16_out, multiplexer_17_out, multiplexer_19_out, multiplexer_20_out,
       multiplexer_21_out, multiplexer_22_out, multiplexer_23_out;
  wire [1:0] multiplexer_25_out, multiplexer_26_out;
  wire [3:0] multiplexer_18_out;
  wire [4:0] multiplexer_24_out;
  wire [31:0] multiplexer_1_out, multiplexer_2_out, multiplexer_3_out, multiplexer_4_out, multiplexer_5_out,
       multiplexer_6_out, multiplexer_7_out, multiplexer_8_out, multiplexer_9_out;

  Multiplexer #(.select(1), .width(32), .disabled("Z"), .enable("false")) multiplexer_1 (
    .in0(PCin), .in1({32{1'b0}}), .out(multiplexer_1_out), .sel(RST));
  Multiplexer #(.select(1), .width(32), .disabled("Z"), .enable("false")) multiplexer_2 (
    .in0(IRin), .in1({32{1'b0}}), .out(multiplexer_2_out), .sel(RST));
  Multiplexer #(.select(1), .width(32), .disabled("Z"), .enable("false")) multiplexer_3 (
    .in0(Imm_I_in), .in1({32{1'b0}}), .out(multiplexer_3_out), .sel(RST));
  Multiplexer #(.select(1), .width(32), .disabled("Z"), .enable("false")) multiplexer_4 (
    .in0(Imm_S_in), .in1({32{1'b0}}), .out(multiplexer_4_out), .sel(RST));
  Multiplexer #(.select(1), .width(32), .disabled("Z"), .enable("false")) multiplexer_5 (
    .in0(Imm_B_in), .in1({32{1'b0}}), .out(multiplexer_5_out), .sel(RST));
  Multiplexer #(.select(1), .width(32), .disabled("Z"), .enable("false")) multiplexer_6 (
    .in0(Imm_J_in), .in1({32{1'b0}}), .out(multiplexer_6_out), .sel(RST));
  Multiplexer #(.select(1), .width(32), .disabled("Z"), .enable("false")) multiplexer_7 (
    .in0(Imm_U_in), .in1({32{1'b0}}), .out(multiplexer_7_out), .sel(RST));
  Multiplexer #(.select(1), .width(32), .disabled("Z"), .enable("false")) multiplexer_8 (
    .in0(R1in), .in1({32{1'b0}}), .out(multiplexer_8_out), .sel(RST));
  Multiplexer #(.select(1), .width(32), .disabled("Z"), .enable("false")) multiplexer_9 (
    .in0(R2in), .in1({32{1'b0}}), .out(multiplexer_9_out), .sel(RST));
  Register #(.width(32), .trigger("rising"), .Select("low")) register_1 (
    .D(multiplexer_1_out), .en(EN_H), .Q(PCout), .clk(CLK));  // open: clr
  Register #(.width(32), .trigger("rising"), .Select("low")) register_2 (
    .D(multiplexer_2_out), .en(EN_H), .Q(IRout), .clk(CLK));  // open: clr
  Register #(.width(32), .trigger("rising"), .Select("low")) register_3 (
    .D(multiplexer_3_out), .en(EN_H), .Q(Imm_I_out), .clk(CLK));  // open: clr
  Register #(.width(32), .trigger("rising"), .Select("low")) register_4 (
    .D(multiplexer_4_out), .en(EN_H), .Q(Imm_S_out), .clk(CLK));  // open: clr
  Register #(.width(32), .trigger("rising"), .Select("low")) register_5 (
    .D(multiplexer_5_out), .en(EN_H), .Q(Imm_B_out), .clk(CLK));  // open: clr
  Register #(.width(32), .trigger("rising"), .Select("low")) register_6 (
    .D(multiplexer_6_out), .en(EN_H), .Q(Imm_J_out), .clk(CLK));  // open: clr
  Register #(.width(32), .trigger("rising"), .Select("low")) register_7 (
    .D(multiplexer_7_out), .en(EN_H), .Q(Imm_U_out), .clk(CLK));  // open: clr
  Register #(.width(32), .trigger("rising"), .Select("low")) register_8 (
    .D(multiplexer_8_out), .en(EN_H), .Q(R1out), .clk(CLK));  // open: clr
  Register #(.width(32), .trigger("rising"), .Select("low")) register_9 (
    .D(multiplexer_9_out), .en(EN_H), .Q(R2out), .clk(CLK));  // open: clr
  Multiplexer #(.select(1), .width(1), .disabled("Z"), .enable("false")) multiplexer_10 (
    .in0(Lhuin), .in1(1'b0), .out(multiplexer_10_out), .sel(RST));
  Multiplexer #(.select(1), .width(1), .disabled("Z"), .enable("false")) multiplexer_11 (
    .in0(Jalrin), .in1(1'b0), .out(multiplexer_11_out), .sel(RST));
  Multiplexer #(.select(1), .width(1), .disabled("Z"), .enable("false")) multiplexer_12 (
    .in0(Jalin), .in1(1'b0), .out(multiplexer_12_out), .sel(RST));
  Multiplexer #(.select(1), .width(1), .disabled("Z"), .enable("false")) multiplexer_13 (
    .in0(Beqin), .in1(1'b0), .out(multiplexer_13_out), .sel(RST));
  Multiplexer #(.select(1), .width(1), .disabled("Z"), .enable("false")) multiplexer_14 (
    .in0(Bgeuin), .in1(1'b0), .out(multiplexer_14_out), .sel(RST));
  Multiplexer #(.select(1), .width(1), .disabled("Z"), .enable("false")) multiplexer_15 (
    .in0(Bnein), .in1(1'b0), .out(multiplexer_15_out), .sel(RST));
  Multiplexer #(.select(1), .width(1), .disabled("Z"), .enable("false")) multiplexer_16 (
    .in0(MemToRegin), .in1(1'b0), .out(multiplexer_16_out), .sel(RST));
  Multiplexer #(.select(1), .width(1), .disabled("Z"), .enable("false")) multiplexer_17 (
    .in0(MemWritein), .in1(1'b0), .out(multiplexer_17_out), .sel(RST));
  Multiplexer #(.select(1), .width(4), .disabled("Z"), .enable("false")) multiplexer_18 (
    .in0(AluOpin), .in1(4'b0000), .out(multiplexer_18_out), .sel(RST));
  Multiplexer #(.select(1), .width(1), .disabled("Z"), .enable("false")) multiplexer_19 (
    .in0(AluSrcBin), .in1(1'b0), .out(multiplexer_19_out), .sel(RST));
  Multiplexer #(.select(1), .width(1), .disabled("Z"), .enable("false")) multiplexer_20 (
    .in0(RegWritein), .in1(1'b0), .out(multiplexer_20_out), .sel(RST));
  Multiplexer #(.select(1), .width(1), .disabled("Z"), .enable("false")) multiplexer_21 (
    .in0(U_Typein), .in1(1'b0), .out(multiplexer_21_out), .sel(RST));
  Multiplexer #(.select(1), .width(1), .disabled("Z"), .enable("false")) multiplexer_22 (
    .in0(S_Typein), .in1(1'b0), .out(multiplexer_22_out), .sel(RST));
  Multiplexer #(.select(1), .width(1), .disabled("Z"), .enable("false")) multiplexer_23 (
    .in0(Ecallin), .in1(1'b0), .out(multiplexer_23_out), .sel(RST));
  Multiplexer #(.select(1), .width(5), .disabled("Z"), .enable("false")) multiplexer_24 (
    .in0(W_in), .in1({5{1'b0}}), .out(multiplexer_24_out), .sel(RST));
  Multiplexer #(.select(1), .width(2), .disabled("Z"), .enable("false")) multiplexer_25 (
    .in0(R1Forwardin), .in1(2'b00), .out(multiplexer_25_out), .sel(RST));
  Multiplexer #(.select(1), .width(2), .disabled("Z"), .enable("false")) multiplexer_26 (
    .in0(R2Forwardin), .in1(2'b00), .out(multiplexer_26_out), .sel(RST));
  Register #(.width(1), .trigger("rising"), .Select("low")) register_10 (
    .D(multiplexer_10_out), .en(EN_H), .Q(Lhuout), .clk(CLK));  // open: clr
  Register #(.width(1), .trigger("rising"), .Select("low")) register_11 (
    .D(multiplexer_11_out), .en(EN_H), .Q(Jalrout), .clk(CLK));  // open: clr
  Register #(.width(1), .trigger("rising"), .Select("low")) register_12 (
    .D(multiplexer_12_out), .en(EN_H), .Q(Jalout), .clk(CLK));  // open: clr
  Register #(.width(1), .trigger("rising"), .Select("low")) register_13 (
    .D(multiplexer_13_out), .en(EN_H), .Q(Beqout), .clk(CLK));  // open: clr
  Register #(.width(1), .trigger("rising"), .Select("low")) register_14 (
    .D(multiplexer_14_out), .en(EN_H), .Q(Bgeuout), .clk(CLK));  // open: clr
  Register #(.width(1), .trigger("rising"), .Select("low")) register_15 (
    .D(multiplexer_15_out), .en(EN_H), .Q(Bneout), .clk(CLK));  // open: clr
  Register #(.width(1), .trigger("rising"), .Select("low")) register_16 (
    .D(multiplexer_16_out), .en(EN_H), .Q(MemToRegout), .clk(CLK));  // open: clr
  Register #(.width(1), .trigger("rising"), .Select("low")) register_17 (
    .D(multiplexer_17_out), .en(EN_H), .Q(MemWriteout), .clk(CLK));  // open: clr
  Register #(.width(4), .trigger("rising"), .Select("low")) register_18 (
    .D(multiplexer_18_out), .en(EN_H), .Q(AluOpout), .clk(CLK));  // open: clr
  Register #(.width(1), .trigger("rising"), .Select("low")) register_19 (
    .D(multiplexer_19_out), .en(EN_H), .Q(AluSrcBout), .clk(CLK));  // open: clr
  Register #(.width(1), .trigger("rising"), .Select("low")) register_20 (
    .D(multiplexer_20_out), .en(EN_H), .Q(RegWriteout), .clk(CLK));  // open: clr
  Register #(.width(1), .trigger("rising"), .Select("low")) register_21 (
    .D(multiplexer_21_out), .en(EN_H), .Q(U_Tpyeout), .clk(CLK));  // open: clr
  Register #(.width(1), .trigger("rising"), .Select("low")) register_22 (
    .D(multiplexer_22_out), .en(EN_H), .Q(S_Tpyeout), .clk(CLK));  // open: clr
  Register #(.width(1), .trigger("rising"), .Select("low")) register_23 (
    .D(multiplexer_23_out), .en(EN_H), .Q(Ecallout), .clk(CLK));  // open: clr
  Register #(.width(5), .trigger("rising"), .Select("low")) register_24 (
    .D(multiplexer_24_out), .en(EN_H), .Q(W_out), .clk(CLK));  // open: clr
  Register #(.width(2), .trigger("rising"), .Select("low")) register_25 (
    .D(multiplexer_25_out), .en(EN_H), .Q(R1Forwardout), .clk(CLK));  // open: clr
  Register #(.width(2), .trigger("rising"), .Select("low")) register_26 (
    .D(multiplexer_26_out), .en(EN_H), .Q(R2Forwardout), .clk(CLK));  // open: clr
endmodule
// EX/MEM
module EX_MEM (
  input  Lhuin,
  input  [31:0] PCin,
  input  Jalrin,
  input  Jalin,
  input  [31:0] IRin,
  input  MemToRegin,
  input  [31:0] Imm_U_in,
  input  MemWritein,
  input  [31:0] Resultin,
  input  RegWritein,
  input  U_Typein,
  input  [31:0] WMdatain,
  input  Haltin,
  input  [4:0] W_in,
  input  RST,
  input  EN_H,
  input  CLK,
  output Lhuout,
  output [31:0] PCout,
  output Jalrout,
  output Jalout,
  output [31:0] IRout,
  output MemToRegout,
  output [31:0] Imm_U_out,
  output MemWriteout,
  output [31:0] Resultout,
  output RegWriteout,
  output U_Tpyeout,
  output [31:0] WMdataout,
  output Haltout,
  output [4:0] W_out
);

  wire multiplexer_6_out, multiplexer_7_out, multiplexer_8_out, multiplexer_9_out, multiplexer_10_out,
       multiplexer_11_out, multiplexer_12_out, multiplexer_13_out;
  wire [4:0] multiplexer_14_out;
  wire [31:0] multiplexer_1_out, multiplexer_2_out, multiplexer_3_out, multiplexer_4_out, multiplexer_5_out;

  Multiplexer #(.select(1), .width(32), .disabled("Z"), .enable("false")) multiplexer_1 (
    .in0(PCin), .in1({32{1'b0}}), .out(multiplexer_1_out), .sel(RST));
  Multiplexer #(.select(1), .width(32), .disabled("Z"), .enable("false")) multiplexer_2 (
    .in0(IRin), .in1({32{1'b0}}), .out(multiplexer_2_out), .sel(RST));
  Multiplexer #(.select(1), .width(32), .disabled("Z"), .enable("false")) multiplexer_3 (
    .in0(Imm_U_in), .in1({32{1'b0}}), .out(multiplexer_3_out), .sel(RST));
  Multiplexer #(.select(1), .width(32), .disabled("Z"), .enable("false")) multiplexer_4 (
    .in0(Resultin), .in1({32{1'b0}}), .out(multiplexer_4_out), .sel(RST));
  Multiplexer #(.select(1), .width(32), .disabled("Z"), .enable("false")) multiplexer_5 (
    .in0(WMdatain), .in1({32{1'b0}}), .out(multiplexer_5_out), .sel(RST));
  Register #(.width(32), .trigger("rising"), .Select("low")) register_1 (
    .D(multiplexer_1_out), .en(EN_H), .Q(PCout), .clk(CLK));  // open: clr
  Register #(.width(32), .trigger("rising"), .Select("low")) register_2 (
    .D(multiplexer_2_out), .en(EN_H), .Q(IRout), .clk(CLK));  // open: clr
  Register #(.width(32), .trigger("rising"), .Select("low")) register_3 (
    .D(multiplexer_3_out), .en(EN_H), .Q(Imm_U_out), .clk(CLK));  // open: clr
  Register #(.width(32), .trigger("rising"), .Select("low")) register_4 (
    .D(multiplexer_4_out), .en(EN_H), .Q(Resultout), .clk(CLK));  // open: clr
  Register #(.width(32), .trigger("rising"), .Select("low")) register_5 (
    .D(multiplexer_5_out), .en(EN_H), .Q(WMdataout), .clk(CLK));  // open: clr
  Multiplexer #(.select(1), .width(1), .disabled("Z"), .enable("false")) multiplexer_6 (
    .in0(Lhuin), .in1(1'b0), .out(multiplexer_6_out), .sel(RST));
  Multiplexer #(.select(1), .width(1), .disabled("Z"), .enable("false")) multiplexer_7 (
    .in0(Jalrin), .in1(1'b0), .out(multiplexer_7_out), .sel(RST));
  Multiplexer #(.select(1), .width(1), .disabled("Z"), .enable("false")) multiplexer_8 (
    .in0(Jalin), .in1(1'b0), .out(multiplexer_8_out), .sel(RST));
  Multiplexer #(.select(1), .width(1), .disabled("Z"), .enable("false")) multiplexer_9 (
    .in0(MemToRegin), .in1(1'b0), .out(multiplexer_9_out), .sel(RST));
  Multiplexer #(.select(1), .width(1), .disabled("Z"), .enable("false")) multiplexer_10 (
    .in0(MemWritein), .in1(1'b0), .out(multiplexer_10_out), .sel(RST));
  Multiplexer #(.select(1), .width(1), .disabled("Z"), .enable("false")) multiplexer_11 (
    .in0(RegWritein), .in1(1'b0), .out(multiplexer_11_out), .sel(RST));
  Multiplexer #(.select(1), .width(1), .disabled("Z"), .enable("false")) multiplexer_12 (
    .in0(U_Typein), .in1(1'b0), .out(multiplexer_12_out), .sel(RST));
  Multiplexer #(.select(1), .width(1), .disabled("Z"), .enable("false")) multiplexer_13 (
    .in0(Haltin), .in1(1'b0), .out(multiplexer_13_out), .sel(RST));
  Multiplexer #(.select(1), .width(5), .disabled("Z"), .enable("false")) multiplexer_14 (
    .in0(W_in), .in1({5{1'b0}}), .out(multiplexer_14_out), .sel(RST));
  Register #(.width(1), .trigger("rising"), .Select("low")) register_6 (
    .D(multiplexer_6_out), .en(EN_H), .Q(Lhuout), .clk(CLK));  // open: clr
  Register #(.width(1), .trigger("rising"), .Select("low")) register_7 (
    .D(multiplexer_7_out), .en(EN_H), .Q(Jalrout), .clk(CLK));  // open: clr
  Register #(.width(1), .trigger("rising"), .Select("low")) register_8 (
    .D(multiplexer_8_out), .en(EN_H), .Q(Jalout), .clk(CLK));  // open: clr
  Register #(.width(1), .trigger("rising"), .Select("low")) register_9 (
    .D(multiplexer_9_out), .en(EN_H), .Q(MemToRegout), .clk(CLK));  // open: clr
  Register #(.width(1), .trigger("rising"), .Select("low")) register_10 (
    .D(multiplexer_10_out), .en(EN_H), .Q(MemWriteout), .clk(CLK));  // open: clr
  Register #(.width(1), .trigger("rising"), .Select("low")) register_11 (
    .D(multiplexer_11_out), .en(EN_H), .Q(RegWriteout), .clk(CLK));  // open: clr
  Register #(.width(1), .trigger("rising"), .Select("low")) register_12 (
    .D(multiplexer_12_out), .en(EN_H), .Q(U_Tpyeout), .clk(CLK));  // open: clr
  Register #(.width(1), .trigger("rising"), .Select("low")) register_13 (
    .D(multiplexer_13_out), .en(EN_H), .Q(Haltout), .clk(CLK));  // open: clr
  Register #(.width(5), .trigger("rising"), .Select("low")) register_14 (
    .D(multiplexer_14_out), .en(EN_H), .Q(W_out), .clk(CLK));  // open: clr
endmodule

// MEM/WB
module MEM_WB (
  input  Lhuin,
  input  [31:0] PCin,
  input  Jalrin,
  input  Jalin,
  input  [31:0] IRin,
  input  MemToRegin,
  input  [31:0] Imm_U_in,
  input  RegWritein,
  input  [31:0] AluResultin,
  input  U_Typein,
  input  Xin,
  input  [31:0] RMdatain,
  input  Haltin,
  input  [4:0] W_in,
  input  RST,
  input  EN_H,
  input  CLK,
  output Lhuout,
  output [31:0] PCout,
  output Jalrout,
  output Jalout,
  output [31:0] IRout,
  output MemToRegout,
  output [31:0] Imm_U_out,
  output RegWriteout,
  output [31:0] AluResultout,
  output U_Tpyeout,
  output Xout,
  output [31:0] RMdataout,
  output Haltout,
  output [4:0] W_out
);

  wire multiplexer_6_out, multiplexer_7_out, multiplexer_8_out, multiplexer_9_out, multiplexer_10_out,
       multiplexer_11_out, multiplexer_12_out, multiplexer_13_out;
  wire [4:0] multiplexer_14_out;
  wire [31:0] multiplexer_1_out, multiplexer_2_out, multiplexer_3_out, multiplexer_4_out, multiplexer_5_out;

  Multiplexer #(.select(1), .width(32), .disabled("Z"), .enable("false")) multiplexer_1 (
    .in0(PCin), .in1({32{1'b0}}), .out(multiplexer_1_out), .sel(RST));
  Multiplexer #(.select(1), .width(32), .disabled("Z"), .enable("false")) multiplexer_2 (
    .in0(IRin), .in1({32{1'b0}}), .out(multiplexer_2_out), .sel(RST));
  Multiplexer #(.select(1), .width(32), .disabled("Z"), .enable("false")) multiplexer_3 (
    .in0(Imm_U_in), .in1({32{1'b0}}), .out(multiplexer_3_out), .sel(RST));
  Multiplexer #(.select(1), .width(32), .disabled("Z"), .enable("false")) multiplexer_4 (
    .in0(AluResultin), .in1({32{1'b0}}), .out(multiplexer_4_out), .sel(RST));
  Multiplexer #(.select(1), .width(32), .disabled("Z"), .enable("false")) multiplexer_5 (
    .in0(RMdatain), .in1({32{1'b0}}), .out(multiplexer_5_out), .sel(RST));
  Register #(.width(32), .trigger("rising"), .Select("low")) register_1 (
    .D(multiplexer_1_out), .en(EN_H), .Q(PCout), .clk(CLK));  // open: clr
  Register #(.width(32), .trigger("rising"), .Select("low")) register_2 (
    .D(multiplexer_2_out), .en(EN_H), .Q(IRout), .clk(CLK));  // open: clr
  Register #(.width(32), .trigger("rising"), .Select("low")) register_3 (
    .D(multiplexer_3_out), .en(EN_H), .Q(Imm_U_out), .clk(CLK));  // open: clr
  Register #(.width(32), .trigger("rising"), .Select("low")) register_4 (
    .D(multiplexer_4_out), .en(EN_H), .Q(AluResultout), .clk(CLK));  // open: clr
  Register #(.width(32), .trigger("rising"), .Select("low")) register_5 (
    .D(multiplexer_5_out), .en(EN_H), .Q(RMdataout), .clk(CLK));  // open: clr
  Multiplexer #(.select(1), .width(1), .disabled("Z"), .enable("false")) multiplexer_6 (
    .in0(Lhuin), .in1(1'b0), .out(multiplexer_6_out), .sel(RST));
  Multiplexer #(.select(1), .width(1), .disabled("Z"), .enable("false")) multiplexer_7 (
    .in0(Jalrin), .in1(1'b0), .out(multiplexer_7_out), .sel(RST));
  Multiplexer #(.select(1), .width(1), .disabled("Z"), .enable("false")) multiplexer_8 (
    .in0(Jalin), .in1(1'b0), .out(multiplexer_8_out), .sel(RST));
  Multiplexer #(.select(1), .width(1), .disabled("Z"), .enable("false")) multiplexer_9 (
    .in0(MemToRegin), .in1(1'b0), .out(multiplexer_9_out), .sel(RST));
  Multiplexer #(.select(1), .width(1), .disabled("Z"), .enable("false")) multiplexer_10 (
    .in0(RegWritein), .in1(1'b0), .out(multiplexer_10_out), .sel(RST));
  Multiplexer #(.select(1), .width(1), .disabled("Z"), .enable("false")) multiplexer_11 (
    .in0(U_Typein), .in1(1'b0), .out(multiplexer_11_out), .sel(RST));
  Multiplexer #(.select(1), .width(1), .disabled("Z"), .enable("false")) multiplexer_12 (
    .in0(Xin), .in1(1'b0), .out(multiplexer_12_out), .sel(RST));
  Multiplexer #(.select(1), .width(1), .disabled("Z"), .enable("false")) multiplexer_13 (
    .in0(Haltin), .in1(1'b0), .out(multiplexer_13_out), .sel(RST));
  Multiplexer #(.select(1), .width(5), .disabled("Z"), .enable("false")) multiplexer_14 (
    .in0(W_in), .in1({5{1'b0}}), .out(multiplexer_14_out), .sel(RST));
  Register #(.width(1), .trigger("rising"), .Select("low")) register_6 (
    .D(multiplexer_6_out), .en(EN_H), .Q(Lhuout), .clk(CLK));  // open: clr
  Register #(.width(1), .trigger("rising"), .Select("low")) register_7 (
    .D(multiplexer_7_out), .en(EN_H), .Q(Jalrout), .clk(CLK));  // open: clr
  Register #(.width(1), .trigger("rising"), .Select("low")) register_8 (
    .D(multiplexer_8_out), .en(EN_H), .Q(Jalout), .clk(CLK));  // open: clr
  Register #(.width(1), .trigger("rising"), .Select("low")) register_9 (
    .D(multiplexer_9_out), .en(EN_H), .Q(MemToRegout), .clk(CLK));  // open: clr
  Register #(.width(1), .trigger("rising"), .Select("low")) register_10 (
    .D(multiplexer_10_out), .en(EN_H), .Q(RegWriteout), .clk(CLK));  // open: clr
  Register #(.width(1), .trigger("rising"), .Select("low")) register_11 (
    .D(multiplexer_11_out), .en(EN_H), .Q(U_Tpyeout), .clk(CLK));  // open: clr
  Register #(.width(1), .trigger("rising"), .Select("low")) register_12 (
    .D(multiplexer_12_out), .en(EN_H), .Q(Xout), .clk(CLK));  // open: clr
  Register #(.width(1), .trigger("rising"), .Select("low")) register_13 (
    .D(multiplexer_13_out), .en(EN_H), .Q(Haltout), .clk(CLK));  // open: clr
  Register #(.width(5), .trigger("rising"), .Select("low")) register_14 (
    .D(multiplexer_14_out), .en(EN_H), .Q(W_out), .clk(CLK));  // open: clr
endmodule
