// Logisim project cpu21-riscv.circ as structural Verilog: 27 circuits, main circuit ◇单周期RISC-V
// 单周期硬布线控制器
module \单周期硬布线控制器  (
  input  [4:0] OP,
  input  [4:0] Funct,
  input  in_3,
  output [3:0] ALU_OP,
  output uret,
  output MemToReg,
  output ecall,
  output MemWrite,
  output ALU_SRC,
  output RegWrite,
  output S_type,
  output Beq,
  output Bne,
  output Jalr,
  output JAL,
  output half,
  output blt,
  output CSR,
  output auipc,
  output lui,
  output sh
);

  wire \控制信号自动生成_1_ecall ;

  \运算控制器自动生成  \u_运算控制器自动生成_1  (
    .OP2(OP[0]), .OP3(OP[1]), .OP4(OP[2]), .OP5(OP[3]), .OP6(OP[4]), .F12(Funct[0]), .F13(Funct[1]),
    .F14(Funct[2]), .F25(Funct[3]), .F30(Funct[4]), .S0(ALU_OP[0]), .S1(ALU_OP[1]), .S2(ALU_OP[2]),
    .S3(ALU_OP[3]));
  \控制信号自动生成  \u_控制信号自动生成_1  (
    .OP2(OP[0]), .OP3(OP[1]), .OP4(OP[2]), .OP5(OP[3]), .MemToReg(MemToReg), .OP6(OP[4]), .F12(Funct[0]),
    .F13(Funct[1]), .F14(Funct[2]), .F25(Funct[3]), .F30(Funct[4]), .MemWrite(MemWrite), .ALU_SRC(ALU_SRC),
    .RegWrite(RegWrite), .ecall(\控制信号自动生成_1_ecall ), .S_Type(S_type), .BEQ(Beq), .BNE(Bne), .JALR(Jalr),
    .JAL(JAL), .half(half), .CSR(CSR), .AUIPC(auipc), .LUI(lui), .SH(sh), .BLT(blt));
  and and_1 (uret, in_3, \控制信号自动生成_1_ecall );
  and and_2 (ecall, ~in_3, \控制信号自动生成_1_ecall );  // AND_Gate

  // Other names for the same wires on the sheet: IR21 = in_3; OP_CODE[4:0] = OP

  // Notes on the sheet:
  //   运算器控制器，根据指令生成运算器功能选择信号
endmodule

module \单周期RISC_V  (
  input  IR1,
  input  IR2,
  input  IR3,
  output RegWrite,
  output MemWrite,
  output [31:0] PC,
  output [31:0] IR,
  output [31:0] RDin,
  output [31:0] MDin,
  output [31:0] LedData
);

  wire alu_1_equal, alu_1_out_6, and_3_out, and_4_out, and_5_out, auipc, B, blt, CLK, clock_1_out,
       comparator_1_eq, comparator_2_eq, comparator_2_lt, d_ff_1_q, ecall, Go, half, halt, IR1_t, IR2_t,
       IR3_t, IRA, IRB, IRC, J, jal, jalr, led, lui, nand_1_out, not_1_out, not_2_out, not_3_out, not_4_out,
       or_1_out, or_6_out, or_8_out, riscv_probe_1_p2, RST, sh, W1, W2, W3, \单周期硬布线控制器_1_alu_src ,
       \单周期硬布线控制器_1_beq , \单周期硬布线控制器_1_bne , \单周期硬布线控制器_1_memtoreg , \单周期硬布线控制器_1_s_type ;
  wire [1:0] priority_encoder_1_out;
  wire [3:0] \单周期硬布线控制器_1_alu_op ;
  wire [4:0] multiplexer_1_out, multiplexer_2_out, multiplexer_12_out;
  wire [11:0] multiplexer_3_out;
  wire [12:0] CNT_num;
  wire [15:0] \总周期数 ;
  wire [31:0] adder_1_out, adder_2_out, adder_3_out, adder_4_out, aluresult, and_1_out, and_2_out, and_7_out,
       bit_extender_1_out, bit_extender_2_out, bit_extender_3_out, bit_extender_4_out, bit_extender_5_out,
       inn, multiplexer_4_out, multiplexer_5_out, multiplexer_6_out, multiplexer_8_out, multiplexer_10_out,
       multiplexer_11_out, multiplexer_13_out, multiplexer_14_out, r2, regifile_1_r1, result, shifter_2_out,
       shifter_3_out, shifter_4_out, shifter_5_out, U_imm, \use ;

  Button \u_继续运行  (.out(Go));
  Button _1 (.out(IRA));
  Button _2 (.out(IRB));
  Button _3 (.out(IRC));
  Button u_RST (.out(RST));
  LED #(.active("true")) led_1 (.in(W1));
  LED #(.active("true")) led_2 (.in(W2));
  LED #(.active("true")) led_3 (.in(W3));
  Hex_Digit_Display hex_digit_display_1 (.value(LedData[31:28]));  // open: dp
  or or_1 (or_1_out, Go, not_1_out);
  not not_1 (not_1_out, halt);
  Hex_Digit_Display hex_digit_display_2 (.value(LedData[27:24]));  // open: dp
  Hex_Digit_Display hex_digit_display_3 (.value(LedData[23:20]));  // open: dp
  Register #(.width(32), .trigger("rising"), .Select("low")) u_PC (
    .D(multiplexer_8_out), .en(or_1_out), .Q(PC), .clk(CLK), .clr(RST));
  Hex_Digit_Display hex_digit_display_4 (.value(LedData[19:16]));  // open: dp
  Hex_Digit_Display hex_digit_display_5 (.value(LedData[15:12]));  // open: dp
  Hex_Digit_Display hex_digit_display_6 (.value(LedData[11:8]));  // open: dp
  Hex_Digit_Display hex_digit_display_7 (.value(LedData[7:4]));  // open: dp
  // Probe on \总周期数 
  // Probe on \总周期数 
  or or_2 (J, jal, jalr);
  // RiscV_Probe riscv_probe_1: pin names not known; wires that end beside it: IR, riscv_probe_1_p2
  Hex_Digit_Display hex_digit_display_8 (.value(LedData[3:0]));  // open: dp
  ROM #(.addrWidth(10), .dataWidth(32), .Select("high")) rom_1 (.addr(PC[11:2]), .data(IR));
  assign bit_extender_1_out = {{12{IR[31]}}, IR[31:12]};  // Bit_Extender bit_extender_1
  or or_3 (IR1_t, IR1, IRA);
  \单周期硬布线控制器  \u_单周期硬布线控制器_1  (
    .Funct({IR[30], IR[25], IR[14:12]}), .OP(IR[6:2]), .ALU_OP(\单周期硬布线控制器_1_alu_op ),
    .MemToReg(\单周期硬布线控制器_1_memtoreg ), .MemWrite(MemWrite), .ALU_SRC(\单周期硬布线控制器_1_alu_src ),
    .RegWrite(RegWrite), .ecall(ecall), .S_type(\单周期硬布线控制器_1_s_type ), .Jalr(jalr), .Beq(\单周期硬布线控制器_1_beq ),
    .JAL(jal), .Bne(\单周期硬布线控制器_1_bne ), .in_3(IR[21]), .uret(riscv_probe_1_p2), .half(half), .blt(blt),
    .sh(sh), .auipc(auipc), .lui(lui));  // open: CSR
  Multiplexer #(.select(1), .width(5), .disabled("Z"), .enable("false")) multiplexer_1 (
    .in0(IR[19:15]), .in1(5'b10001), .out(multiplexer_1_out), .sel(ecall));
  Multiplexer #(.select(1), .width(5), .disabled("Z"), .enable("false")) multiplexer_2 (
    .in0(IR[24:20]), .in1(5'b01010), .out(multiplexer_2_out), .sel(ecall));
  Multiplexer #(.select(1), .width(12), .disabled("Z"), .enable("false")) multiplexer_3 (
    .in0(IR[31:20]), .in1({IR[31:25], IR[11:7]}), .out(multiplexer_3_out), .sel(\单周期硬布线控制器_1_s_type ));
  Shifter #(.width(32), .shift("ll")) shifter_1 (.in(bit_extender_1_out), .\dist (5'b01100), .out(U_imm));
  assign bit_extender_2_out = {{20{IR[31]}}, {IR[31], IR[7], IR[30:25], IR[11:8]}};  // Bit_Extender bit_extender_2
  assign bit_extender_3_out = {{12{IR[31]}}, {IR[31], IR[19:12], IR[20], IR[30:21]}};  // Bit_Extender bit_extender_3
  or or_4 (IR2_t, IR2, IRB);
  Shifter #(.width(32), .shift("lr")) shifter_2 (.in(result), .\dist (5'b10000), .out(shifter_2_out));
  Shifter #(.width(32), .shift("ll")) shifter_3 (.in(bit_extender_2_out), .\dist (5'b00001), .out(shifter_3_out));
  Shifter #(.width(32), .shift("ll")) shifter_4 (.in(bit_extender_3_out), .\dist (5'b00001), .out(shifter_4_out));
  Regifile regifile_1 (
    .Din(RDin), .Clk(CLK), .R1(regifile_1_r1), .R2(r2), .WE(RegWrite), .W_num(IR[11:7]),
    .R1_num(multiplexer_1_out), .R2_num(multiplexer_2_out));
  assign bit_extender_4_out = {{20{multiplexer_3_out[11]}}, multiplexer_3_out};  // Bit_Extender bit_extender_4
  Multiplexer #(.select(1), .width(32), .disabled("Z"), .enable("false")) multiplexer_4 (
    .in0(result), .in1(shifter_2_out), .out(multiplexer_4_out), .sel(aluresult[1]));
  Adder #(.width(32)) adder_1 (.a(PC), .b(32'h4), .out(adder_1_out));  // open: cin, cout
  Adder #(.width(32)) adder_2 (.a(shifter_3_out), .b(PC), .out(adder_2_out));  // open: cin, cout
  Adder #(.width(32)) adder_3 (.a(shifter_4_out), .b(PC), .out(adder_3_out));  // open: cin, cout
  assign and_1_out = aluresult & 32'hfffffffe;  // AND_Gate and_1, 32 bits wide
  or or_5 (IR3_t, IR3, IRC);
  Comparator #(.width(32), .mode("twosComplement")) comparator_1 (
    .a(32'h22), .b(regifile_1_r1), .eq(comparator_1_eq));  // open: gt, lt
  Multiplexer #(.select(1), .width(32), .disabled("Z"), .enable("false")) multiplexer_5 (
    .in0(r2), .in1(bit_extender_4_out), .out(multiplexer_5_out), .sel(\单周期硬布线控制器_1_alu_src ));
  Multiplexer #(.select(1), .width(32), .disabled("Z"), .enable("false")) multiplexer_6 (
    .in0(result), .in1(and_2_out), .out(multiplexer_6_out), .sel(half));
  assign and_2_out = multiplexer_4_out & 32'hffff;  // AND_Gate and_2, 32 bits wide
  and and_3 (and_3_out, alu_1_equal, \单周期硬布线控制器_1_beq );
  not not_2 (not_2_out, alu_1_equal);
  and and_4 (and_4_out, blt, alu_1_out_6);
  ALU alu_1 (
    .X(regifile_1_r1), .Y(multiplexer_5_out), .AluOP(\单周期硬布线控制器_1_alu_op ), .Equal(alu_1_equal),
    .Result(aluresult), .out_6(alu_1_out_6));  // open: Result_2, out_4
  Multiplexer #(.select(1), .width(32), .disabled("Z"), .enable("false")) multiplexer_7 (
    .in0(multiplexer_6_out), .in1(adder_1_out), .out(RDin), .sel(J));
  Priority_Encoder #(.select(2), .disabled("Z")) priority_encoder_1 (
    .in0(1'b1), .in1(B), .in2(jal), .in3(jalr), .out(priority_encoder_1_out));  // open: gs, en_out, en_in
  Multiplexer #(.select(2), .width(32), .disabled("Z"), .enable("false")) multiplexer_8 (
    .in0(adder_1_out), .in1(adder_2_out), .in2(adder_3_out), .in3(and_1_out), .out(multiplexer_8_out),
    .sel(priority_encoder_1_out));
  and and_5 (and_5_out, not_2_out, \单周期硬布线控制器_1_bne );
  or or_6 (or_6_out, and_3_out, and_5_out);
  or or_7 (B, or_6_out, and_4_out);
  and and_6 (led, ecall, comparator_1_eq);
  Multiplexer #(.select(1), .width(32), .disabled("Z"), .enable("false")) multiplexer_9 (
    .in0(r2), .in1(inn), .out(MDin), .sel(sh));
  Multiplexer #(.select(1), .width(32), .disabled("Z"), .enable("false")) multiplexer_10 (
    .in0({32{1'b0}}), .in1(r2), .out(multiplexer_10_out), .sel(led));
  Multiplexer #(.select(1), .width(32), .disabled("Z"), .enable("false")) multiplexer_11 (
    .in0(32'hffff0000), .in1(32'hffff), .out(multiplexer_11_out), .sel(aluresult[1]));
  not not_3 (not_3_out, comparator_1_eq);
  assign bit_extender_5_out = {{16{1'b0}}, r2[15:0]};  // Bit_Extender bit_extender_5
  Multiplexer #(.select(1), .width(5), .disabled("Z"), .enable("false")) multiplexer_12 (
    .in0({5{1'b0}}), .in1(5'b10000), .out(multiplexer_12_out), .sel(aluresult[1]));
  assign and_7_out = \use  & multiplexer_11_out;  // AND_Gate and_7, 32 bits wide
  and and_8 (halt, ecall, not_3_out);
  RAM #(.addrWidth(10), .dataWidth(32), .bus("separate"), .Select("high")) ram_1 (
    .addr(aluresult[11:2]), .din(MDin), .data(\use ), .str(MemWrite), .clk(CLK), .ld(1'b1));  // open: sel, clr
  Register #(.width(32), .trigger("rising"), .Select("low")) register_1 (
    .D(multiplexer_10_out), .en(led), .Q(LedData), .clk(CLK), .clr(RST));
  Shifter #(.width(32), .shift("ll")) shifter_5 (
    .in(bit_extender_5_out), .\dist (multiplexer_12_out), .out(shifter_5_out));
  D_Flip_Flop #(.trigger("high"), .Pre_Clr_Positions("LEGACY"), .NegatePresetClear("false"), .enable("true"), .NewFFLayout("false")) d_ff_1 (.Q(d_ff_1_q));  // open: clk, D, Qn, preset, en, reset
  // Probe on 13'hc
  Multiplexer #(.select(1), .width(32), .disabled("Z"), .enable("false")) multiplexer_13 (
    .in0(aluresult), .in1(\use ), .out(multiplexer_13_out), .sel(\单周期硬布线控制器_1_memtoreg ));
  Adder #(.width(32)) adder_4 (.a(PC), .b(U_imm), .out(adder_4_out));  // open: cin, cout
  Comparator #(.width(13), .mode("twosComplement")) comparator_2 (
    .a(CNT_num), .b(13'hc), .eq(comparator_2_eq), .lt(comparator_2_lt));  // open: gt
  Clock #(.highDuration(1), .lowDuration(1)) clock_1 (.out(clock_1_out));
  or or_8 (or_8_out, Go, not_4_out);
  Counter #(.width(16), .max('hffff), .ongoal("wrap"), .trigger("rising"), .behavior("new")) counter_1 (
    .count(or_8_out), .Q(\总周期数 ), .clk(CLK), .clr(RST));  // open: load, D, carry, preset, down
  not not_4 (not_4_out, halt);
  Multiplexer #(.select(1), .width(32), .disabled("Z"), .enable("false")) multiplexer_14 (
    .in0(multiplexer_13_out), .in1(adder_4_out), .out(multiplexer_14_out), .sel(auipc));
  assign inn = shifter_5_out | and_7_out;  // OR_Gate or_9, 32 bits wide
  Counter #(.width(13), .max('h1fff), .ongoal("stay"), .trigger("rising"), .behavior("old")) counter_2 (
    .count(comparator_2_lt), .Q(CNT_num), .clk(clock_1_out));  // open: load, D, carry, clr, preset
  Multiplexer #(.select(1), .width(32), .disabled("Z"), .enable("false")) multiplexer_15 (
    .in0(multiplexer_14_out), .in1(U_imm), .out(result), .sel(lui));
  nand nand_1 (nand_1_out, d_ff_1_q, comparator_2_eq);
  assign CLK = nand_1_out ? clock_1_out : 1'bz;  // Controlled_Buffer controlled_buffer_1
  Pull_Resistor #(.pull(1)) pull_resistor_1 (.node(CLK));

  // Other names for the same wires on the sheet: high = aluresult[1]

  // Notes on the sheet:
  //   中断源
  //   中断等待指示
  //   数码管输出应该用寄存器锁存，否则显示数据只能一闪而过
  //   数码管输出
  //   指令探针
  //   指令存储器
  //   指令字
  //   contents of rom_1 (hex, n*v repeats v):
  //   100493 100006f 100493 200913 300993 100006f 100493 200913 300993 100006f 100493 200913 300993
  //   100006f 100493 200913 300993 29c000ef 100413 100493 1f49493 900533 2200893 73 24d493 48463 fedff06f
  //   900533 2200893 73 100493 249493 900533 2200893 73 48463 fedff06f 100493 1f49493 900533 2200893 73
  //   4034d493 900533 2200893 73 4044d493 900533 2200893 73 4044d493 900533 2200893 73 4044d493 900533
  //   2200893 73 4044d493 900533 2200893 73 4044d493 900533 2200893 73 4044d493 900533 2200893 73 4044d493
  //   900533 2200893 73 100413 1f41993 41f9d993 433 c00913 300b13 140413 f47413 800293 100313 499993
  //   89e9b3 1300533 2200893 73 406282b3 fe0294e3 140413 f00f93 1f47433 1c41413 800293 100313 49d993
  //   89e9b3 1300533 2200893 73 406282b3 fe0294e3 1c45413 406b0b33 b0463 f95ff06f 2b3 fff2c293 829293
  //   ff2e293 500533 2200893 73 fff00413 493 84a023 140413 448493 84a023 140413 448493 84a023 140413
  //   448493 84a023 140413 448493 84a023 140413 448493 84a023 140413 448493 84a023 140413 448493 84a023
  //   140413 448493 84a023 140413 448493 84a023 140413 448493 84a023 140413 448493 84a023 140413 448493
  //   84a023 140413 448493 84a023 140413 448493 84a023 140413 448493 84a023 140413 448493 140413 433
  //   3c00493 42983 4aa03 149a2b3 28663 134a023 1442023 ffc48493 fe9412e3 800533 2200893 73 440413 3c00493
  //   fc9416e3 a00893 73 413 140413 800533 2200893 73 240413 800533 2200893 73 340413 800533 2200893 73
  //   440413 800533 2200893 73 540413 800533 2200893 73 640413 800533 2200893 73 740413 800533 2200893 73
  //   840413 800533 2200893 2200893 73 8067
  //   I型指令
  //   s型指令
  //   JAL
  //   JALR
  //   URET
  //   B型指令
  //   J型指令
  //   Beq
  //   Bne
  //   MemToReg
  //   MemWrite
  //   AluOP
  //   AluSrcB
  //   RegWrite
  //   half
  //   PC+4
  //   BEQ/BNE
  //   JAL
  //   JALR
  //   为方便自动评测，需要输出PC，IR，寄存器堆写如数据RDin
  //   RAM写使能MemWrite、RAM写入数据MDin等信号
  //   数据存储器
  //   控制位
  //   暂停节拍，不能为0
  //   戳工具置1进入计数暂停模式，ctrl+k时钟自动运行到对应节拍暂停
  //   ctrl+k关闭时钟连续运行，将控制位置零，进入单步调试模式调试
  //   用这个时钟源需要去掉电路中的其他时钟源
  //   可计数暂停的时钟源
endmodule

// 运算器控制器
module \运算控制器自动生成  (
  input  OP2,
  input  OP3,
  input  OP4,
  input  OP5,
  input  OP6,
  input  F12,
  input  F13,
  input  F14,
  input  F25,
  input  F30,
  output S0,
  output S1,
  output S2,
  output S3
);

  wire and_1_out, and_2_out, and_3_out, and_4_out, and_5_out, and_6_out, and_7_out, and_8_out, and_9_out,
       and_10_out, and_11_out, and_12_out, and_13_out, and_14_out, and_15_out, and_16_out, and_17_out,
       and_18_out, and_19_out, and_20_out, and_21_out, and_22_out, and_23_out, and_24_out, and_25_out,
       and_26_out, and_27_out, and_28_out, and_29_out, and_30_out, and_31_out, and_32_out, and_33_out,
       and_34_out, and_35_out, and_36_out, and_37_out, and_38_out, and_39_out, and_40_out, and_41_out,
       and_42_out, and_43_out, and_44_out, and_45_out, not_1_out, not_2_out, not_3_out, not_4_out, not_5_out,
       not_6_out, not_7_out, not_8_out, not_9_out, not_10_out, not_11_out, not_12_out, not_13_out,
       not_14_out, not_15_out, not_16_out, not_17_out, not_18_out, not_19_out, not_20_out, not_21_out,
       not_22_out, not_23_out, not_24_out, not_25_out, not_26_out, not_27_out, not_28_out, not_29_out,
       not_30_out, not_31_out, not_32_out, not_33_out, not_34_out, not_35_out, not_36_out, not_37_out,
       not_38_out, not_39_out, not_40_out, not_41_out, not_42_out, not_43_out, not_44_out, not_45_out,
       not_46_out, not_47_out, not_48_out, not_49_out, not_50_out, not_51_out, not_52_out, not_53_out,
       not_54_out, not_55_out, not_56_out, not_57_out, not_58_out, not_59_out, not_60_out, not_61_out,
       not_62_out, not_63_out, not_64_out, not_65_out, not_66_out, not_67_out, not_68_out, not_69_out,
       not_70_out, not_71_out, not_72_out, not_73_out, not_74_out, not_75_out, not_76_out, not_77_out,
       not_78_out, not_79_out, not_80_out, not_81_out, not_82_out, not_83_out, not_84_out, not_85_out,
       not_86_out, not_87_out, not_88_out, not_89_out, not_90_out, not_91_out, not_92_out, not_93_out,
       not_94_out, not_95_out, not_96_out, not_97_out, not_98_out, not_99_out, not_100_out, not_101_out,
       not_102_out, not_103_out, not_104_out, not_105_out, not_106_out, not_107_out, not_108_out,
       not_109_out, not_110_out, not_111_out, not_112_out, not_113_out, not_114_out, not_115_out,
       not_116_out, not_117_out, not_118_out, not_119_out, not_120_out, not_121_out, not_122_out,
       not_123_out, not_124_out, not_125_out, not_126_out, not_127_out, not_128_out, not_129_out,
       not_130_out, not_131_out, not_132_out, not_133_out, not_134_out, not_135_out, not_136_out,
       not_137_out, not_138_out, not_139_out, not_140_out, not_141_out, not_142_out, not_143_out,
       not_144_out, not_145_out, not_146_out, not_147_out, not_148_out, not_149_out, not_150_out,
       not_151_out, not_152_out, not_153_out, not_154_out, not_155_out, not_156_out, not_157_out,
       not_158_out, not_159_out, not_160_out, not_161_out, not_162_out, not_163_out, not_164_out,
       not_165_out, not_166_out, not_167_out, not_168_out, not_169_out, not_170_out, not_171_out,
       not_172_out, not_173_out, not_174_out, not_175_out, not_176_out, not_177_out, not_178_out,
       not_179_out, not_180_out, not_181_out, not_182_out, not_183_out, not_184_out, not_185_out,
       not_186_out, not_187_out, not_188_out, not_189_out, not_190_out, not_191_out, not_192_out,
       not_193_out, not_194_out, not_195_out, not_196_out, not_197_out, not_198_out, not_199_out,
       not_200_out, not_201_out, not_202_out, not_203_out, not_204_out, not_205_out, not_206_out,
       not_207_out, not_208_out, not_209_out, not_210_out, not_211_out, not_212_out, not_213_out,
       not_214_out, not_215_out, not_216_out, not_217_out, not_218_out, not_219_out, not_220_out,
       not_221_out, not_222_out, not_223_out, not_224_out, not_225_out, not_226_out, not_227_out,
       not_228_out, not_229_out, not_230_out, not_231_out, not_232_out, not_233_out, not_234_out,
       not_235_out, not_236_out, not_237_out, not_238_out, not_239_out, not_240_out, not_241_out,
       not_242_out, not_243_out, not_244_out, not_245_out, not_246_out, not_247_out, not_248_out,
       not_249_out, not_250_out, not_251_out, not_252_out, not_253_out, not_254_out, not_255_out, not_256_out;

  not not_1 (not_1_out, F30);
  not not_2 (not_2_out, F25);
  not not_3 (not_3_out, F14);
  not not_4 (not_4_out, F13);
  not not_5 (not_5_out, F12);
  not not_6 (not_6_out, OP6);
  not not_7 (not_7_out, OP3);
  not not_8 (not_8_out, OP2);
  not not_9 (not_9_out, F30);
  not not_10 (not_10_out, F25);
  not not_11 (not_11_out, OP6);
  not not_12 (not_12_out, OP3);
  not not_13 (not_13_out, OP2);
  not not_14 (not_14_out, F30);
  not not_15 (not_15_out, F25);
  not not_16 (not_16_out, F14);
  not not_17 (not_17_out, F12);
  not not_18 (not_18_out, OP6);
  not not_19 (not_19_out, OP3);
  not not_20 (not_20_out, OP2);
  not not_21 (not_21_out, F14);
  not not_22 (not_22_out, F13);
  not not_23 (not_23_out, F12);
  not not_24 (not_24_out, OP6);
  not not_25 (not_25_out, OP5);
  not not_26 (not_26_out, OP3);
  not not_27 (not_27_out, OP2);
  not not_28 (not_28_out, OP6);
  not not_29 (not_29_out, OP5);
  not not_30 (not_30_out, OP3);
  not not_31 (not_31_out, OP2);
  not not_32 (not_32_out, F13);
  not not_33 (not_33_out, F12);
  not not_34 (not_34_out, OP6);
  not not_35 (not_35_out, OP5);
  not not_36 (not_36_out, OP3);
  not not_37 (not_37_out, OP2);
  not not_38 (not_38_out, F14);
  not not_39 (not_39_out, F12);
  not not_40 (not_40_out, OP6);
  not not_41 (not_41_out, OP5);
  not not_42 (not_42_out, OP3);
  not not_43 (not_43_out, OP2);
  not not_44 (not_44_out, F25);
  not not_45 (not_45_out, F13);
  not not_46 (not_46_out, OP6);
  not not_47 (not_47_out, OP5);
  not not_48 (not_48_out, OP3);
  not not_49 (not_49_out, OP2);
  not not_50 (not_50_out, F14);
  not not_51 (not_51_out, F12);
  not not_52 (not_52_out, OP6);
  not not_53 (not_53_out, OP5);
  not not_54 (not_54_out, OP4);
  not not_55 (not_55_out, OP3);
  not not_56 (not_56_out, OP2);
  not not_57 (not_57_out, F14);
  not not_58 (not_58_out, F12);
  not not_59 (not_59_out, OP6);
  not not_60 (not_60_out, OP4);
  not not_61 (not_61_out, OP3);
  not not_62 (not_62_out, OP2);
  not not_63 (not_63_out, F14);
  not not_64 (not_64_out, F13);
  not not_65 (not_65_out, F12);
  not not_66 (not_66_out, OP4);
  not not_67 (not_67_out, OP3);
  not not_68 (not_68_out, OP3);
  not not_69 (not_69_out, OP2);
  not not_70 (not_70_out, F30);
  not not_71 (not_71_out, F25);
  not not_72 (not_72_out, F13);
  not not_73 (not_73_out, F12);
  not not_74 (not_74_out, OP6);
  not not_75 (not_75_out, OP3);
  not not_76 (not_76_out, OP2);
  not not_77 (not_77_out, F13);
  not not_78 (not_78_out, OP6);
  not not_79 (not_79_out, OP5);
  not not_80 (not_80_out, OP4);
  not not_81 (not_81_out, OP3);
  not not_82 (not_82_out, OP2);
  not not_83 (not_83_out, F13);
  not not_84 (not_84_out, F12);
  not not_85 (not_85_out, OP4);
  not not_86 (not_86_out, OP3);
  not not_87 (not_87_out, OP2);
  not not_88 (not_88_out, F14);
  not not_89 (not_89_out, F13);
  not not_90 (not_90_out, OP6);
  not not_91 (not_91_out, OP4);
  not not_92 (not_92_out, OP3);
  not not_93 (not_93_out, OP2);
  not not_94 (not_94_out, F25);
  not not_95 (not_95_out, F14);
  not not_96 (not_96_out, F13);
  not not_97 (not_97_out, F12);
  not not_98 (not_98_out, OP6);
  not not_99 (not_99_out, OP3);
  not not_100 (not_100_out, OP2);
  not not_101 (not_101_out, F30);
  not not_102 (not_102_out, F25);
  not not_103 (not_103_out, OP6);
  not not_104 (not_104_out, OP3);
  not not_105 (not_105_out, OP2);
  not not_106 (not_106_out, F30);
  not not_107 (not_107_out, F25);
  not not_108 (not_108_out, F14);
  not not_109 (not_109_out, F12);
  not not_110 (not_110_out, OP6);
  not not_111 (not_111_out, OP3);
  not not_112 (not_112_out, OP2);
  not not_113 (not_113_out, OP6);
  not not_114 (not_114_out, OP5);
  not not_115 (not_115_out, OP3);
  not not_116 (not_116_out, OP2);
  not not_117 (not_117_out, F14);
  not not_118 (not_118_out, F12);
  not not_119 (not_119_out, OP6);
  not not_120 (not_120_out, OP5);
  not not_121 (not_121_out, OP3);
  not not_122 (not_122_out, OP2);
  not not_123 (not_123_out, F30);
  not not_124 (not_124_out, F25);
  not not_125 (not_125_out, F13);
  not not_126 (not_126_out, OP6);
  not not_127 (not_127_out, OP5);
  not not_128 (not_128_out, OP3);
  not not_129 (not_129_out, OP2);
  not not_130 (not_130_out, OP3);
  not not_131 (not_131_out, OP2);
  not not_132 (not_132_out, F13);
  not not_133 (not_133_out, F12);
  not not_134 (not_134_out, OP4);
  not not_135 (not_135_out, OP3);
  not not_136 (not_136_out, OP2);
  not not_137 (not_137_out, F30);
  not not_138 (not_138_out, F25);
  not not_139 (not_139_out, F14);
  not not_140 (not_140_out, F13);
  not not_141 (not_141_out, F12);
  not not_142 (not_142_out, OP6);
  not not_143 (not_143_out, OP3);
  not not_144 (not_144_out, OP2);
  not not_145 (not_145_out, F25);
  not not_146 (not_146_out, F14);
  not not_147 (not_147_out, F13);
  not not_148 (not_148_out, F12);
  not not_149 (not_149_out, OP6);
  not not_150 (not_150_out, OP3);
  not not_151 (not_151_out, OP2);
  not not_152 (not_152_out, F30);
  not not_153 (not_153_out, F25);
  not not_154 (not_154_out, OP6);
  not not_155 (not_155_out, OP3);
  not not_156 (not_156_out, OP2);
  not not_157 (not_157_out, F30);
  not not_158 (not_158_out, F25);
  not not_159 (not_159_out, F14);
  not not_160 (not_160_out, OP6);
  not not_161 (not_161_out, OP3);
  not not_162 (not_162_out, OP2);
  not not_163 (not_163_out, F14);
  not not_164 (not_164_out, F13);
  not not_165 (not_165_out, F12);
  not not_166 (not_166_out, OP6);
  not not_167 (not_167_out, OP5);
  not not_168 (not_168_out, OP3);
  not not_169 (not_169_out, OP2);
  not not_170 (not_170_out, OP6);
  not not_171 (not_171_out, OP5);
  not not_172 (not_172_out, OP3);
  not not_173 (not_173_out, OP2);
  not not_174 (not_174_out, F14);
  not not_175 (not_175_out, F12);
  not not_176 (not_176_out, OP6);
  not not_177 (not_177_out, OP5);
  not not_178 (not_178_out, OP4);
  not not_179 (not_179_out, OP3);
  not not_180 (not_180_out, OP2);
  not not_181 (not_181_out, F14);
  not not_182 (not_182_out, F12);
  not not_183 (not_183_out, OP6);
  not not_184 (not_184_out, OP4);
  not not_185 (not_185_out, OP3);
  not not_186 (not_186_out, OP2);
  not not_187 (not_187_out, F14);
  not not_188 (not_188_out, F13);
  not not_189 (not_189_out, F12);
  not not_190 (not_190_out, OP4);
  not not_191 (not_191_out, OP3);
  not not_192 (not_192_out, OP3);
  not not_193 (not_193_out, OP2);
  not not_194 (not_194_out, F13);
  not not_195 (not_195_out, OP6);
  not not_196 (not_196_out, OP5);
  not not_197 (not_197_out, OP4);
  not not_198 (not_198_out, OP3);
  not not_199 (not_199_out, OP2);
  not not_200 (not_200_out, F14);
  not not_201 (not_201_out, F13);
  not not_202 (not_202_out, OP6);
  not not_203 (not_203_out, OP4);
  not not_204 (not_204_out, OP3);
  not not_205 (not_205_out, OP2);
  not not_206 (not_206_out, F30);
  not not_207 (not_207_out, F25);
  not not_208 (not_208_out, F12);
  not not_209 (not_209_out, OP6);
  not not_210 (not_210_out, OP3);
  not not_211 (not_211_out, OP2);
  not not_212 (not_212_out, F30);
  not not_213 (not_213_out, F25);
  not not_214 (not_214_out, F14);
  not not_215 (not_215_out, F12);
  not not_216 (not_216_out, OP6);
  not not_217 (not_217_out, OP3);
  not not_218 (not_218_out, OP2);
  not not_219 (not_219_out, F30);
  not not_220 (not_220_out, F25);
  not not_221 (not_221_out, F14);
  not not_222 (not_222_out, OP6);
  not not_223 (not_223_out, OP3);
  not not_224 (not_224_out, OP2);
  not not_225 (not_225_out, F12);
  not not_226 (not_226_out, OP6);
  not not_227 (not_227_out, OP5);
  not not_228 (not_228_out, OP3);
  not not_229 (not_229_out, OP2);
  not not_230 (not_230_out, F13);
  not not_231 (not_231_out, F12);
  not not_232 (not_232_out, OP6);
  not not_233 (not_233_out, OP5);
  not not_234 (not_234_out, OP3);
  not not_235 (not_235_out, OP2);
  not not_236 (not_236_out, F14);
  not not_237 (not_237_out, F12);
  not not_238 (not_238_out, OP6);
  not not_239 (not_239_out, OP5);
  not not_240 (not_240_out, OP3);
  not not_241 (not_241_out, OP2);
  not not_242 (not_242_out, F12);
  not not_243 (not_243_out, OP3);
  not not_244 (not_244_out, OP2);
  not not_245 (not_245_out, F30);
  not not_246 (not_246_out, F25);
  not not_247 (not_247_out, F13);
  not not_248 (not_248_out, F12);
  not not_249 (not_249_out, OP6);
  not not_250 (not_250_out, OP3);
  not not_251 (not_251_out, OP2);
  not not_252 (not_252_out, F13);
  not not_253 (not_253_out, F12);
  not not_254 (not_254_out, OP4);
  not not_255 (not_255_out, OP3);
  not not_256 (not_256_out, OP2);
  and and_1 (and_1_out, not_1_out, not_2_out, not_3_out, not_4_out, not_5_out, not_6_out, OP5, OP4, not_7_out, not_8_out);
  and and_2 (and_2_out, not_9_out, not_10_out, F14, F13, F12, not_11_out, OP5, OP4, not_12_out, not_13_out);
  and and_3 (and_3_out, not_14_out, not_15_out, not_16_out, F13, not_17_out, not_18_out, OP5, OP4, not_19_out, not_20_out);
  and and_4 (and_4_out, not_21_out, not_22_out, not_23_out, not_24_out, not_25_out, OP4, not_26_out, not_27_out);
  and and_5 (and_5_out, F14, F13, F12, not_28_out, not_29_out, OP4, not_30_out, not_31_out);
  and and_6 (and_6_out, F14, not_32_out, not_33_out, not_34_out, not_35_out, OP4, not_36_out, not_37_out);
  and and_7 (and_7_out, not_38_out, F13, not_39_out, not_40_out, not_41_out, OP4, not_42_out, not_43_out);
  and and_8 (and_8_out, F30, not_44_out, F14, not_45_out, F12, not_46_out, not_47_out, OP4, not_48_out, not_49_out);
  and and_9 (and_9_out, not_50_out, F13, not_51_out, not_52_out, not_53_out, not_54_out, not_55_out, not_56_out);
  and and_10 (and_10_out, not_57_out, F13, not_58_out, not_59_out, OP5, not_60_out, not_61_out, not_62_out);
  and and_11 (and_11_out, not_63_out, not_64_out, not_65_out, OP6, OP5, not_66_out, not_67_out, OP2);
  and and_12 (and_12_out, F14, F13, F12, OP6, OP5, OP4, not_68_out, not_69_out);
  and and_13 (and_13_out, not_70_out, not_71_out, F14, not_72_out, not_73_out, not_74_out, OP5, OP4, not_75_out, not_76_out);
  and and_14 (and_14_out, F14, not_77_out, F12, not_78_out, not_79_out, not_80_out, not_81_out, not_82_out);
  and and_15 (and_15_out, F14, not_83_out, not_84_out, OP6, OP5, not_85_out, not_86_out, not_87_out);
  and and_16 (and_16_out, not_88_out, not_89_out, F12, not_90_out, OP5, not_91_out, not_92_out, not_93_out);
  and and_17 (and_17_out, F30, not_94_out, not_95_out, not_96_out, not_97_out, not_98_out, OP5, OP4, not_99_out, not_100_out);
  and and_18 (and_18_out, not_101_out, not_102_out, F14, F13, F12, not_103_out, OP5, OP4, not_104_out, not_105_out);
  and and_19 (and_19_out, not_106_out, not_107_out, not_108_out, F13, not_109_out, not_110_out, OP5, OP4, not_111_out, not_112_out);
  and and_20 (and_20_out, F14, F13, F12, not_113_out, not_114_out, OP4, not_115_out, not_116_out);
  and and_21 (and_21_out, not_117_out, F13, not_118_out, not_119_out, not_120_out, OP4, not_121_out, not_122_out);
  and and_22 (and_22_out, not_123_out, not_124_out, F14, not_125_out, F12, not_126_out, not_127_out, OP4, not_128_out, not_129_out);
  and and_23 (and_23_out, F14, F13, F12, OP6, OP5, OP4, not_130_out, not_131_out);
  and and_24 (and_24_out, F14, not_132_out, not_133_out, OP6, OP5, not_134_out, not_135_out, not_136_out);
  and and_25 (and_25_out, not_137_out, not_138_out, not_139_out, not_140_out, not_141_out, not_142_out, OP5, OP4, not_143_out, not_144_out);
  and and_26 (and_26_out, F30, not_145_out, not_146_out, not_147_out, not_148_out, not_149_out, OP5, OP4, not_150_out, not_151_out);
  and and_27 (and_27_out, not_152_out, not_153_out, F14, F13, F12, not_154_out, OP5, OP4, not_155_out, not_156_out);
  and and_28 (and_28_out, not_157_out, not_158_out, not_159_out, F13, F12, not_160_out, OP5, OP4, not_161_out, not_162_out);
  and and_29 (and_29_out, not_163_out, not_164_out, not_165_out, not_166_out, not_167_out, OP4, not_168_out, not_169_out);
  and and_30 (and_30_out, F14, F13, F12, not_170_out, not_171_out, OP4, not_172_out, not_173_out);
  and and_31 (and_31_out, not_174_out, F13, not_175_out, not_176_out, not_177_out, not_178_out, not_179_out, not_180_out);
  and and_32 (and_32_out, not_181_out, F13, not_182_out, not_183_out, OP5, not_184_out, not_185_out, not_186_out);
  and and_33 (and_33_out, not_187_out, not_188_out, not_189_out, OP6, OP5, not_190_out, not_191_out, OP2);
  and and_34 (and_34_out, F14, F13, F12, OP6, OP5, OP4, not_192_out, not_193_out);
  and and_35 (and_35_out, F14, not_194_out, F12, not_195_out, not_196_out, not_197_out, not_198_out, not_199_out);
  and and_36 (and_36_out, not_200_out, not_201_out, F12, not_202_out, OP5, not_203_out, not_204_out, not_205_out);
  and and_37 (and_37_out, not_206_out, not_207_out, F14, F13, not_208_out, not_209_out, OP5, OP4, not_210_out, not_211_out);
  and and_38 (and_38_out, not_212_out, not_213_out, not_214_out, F13, not_215_out, not_216_out, OP5, OP4, not_217_out, not_218_out);
  and and_39 (and_39_out, not_219_out, not_220_out, not_221_out, F13, F12, not_222_out, OP5, OP4, not_223_out, not_224_out);
  and and_40 (and_40_out, F14, F13, not_225_out, not_226_out, not_227_out, OP4, not_228_out, not_229_out);
  and and_41 (and_41_out, F14, not_230_out, not_231_out, not_232_out, not_233_out, OP4, not_234_out, not_235_out);
  and and_42 (and_42_out, not_236_out, F13, not_237_out, not_238_out, not_239_out, OP4, not_240_out, not_241_out);
  and and_43 (and_43_out, F14, F13, not_242_out, OP6, OP5, OP4, not_243_out, not_244_out);
  and and_44 (and_44_out, not_245_out, not_246_out, F14, not_247_out, not_248_out, not_249_out, OP5, OP4, not_250_out, not_251_out);
  and and_45 (and_45_out, F14, not_252_out, not_253_out, OP6, OP5, not_254_out, not_255_out, not_256_out);
  or or_1 (S0, and_1_out, and_2_out, and_3_out, and_4_out, and_5_out, and_6_out, and_7_out, and_8_out, and_9_out, and_10_out, and_11_out, and_12_out, and_13_out, and_14_out, and_15_out, and_16_out);
  or or_2 (S1, and_17_out, and_18_out, and_19_out, and_20_out, and_21_out, and_22_out, and_23_out, and_24_out);
  or or_3 (S2, and_25_out, and_26_out, and_27_out, and_28_out, and_29_out, and_30_out, and_31_out, and_32_out, and_33_out, and_34_out, and_35_out, and_36_out);
  or or_4 (S3, and_37_out, and_38_out, and_39_out, and_40_out, and_41_out, and_42_out, and_43_out, and_44_out, and_45_out);
endmodule

// 控制信号生成
module \控制信号自动生成  (
  input  OP2,
  input  OP3,
  input  OP4,
  input  OP5,
  input  OP6,
  input  F12,
  input  F13,
  input  F14,
  input  F25,
  input  F30,
  output MemToReg,
  output MemWrite,
  output ALU_SRC,
  output RegWrite,
  output ecall,
  output S_Type,
  output BEQ,
  output BNE,
  output JALR,
  output JAL,
  output half,
  output CSR,
  output AUIPC,
  output LUI,
  output SH,
  output BLT
);

  wire and_1_out, and_2_out, and_3_out, and_4_out, and_5_out, and_6_out, and_7_out, and_8_out, and_9_out,
       and_10_out, and_11_out, and_12_out, and_13_out, and_14_out, and_15_out, and_16_out, and_17_out,
       and_18_out, and_19_out, and_20_out, and_21_out, and_22_out, and_23_out, and_24_out, and_25_out,
       and_26_out, and_27_out, and_28_out, and_29_out, and_30_out, and_31_out, and_32_out, and_33_out,
       and_34_out, and_35_out, and_36_out, and_37_out, and_38_out, and_39_out, and_40_out, and_41_out,
       and_42_out, and_43_out, and_44_out, and_45_out, and_51_out, and_52_out, not_1_out, not_2_out,
       not_3_out, not_4_out, not_5_out, not_6_out, not_7_out, not_8_out, not_9_out, not_10_out, not_11_out,
       not_12_out, not_13_out, not_14_out, not_15_out, not_16_out, not_17_out, not_18_out, not_19_out,
       not_20_out, not_21_out, not_22_out, not_23_out, not_24_out, not_25_out, not_26_out, not_27_out,
       not_28_out, not_29_out, not_30_out, not_31_out, not_32_out, not_33_out, not_34_out, not_35_out,
       not_36_out, not_37_out, not_38_out, not_39_out, not_40_out, not_41_out, not_42_out, not_43_out,
       not_44_out, not_45_out, not_46_out, not_47_out, not_48_out, not_49_out, not_50_out, not_51_out,
       not_52_out, not_53_out, not_54_out, not_55_out, not_56_out, not_57_out, not_58_out, not_59_out,
       not_60_out, not_61_out, not_62_out, not_63_out, not_64_out, not_65_out, not_66_out, not_67_out,
       not_68_out, not_69_out, not_70_out, not_71_out, not_72_out, not_73_out, not_74_out, not_75_out,
       not_76_out, not_77_out, not_78_out, not_79_out, not_80_out, not_81_out, not_82_out, not_83_out,
       not_84_out, not_85_out, not_86_out, not_87_out, not_88_out, not_89_out, not_90_out, not_91_out,
       not_92_out, not_93_out, not_94_out, not_95_out, not_96_out, not_97_out, not_98_out, not_99_out,
       not_100_out, not_101_out, not_102_out, not_103_out, not_104_out, not_105_out, not_106_out,
       not_107_out, not_108_out, not_109_out, not_110_out, not_111_out, not_112_out, not_113_out,
       not_114_out, not_115_out, not_116_out, not_117_out, not_118_out, not_119_out, not_120_out,
       not_121_out, not_122_out, not_123_out, not_124_out, not_125_out, not_126_out, not_127_out,
       not_128_out, not_129_out, not_130_out, not_131_out, not_132_out, not_133_out, not_134_out,
       not_135_out, not_136_out, not_137_out, not_138_out, not_139_out, not_140_out, not_141_out,
       not_142_out, not_143_out, not_144_out, not_145_out, not_146_out, not_147_out, not_148_out,
       not_149_out, not_150_out, not_151_out, not_152_out, not_153_out, not_154_out, not_155_out,
       not_156_out, not_157_out, not_158_out, not_159_out, not_160_out, not_161_out, not_162_out,
       not_163_out, not_164_out, not_165_out, not_166_out, not_167_out, not_168_out, not_169_out,
       not_170_out, not_171_out, not_172_out, not_173_out, not_174_out, not_175_out, not_176_out,
       not_177_out, not_178_out, not_179_out, not_180_out, not_181_out, not_182_out, not_183_out,
       not_184_out, not_185_out, not_186_out, not_187_out, not_188_out, not_189_out, not_190_out,
       not_191_out, not_192_out, not_193_out, not_194_out, not_195_out, not_196_out, not_197_out,
       not_198_out, not_199_out, not_200_out, not_201_out, not_202_out, not_203_out, not_204_out,
       not_205_out, not_206_out, not_207_out, not_208_out, not_209_out, not_210_out, not_211_out,
       not_212_out, not_213_out, not_214_out, not_215_out, not_216_out, not_217_out, not_218_out,
       not_219_out, not_220_out, not_221_out, not_222_out, not_223_out, not_224_out, not_225_out,
       not_226_out, not_227_out, not_228_out, not_229_out, not_230_out, not_231_out, not_232_out,
       not_233_out, not_234_out, not_235_out, not_236_out, not_237_out, not_238_out, not_239_out,
       not_240_out, not_241_out, not_242_out, not_243_out, not_244_out, not_245_out, not_246_out,
       not_247_out, not_248_out, not_249_out, not_250_out, not_251_out, not_252_out, not_253_out,
       not_254_out, not_255_out, not_256_out, not_257_out, not_258_out, not_259_out, not_260_out,
       not_261_out, not_262_out, not_263_out, not_264_out, not_265_out, not_266_out, not_267_out,
       not_268_out, not_269_out, not_270_out, not_271_out, not_272_out, not_273_out, not_274_out,
       not_275_out, not_276_out, not_277_out, not_278_out, not_279_out, not_280_out, not_281_out,
       not_282_out, not_283_out, not_284_out, not_285_out, not_286_out, not_287_out, not_288_out,
       not_289_out, not_290_out, not_291_out, not_292_out, not_293_out, not_294_out, not_295_out,
       not_296_out, not_297_out, not_298_out, not_299_out, not_300_out, not_301_out, not_302_out, not_303_out;

  not not_1 (not_1_out, F14);
  not not_2 (not_2_out, F12);
  not not_3 (not_3_out, OP6);
  not not_4 (not_4_out, OP5);
  not not_5 (not_5_out, OP4);
  not not_6 (not_6_out, OP3);
  not not_7 (not_7_out, OP2);
  not not_8 (not_8_out, F13);
  not not_9 (not_9_out, OP6);
  not not_10 (not_10_out, OP5);
  not not_11 (not_11_out, OP4);
  not not_12 (not_12_out, OP3);
  not not_13 (not_13_out, OP2);
  not not_14 (not_14_out, F14);
  not not_15 (not_15_out, F12);
  not not_16 (not_16_out, OP6);
  not not_17 (not_17_out, OP4);
  not not_18 (not_18_out, OP3);
  not not_19 (not_19_out, OP2);
  not not_20 (not_20_out, F14);
  not not_21 (not_21_out, F13);
  not not_22 (not_22_out, OP6);
  not not_23 (not_23_out, OP4);
  not not_24 (not_24_out, OP3);
  not not_25 (not_25_out, OP2);
  not not_26 (not_26_out, F14);
  not not_27 (not_27_out, F13);
  not not_28 (not_28_out, F12);
  not not_29 (not_29_out, OP6);
  not not_30 (not_30_out, OP5);
  not not_31 (not_31_out, OP3);
  not not_32 (not_32_out, OP2);
  not not_33 (not_33_out, OP6);
  not not_34 (not_34_out, OP5);
  not not_35 (not_35_out, OP3);
  not not_36 (not_36_out, OP2);
  not not_37 (not_37_out, F12);
  not not_38 (not_38_out, OP6);
  not not_39 (not_39_out, OP5);
  not not_40 (not_40_out, OP3);
  not not_41 (not_41_out, OP2);
  not not_42 (not_42_out, F13);
  not not_43 (not_43_out, F12);
  not not_44 (not_44_out, OP6);
  not not_45 (not_45_out, OP5);
  not not_46 (not_46_out, OP3);
  not not_47 (not_47_out, OP2);
  not not_48 (not_48_out, F14);
  not not_49 (not_49_out, F12);
  not not_50 (not_50_out, OP6);
  not not_51 (not_51_out, OP5);
  not not_52 (not_52_out, OP3);
  not not_53 (not_53_out, OP2);
  not not_54 (not_54_out, F30);
  not not_55 (not_55_out, F25);
  not not_56 (not_56_out, F14);
  not not_57 (not_57_out, F13);
  not not_58 (not_58_out, OP6);
  not not_59 (not_59_out, OP5);
  not not_60 (not_60_out, OP3);
  not not_61 (not_61_out, OP2);
  not not_62 (not_62_out, F30);
  not not_63 (not_63_out, F25);
  not not_64 (not_64_out, F13);
  not not_65 (not_65_out, OP6);
  not not_66 (not_66_out, OP5);
  not not_67 (not_67_out, OP3);
  not not_68 (not_68_out, OP2);
  not not_69 (not_69_out, F25);
  not not_70 (not_70_out, F13);
  not not_71 (not_71_out, OP6);
  not not_72 (not_72_out, OP5);
  not not_73 (not_73_out, OP3);
  not not_74 (not_74_out, OP2);
  not not_75 (not_75_out, F14);
  not not_76 (not_76_out, F12);
  not not_77 (not_77_out, OP6);
  not not_78 (not_78_out, OP5);
  not not_79 (not_79_out, OP4);
  not not_80 (not_80_out, OP3);
  not not_81 (not_81_out, OP2);
  not not_82 (not_82_out, F14);
  not not_83 (not_83_out, F12);
  not not_84 (not_84_out, OP6);
  not not_85 (not_85_out, OP4);
  not not_86 (not_86_out, OP3);
  not not_87 (not_87_out, OP2);
  not not_88 (not_88_out, F14);
  not not_89 (not_89_out, F13);
  not not_90 (not_90_out, F12);
  not not_91 (not_91_out, OP4);
  not not_92 (not_92_out, OP3);
  not not_93 (not_93_out, F12);
  not not_94 (not_94_out, OP3);
  not not_95 (not_95_out, OP2);
  not not_96 (not_96_out, OP3);
  not not_97 (not_97_out, OP2);
  not not_98 (not_98_out, F13);
  not not_99 (not_99_out, OP6);
  not not_100 (not_100_out, OP5);
  not not_101 (not_101_out, OP4);
  not not_102 (not_102_out, OP3);
  not not_103 (not_103_out, OP2);
  not not_104 (not_104_out, F14);
  not not_105 (not_105_out, F13);
  not not_106 (not_106_out, OP6);
  not not_107 (not_107_out, OP4);
  not not_108 (not_108_out, OP3);
  not not_109 (not_109_out, OP2);
  not not_110 (not_110_out, F30);
  not not_111 (not_111_out, F25);
  not not_112 (not_112_out, F14);
  not not_113 (not_113_out, F13);
  not not_114 (not_114_out, F12);
  not not_115 (not_115_out, OP6);
  not not_116 (not_116_out, OP3);
  not not_117 (not_117_out, OP2);
  not not_118 (not_118_out, F25);
  not not_119 (not_119_out, F14);
  not not_120 (not_120_out, F13);
  not not_121 (not_121_out, F12);
  not not_122 (not_122_out, OP6);
  not not_123 (not_123_out, OP3);
  not not_124 (not_124_out, OP2);
  not not_125 (not_125_out, F30);
  not not_126 (not_126_out, F25);
  not not_127 (not_127_out, OP6);
  not not_128 (not_128_out, OP3);
  not not_129 (not_129_out, OP2);
  not not_130 (not_130_out, F30);
  not not_131 (not_131_out, F25);
  not not_132 (not_132_out, F12);
  not not_133 (not_133_out, OP6);
  not not_134 (not_134_out, OP3);
  not not_135 (not_135_out, OP2);
  not not_136 (not_136_out, F30);
  not not_137 (not_137_out, F25);
  not not_138 (not_138_out, F14);
  not not_139 (not_139_out, F12);
  not not_140 (not_140_out, OP6);
  not not_141 (not_141_out, OP3);
  not not_142 (not_142_out, OP2);
  not not_143 (not_143_out, F30);
  not not_144 (not_144_out, F25);
  not not_145 (not_145_out, F14);
  not not_146 (not_146_out, OP6);
  not not_147 (not_147_out, OP3);
  not not_148 (not_148_out, OP2);
  not not_149 (not_149_out, F14);
  not not_150 (not_150_out, F13);
  not not_151 (not_151_out, F12);
  not not_152 (not_152_out, OP6);
  not not_153 (not_153_out, OP5);
  not not_154 (not_154_out, OP3);
  not not_155 (not_155_out, OP2);
  not not_156 (not_156_out, OP6);
  not not_157 (not_157_out, OP5);
  not not_158 (not_158_out, OP3);
  not not_159 (not_159_out, OP2);
  not not_160 (not_160_out, F12);
  not not_161 (not_161_out, OP6);
  not not_162 (not_162_out, OP5);
  not not_163 (not_163_out, OP3);
  not not_164 (not_164_out, OP2);
  not not_165 (not_165_out, F13);
  not not_166 (not_166_out, F12);
  not not_167 (not_167_out, OP6);
  not not_168 (not_168_out, OP5);
  not not_169 (not_169_out, OP3);
  not not_170 (not_170_out, OP2);
  not not_171 (not_171_out, F14);
  not not_172 (not_172_out, F12);
  not not_173 (not_173_out, OP6);
  not not_174 (not_174_out, OP5);
  not not_175 (not_175_out, OP3);
  not not_176 (not_176_out, OP2);
  not not_177 (not_177_out, F30);
  not not_178 (not_178_out, F25);
  not not_179 (not_179_out, F14);
  not not_180 (not_180_out, F13);
  not not_181 (not_181_out, OP6);
  not not_182 (not_182_out, OP5);
  not not_183 (not_183_out, OP3);
  not not_184 (not_184_out, OP2);
  not not_185 (not_185_out, F30);
  not not_186 (not_186_out, F25);
  not not_187 (not_187_out, F13);
  not not_188 (not_188_out, OP6);
  not not_189 (not_189_out, OP5);
  not not_190 (not_190_out, OP3);
  not not_191 (not_191_out, OP2);
  not not_192 (not_192_out, F25);
  not not_193 (not_193_out, F13);
  not not_194 (not_194_out, OP6);
  not not_195 (not_195_out, OP5);
  not not_196 (not_196_out, OP3);
  not not_197 (not_197_out, OP2);
  not not_198 (not_198_out, F14);
  not not_199 (not_199_out, F12);
  not not_200 (not_200_out, OP6);
  not not_201 (not_201_out, OP5);
  not not_202 (not_202_out, OP4);
  not not_203 (not_203_out, OP3);
  not not_204 (not_204_out, OP2);
  not not_205 (not_205_out, OP4);
  not not_206 (not_206_out, F14);
  not not_207 (not_207_out, F13);
  not not_208 (not_208_out, F12);
  not not_209 (not_209_out, OP4);
  not not_210 (not_210_out, OP3);
  not not_211 (not_211_out, F30);
  not not_212 (not_212_out, F25);
  not not_213 (not_213_out, F14);
  not not_214 (not_214_out, F13);
  not not_215 (not_215_out, OP6);
  not not_216 (not_216_out, OP3);
  not not_217 (not_217_out, OP2);
  not not_218 (not_218_out, F30);
  not not_219 (not_219_out, F25);
  not not_220 (not_220_out, F13);
  not not_221 (not_221_out, F12);
  not not_222 (not_222_out, OP6);
  not not_223 (not_223_out, OP3);
  not not_224 (not_224_out, OP2);
  not not_225 (not_225_out, F13);
  not not_226 (not_226_out, OP6);
  not not_227 (not_227_out, OP5);
  not not_228 (not_228_out, OP4);
  not not_229 (not_229_out, OP3);
  not not_230 (not_230_out, OP2);
  not not_231 (not_231_out, OP6);
  not not_232 (not_232_out, OP5);
  not not_233 (not_233_out, OP3);
  not not_234 (not_234_out, OP6);
  not not_235 (not_235_out, OP3);
  not not_236 (not_236_out, F30);
  not not_237 (not_237_out, F25);
  not not_238 (not_238_out, F14);
  not not_239 (not_239_out, F13);
  not not_240 (not_240_out, F12);
  not not_241 (not_241_out, OP3);
  not not_242 (not_242_out, OP2);
  not not_243 (not_243_out, F14);
  not not_244 (not_244_out, F13);
  not not_245 (not_245_out, F12);
  not not_246 (not_246_out, OP3);
  not not_247 (not_247_out, OP2);
  not not_248 (not_248_out, F14);
  not not_249 (not_249_out, F12);
  not not_250 (not_250_out, OP6);
  not not_251 (not_251_out, OP4);
  not not_252 (not_252_out, OP3);
  not not_253 (not_253_out, OP2);
  not not_254 (not_254_out, F14);
  not not_255 (not_255_out, F13);
  not not_256 (not_256_out, OP6);
  not not_257 (not_257_out, OP4);
  not not_258 (not_258_out, OP3);
  not not_259 (not_259_out, OP2);
  not not_260 (not_260_out, F14);
  not not_261 (not_261_out, F13);
  not not_262 (not_262_out, F12);
  not not_263 (not_263_out, OP4);
  not not_264 (not_264_out, OP3);
  not not_265 (not_265_out, OP2);
  not not_266 (not_266_out, F14);
  not not_267 (not_267_out, F13);
  not not_268 (not_268_out, OP4);
  not not_269 (not_269_out, OP3);
  not not_270 (not_270_out, OP2);
  not not_271 (not_271_out, F14);
  not not_272 (not_272_out, F13);
  not not_273 (not_273_out, F12);
  not not_274 (not_274_out, OP4);
  not not_275 (not_275_out, OP3);
  not not_276 (not_276_out, OP4);
  not not_277 (not_277_out, F13);
  not not_278 (not_278_out, OP6);
  not not_279 (not_279_out, OP5);
  not not_280 (not_280_out, OP4);
  not not_281 (not_281_out, OP3);
  not not_282 (not_282_out, OP2);
  not not_283 (not_283_out, F12);
  not not_284 (not_284_out, OP3);
  not not_285 (not_285_out, OP2);
  not not_286 (not_286_out, OP3);
  not not_287 (not_287_out, OP2);
  not not_288 (not_288_out, OP6);
  not not_289 (not_289_out, OP5);
  not not_290 (not_290_out, OP3);
  not not_291 (not_291_out, OP6);
  not not_292 (not_292_out, OP3);
  not not_293 (not_293_out, F14);
  not not_294 (not_294_out, F13);
  not not_295 (not_295_out, OP6);
  not not_296 (not_296_out, OP4);
  not not_297 (not_297_out, OP3);
  not not_298 (not_298_out, OP2);
  not not_299 (not_299_out, F13);
  not not_300 (not_300_out, F12);
  not not_301 (not_301_out, OP4);
  not not_302 (not_302_out, OP3);
  not not_303 (not_303_out, OP2);
  and and_1 (and_1_out, not_1_out, F13, not_2_out, not_3_out, not_4_out, not_5_out, not_6_out, not_7_out);
  and and_2 (and_2_out, F14, not_8_out, F12, not_9_out, not_10_out, not_11_out, not_12_out, not_13_out);
  and and_3 (and_3_out, not_14_out, F13, not_15_out, not_16_out, OP5, not_17_out, not_18_out, not_19_out);
  and and_4 (and_4_out, not_20_out, not_21_out, F12, not_22_out, OP5, not_23_out, not_24_out, not_25_out);
  and and_5 (and_5_out, not_26_out, not_27_out, not_28_out, not_29_out, not_30_out, OP4, not_31_out, not_32_out);
  and and_6 (and_6_out, F14, F13, F12, not_33_out, not_34_out, OP4, not_35_out, not_36_out);
  and and_7 (and_7_out, F14, F13, not_37_out, not_38_out, not_39_out, OP4, not_40_out, not_41_out);
  and and_8 (and_8_out, F14, not_42_out, not_43_out, not_44_out, not_45_out, OP4, not_46_out, not_47_out);
  and and_9 (and_9_out, not_48_out, F13, not_49_out, not_50_out, not_51_out, OP4, not_52_out, not_53_out);
  and and_10 (and_10_out, not_54_out, not_55_out, not_56_out, not_57_out, F12, not_58_out, not_59_out, OP4, not_60_out, not_61_out);
  and and_11 (and_11_out, not_62_out, not_63_out, F14, not_64_out, F12, not_65_out, not_66_out, OP4, not_67_out, not_68_out);
  and and_12 (and_12_out, F30, not_69_out, F14, not_70_out, F12, not_71_out, not_72_out, OP4, not_73_out, not_74_out);
  and and_13 (and_13_out, not_75_out, F13, not_76_out, not_77_out, not_78_out, not_79_out, not_80_out, not_81_out);
  and and_14 (and_14_out, not_82_out, F13, not_83_out, not_84_out, OP5, not_85_out, not_86_out, not_87_out);
  and and_15 (and_15_out, not_88_out, not_89_out, not_90_out, OP6, OP5, not_91_out, not_92_out, OP2);
  and and_16 (and_16_out, F14, F13, not_93_out, OP6, OP5, OP4, not_94_out, not_95_out);
  and and_17 (and_17_out, F14, F13, F12, OP6, OP5, OP4, not_96_out, not_97_out);
  and and_18 (and_18_out, F14, not_98_out, F12, not_99_out, not_100_out, not_101_out, not_102_out, not_103_out);
  and and_19 (and_19_out, not_104_out, not_105_out, F12, not_106_out, OP5, not_107_out, not_108_out, not_109_out);
  and and_20 (and_20_out, not_110_out, not_111_out, not_112_out, not_113_out, not_114_out, not_115_out, OP5, OP4, not_116_out, not_117_out);
  and and_21 (and_21_out, F30, not_118_out, not_119_out, not_120_out, not_121_out, not_122_out, OP5, OP4, not_123_out, not_124_out);
  and and_22 (and_22_out, not_125_out, not_126_out, F14, F13, F12, not_127_out, OP5, OP4, not_128_out, not_129_out);
  and and_23 (and_23_out, not_130_out, not_131_out, F14, F13, not_132_out, not_133_out, OP5, OP4, not_134_out, not_135_out);
  and and_24 (and_24_out, not_136_out, not_137_out, not_138_out, F13, not_139_out, not_140_out, OP5, OP4, not_141_out, not_142_out);
  and and_25 (and_25_out, not_143_out, not_144_out, not_145_out, F13, F12, not_146_out, OP5, OP4, not_147_out, not_148_out);
  and and_26 (and_26_out, not_149_out, not_150_out, not_151_out, not_152_out, not_153_out, OP4, not_154_out, not_155_out);
  and and_27 (and_27_out, F14, F13, F12, not_156_out, not_157_out, OP4, not_158_out, not_159_out);
  and and_28 (and_28_out, F14, F13, not_160_out, not_161_out, not_162_out, OP4, not_163_out, not_164_out);
  and and_29 (and_29_out, F14, not_165_out, not_166_out, not_167_out, not_168_out, OP4, not_169_out, not_170_out);
  and and_30 (and_30_out, not_171_out, F13, not_172_out, not_173_out, not_174_out, OP4, not_175_out, not_176_out);
  and and_31 (and_31_out, not_177_out, not_178_out, not_179_out, not_180_out, F12, not_181_out, not_182_out, OP4, not_183_out, not_184_out);
  and and_32 (and_32_out, not_185_out, not_186_out, F14, not_187_out, F12, not_188_out, not_189_out, OP4, not_190_out, not_191_out);
  and and_33 (and_33_out, F30, not_192_out, F14, not_193_out, F12, not_194_out, not_195_out, OP4, not_196_out, not_197_out);
  and and_34 (and_34_out, not_198_out, F13, not_199_out, not_200_out, not_201_out, not_202_out, not_203_out, not_204_out);
  and and_35 (and_35_out, OP6, OP5, not_205_out, OP3, OP2);
  and and_36 (and_36_out, not_206_out, not_207_out, not_208_out, OP6, OP5, not_209_out, not_210_out, OP2);
  and and_37 (and_37_out, not_211_out, not_212_out, not_213_out, not_214_out, F12, not_215_out, OP5, OP4, not_216_out, not_217_out);
  and and_38 (and_38_out, not_218_out, not_219_out, F14, not_220_out, not_221_out, not_222_out, OP5, OP4, not_223_out, not_224_out);
  and and_39 (and_39_out, F14, not_225_out, F12, not_226_out, not_227_out, not_228_out, not_229_out, not_230_out);
  and and_40 (and_40_out, not_231_out, not_232_out, OP4, not_233_out, OP2);
  and and_41 (and_41_out, not_234_out, OP5, OP4, not_235_out, OP2);
  and and_42 (and_42_out, not_236_out, not_237_out, not_238_out, not_239_out, not_240_out, OP6, OP5, OP4, not_241_out, not_242_out);
  and and_43 (and_43_out, not_243_out, not_244_out, not_245_out, OP6, OP5, OP4, not_246_out, not_247_out);
  and and_44 (and_44_out, not_248_out, F13, not_249_out, not_250_out, OP5, not_251_out, not_252_out, not_253_out);
  and and_45 (and_45_out, not_254_out, not_255_out, F12, not_256_out, OP5, not_257_out, not_258_out, not_259_out);
  and and_46 (BEQ, not_260_out, not_261_out, not_262_out, OP6, OP5, not_263_out, not_264_out, not_265_out);
  and and_47 (BNE, not_266_out, not_267_out, F12, OP6, OP5, not_268_out, not_269_out, not_270_out);
  and and_48 (JALR, not_271_out, not_272_out, not_273_out, OP6, OP5, not_274_out, not_275_out, OP2);
  and and_49 (JAL, OP6, OP5, not_276_out, OP3, OP2);
  and and_50 (half, F14, not_277_out, F12, not_278_out, not_279_out, not_280_out, not_281_out, not_282_out);
  and and_51 (and_51_out, F14, F13, not_283_out, OP6, OP5, OP4, not_284_out, not_285_out);
  and and_52 (and_52_out, F14, F13, F12, OP6, OP5, OP4, not_286_out, not_287_out);
  and and_53 (AUIPC, not_288_out, not_289_out, OP4, not_290_out, OP2);
  and and_54 (LUI, not_291_out, OP5, OP4, not_292_out, OP2);
  and and_55 (SH, not_293_out, not_294_out, F12, not_295_out, OP5, not_296_out, not_297_out, not_298_out);
  and and_56 (BLT, F14, not_299_out, not_300_out, OP6, OP5, not_301_out, not_302_out, not_303_out);
  or or_1 (MemToReg, and_1_out, and_2_out);
  or or_2 (MemWrite, and_3_out, and_4_out);
  or or_3 (ecall, and_42_out, and_43_out);
  or or_4 (S_Type, and_44_out, and_45_out);
  or or_5 (CSR, and_51_out, and_52_out);
  or or_6 (ALU_SRC, and_5_out, and_6_out, and_7_out, and_8_out, and_9_out, and_10_out, and_11_out, and_12_out, and_13_out, and_14_out, and_15_out, and_16_out, and_17_out, and_18_out, and_19_out);
  or or_7 (RegWrite, and_20_out, and_21_out, and_22_out, and_23_out, and_24_out, and_25_out, and_26_out, and_27_out, and_28_out, and_29_out, and_30_out, and_31_out, and_32_out, and_33_out, and_34_out, and_35_out, and_36_out, and_37_out, and_38_out, and_39_out, and_40_out, and_41_out);
endmodule

// ALU
module ALU (
  input  [31:0] X,
  input  [31:0] Y,
  input  [3:0] AluOP,
  output out_4,
  output Equal,
  output out_6,
  output [31:0] Result,
  output [31:0] Result_2
);

  wire [0:0] comparator_1_lt, comparator_2_lt;
  wire [31:0] adder_1_out, AND_out, divider_1_out, divider_1_rem, multiplier_1_cout, multiplier_1_out,
       NOR_out, OR_out, shifter_1_out, shifter_2_out, shifter_3_out, subtractor_1_out, XOR_out;

  assign AND_out = X & Y;  // AND_Gate AND, 32 bits wide
  assign OR_out = X | Y;  // OR_Gate OR, 32 bits wide
  Shifter #(.width(32), .shift("ll")) shifter_1 (.in(X), .\dist (Y[4:0]), .out(shifter_1_out));
  Shifter #(.width(32), .shift("ar")) shifter_2 (.in(X), .\dist (Y[4:0]), .out(shifter_2_out));
  Shifter #(.width(32), .shift("lr")) shifter_3 (.in(X), .\dist (Y[4:0]), .out(shifter_3_out));
  Multiplier #(.width(32)) multiplier_1 (.a(X), .b(Y), .out(multiplier_1_out), .cout(multiplier_1_cout));  // open: cin
  Divider #(.width(32)) divider_1 (.a(X), .b(Y), .out(divider_1_out), .rem(divider_1_rem));  // open: upper
  Adder #(.width(32)) adder_1 (.a(X), .b(Y), .out(adder_1_out));  // open: cin, cout
  Subtractor #(.width(32)) subtractor_1 (.a(X), .b(Y), .out(subtractor_1_out));  // open: bin, bout
  assign XOR_out = X ^ Y;  // XOR_Gate XOR, 32 bits wide
  assign NOR_out = ~(X | Y);  // NOR_Gate NOR, 32 bits wide
  Comparator #(.width(32), .mode("twosComplement")) comparator_1 (
    .a(X), .b(Y), .eq(Equal), .lt(comparator_1_lt[0]));  // open: gt
  Comparator #(.width(32), .mode("unsigned")) comparator_2 (.a(X), .b(Y), .lt(comparator_2_lt[0]));  // open: gt, eq
  Multiplexer #(.select(4), .width(32), .disabled("Z"), .enable("false")) multiplexer_1 (
    .in0(shifter_1_out), .in1(shifter_2_out), .in2(shifter_3_out), .in3(multiplier_1_out),
    .in4(divider_1_out), .in5(adder_1_out), .in6(subtractor_1_out), .in7(AND_out), .in8(OR_out),
    .in9(XOR_out), .in10(NOR_out), .in11({{31{1'b0}}, comparator_1_lt[0]}),
    .in12({{31{1'b0}}, comparator_2_lt[0]}), .in13({32{1'b0}}), .in14({32{1'b0}}), .in15({32{1'b0}}),
    .out(Result), .sel(AluOP));
  Multiplexer #(.select(4), .width(32), .disabled("Z"), .enable("false")) multiplexer_2 (
    .in0({32{1'b0}}), .in1({32{1'b0}}), .in2({32{1'b0}}), .in3(multiplier_1_cout), .in4(divider_1_rem),
    .in5({32{1'b0}}), .in6({32{1'b0}}), .in7({32{1'b0}}), .in8({32{1'b0}}), .in9({32{1'b0}}),
    .in10({32{1'b0}}), .in11({32{1'b0}}), .in12({32{1'b0}}), .in13({32{1'b0}}), .in14({32{1'b0}}),
    .in15({32{1'b0}}), .out(Result_2), .sel(AluOP));
  Multiplexer #(.select(4), .width(1), .disabled("Z"), .enable("false")) multiplexer_3 (
    .in0(1'b0), .in1(1'b0), .in2(1'b0), .in3(1'b0), .in4(1'b0), .in5(1'b0), .in6(1'b0), .in7(1'b0),
    .in8(1'b0), .in9(1'b0), .in10(1'b0), .in11(comparator_1_lt[0]), .in12(comparator_2_lt[0]), .in13(1'b0),
    .in14(1'b0), .in15(1'b0), .out(out_6), .sel(AluOP));
  not not_1 (out_4, out_6);

  // Other names for the same wires on the sheet: Result2[31:0] = Result_2; S[3:0] = AluOP; tunnel = out_6;
  //   tunnel_t = out_4

  // Notes on the sheet:
  //   不要改变此引脚区域内容，也不要改变ALU封装形式
  //   输入引脚
  //   输出引脚
endmodule

module Regifile (
  input  [31:0] Din,
  input  Clk,
  input  WE,
  input  [4:0] R1_num,
  input  [4:0] W_num,
  input  [4:0] R2_num,
  output [31:0] R1,
  output [31:0] R2
);

  // RegisterFile registerfile_1: pin names not known; wires that end beside it: Din, Clk, WE, W_num, R1_num, R2_num, R1, R2
endmodule

module \理想流水线  (
  output RegWrite,
  output MemWrite,
  output [31:0] IF_PC,
  output [31:0] ID_PC,
  output [31:0] EX_PC,
  output [31:0] M_PC,
  output [31:0] WB_PC,
  output [31:0] RDin,
  output [31:0] MDin,
  output [31:0] LedData
);

  wire alu_1_equal, alu_1_out_6, and_1_out, and_3_out, and_4_out, and_6_out, auipc, auipc1, auipc2, auipc3,
       B, blt, blt1, CLK, clock_1_out, comparator_1_eq, comparator_1_lt, comparator_2_eq, d_ff_1_q, ecall,
       ex_mem_1_halfout, ex_mem_1_haltout, ex_mem_1_jout, ex_mem_1_memtoregout, ex_mem_1_regwriteout, Go,
       halt, high, id_ex_1_alusrcout, id_ex_1_beqout, id_ex_1_bneout, id_ex_1_ecallout, id_ex_1_halfout,
       id_ex_1_memtoregout, id_ex_1_memwriteout, id_ex_1_regwriteout, IR1, IR2, IR3, jal, jalr, led, lui,
       lui1, lui2, lui3, mem_wb_1_halfout, mem_wb_1_highout, mem_wb_1_jout, mem_wb_1_memtoregout, nand_1_out,
       nor_1_out, not_1_out, not_2_out, not_3_out, not_4_out, not_5_out, or_1_out, or_2_out, or_3_out,
       or_4_out, RST, sh, sh1, sh2, W1, W2, W3, \单周期硬布线控制器_1_alu_src , \单周期硬布线控制器_1_beq , \单周期硬布线控制器_1_bne ,
       \单周期硬布线控制器_1_half , \单周期硬布线控制器_1_jal , \单周期硬布线控制器_1_jalr , \单周期硬布线控制器_1_memtoreg ,
       \单周期硬布线控制器_1_memwrite , \单周期硬布线控制器_1_regwrite , \单周期硬布线控制器_1_s_type , \单周期硬布线控制器_1_uret ;
  wire [1:0] priority_encoder_1_out;
  wire [3:0] id_ex_1_aluopout, \单周期硬布线控制器_1_alu_op ;
  wire [4:0] ex_mem_1_writeregout, id_ex_1_writeregout_prime, mem_wb_1_writeregout, multiplexer_2_out,
       multiplexer_3_out, multiplexer_10_out;
  wire [11:0] multiplexer_4_out;
  wire [12:0] CNT_num;
  wire [15:0] \总周期数 ;
  wire [31:0] adder_1_out, adder_2_out, adder_3_out, adder_4_out, adder_5_out, aluresult, and_2_out,
       and_7_out, and_8_out, bit_extender_1_out, bit_extender_2_out, bit_extender_3_out, bit_extender_4_out,
       bit_extender_5_out, EX_IR, ex_mem_1_aluresultout, ex_mem_1_immout, id_ex_1_imm1out_prime,
       id_ex_1_imm2out_prime, id_ex_1_imm3out_prime, id_ex_1_r1out, id_ex_1_r2out_prime, ID_IR, IF_IR, inn,
       MEM_IR, mem_wb_1_aluresultout, mem_wb_1_immout, mem_wb_1_memdataout, multiplexer_1_out,
       multiplexer_5_out, multiplexer_6_out, multiplexer_7_out, multiplexer_8_out, multiplexer_9_out,
       multiplexer_11_out, multiplexer_12_out, multiplexer_13_out, r2, regifile_1_r1, regifile_1_r2,
       shifter_2_out, shifter_3_out, shifter_4_out, shifter_5_out, u_imm, u_imm1, u_imm2, u_imm3, \use ,
       WB_IR;

  Button \u_总复位  (.out(RST));
  Button _1 (.out(IR1));
  Button _2 (.out(IR2));
  Button _3 (.out(IR3));
  // Probe on \总周期数 
  // Probe on \总周期数 
  or or_1 (or_1_out, Go, not_1_out);
  not not_1 (not_1_out, halt);
  Button \u_继续运行  (.out(Go));
  LED #(.active("true")) led_1 (.in(W1));
  LED #(.active("true")) led_2 (.in(W2));
  LED #(.active("true")) led_3 (.in(W3));
  Counter #(.width(16), .max('hffff), .ongoal("wrap"), .trigger("rising"), .behavior("new")) counter_1 (
    .count(or_1_out), .Q(\总周期数 ), .clk(CLK));  // open: load, D, carry, clr, preset, down
  Register #(.width(32), .trigger("rising"), .Select("low")) PC (
    .D(multiplexer_1_out), .en(or_2_out), .Q(IF_PC), .clk(CLK), .clr(RST));
  or or_2 (or_2_out, Go, not_2_out);
  not not_2 (not_2_out, halt);
  Hex_Digit_Display hex_digit_display_1 (.value(LedData[31:28]));  // open: dp
  // Probe on IF_PC[19:0]
  // RiscV_Probe riscv_probe_1: pin names not known; wires that end beside it: IF_IR
  Multiplexer #(.select(2), .width(32), .disabled("Z"), .enable("false")) multiplexer_1 (
    .in0(adder_1_out), .in1(adder_3_out), .in2(adder_4_out), .in3(and_2_out), .out(multiplexer_1_out),
    .sel(priority_encoder_1_out));
  Hex_Digit_Display hex_digit_display_2 (.value(LedData[27:24]));  // open: dp
  Hex_Digit_Display hex_digit_display_3 (.value(LedData[23:20]));  // open: dp
  // Probe on ID_PC[19:0]
  // RiscV_Probe riscv_probe_2: pin names not known; wires that end beside it: ID_IR
  Adder #(.width(32)) adder_1 (.a(IF_PC), .b(32'h4), .out(adder_1_out));  // open: cin, cout
  Priority_Encoder #(.select(2), .disabled("Z")) priority_encoder_1 (
    .in0(1'b1), .in1(B), .in2(jal), .in3(jalr), .out(priority_encoder_1_out));  // open: gs, en_out, en_in
  Hex_Digit_Display hex_digit_display_4 (.value(LedData[15:12]));  // open: dp
  Hex_Digit_Display hex_digit_display_5 (.value(LedData[19:16]));  // open: dp
  ROM #(.addrWidth(10), .dataWidth(32), .Select("high")) rom_1 (.addr(IF_PC[11:2]), .data(IF_IR));
  nor nor_1 (nor_1_out, Go, not_3_out);
  not not_3 (not_3_out, halt);
  Hex_Digit_Display hex_digit_display_6 (.value(LedData[11:8]));  // open: dp
  Hex_Digit_Display hex_digit_display_7 (.value(LedData[7:4]));  // open: dp
  // Probe on EX_PC[19:0]
  // RiscV_Probe riscv_probe_3: pin names not known; wires that end beside it: EX_IR
  Hex_Digit_Display hex_digit_display_8 (.value(LedData[3:0]));  // open: dp
  IF_ID if_id_1 (
    .IR(IF_IR), .PC(IF_PC), .IROUT(ID_IR), .PCOUT(ID_PC), .CLK(CLK), .RST(RST), .FLUSH(1'b0), .EN(nor_1_out));  // open: PREDICT, PREDICTOUT
  // Probe on \总周期数 
  // Probe on M_PC[19:0]
  // RiscV_Probe riscv_probe_4: pin names not known; wires that end beside it: MEM_IR
  // RiscV_Probe riscv_probe_5: pin names not known; wires that end beside it: CLK, RST, ID_IR
  // Probe on \总周期数 
  // Probe on {16{1'b0}}
  // Probe on {16{1'b0}}
  // Probe on {16{1'b0}}
  // Probe on {16{1'b0}}
  // Probe on IF_PC[11:0]
  // Probe on WB_PC[19:0]
  // RiscV_Probe riscv_probe_6: pin names not known; wires that end beside it: WB_IR
  \单周期硬布线控制器  \u_单周期硬布线控制器_1  (
    .Funct({ID_IR[30], ID_IR[25], ID_IR[14:12]}), .OP(ID_IR[6:2]), .ALU_OP(\单周期硬布线控制器_1_alu_op ),
    .MemToReg(\单周期硬布线控制器_1_memtoreg ), .MemWrite(\单周期硬布线控制器_1_memwrite ), .ALU_SRC(\单周期硬布线控制器_1_alu_src ),
    .RegWrite(\单周期硬布线控制器_1_regwrite ), .ecall(ecall), .S_type(\单周期硬布线控制器_1_s_type ),
    .Jalr(\单周期硬布线控制器_1_jalr ), .Beq(\单周期硬布线控制器_1_beq ), .JAL(\单周期硬布线控制器_1_jal ), .Bne(\单周期硬布线控制器_1_bne ),
    .in_3(ID_IR[21]), .uret(\单周期硬布线控制器_1_uret ), .half(\单周期硬布线控制器_1_half ), .blt(blt1), .sh(sh1),
    .auipc(auipc1), .lui(lui1));  // open: CSR
  Multiplexer #(.select(1), .width(5), .disabled("Z"), .enable("false")) multiplexer_2 (
    .in0(ID_IR[19:15]), .in1(5'b10001), .out(multiplexer_2_out), .sel(ecall));
  assign bit_extender_1_out = {{12{ID_IR[31]}}, ID_IR[31:12]};  // Bit_Extender bit_extender_1
  // Probe on EX_PC[11:0]
  // Probe on ID_PC[11:0]
  Multiplexer #(.select(1), .width(5), .disabled("Z"), .enable("false")) multiplexer_3 (
    .in0(ID_IR[24:20]), .in1(5'b01010), .out(multiplexer_3_out), .sel(ecall));
  Multiplexer #(.select(1), .width(12), .disabled("Z"), .enable("false")) multiplexer_4 (
    .in0(ID_IR[31:20]), .in1({ID_IR[31:25], ID_IR[11:7]}), .out(multiplexer_4_out), .sel(\单周期硬布线控制器_1_s_type ));
  Shifter #(.width(32), .shift("ll")) shifter_1 (.in(bit_extender_1_out), .\dist (5'b01100), .out(u_imm1));
  assign bit_extender_2_out = {{20{ID_IR[31]}}, {ID_IR[31], ID_IR[7], ID_IR[30:25], ID_IR[11:8]}};  // Bit_Extender bit_extender_2
  assign bit_extender_3_out = {{12{ID_IR[31]}}, {ID_IR[31], ID_IR[19:12], ID_IR[20], ID_IR[30:21]}};  // Bit_Extender bit_extender_3
  // Probe on M_PC[11:0]
  D_Flip_Flop #(.trigger("high"), .Pre_Clr_Positions("LEGACY"), .NegatePresetClear("false"), .enable("true"), .NewFFLayout("false")) d_ff_1 (.Q(d_ff_1_q));  // open: clk, D, Qn, preset, en, reset
  // Probe on 13'hc
  // Probe on WB_PC[11:0]
  Comparator #(.width(13), .mode("twosComplement")) comparator_1 (
    .a(CNT_num), .b(13'hc), .eq(comparator_1_eq), .lt(comparator_1_lt));  // open: gt
  Clock #(.highDuration(1), .lowDuration(1)) clock_1 (.out(clock_1_out));
  Regifile regifile_1 (
    .Din(RDin), .Clk(CLK), .R1(regifile_1_r1), .R2(regifile_1_r2), .WE(RegWrite),
    .W_num(mem_wb_1_writeregout), .R1_num(multiplexer_2_out), .R2_num(multiplexer_3_out));
  assign bit_extender_4_out = {{20{multiplexer_4_out[11]}}, multiplexer_4_out};  // Bit_Extender bit_extender_4
  nand nand_1 (nand_1_out, d_ff_1_q, comparator_1_eq);
  Counter #(.width(13), .max('h1fff), .ongoal("stay"), .trigger("rising"), .behavior("old")) counter_2 (
    .count(comparator_1_lt), .Q(CNT_num), .clk(clock_1_out));  // open: load, D, carry, clr, preset
  assign CLK = nand_1_out ? clock_1_out : 1'bz;  // Controlled_Buffer controlled_buffer_1
  Pull_Resistor #(.pull(1)) pull_resistor_1 (.node(CLK));
  ID_EX id_ex_1 (
    .JAL(\单周期硬布线控制器_1_jal ), .JALR(\单周期硬布线控制器_1_jalr ), .URET(\单周期硬布线控制器_1_uret ), .beq(\单周期硬布线控制器_1_beq ),
    .MEMTOREG(\单周期硬布线控制器_1_memtoreg ), .MEMWRITE(\单周期硬布线控制器_1_memwrite ), .ALUSRC(\单周期硬布线控制器_1_alu_src ),
    .R1(regifile_1_r1), .R2(regifile_1_r2), .PC(ID_PC), .IMM1(bit_extender_4_out), .IMM2(bit_extender_2_out),
    .IMM3(bit_extender_3_out), .JALOUT(jal), .JALROUT(jalr), .BEQOUT(id_ex_1_beqout),
    .MEMTOREGOUT(id_ex_1_memtoregout), .MEMWRITEOUT(id_ex_1_memwriteout), .ALUSRCOUT(id_ex_1_alusrcout),
    .R1OUT(id_ex_1_r1out), .R2OUT_prime(id_ex_1_r2out_prime), .PCOUT_prime(EX_PC),
    .IMM1OUT_prime(id_ex_1_imm1out_prime), .IMM2OUT_prime(id_ex_1_imm2out_prime),
    .IMM3OUT_prime(id_ex_1_imm3out_prime), .CLK(CLK), .RST(RST), .BNE(\单周期硬布线控制器_1_bne ),
    .BNEOUT(id_ex_1_bneout), .ALUOP(\单周期硬布线控制器_1_alu_op ), .ALUOPOUT(id_ex_1_aluopout),
    .REGWRITE(\单周期硬布线控制器_1_regwrite ), .REGWRITEOUT(id_ex_1_regwriteout), .half(\单周期硬布线控制器_1_half ),
    .halfOUT(id_ex_1_halfout), .ECALL(ecall), .ECALLOUT(id_ex_1_ecallout), .WRITEREG(ID_IR[11:7]),
    .WRITEREGOUT_prime(id_ex_1_writeregout_prime), .IR(ID_IR), .IROUT_prime(EX_IR), .FLUSH(1'b0),
    .EN(nor_1_out));  // open: URETOUT, R1F, R1FOUT, R2F, R2FOUT, CSR, CSROUT, PREDICT, PREDICTOUT
  ID_EX_ccab id_ex_ccab_1 (
    .c1(sh1), .c2(blt1), .b1(auipc1), .a1(lui1), .c1out(sh2), .c2out(blt), .b1out(auipc2), .a1out(lui2),
    .CLK(CLK), .flush(1'b0), .en(nor_1_out));  // open: RST
  Register #(.width(32), .trigger("rising"), .Select("low")) register_1 (
    .D(u_imm1), .en(nor_1_out), .Q(u_imm2), .clk(CLK));  // open: clr
  or or_3 (or_3_out, jal, jalr);
  Comparator #(.width(32), .mode("twosComplement")) comparator_2 (
    .a(32'h22), .b(id_ex_1_r1out), .eq(comparator_2_eq));  // open: gt, lt
  Multiplexer #(.select(1), .width(32), .disabled("Z"), .enable("false")) multiplexer_5 (
    .in0(id_ex_1_r2out_prime), .in1(id_ex_1_imm1out_prime), .out(multiplexer_5_out), .sel(id_ex_1_alusrcout));
  Adder #(.width(32)) adder_2 (.a(EX_PC), .b(32'h4), .out(adder_2_out));  // open: cin, cout
  Shifter #(.width(32), .shift("ll")) shifter_2 (.in(id_ex_1_imm2out_prime), .\dist (5'b00001), .out(shifter_2_out));
  Shifter #(.width(32), .shift("ll")) shifter_3 (.in(id_ex_1_imm3out_prime), .\dist (5'b00001), .out(shifter_3_out));
  not not_4 (not_4_out, alu_1_equal);
  and and_1 (and_1_out, blt, alu_1_out_6);
  ALU alu_1 (
    .X(id_ex_1_r1out), .Y(multiplexer_5_out), .AluOP(id_ex_1_aluopout), .Equal(alu_1_equal),
    .Result(aluresult), .out_6(alu_1_out_6));  // open: Result_2, out_4
  Adder #(.width(32)) adder_3 (.a(shifter_2_out), .b(EX_PC), .out(adder_3_out));  // open: cin, cout
  Adder #(.width(32)) adder_4 (.a(shifter_3_out), .b(EX_PC), .out(adder_4_out));  // open: cin, cout
  assign and_2_out = aluresult & 32'hfffffffe;  // AND_Gate and_2, 32 bits wide
  and and_3 (and_3_out, alu_1_equal, id_ex_1_beqout);
  and and_4 (and_4_out, not_4_out, id_ex_1_bneout);
  or or_4 (or_4_out, and_3_out, and_4_out);
  and and_5 (led, id_ex_1_ecallout, comparator_2_eq);
  Multiplexer #(.select(1), .width(32), .disabled("Z"), .enable("false")) multiplexer_6 (
    .in0({32{1'b0}}), .in1(id_ex_1_r2out_prime), .out(multiplexer_6_out), .sel(led));
  Register #(.width(32), .trigger("rising"), .Select("low")) register_2 (
    .D(multiplexer_6_out), .en(led), .Q(LedData), .clk(CLK));  // open: clr
  or or_5 (B, or_4_out, and_1_out);
  and and_6 (and_6_out, id_ex_1_ecallout, not_5_out);
  not not_5 (not_5_out, comparator_2_eq);
  EX_MEM ex_mem_1 (
    .MEMTOREGWRITE(id_ex_1_memtoregout), .HALF(id_ex_1_halfout), .ALURESULT(aluresult),
    .WRITEDATA(id_ex_1_r2out_prime), .MEMTOREGOUT(ex_mem_1_memtoregout), .HALFOUT(ex_mem_1_halfout),
    .ALURESULTOUT({ex_mem_1_aluresultout[31:2], high, ex_mem_1_aluresultout[0]}), .WRITEDATAOUT(r2),
    .CLK(CLK), .RST(RST), .MEMWRITE(id_ex_1_memwriteout), .MEMWRITEOUT(MemWrite), .J(or_3_out),
    .JOUT(ex_mem_1_jout), .REGWRITEOUT(ex_mem_1_regwriteout), .REGWRITE(id_ex_1_regwriteout),
    .WRITEREG(id_ex_1_writeregout_prime), .WRITEREGOUT(ex_mem_1_writeregout), .PC(EX_PC), .PCOUT(M_PC),
    .IR(EX_IR), .IROUT(MEM_IR), .IMM(adder_2_out), .IMMOUT(ex_mem_1_immout), .HALT(and_6_out),
    .HALTOUT(ex_mem_1_haltout), .FLUSH(1'b0), .EN(nor_1_out));
  ID_EX_ccab id_ex_ccab_2 (
    .c1(sh2), .b1(auipc2), .a1(lui2), .c1out(sh), .b1out(auipc3), .a1out(lui3), .CLK(CLK), .flush(1'b0),
    .en(nor_1_out));  // open: c2, c2out, RST
  Register #(.width(32), .trigger("rising"), .Select("low")) register_3 (
    .D(u_imm2), .en(nor_1_out), .Q(u_imm3), .clk(CLK));  // open: clr
  RAM #(.addrWidth(10), .dataWidth(32), .bus("separate"), .Select("high")) ram_1 (
    .addr(ex_mem_1_aluresultout[11:2]), .din(MDin), .data(\use ), .str(MemWrite), .clk(CLK), .ld(1'b1));  // open: sel, clr
  MEM_WB mem_wb_1 (
    .MEMTOREG(ex_mem_1_memtoregout),
    .ALURESULT({ex_mem_1_aluresultout[31:2], high, ex_mem_1_aluresultout[0]}), .MEMDATA(\use ),
    .MEMTOREGOUT(mem_wb_1_memtoregout), .ALURESULTOUT(mem_wb_1_aluresultout),
    .MEMDATAOUT(mem_wb_1_memdataout), .in_1(CLK), .in_2(RST), .HALF(ex_mem_1_halfout),
    .HALFOUT(mem_wb_1_halfout), .J(ex_mem_1_jout), .JOUT(mem_wb_1_jout), .WRITEREG(ex_mem_1_writeregout),
    .WRITEREGOUT(mem_wb_1_writeregout), .REGWRITE(ex_mem_1_regwriteout), .REGWRITEOUT(RegWrite), .PC(M_PC),
    .PCOUT(WB_PC), .IR(MEM_IR), .IROUT(WB_IR), .IMM(ex_mem_1_immout), .IMMOUT(mem_wb_1_immout),
    .HALT(ex_mem_1_haltout), .HALTOUT(halt), .HIGH(high), .HIGHOUT(mem_wb_1_highout), .FLUSH(1'b0),
    .EN(nor_1_out));
  ID_EX_ccab id_ex_ccab_3 (
    .b1(auipc3), .a1(lui3), .b1out(auipc), .a1out(lui), .CLK(CLK), .flush(1'b0), .en(nor_1_out));  // open: c1, c2, c1out, c2out, RST
  Register #(.width(32), .trigger("rising"), .Select("low")) register_4 (
    .D(u_imm3), .en(nor_1_out), .Q(u_imm), .clk(CLK));  // open: clr
  Multiplexer #(.select(1), .width(32), .disabled("Z"), .enable("false")) multiplexer_7 (
    .in0(mem_wb_1_aluresultout), .in1(mem_wb_1_memdataout), .out(multiplexer_7_out),
    .sel(mem_wb_1_memtoregout));
  Shifter #(.width(32), .shift("lr")) shifter_4 (.in(multiplexer_7_out), .\dist (5'b10000), .out(shifter_4_out));
  Multiplexer #(.select(1), .width(32), .disabled("Z"), .enable("false")) multiplexer_8 (
    .in0(32'hffff0000), .in1(32'hffff), .out(multiplexer_8_out), .sel(high));
  Multiplexer #(.select(1), .width(32), .disabled("Z"), .enable("false")) multiplexer_9 (
    .in0(multiplexer_7_out), .in1(shifter_4_out), .out(multiplexer_9_out), .sel(mem_wb_1_highout));
  assign bit_extender_5_out = {{16{1'b0}}, r2[15:0]};  // Bit_Extender bit_extender_5
  Multiplexer #(.select(1), .width(5), .disabled("Z"), .enable("false")) multiplexer_10 (
    .in0({5{1'b0}}), .in1(5'b10000), .out(multiplexer_10_out), .sel(high));
  assign and_7_out = \use  & multiplexer_8_out;  // AND_Gate and_7, 32 bits wide
  Shifter #(.width(32), .shift("ll")) shifter_5 (
    .in(bit_extender_5_out), .\dist (multiplexer_10_out), .out(shifter_5_out));
  Multiplexer #(.select(1), .width(32), .disabled("Z"), .enable("false")) multiplexer_11 (
    .in0(multiplexer_7_out), .in1(and_8_out), .out(multiplexer_11_out), .sel(mem_wb_1_halfout));
  assign and_8_out = multiplexer_9_out & 32'hffff;  // AND_Gate and_8, 32 bits wide
  assign inn = shifter_5_out | and_7_out;  // OR_Gate or_6, 32 bits wide
  Multiplexer #(.select(1), .width(32), .disabled("Z"), .enable("false")) multiplexer_12 (
    .in0(multiplexer_11_out), .in1(mem_wb_1_immout), .out(multiplexer_12_out), .sel(mem_wb_1_jout));
  Adder #(.width(32)) adder_5 (.a(WB_PC), .b(u_imm), .out(adder_5_out));  // open: cin, cout
  Multiplexer #(.select(1), .width(32), .disabled("Z"), .enable("false")) multiplexer_13 (
    .in0(multiplexer_12_out), .in1(adder_5_out), .out(multiplexer_13_out), .sel(auipc));
  Multiplexer #(.select(1), .width(32), .disabled("Z"), .enable("false")) multiplexer_14 (
    .in0(r2), .in1(inn), .out(MDin), .sel(sh));
  Multiplexer #(.select(1), .width(32), .disabled("Z"), .enable("false")) multiplexer_15 (
    .in0(multiplexer_13_out), .in1(u_imm), .out(RDin), .sel(lui));

  // Other names for the same wires on the sheet: WRITEREG[4:0] = ID_IR[11:7]; MEM_PC[31:0] = M_PC

  // Notes on the sheet:
  //   中断源
  //   时空图监测，可删除
  //   中断等待指示
  //   指令存储器
  //   PC+4
  //   数码管输出
  //   contents of rom_1 (hex, n*v repeats v):
  //   13 430497 900533 2200893 73 430497 900533 2200893 73 430497 900533 2200893 73 430497 900533 2200893
  //   73 430497 900533 2200893 73 430497 900533 2200893 73 430497 900533 2200893 73 430497 900533 2200893
  //   73 a00893 73
  //   指令探针
  //   指令字
  //   JAL
  //   JALR
  //   URET
  //   I型指令
  //   s型指令
  //   B型指令
  //   J型指令
  //   Beq
  //   Bne
  //   MemToReg
  //   MemWrite
  //   AluOP
  //   AluSrcB
  //   RegWrite
  //   half
  //   控制位
  //   imm
  //   流水调试日志用
  //   暂停节拍，不能为0
  //   可计数暂停的时钟源
  //   用这个时钟源需要去掉电路中的其他时钟源
  //   为方便自动评测，需要输出流水线各段保存的PC值，注意是PC不是PC+4，另外ID段寄存器写入信息，Mem段内存写入信息也要输出
  //   戳工具置1进入计数暂停模式，ctrl+k时钟自动运行到对应节拍暂停
  //   ctrl+k关闭时钟连续运行，将控制位置零，进入单步调试模式调试
  //   PC+4
  //   BEQ/BNE
  //   JAL
  //   JALR
  //   数据存储器
endmodule

module \气泡流水线  (
  output RegWrite,
  output MemWrite,
  output [31:0] IF_PC,
  output [31:0] ID_PC,
  output [31:0] EX_PC,
  output [31:0] M_PC,
  output [31:0] WB_PC,
  output [31:0] RDin,
  output [31:0] MDin,
  output [31:0] LedData
);

  wire alu_1_equal, alu_1_out_6, and_1_out, and_2_out, and_3_out, and_5_out, and_6_out, and_8_out, and_9_out,
       auipc, auipc1, auipc2, auipc3, B, blt, blt1, BRANCHTAKEN, CLK, clock_1_out, comparator_1_eq,
       comparator_1_lt, comparator_2_eq, d_ff_1_q, DATAHAZZARD, ex_mem_1_halfout, ex_mem_1_haltout,
       ex_mem_1_jout, ex_mem_1_memtoregout, EX_REGWRITE, Go, halt, high, id_ex_1_alusrcout, id_ex_1_beqout,
       id_ex_1_bneout, id_ex_1_ecallout, id_ex_1_halfout, id_ex_1_memtoregout, id_ex_1_memwriteout, IR1, IR2,
       IR3, jal, jalr, led, lui, lui1, lui2, lui3, MEM_REGWRITE, mem_wb_1_halfout, mem_wb_1_highout,
       mem_wb_1_jout, mem_wb_1_memtoregout, nand_1_out, not_1_out, not_2_out, not_3_out, not_4_out,
       not_5_out, not_6_out, not_7_out, or_1_out, or_2_out, or_4_out, or_5_out, or_6_out, or_7_out, or_8_out,
       or_9_out, RST, sh, sh1, sh2, W1, W2, W3, \单周期硬布线控制器_1_alu_src , \单周期硬布线控制器_1_beq , \单周期硬布线控制器_1_bne ,
       \单周期硬布线控制器_1_ecall , \单周期硬布线控制器_1_half , \单周期硬布线控制器_1_jal , \单周期硬布线控制器_1_jalr ,
       \单周期硬布线控制器_1_memtoreg , \单周期硬布线控制器_1_memwrite , \单周期硬布线控制器_1_regwrite , \单周期硬布线控制器_1_s_type ,
       \单周期硬布线控制器_1_uret ;
  wire [1:0] priority_encoder_1_out;
  wire [3:0] id_ex_1_aluopout, \单周期硬布线控制器_1_alu_op ;
  wire [4:0] EX_WRITEREG, mem_wb_1_writeregout, MEM_WRITEREG, multiplexer_2_out, multiplexer_4_out,
       multiplexer_10_out;
  wire [11:0] multiplexer_3_out;
  wire [12:0] CNT_num;
  wire [15:0] \总周期数 , \插入气泡数 , \无条件分支数 , \条件分支成功数 ;
  wire [31:0] adder_1_out, adder_2_out, adder_3_out, adder_4_out, adder_5_out, aluresult, and_4_out,
       and_10_out, and_11_out, bit_extender_1_out, bit_extender_2_out, bit_extender_3_out,
       bit_extender_4_out, bit_extender_5_out, EX_IR, ex_mem_1_aluresultout, ex_mem_1_immout,
       id_ex_1_imm1out_prime, id_ex_1_imm2out_prime, id_ex_1_imm3out_prime, id_ex_1_r1out,
       id_ex_1_r2out_prime, ID_IR, IF_IR, inn, MEM_IR, mem_wb_1_aluresultout, mem_wb_1_immout,
       mem_wb_1_memdataout, multiplexer_1_out, multiplexer_5_out, multiplexer_6_out, multiplexer_7_out,
       multiplexer_8_out, multiplexer_9_out, multiplexer_11_out, multiplexer_12_out, multiplexer_13_out,
       multiplexer_14_out, r2, \regifile_气泡_1_r1 , \regifile_气泡_1_r2 , shifter_2_out, shifter_3_out,
       shifter_4_out, shifter_5_out, u_imm, u_imm1, u_imm2, u_imm3, \use , WB_IR;

  Button \u_总复位  (.out(RST));
  Button _1 (.out(IR1));
  Button _2 (.out(IR2));
  Button _3 (.out(IR3));
  // Probe on \总周期数 
  // Probe on \总周期数 
  Button \u_继续运行  (.out(Go));
  LED #(.active("true")) led_1 (.in(W1));
  LED #(.active("true")) led_2 (.in(W2));
  LED #(.active("true")) led_3 (.in(W3));
  or or_1 (or_1_out, Go, not_1_out);
  not not_1 (not_1_out, halt);
  and and_1 (and_1_out, ~DATAHAZZARD, or_2_out);  // AND_Gate
  or or_2 (or_2_out, Go, not_2_out);
  Hex_Digit_Display hex_digit_display_1 (.value(LedData[31:28]));  // open: dp
  // Probe on IF_PC[19:0]
  // RiscV_Probe riscv_probe_1: pin names not known; wires that end beside it: IF_IR
  Counter #(.width(16), .max('hffff), .ongoal("wrap"), .trigger("rising"), .behavior("new")) counter_1 (
    .count(or_1_out), .Q(\总周期数 ), .clk(CLK), .clr(RST));  // open: load, D, carry, preset, down
  Register #(.width(32), .trigger("rising"), .Select("low")) PC (
    .D(multiplexer_1_out), .en(and_1_out), .Q(IF_PC), .clk(CLK), .clr(RST));
  not not_2 (not_2_out, halt);
  Hex_Digit_Display hex_digit_display_2 (.value(LedData[23:20]));  // open: dp
  Hex_Digit_Display hex_digit_display_3 (.value(LedData[27:24]));  // open: dp
  // Probe on ID_PC[19:0]
  // RiscV_Probe riscv_probe_2: pin names not known; wires that end beside it: ID_IR
  Multiplexer #(.select(2), .width(32), .disabled("Z"), .enable("false")) multiplexer_1 (
    .in0(adder_1_out), .in1(adder_3_out), .in2(adder_4_out), .in3(and_4_out), .out(multiplexer_1_out),
    .sel(priority_encoder_1_out));
  Priority_Encoder #(.select(2), .disabled("Z")) priority_encoder_1 (
    .in0(1'b1), .in1(B), .in2(jal), .in3(jalr), .out(priority_encoder_1_out));  // open: gs, en_out, en_in
  Hex_Digit_Display hex_digit_display_4 (.value(LedData[15:12]));  // open: dp
  Hex_Digit_Display hex_digit_display_5 (.value(LedData[19:16]));  // open: dp
  Adder #(.width(32)) adder_1 (.a(IF_PC), .b(32'h4), .out(adder_1_out));  // open: cin, cout
  or or_3 (BRANCHTAKEN, B, jal, jalr);
  Hex_Digit_Display hex_digit_display_6 (.value(LedData[11:8]));  // open: dp
  Hex_Digit_Display hex_digit_display_7 (.value(LedData[7:4]));  // open: dp
  // Probe on EX_PC[19:0]
  // RiscV_Probe riscv_probe_3: pin names not known; wires that end beside it: EX_IR
  \中断按键参考电路  \u_中断按键参考电路_1  ();  // open: 与中断屏蔽位与, 同步清零信号
  ROM #(.addrWidth(10), .dataWidth(32), .Select("high")) rom_1 (.addr(IF_PC[11:2]), .data(IF_IR));
  \冲突检测逻辑_气泡  \u_冲突检测逻辑_气泡_1  (
    .MEM_REGWRITE(MEM_REGWRITE), .EX_REGWRITE(EX_REGWRITE), .EX_WRITEREG(EX_WRITEREG),
    .MEM_WRITEREG(MEM_WRITEREG), .ID_IR(ID_IR), .STALL(DATAHAZZARD));
  Hex_Digit_Display hex_digit_display_8 (.value(LedData[3:0]));  // open: dp
  // Probe on \总周期数 
  // Probe on M_PC[19:0]
  // RiscV_Probe riscv_probe_4: pin names not known; wires that end beside it: MEM_IR
  IF_ID if_id_1 (
    .IR(IF_IR), .PC(IF_PC), .IROUT(ID_IR), .PCOUT(ID_PC), .CLK(CLK), .RST(RST), .FLUSH(BRANCHTAKEN),
    .EN(or_4_out));  // open: PREDICT, PREDICTOUT
  or or_4 (or_4_out, DATAHAZZARD, and_2_out);
  and and_2 (and_2_out, halt, ~Go);  // AND_Gate
  // Probe on \总周期数 
  // Probe on \无条件分支数 
  // Probe on \条件分支成功数 
  // Probe on \插入气泡数 
  // Probe on {16{1'b0}}
  // RiscV_Probe riscv_probe_5: pin names not known; wires that end beside it: CLK, RST, ID_IR, blt1
  // Probe on IF_PC[11:0]
  // Probe on WB_PC[19:0]
  // RiscV_Probe riscv_probe_6: pin names not known; wires that end beside it: WB_IR
  Counter #(.width(16), .max('hffff), .ongoal("wrap"), .trigger("rising"), .behavior("new")) counter_2 (
    .count(DATAHAZZARD), .Q(\插入气泡数 ), .clk(CLK), .clr(RST));  // open: load, D, carry, preset, down
  // Probe on ID_PC[11:0]
  // Probe on EX_PC[11:0]
  \单周期硬布线控制器  \u_单周期硬布线控制器_1  (
    .Funct({ID_IR[30], ID_IR[25], ID_IR[14:12]}), .OP(ID_IR[6:2]), .ALU_OP(\单周期硬布线控制器_1_alu_op ),
    .MemToReg(\单周期硬布线控制器_1_memtoreg ), .MemWrite(\单周期硬布线控制器_1_memwrite ), .ALU_SRC(\单周期硬布线控制器_1_alu_src ),
    .RegWrite(\单周期硬布线控制器_1_regwrite ), .ecall(\单周期硬布线控制器_1_ecall ), .S_type(\单周期硬布线控制器_1_s_type ),
    .Jalr(\单周期硬布线控制器_1_jalr ), .Beq(\单周期硬布线控制器_1_beq ), .JAL(\单周期硬布线控制器_1_jal ), .Bne(\单周期硬布线控制器_1_bne ),
    .in_3(ID_IR[21]), .uret(\单周期硬布线控制器_1_uret ), .half(\单周期硬布线控制器_1_half ), .blt(blt1), .sh(sh1),
    .auipc(auipc1), .lui(lui1));  // open: CSR
  Multiplexer #(.select(1), .width(5), .disabled("Z"), .enable("false")) multiplexer_2 (
    .in0(ID_IR[19:15]), .in1(5'b10001), .out(multiplexer_2_out), .sel(\单周期硬布线控制器_1_ecall ));
  Multiplexer #(.select(1), .width(12), .disabled("Z"), .enable("false")) multiplexer_3 (
    .in0(ID_IR[31:20]), .in1({ID_IR[31:25], ID_IR[11:7]}), .out(multiplexer_3_out), .sel(\单周期硬布线控制器_1_s_type ));
  assign bit_extender_1_out = {{12{ID_IR[31]}}, ID_IR[31:12]};  // Bit_Extender bit_extender_1
  // Probe on M_PC[11:0]
  D_Flip_Flop #(.trigger("high"), .Pre_Clr_Positions("LEGACY"), .NegatePresetClear("false"), .enable("true"), .NewFFLayout("false")) d_ff_1 (.Q(d_ff_1_q));  // open: clk, D, Qn, preset, en, reset
  // Probe on 13'hc
  Multiplexer #(.select(1), .width(5), .disabled("Z"), .enable("false")) multiplexer_4 (
    .in0(ID_IR[24:20]), .in1(5'b01010), .out(multiplexer_4_out), .sel(\单周期硬布线控制器_1_ecall ));
  Shifter #(.width(32), .shift("ll")) shifter_1 (.in(bit_extender_1_out), .\dist (5'b01100), .out(u_imm1));
  assign bit_extender_2_out = {{20{ID_IR[31]}}, {ID_IR[31], ID_IR[7], ID_IR[30:25], ID_IR[11:8]}};  // Bit_Extender bit_extender_2
  assign bit_extender_3_out = {{12{ID_IR[31]}}, {ID_IR[31], ID_IR[19:12], ID_IR[20], ID_IR[30:21]}};  // Bit_Extender bit_extender_3
  // Probe on WB_PC[11:0]
  Comparator #(.width(13), .mode("twosComplement")) comparator_1 (
    .a(CNT_num), .b(13'hc), .eq(comparator_1_eq), .lt(comparator_1_lt));  // open: gt
  Clock #(.highDuration(1), .lowDuration(1)) clock_1 (.out(clock_1_out));
  assign bit_extender_4_out = {{20{multiplexer_3_out[11]}}, multiplexer_3_out};  // Bit_Extender bit_extender_4
  nand nand_1 (nand_1_out, d_ff_1_q, comparator_1_eq);
  Counter #(.width(13), .max('h1fff), .ongoal("stay"), .trigger("rising"), .behavior("old")) counter_3 (
    .count(comparator_1_lt), .Q(CNT_num), .clk(clock_1_out));  // open: load, D, carry, clr, preset
  \regifile_气泡  \regifile_气泡_1  (
    .Din(RDin), .Clk(CLK), .R1(\regifile_气泡_1_r1 ), .R2(\regifile_气泡_1_r2 ), .WE(RegWrite),
    .W_num(mem_wb_1_writeregout), .R1_num(multiplexer_2_out), .R2_num(multiplexer_4_out));
  assign CLK = nand_1_out ? clock_1_out : 1'bz;  // Controlled_Buffer controlled_buffer_1
  Pull_Resistor #(.pull(1)) pull_resistor_1 (.node(CLK));
  ID_EX id_ex_1 (
    .JAL(\单周期硬布线控制器_1_jal ), .JALR(\单周期硬布线控制器_1_jalr ), .URET(\单周期硬布线控制器_1_uret ), .beq(\单周期硬布线控制器_1_beq ),
    .MEMTOREG(\单周期硬布线控制器_1_memtoreg ), .MEMWRITE(\单周期硬布线控制器_1_memwrite ), .ALUSRC(\单周期硬布线控制器_1_alu_src ),
    .R1(\regifile_气泡_1_r1 ), .R2(\regifile_气泡_1_r2 ), .PC(ID_PC), .IMM1(bit_extender_4_out),
    .IMM2(bit_extender_2_out), .IMM3(bit_extender_3_out), .JALOUT(jal), .JALROUT(jalr),
    .BEQOUT(id_ex_1_beqout), .MEMTOREGOUT(id_ex_1_memtoregout), .MEMWRITEOUT(id_ex_1_memwriteout),
    .ALUSRCOUT(id_ex_1_alusrcout), .R1OUT(id_ex_1_r1out), .R2OUT_prime(id_ex_1_r2out_prime),
    .PCOUT_prime(EX_PC), .IMM1OUT_prime(id_ex_1_imm1out_prime), .IMM2OUT_prime(id_ex_1_imm2out_prime),
    .IMM3OUT_prime(id_ex_1_imm3out_prime), .CLK(CLK), .RST(RST), .BNE(\单周期硬布线控制器_1_bne ),
    .BNEOUT(id_ex_1_bneout), .ALUOP(\单周期硬布线控制器_1_alu_op ), .ALUOPOUT(id_ex_1_aluopout),
    .REGWRITE(\单周期硬布线控制器_1_regwrite ), .REGWRITEOUT(EX_REGWRITE), .half(\单周期硬布线控制器_1_half ),
    .halfOUT(id_ex_1_halfout), .ECALL(\单周期硬布线控制器_1_ecall ), .ECALLOUT(id_ex_1_ecallout),
    .WRITEREG(ID_IR[11:7]), .WRITEREGOUT_prime(EX_WRITEREG), .IR(ID_IR), .IROUT_prime(EX_IR),
    .FLUSH(or_5_out), .EN(and_3_out));  // open: URETOUT, R1F, R1FOUT, R2F, R2FOUT, CSR, CSROUT, PREDICT, PREDICTOUT
  or or_5 (or_5_out, BRANCHTAKEN, DATAHAZZARD);
  Multiplexer #(.select(1), .width(32), .disabled("Z"), .enable("false")) multiplexer_5 (
    .in0(u_imm1), .in1({32{1'b0}}), .out(multiplexer_5_out), .sel(or_5_out));
  and and_3 (and_3_out, halt, ~Go);  // AND_Gate
  ID_EX_ccab id_ex_ccab_1 (
    .c1(sh1), .c2(blt1), .b1(auipc1), .a1(lui1), .c1out(sh2), .c2out(blt), .b1out(auipc2), .a1out(lui2),
    .CLK(CLK), .RST(RST), .flush(or_5_out), .en(and_3_out));
  Register #(.width(32), .trigger("rising"), .Select("low")) register_1 (
    .D(multiplexer_5_out), .en(not_3_out), .Q(u_imm2), .clk(CLK), .clr(RST));
  not not_3 (not_3_out, and_3_out);
  or or_6 (or_6_out, RST, or_7_out);
  or or_7 (or_7_out, jal, jalr);
  Shifter #(.width(32), .shift("ll")) shifter_2 (.in(id_ex_1_imm2out_prime), .\dist (5'b00001), .out(shifter_2_out));
  Shifter #(.width(32), .shift("ll")) shifter_3 (.in(id_ex_1_imm3out_prime), .\dist (5'b00001), .out(shifter_3_out));
  Counter #(.width(16), .max('hffff), .ongoal("wrap"), .trigger("rising"), .behavior("new")) counter_4 (
    .count(or_6_out), .Q(\无条件分支数 ), .clk(CLK), .clr(RST));  // open: load, D, carry, preset, down
  Comparator #(.width(32), .mode("twosComplement")) comparator_2 (
    .a(32'h22), .b(id_ex_1_r1out), .eq(comparator_2_eq));  // open: gt, lt
  Multiplexer #(.select(1), .width(32), .disabled("Z"), .enable("false")) multiplexer_6 (
    .in0(id_ex_1_r2out_prime), .in1(id_ex_1_imm1out_prime), .out(multiplexer_6_out), .sel(id_ex_1_alusrcout));
  Adder #(.width(32)) adder_2 (.a(EX_PC), .b(32'h4), .out(adder_2_out));  // open: cin, cout
  Adder #(.width(32)) adder_3 (.a(shifter_2_out), .b(EX_PC), .out(adder_3_out));  // open: cin, cout
  Adder #(.width(32)) adder_4 (.a(shifter_3_out), .b(EX_PC), .out(adder_4_out));  // open: cin, cout
  assign and_4_out = aluresult & 32'hfffffffe;  // AND_Gate and_4, 32 bits wide
  not not_4 (not_4_out, alu_1_equal);
  ALU alu_1 (
    .X(id_ex_1_r1out), .Y(multiplexer_6_out), .AluOP(id_ex_1_aluopout), .Equal(alu_1_equal),
    .Result(aluresult), .out_6(alu_1_out_6));  // open: Result_2, out_4
  and and_5 (and_5_out, alu_1_equal, id_ex_1_beqout);
  and and_6 (and_6_out, not_4_out, id_ex_1_bneout);
  Multiplexer #(.select(1), .width(32), .disabled("Z"), .enable("false")) multiplexer_7 (
    .in0({32{1'b0}}), .in1(id_ex_1_r2out_prime), .out(multiplexer_7_out), .sel(led));
  or or_8 (or_8_out, RST, B);
  or or_9 (or_9_out, and_5_out, and_6_out);
  or or_10 (B, or_9_out, alu_1_out_6);
  and and_7 (led, id_ex_1_ecallout, comparator_2_eq);
  Register #(.width(32), .trigger("rising"), .Select("low")) register_2 (
    .D(multiplexer_7_out), .en(led), .Q(LedData), .clk(CLK));  // open: clr
  Counter #(.width(16), .max('hffff), .ongoal("wrap"), .trigger("rising"), .behavior("new")) counter_5 (
    .count(or_8_out), .Q(\条件分支成功数 ), .clk(CLK), .clr(RST));  // open: load, D, carry, preset, down
  and and_8 (and_8_out, id_ex_1_ecallout, not_5_out);
  not not_5 (not_5_out, comparator_2_eq);
  not not_6 (not_6_out, and_9_out);
  EX_MEM ex_mem_1 (
    .MEMTOREGWRITE(id_ex_1_memtoregout), .HALF(id_ex_1_halfout), .ALURESULT(aluresult),
    .WRITEDATA(id_ex_1_r2out_prime), .MEMTOREGOUT(ex_mem_1_memtoregout), .HALFOUT(ex_mem_1_halfout),
    .ALURESULTOUT({ex_mem_1_aluresultout[31:2], high, ex_mem_1_aluresultout[0]}), .WRITEDATAOUT(r2),
    .CLK(CLK), .RST(RST), .MEMWRITE(id_ex_1_memwriteout), .MEMWRITEOUT(MemWrite), .J(or_7_out),
    .JOUT(ex_mem_1_jout), .REGWRITEOUT(MEM_REGWRITE), .REGWRITE(EX_REGWRITE), .WRITEREG(EX_WRITEREG),
    .WRITEREGOUT(MEM_WRITEREG), .PC(EX_PC), .PCOUT(M_PC), .IR(EX_IR), .IROUT(MEM_IR), .IMM(adder_2_out),
    .IMMOUT(ex_mem_1_immout), .HALT(and_8_out), .HALTOUT(ex_mem_1_haltout), .FLUSH(1'b0), .EN(and_9_out));
  ID_EX_ccab id_ex_ccab_2 (
    .c1(sh2), .b1(auipc2), .a1(lui2), .c1out(sh), .b1out(auipc3), .a1out(lui3), .CLK(CLK), .RST(RST),
    .flush(1'b0), .en(and_9_out));  // open: c2, c2out
  Register #(.width(32), .trigger("rising"), .Select("low")) register_3 (
    .D(u_imm2), .en(not_6_out), .Q(u_imm3), .clk(CLK), .clr(RST));
  RAM #(.addrWidth(10), .dataWidth(32), .bus("separate"), .Select("high")) ram_1 (
    .addr(ex_mem_1_aluresultout[11:2]), .din(MDin), .data(\use ), .str(MemWrite), .clk(CLK), .ld(1'b1));  // open: sel, clr
  and and_9 (and_9_out, halt, ~Go);  // AND_Gate
  not not_7 (not_7_out, and_9_out);
  MEM_WB mem_wb_1 (
    .MEMTOREG(ex_mem_1_memtoregout),
    .ALURESULT({ex_mem_1_aluresultout[31:2], high, ex_mem_1_aluresultout[0]}), .MEMDATA(\use ),
    .MEMTOREGOUT(mem_wb_1_memtoregout), .ALURESULTOUT(mem_wb_1_aluresultout),
    .MEMDATAOUT(mem_wb_1_memdataout), .in_1(CLK), .in_2(RST), .HALF(ex_mem_1_halfout),
    .HALFOUT(mem_wb_1_halfout), .J(ex_mem_1_jout), .JOUT(mem_wb_1_jout), .WRITEREG(MEM_WRITEREG),
    .WRITEREGOUT(mem_wb_1_writeregout), .REGWRITE(MEM_REGWRITE), .REGWRITEOUT(RegWrite), .PC(M_PC),
    .PCOUT(WB_PC), .IR(MEM_IR), .IROUT(WB_IR), .IMM(ex_mem_1_immout), .IMMOUT(mem_wb_1_immout),
    .HALT(ex_mem_1_haltout), .HALTOUT(halt), .HIGH(high), .HIGHOUT(mem_wb_1_highout), .FLUSH(1'b0),
    .EN(and_9_out));
  Multiplexer #(.select(1), .width(32), .disabled("Z"), .enable("false")) multiplexer_8 (
    .in0(mem_wb_1_aluresultout), .in1(mem_wb_1_memdataout), .out(multiplexer_8_out),
    .sel(mem_wb_1_memtoregout));
  ID_EX_ccab id_ex_ccab_3 (
    .b1(auipc3), .a1(lui3), .b1out(auipc), .a1out(lui), .CLK(CLK), .RST(RST), .flush(1'b0), .en(and_9_out));  // open: c1, c2, c1out, c2out
  Register #(.width(32), .trigger("rising"), .Select("low")) register_4 (
    .D(u_imm3), .en(not_7_out), .Q(u_imm), .clk(CLK), .clr(RST));
  Shifter #(.width(32), .shift("lr")) shifter_4 (.in(multiplexer_8_out), .\dist (5'b10000), .out(shifter_4_out));
  Multiplexer #(.select(1), .width(32), .disabled("Z"), .enable("false")) multiplexer_9 (
    .in0(multiplexer_8_out), .in1(shifter_4_out), .out(multiplexer_9_out), .sel(mem_wb_1_highout));
  Multiplexer #(.select(1), .width(5), .disabled("Z"), .enable("false")) multiplexer_10 (
    .in0({5{1'b0}}), .in1(5'b10000), .out(multiplexer_10_out), .sel(high));
  Multiplexer #(.select(1), .width(32), .disabled("Z"), .enable("false")) multiplexer_11 (
    .in0(32'hffff0000), .in1(32'hffff), .out(multiplexer_11_out), .sel(high));
  assign and_10_out = multiplexer_9_out & 32'hffff;  // AND_Gate and_10, 32 bits wide
  assign bit_extender_5_out = {{16{1'b0}}, r2[15:0]};  // Bit_Extender bit_extender_5
  Shifter #(.width(32), .shift("ll")) shifter_5 (
    .in(bit_extender_5_out), .\dist (multiplexer_10_out), .out(shifter_5_out));
  assign and_11_out = \use  & multiplexer_11_out;  // AND_Gate and_11, 32 bits wide
  Multiplexer #(.select(1), .width(32), .disabled("Z"), .enable("false")) multiplexer_12 (
    .in0(multiplexer_8_out), .in1(and_10_out), .out(multiplexer_12_out), .sel(mem_wb_1_halfout));
  Multiplexer #(.select(1), .width(32), .disabled("Z"), .enable("false")) multiplexer_13 (
    .in0(multiplexer_12_out), .in1(mem_wb_1_immout), .out(multiplexer_13_out), .sel(mem_wb_1_jout));
  assign inn = shifter_5_out | and_11_out;  // OR_Gate or_11, 32 bits wide
  Multiplexer #(.select(1), .width(32), .disabled("Z"), .enable("false")) multiplexer_14 (
    .in0(multiplexer_13_out), .in1(adder_5_out), .out(multiplexer_14_out), .sel(auipc));
  Adder #(.width(32)) adder_5 (.a(WB_PC), .b(u_imm), .out(adder_5_out));  // open: cin, cout
  Multiplexer #(.select(1), .width(32), .disabled("Z"), .enable("false")) multiplexer_15 (
    .in0(r2), .in1(inn), .out(MDin), .sel(sh));
  Multiplexer #(.select(1), .width(32), .disabled("Z"), .enable("false")) multiplexer_16 (
    .in0(multiplexer_14_out), .in1(u_imm), .out(RDin), .sel(lui));

  // Other names for the same wires on the sheet: WRITEREG[4:0] = ID_IR[11:7]; MEM_PC[31:0] = M_PC

  // Notes on the sheet:
  //   中断源
  //   时空图监测，可删除
  //   中断等待指示
  //   数码管输出
  //   指令存储器
  //   PC+4
  //   contents of rom_1 (hex, n*v repeats v):
  //   100493 100006f 100493 200913 300993 100006f 100493 200913 300993 100006f 100493 200913 300993
  //   100006f 100493 200913 300993 3f8000ef 100413 100493 1f49493 900533 2200893 73 24d493 48463 fedff06f
  //   900533 2200893 73 100493 249493 900533 2200893 73 48463 fedff06f 100493 1f49493 900533 2200893 73
  //   4034d493 900533 2200893 73 4044d493 900533 2200893 73 4044d493 900533 2200893 73 4044d493 900533
  //   2200893 73 4044d493 900533 2200893 73 4044d493 900533 2200893 73 4044d493 900533 2200893 73 4044d493
  //   900533 2200893 73 100413 1f41993 41f9d993 433 c00913 300b13 140413 f47413 800293 100313 499993
  //   89e9b3 1300533 2200893 73 406282b3 fe0294e3 140413 f00f93 1f47433 1c41413 800293 100313 49d993
  //   89e9b3 1300533 2200893 73 406282b3 fe0294e3 1c45413 406b0b33 b0463 f95ff06f 2b3 fff2c293 829293
  //   ff2e293 500533 2200893 73 fff00413 493 84a023 140413 448493 84a023 140413 448493 84a023 140413
  //   448493 84a023 140413 448493 84a023 140413 448493 84a023 140413 448493 84a023 140413 448493 84a023
  //   140413 448493 84a023 140413 448493 84a023 140413 448493 84a023 140413 448493 84a023 140413 448493
  //   84a023 140413 448493 84a023 140413 448493 84a023 140413 448493 84a023 140413 448493 140413 433
  //   3c00493 42983 4aa03 149a2b3 28663 134a023 1442023 ffc48493 fe9412e3 800533 2200893 73 440413 3c00493
  //   fc9416e3 a00893 73 13 430497 900533 2200893 73 430497 900533 2200893 73 430497 900533 2200893 73
  //   430497 900533 2200893 73 430497 900533 2200893 73 430497 900533 2200893 73 430497 900533 2200893 73
  //   430497 900533 2200893 73 a00893 73 800e13 fedc04b7 fff00413 1045413 84e4b3 900533 2200893 73 ba984b7
  //   900533 73 76544b7 900533 73 32104b7 900533 73 fffe0e13 fa0e1ee3 a00893 73 313 2000e13 100493 100913
  //   931023 900533 2200893 73 12484b3 230313 fffe0e13 fe0e12e3 1000e13 313 32483 900533 2200893 73 430313
  //   fffe0e13 fe0e14e3 a00893 73 ff100493 900533 2200893 73 148493 fe04c8e3 a00893 73 413 140413 800533
  //   2200893 73 240413 800533 2200893 73 340413 800533 2200893 73 440413 800533 2200893 73 540413 800533
  //   2200893 73 640413 800533 2200893 73 740413 800533 2200893 73 840413 800533 2200893 2200893 73 8067
  //   指令探针
  //   指令字
  //   JAL
  //   JALR
  //   URET
  //   I型指令
  //   s型指令
  //   B型指令
  //   J型指令
  //   控制位
  //   Beq
  //   Bne
  //   MemToReg
  //   MemWrite
  //   AluOP
  //   AluSrcB
  //   RegWrite
  //   half
  //   流水调试日志用
  //   暂停节拍，不能为0
  //   imm
  //   戳工具置1进入计数暂停模式，ctrl+k时钟自动运行到对应节拍暂停
  //   ctrl+k关闭时钟连续运行，将控制位置零，进入单步调试模式调试
  //   可计数暂停的时钟源
  //   为方便自动评测，需要输出流水线各段保存的PC值，注意是PC不是PC+4，另外ID段寄存器写入信息，Mem段内存写入信息也要输出
  //   PC+4
  //   BEQ/BNE
  //   JAL
  //   JALR
  //   数据存储器
endmodule
module \重定向流水线  (
  output RegWrite,
  output MemWrite,
  output [31:0] IF_PC,
  output [31:0] ID_PC,
  output [31:0] EX_PC,
  output [31:0] M_PC,
  output [31:0] WB_PC,
  output [31:0] RDin,
  output [31:0] MDin,
  output [31:0] LedData
);

  wire alu_1_equal, alu_1_out_6, and_1_out, and_2_out, and_3_out, and_5_out, and_6_out, and_7_out, and_9_out,
       and_10_out, auipc, auipc1, auipc2, auipc3, B, blt, blt1, BRANCHTAKEN, CLK, clock_1_out,
       comparator_1_eq, comparator_1_lt, comparator_2_eq, d_ff_1_q, ecall, ex_mem_1_halfout,
       ex_mem_1_haltout, ex_mem_1_memtoregout, EX_MEMTOREG, EX_REGWRITE, Go, halt, high, id_ex_1_alusrcout,
       id_ex_1_beqout, id_ex_1_bneout, id_ex_1_ecallout, id_ex_1_halfout, id_ex_1_memwriteout, IR1, IR2, IR3,
       jal, jalr, led, LOADUSE, lui, lui1, lui2, lui3, MEM_J, MEM_REGWRITE, mem_wb_1_halfout,
       mem_wb_1_highout, mem_wb_1_jout, mem_wb_1_memtoregout, nand_1_out, not_1_out, not_2_out, not_3_out,
       not_4_out, not_5_out, not_6_out, not_7_out, or_1_out, or_2_out, or_4_out, or_5_out, or_6_out,
       or_7_out, or_8_out, or_9_out, RST, sh, sh1, sh2, W1, W2, W3, \单周期硬布线控制器_1_alu_src , \单周期硬布线控制器_1_beq ,
       \单周期硬布线控制器_1_bne , \单周期硬布线控制器_1_half , \单周期硬布线控制器_1_jal , \单周期硬布线控制器_1_jalr , \单周期硬布线控制器_1_memtoreg ,
       \单周期硬布线控制器_1_memwrite , \单周期硬布线控制器_1_regwrite , \单周期硬布线控制器_1_s_type , \单周期硬布线控制器_1_uret ;
  wire [1:0] EX_R1F, EX_R2F, priority_encoder_1_out, R1FOWARD, R2FOWARD;
  wire [3:0] id_ex_1_aluopout, \单周期硬布线控制器_1_alu_op ;
  wire [4:0] EX_WRITEREG, mem_wb_1_writeregout, MEM_WRITEREG, multiplexer_2_out, multiplexer_4_out,
       multiplexer_15_out;
  wire [11:0] multiplexer_3_out;
  wire [12:0] CNT_num;
  wire [15:0] \LoadUse次数 , \总周期数 , \无条件分支数 , \条件分支成功数 ;
  wire [31:0] adder_1_out, adder_2_out, adder_3_out, adder_4_out, adder_5_out, adder_6_out, aluresult,
       and_4_out, and_11_out, and_12_out, bit_extender_1_out, bit_extender_2_out, bit_extender_3_out,
       bit_extender_4_out, bit_extender_5_out, EX_IR, ex_mem_1_aluresultout, ex_mem_1_immout, EX_R1, EX_R2,
       id_ex_1_imm1out_prime, id_ex_1_imm2out_prime, id_ex_1_imm3out_prime, ID_IR, IF_IR, inn, MEM_IR,
       MEM_RESULT, mem_wb_1_aluresultout, mem_wb_1_immout, mem_wb_1_memdataout, multiplexer_1_out,
       multiplexer_5_out, multiplexer_8_out, multiplexer_9_out, multiplexer_10_out, multiplexer_11_out,
       multiplexer_13_out, multiplexer_14_out, multiplexer_16_out, multiplexer_17_out, multiplexer_18_out,
       multiplexer_20_out, R1R, R2R, \regifile_气泡_1_r1 , \regifile_气泡_1_r2 , Res, shifter_2_out,
       shifter_3_out, shifter_4_out, shifter_5_out, u_imm, u_imm1, u_imm2, u_imm3, \use , WB_IR;

  Button \u_总复位  (.out(RST));
  Button _1 (.out(IR1));
  Button _2 (.out(IR2));
  Button _3 (.out(IR3));
  // Probe on \总周期数 
  // Probe on \总周期数 
  Button \u_继续运行  (.out(Go));
  LED #(.active("true")) led_1 (.in(W1));
  LED #(.active("true")) led_2 (.in(W2));
  LED #(.active("true")) led_3 (.in(W3));
  Hex_Digit_Display hex_digit_display_1 (.value(LedData[31:28]));  // open: dp
  // Probe on IF_PC[19:0]
  // RiscV_Probe riscv_probe_1: pin names not known; wires that end beside it: IF_IR
  Hex_Digit_Display hex_digit_display_2 (.value(LedData[27:24]));  // open: dp
  Hex_Digit_Display hex_digit_display_3 (.value(LedData[23:20]));  // open: dp
  // Probe on ID_PC[19:0]
  // RiscV_Probe riscv_probe_2: pin names not known; wires that end beside it: ID_IR
  or or_1 (or_1_out, Go, not_1_out);
  not not_1 (not_1_out, halt);
  and and_1 (and_1_out, ~LOADUSE, or_2_out);  // AND_Gate
  or or_2 (or_2_out, Go, not_2_out);
  Hex_Digit_Display hex_digit_display_4 (.value(LedData[19:16]));  // open: dp
  Hex_Digit_Display hex_digit_display_5 (.value(LedData[15:12]));  // open: dp
  Counter #(.width(16), .max('hffff), .ongoal("wrap"), .trigger("rising"), .behavior("new")) counter_1 (
    .count(or_1_out), .Q(\总周期数 ), .clk(CLK), .clr(RST));  // open: load, D, carry, preset, down
  Register #(.width(32), .trigger("rising"), .Select("low")) PC (
    .D(multiplexer_1_out), .en(and_1_out), .Q(IF_PC), .clk(CLK), .clr(RST));
  not not_2 (not_2_out, halt);
  Hex_Digit_Display hex_digit_display_6 (.value(LedData[7:4]));  // open: dp
  Hex_Digit_Display hex_digit_display_7 (.value(LedData[11:8]));  // open: dp
  // Probe on EX_PC[19:0]
  // RiscV_Probe riscv_probe_3: pin names not known; wires that end beside it: EX_IR
  Multiplexer #(.select(2), .width(32), .disabled("Z"), .enable("false")) multiplexer_1 (
    .in0(adder_1_out), .in1(adder_3_out), .in2(adder_4_out), .in3(and_4_out), .out(multiplexer_1_out),
    .sel(priority_encoder_1_out));
  Priority_Encoder #(.select(2), .disabled("Z")) priority_encoder_1 (
    .in0(1'b1), .in1(B), .in2(jal), .in3(jalr), .out(priority_encoder_1_out));  // open: gs, en_out, en_in
  or or_3 (BRANCHTAKEN, B, jal, jalr);
  Hex_Digit_Display hex_digit_display_8 (.value(LedData[3:0]));  // open: dp
  Adder #(.width(32)) adder_1 (.a(IF_PC), .b(32'h4), .out(adder_1_out));  // open: cin, cout
  // Probe on \总周期数 
  // Probe on M_PC[19:0]
  // RiscV_Probe riscv_probe_4: pin names not known; wires that end beside it: MEM_IR
  Counter #(.width(16), .max('hffff), .ongoal("wrap"), .trigger("rising"), .behavior("new")) counter_2 (
    .count(LOADUSE), .Q(\LoadUse次数 ), .clk(CLK), .clr(RST));  // open: load, D, carry, preset, down
  ROM #(.addrWidth(10), .dataWidth(32), .Select("high")) rom_1 (.addr(IF_PC[11:2]), .data(IF_IR));
  // Probe on \总周期数 
  // Probe on \无条件分支数 
  // Probe on \条件分支成功数 
  // Probe on \LoadUse次数 
  // Probe on \LoadUse次数 
  IF_ID if_id_1 (
    .IR(IF_IR), .PC(IF_PC), .IROUT(ID_IR), .PCOUT(ID_PC), .CLK(CLK), .RST(RST), .FLUSH(BRANCHTAKEN),
    .EN(or_4_out));  // open: PREDICT, PREDICTOUT
  \冲突检测逻辑_重定向  \u_冲突检测逻辑_重定向_1  (
    .EX_REGWRITE(EX_REGWRITE), .MEM_REGWRITE(MEM_REGWRITE), .MEM_WRITEREG(MEM_WRITEREG),
    .EX_WRITEREG(EX_WRITEREG), .EX_MEMTOREG(EX_MEMTOREG), .ID_IR(ID_IR), .R1FOWARD(R1FOWARD),
    .LOADUSE(LOADUSE), .R2FOWARD(R2FOWARD));
  // Probe on IF_PC[11:0]
  // Probe on WB_PC[19:0]
  // RiscV_Probe riscv_probe_5: pin names not known; wires that end beside it: WB_IR
  // RiscV_Probe riscv_probe_6: pin names not known; wires that end beside it: CLK, RST, ID_IR
  or or_4 (or_4_out, and_2_out, LOADUSE);
  and and_2 (and_2_out, halt, ~Go);  // AND_Gate
  // Probe on ID_PC[11:0]
  // Probe on EX_PC[11:0]
  // Probe on M_PC[11:0]
  D_Flip_Flop #(.trigger("high"), .Pre_Clr_Positions("LEGACY"), .NegatePresetClear("false"), .enable("true"), .NewFFLayout("false")) d_ff_1 (.Q(d_ff_1_q));  // open: clk, D, Qn, preset, en, reset
  // Probe on 13'hc
  // Probe on WB_PC[11:0]
  Comparator #(.width(13), .mode("twosComplement")) comparator_1 (
    .a(CNT_num), .b(13'hc), .eq(comparator_1_eq), .lt(comparator_1_lt));  // open: gt
  Clock #(.highDuration(1), .lowDuration(1)) clock_1 (.out(clock_1_out));
  \单周期硬布线控制器  \u_单周期硬布线控制器_1  (
    .Funct({ID_IR[30], ID_IR[25], ID_IR[14:12]}), .OP(ID_IR[6:2]), .ALU_OP(\单周期硬布线控制器_1_alu_op ),
    .MemToReg(\单周期硬布线控制器_1_memtoreg ), .MemWrite(\单周期硬布线控制器_1_memwrite ), .ALU_SRC(\单周期硬布线控制器_1_alu_src ),
    .RegWrite(\单周期硬布线控制器_1_regwrite ), .ecall(ecall), .S_type(\单周期硬布线控制器_1_s_type ),
    .Jalr(\单周期硬布线控制器_1_jalr ), .Beq(\单周期硬布线控制器_1_beq ), .JAL(\单周期硬布线控制器_1_jal ), .Bne(\单周期硬布线控制器_1_bne ),
    .in_3(ID_IR[21]), .uret(\单周期硬布线控制器_1_uret ), .half(\单周期硬布线控制器_1_half ), .blt(blt1), .sh(sh1),
    .auipc(auipc1), .lui(lui1));  // open: CSR
  Multiplexer #(.select(1), .width(5), .disabled("Z"), .enable("false")) multiplexer_2 (
    .in0(ID_IR[19:15]), .in1(5'b10001), .out(multiplexer_2_out), .sel(ecall));
  Multiplexer #(.select(1), .width(12), .disabled("Z"), .enable("false")) multiplexer_3 (
    .in0(ID_IR[31:20]), .in1({ID_IR[31:25], ID_IR[11:7]}), .out(multiplexer_3_out), .sel(\单周期硬布线控制器_1_s_type ));
  assign bit_extender_1_out = {{12{ID_IR[31]}}, ID_IR[31:12]};  // Bit_Extender bit_extender_1
  nand nand_1 (nand_1_out, d_ff_1_q, comparator_1_eq);
  Counter #(.width(13), .max('h1fff), .ongoal("stay"), .trigger("rising"), .behavior("old")) counter_3 (
    .count(comparator_1_lt), .Q(CNT_num), .clk(clock_1_out));  // open: load, D, carry, clr, preset
  Multiplexer #(.select(1), .width(5), .disabled("Z"), .enable("false")) multiplexer_4 (
    .in0(ID_IR[24:20]), .in1(5'b01010), .out(multiplexer_4_out), .sel(ecall));
  Shifter #(.width(32), .shift("ll")) shifter_1 (.in(bit_extender_1_out), .\dist (5'b01100), .out(u_imm1));
  assign bit_extender_2_out = {{20{ID_IR[31]}}, {ID_IR[31], ID_IR[7], ID_IR[30:25], ID_IR[11:8]}};  // Bit_Extender bit_extender_2
  assign bit_extender_3_out = {{12{ID_IR[31]}}, {ID_IR[31], ID_IR[19:12], ID_IR[20], ID_IR[30:21]}};  // Bit_Extender bit_extender_3
  assign CLK = nand_1_out ? clock_1_out : 1'bz;  // Controlled_Buffer controlled_buffer_1
  assign bit_extender_4_out = {{20{multiplexer_3_out[11]}}, multiplexer_3_out};  // Bit_Extender bit_extender_4
  Pull_Resistor #(.pull(1)) pull_resistor_1 (.node(CLK));
  \regifile_气泡  \regifile_气泡_1  (
    .Din(RDin), .Clk(CLK), .R1(\regifile_气泡_1_r1 ), .R2(\regifile_气泡_1_r2 ), .WE(RegWrite),
    .W_num(mem_wb_1_writeregout), .R1_num(multiplexer_2_out), .R2_num(multiplexer_4_out));
  Multiplexer #(.select(1), .width(32), .disabled("Z"), .enable("false")) multiplexer_5 (
    .in0(u_imm1), .in1({32{1'b0}}), .out(multiplexer_5_out), .sel(or_5_out));
  ID_EX id_ex_1 (
    .JAL(\单周期硬布线控制器_1_jal ), .JALR(\单周期硬布线控制器_1_jalr ), .URET(\单周期硬布线控制器_1_uret ), .beq(\单周期硬布线控制器_1_beq ),
    .MEMTOREG(\单周期硬布线控制器_1_memtoreg ), .MEMWRITE(\单周期硬布线控制器_1_memwrite ), .ALUSRC(\单周期硬布线控制器_1_alu_src ),
    .R1(\regifile_气泡_1_r1 ), .R2(\regifile_气泡_1_r2 ), .PC(ID_PC), .IMM1(bit_extender_4_out),
    .IMM2(bit_extender_2_out), .IMM3(bit_extender_3_out), .JALOUT(jal), .JALROUT(jalr),
    .BEQOUT(id_ex_1_beqout), .MEMTOREGOUT(EX_MEMTOREG), .MEMWRITEOUT(id_ex_1_memwriteout),
    .ALUSRCOUT(id_ex_1_alusrcout), .R1OUT(EX_R1), .R2OUT_prime(EX_R2), .PCOUT_prime(EX_PC),
    .IMM1OUT_prime(id_ex_1_imm1out_prime), .IMM2OUT_prime(id_ex_1_imm2out_prime),
    .IMM3OUT_prime(id_ex_1_imm3out_prime), .CLK(CLK), .RST(RST), .BNE(\单周期硬布线控制器_1_bne ),
    .BNEOUT(id_ex_1_bneout), .ALUOP(\单周期硬布线控制器_1_alu_op ), .ALUOPOUT(id_ex_1_aluopout),
    .REGWRITE(\单周期硬布线控制器_1_regwrite ), .REGWRITEOUT(EX_REGWRITE), .half(\单周期硬布线控制器_1_half ),
    .halfOUT(id_ex_1_halfout), .ECALL(ecall), .ECALLOUT(id_ex_1_ecallout), .WRITEREG(ID_IR[11:7]),
    .WRITEREGOUT_prime(EX_WRITEREG), .IR(ID_IR), .IROUT_prime(EX_IR), .FLUSH(or_5_out), .EN(and_3_out),
    .R1F(R1FOWARD), .R1FOUT(EX_R1F), .R2F(R2FOWARD), .R2FOUT(EX_R2F));  // open: URETOUT, CSR, CSROUT, PREDICT, PREDICTOUT
  or or_5 (or_5_out, BRANCHTAKEN, LOADUSE);
  ID_EX_ccab id_ex_ccab_1 (
    .c1(sh1), .c2(blt1), .b1(auipc1), .a1(lui1), .c1out(sh2), .c2out(blt), .b1out(auipc2), .a1out(lui2),
    .CLK(CLK), .RST(RST), .flush(or_5_out), .en(and_3_out));
  not not_3 (not_3_out, and_3_out);
  Register #(.width(32), .trigger("rising"), .Select("low")) register_1 (
    .D(multiplexer_5_out), .en(not_3_out), .Q(u_imm2), .clk(CLK), .clr(RST));
  and and_3 (and_3_out, halt, ~Go);  // AND_Gate
  or or_6 (or_6_out, RST, or_7_out);
  Counter #(.width(16), .max('hffff), .ongoal("wrap"), .trigger("rising"), .behavior("new")) counter_4 (
    .count(or_6_out), .Q(\无条件分支数 ), .clk(CLK), .clr(RST));  // open: load, D, carry, preset, down
  or or_7 (or_7_out, jal, jalr);
  Comparator #(.width(32), .mode("twosComplement")) comparator_2 (
    .a(32'h22), .b(R1R), .eq(comparator_2_eq));  // open: gt, lt
  Shifter #(.width(32), .shift("ll")) shifter_2 (.in(id_ex_1_imm2out_prime), .\dist (5'b00001), .out(shifter_2_out));
  Shifter #(.width(32), .shift("ll")) shifter_3 (.in(id_ex_1_imm3out_prime), .\dist (5'b00001), .out(shifter_3_out));
  Multiplexer #(.select(2), .width(32), .disabled("Z"), .enable("false")) multiplexer_6 (
    .in0(EX_R1), .in1(RDin), .in2(MEM_RESULT), .in3(MEM_RESULT), .out(R1R), .sel(EX_R1F));
  Multiplexer #(.select(2), .width(32), .disabled("Z"), .enable("false")) multiplexer_7 (
    .in0(EX_R2), .in1(RDin), .in2(MEM_RESULT), .in3(MEM_RESULT), .out(R2R), .sel(EX_R2F));
  Multiplexer #(.select(1), .width(32), .disabled("Z"), .enable("false")) multiplexer_8 (
    .in0(R2R), .in1(id_ex_1_imm1out_prime), .out(multiplexer_8_out), .sel(id_ex_1_alusrcout));
  Adder #(.width(32)) adder_2 (.a(EX_PC), .b(32'h4), .out(adder_2_out));  // open: cin, cout
  Adder #(.width(32)) adder_3 (.a(shifter_2_out), .b(EX_PC), .out(adder_3_out));  // open: cin, cout
  Adder #(.width(32)) adder_4 (.a(shifter_3_out), .b(EX_PC), .out(adder_4_out));  // open: cin, cout
  assign and_4_out = aluresult & 32'hfffffffe;  // AND_Gate and_4, 32 bits wide
  and and_5 (and_5_out, alu_1_equal, id_ex_1_beqout);
  not not_4 (not_4_out, alu_1_equal);
  and and_6 (and_6_out, blt, alu_1_out_6);
  ALU alu_1 (
    .X(R1R), .Y(multiplexer_8_out), .AluOP(id_ex_1_aluopout), .Equal(alu_1_equal), .Result(aluresult),
    .out_6(alu_1_out_6));  // open: Result_2, out_4
  or or_8 (or_8_out, and_5_out, and_7_out);
  and and_7 (and_7_out, not_4_out, id_ex_1_bneout);
  Multiplexer #(.select(1), .width(32), .disabled("Z"), .enable("false")) multiplexer_9 (
    .in0({32{1'b0}}), .in1(R2R), .out(multiplexer_9_out), .sel(led));
  or or_9 (or_9_out, RST, B);
  or or_10 (B, or_8_out, and_6_out);
  and and_8 (led, id_ex_1_ecallout, comparator_2_eq);
  not not_5 (not_5_out, comparator_2_eq);
  Register #(.width(32), .trigger("rising"), .Select("low")) register_2 (
    .D(multiplexer_9_out), .en(led), .Q(LedData), .clk(CLK));  // open: clr
  Counter #(.width(16), .max('hffff), .ongoal("wrap"), .trigger("rising"), .behavior("new")) counter_5 (
    .count(or_9_out), .Q(\条件分支成功数 ), .clk(CLK), .clr(RST));  // open: load, D, carry, preset, down
  and and_9 (and_9_out, id_ex_1_ecallout, not_5_out);
  Register #(.width(32), .trigger("rising"), .Select("low")) register_3 (
    .D(u_imm2), .en(not_6_out), .Q(u_imm3), .clk(CLK), .clr(RST));
  not not_6 (not_6_out, and_10_out);
  EX_MEM ex_mem_1 (
    .MEMTOREGWRITE(EX_MEMTOREG), .HALF(id_ex_1_halfout), .ALURESULT(aluresult), .WRITEDATA(R2R),
    .MEMTOREGOUT(ex_mem_1_memtoregout), .HALFOUT(ex_mem_1_halfout),
    .ALURESULTOUT({ex_mem_1_aluresultout[31:2], high, ex_mem_1_aluresultout[0]}), .WRITEDATAOUT(Res),
    .CLK(CLK), .RST(RST), .MEMWRITE(id_ex_1_memwriteout), .MEMWRITEOUT(MemWrite), .J(or_7_out), .JOUT(MEM_J),
    .REGWRITEOUT(MEM_REGWRITE), .REGWRITE(EX_REGWRITE), .WRITEREG(EX_WRITEREG), .WRITEREGOUT(MEM_WRITEREG),
    .PC(EX_PC), .PCOUT(M_PC), .IR(EX_IR), .IROUT(MEM_IR), .IMM(adder_2_out), .IMMOUT(ex_mem_1_immout),
    .HALT(and_9_out), .HALTOUT(ex_mem_1_haltout), .FLUSH(1'b0), .EN(and_10_out));
  ID_EX_ccab id_ex_ccab_2 (
    .c1(sh2), .b1(auipc2), .a1(lui2), .c1out(sh), .b1out(auipc3), .a1out(lui3), .CLK(CLK), .RST(RST),
    .flush(1'b0), .en(and_10_out));  // open: c2, c2out
  Multiplexer #(.select(1), .width(32), .disabled("Z"), .enable("false")) multiplexer_10 (
    .in0({ex_mem_1_aluresultout[31:2], high, ex_mem_1_aluresultout[0]}), .in1(ex_mem_1_immout),
    .out(multiplexer_10_out), .sel(MEM_J));
  RAM #(.addrWidth(10), .dataWidth(32), .bus("separate"), .Select("high")) ram_1 (
    .addr(ex_mem_1_aluresultout[11:2]), .din(MDin), .data(\use ), .str(MemWrite), .clk(CLK), .ld(1'b1));  // open: sel, clr
  Multiplexer #(.select(1), .width(32), .disabled("Z"), .enable("false")) multiplexer_11 (
    .in0(multiplexer_10_out), .in1(u_imm3), .out(multiplexer_11_out), .sel(lui3));
  Adder #(.width(32)) adder_5 (.a(M_PC), .b(u_imm3), .out(adder_5_out));  // open: cin, cout
  Multiplexer #(.select(1), .width(32), .disabled("Z"), .enable("false")) multiplexer_12 (
    .in0(multiplexer_11_out), .in1(adder_5_out), .out(MEM_RESULT), .sel(auipc3));
  MEM_WB mem_wb_1 (
    .MEMTOREG(ex_mem_1_memtoregout),
    .ALURESULT({ex_mem_1_aluresultout[31:2], high, ex_mem_1_aluresultout[0]}), .MEMDATA(\use ),
    .MEMTOREGOUT(mem_wb_1_memtoregout), .ALURESULTOUT(mem_wb_1_aluresultout),
    .MEMDATAOUT(mem_wb_1_memdataout), .in_1(CLK), .in_2(RST), .HALF(ex_mem_1_halfout),
    .HALFOUT(mem_wb_1_halfout), .J(MEM_J), .JOUT(mem_wb_1_jout), .WRITEREG(MEM_WRITEREG),
    .WRITEREGOUT(mem_wb_1_writeregout), .REGWRITE(MEM_REGWRITE), .REGWRITEOUT(RegWrite), .PC(M_PC),
    .PCOUT(WB_PC), .IR(MEM_IR), .IROUT(WB_IR), .IMM(ex_mem_1_immout), .IMMOUT(mem_wb_1_immout),
    .HALT(ex_mem_1_haltout), .HALTOUT(halt), .HIGH(high), .HIGHOUT(mem_wb_1_highout), .FLUSH(1'b0),
    .EN(and_10_out));
  ID_EX_ccab id_ex_ccab_3 (
    .b1(auipc3), .a1(lui3), .b1out(auipc), .a1out(lui), .CLK(CLK), .RST(RST), .flush(1'b0), .en(and_10_out));  // open: c1, c2, c1out, c2out
  Register #(.width(32), .trigger("rising"), .Select("low")) register_4 (
    .D(u_imm3), .en(not_7_out), .Q(u_imm), .clk(CLK), .clr(RST));
  not not_7 (not_7_out, and_10_out);
  Multiplexer #(.select(1), .width(32), .disabled("Z"), .enable("false")) multiplexer_13 (
    .in0(mem_wb_1_aluresultout), .in1(mem_wb_1_memdataout), .out(multiplexer_13_out),
    .sel(mem_wb_1_memtoregout));
  and and_10 (and_10_out, halt, ~Go);  // AND_Gate
  Shifter #(.width(32), .shift("lr")) shifter_4 (.in(multiplexer_13_out), .\dist (5'b10000), .out(shifter_4_out));
  Multiplexer #(.select(1), .width(32), .disabled("Z"), .enable("false")) multiplexer_14 (
    .in0(multiplexer_13_out), .in1(shifter_4_out), .out(multiplexer_14_out), .sel(mem_wb_1_highout));
  assign bit_extender_5_out = {{16{1'b0}}, Res[15:0]};  // Bit_Extender bit_extender_5
  Multiplexer #(.select(1), .width(5), .disabled("Z"), .enable("false")) multiplexer_15 (
    .in0({5{1'b0}}), .in1(5'b10000), .out(multiplexer_15_out), .sel(high));
  Multiplexer #(.select(1), .width(32), .disabled("Z"), .enable("false")) multiplexer_16 (
    .in0(32'hffff0000), .in1(32'hffff), .out(multiplexer_16_out), .sel(high));
  assign and_11_out = multiplexer_14_out & 32'hffff;  // AND_Gate and_11, 32 bits wide
  Shifter #(.width(32), .shift("ll")) shifter_5 (
    .in(bit_extender_5_out), .\dist (multiplexer_15_out), .out(shifter_5_out));
  assign and_12_out = \use  & multiplexer_16_out;  // AND_Gate and_12, 32 bits wide
  Multiplexer #(.select(1), .width(32), .disabled("Z"), .enable("false")) multiplexer_17 (
    .in0(multiplexer_13_out), .in1(and_11_out), .out(multiplexer_17_out), .sel(mem_wb_1_halfout));
  Multiplexer #(.select(1), .width(32), .disabled("Z"), .enable("false")) multiplexer_18 (
    .in0(multiplexer_17_out), .in1(mem_wb_1_immout), .out(multiplexer_18_out), .sel(mem_wb_1_jout));
  assign inn = shifter_5_out | and_12_out;  // OR_Gate or_11, 32 bits wide
  Adder #(.width(32)) adder_6 (.a(WB_PC), .b(u_imm), .out(adder_6_out));  // open: cin, cout
  Multiplexer #(.select(1), .width(32), .disabled("Z"), .enable("false")) multiplexer_19 (
    .in0(Res), .in1(inn), .out(MDin), .sel(sh));
  Multiplexer #(.select(1), .width(32), .disabled("Z"), .enable("false")) multiplexer_20 (
    .in0(multiplexer_18_out), .in1(adder_6_out), .out(multiplexer_20_out), .sel(auipc));
  Multiplexer #(.select(1), .width(32), .disabled("Z"), .enable("false")) multiplexer_21 (
    .in0(multiplexer_20_out), .in1(u_imm), .out(RDin), .sel(lui));

  // Other names for the same wires on the sheet: WRITEREG[4:0] = ID_IR[11:7]; MEM_PC[31:0] = M_PC;
  //   插入气泡数[15:0] = \LoadUse次数 

  // Notes on the sheet:
  //   中断源
  //   时空图监测，可删除
  //   中断等待指示
  //   数码管输出
  //   指令存储器
  //   PC+4
  //   contents of rom_1 (hex, n*v repeats v):
  //   13 430497 900533 2200893 73 430497 900533 2200893 73 430497 900533 2200893 73 430497 900533 2200893
  //   73 430497 900533 2200893 73 430497 900533 2200893 73 430497 900533 2200893 73 430497 900533 2200893
  //   73 a00893 73
  //   指令探针
  //   控制位
  //   指令字
  //   流水调试日志用
  //   暂停节拍，不能为0
  //   JAL
  //   JALR
  //   URET
  //   I型指令
  //   s型指令
  //   B型指令
  //   J型指令
  //   戳工具置1进入计数暂停模式，ctrl+k时钟自动运行到对应节拍暂停
  //   ctrl+k关闭时钟连续运行，将控制位置零，进入单步调试模式调试
  //   Beq
  //   Bne
  //   MemToReg
  //   MemWrite
  //   AluOP
  //   AluSrcB
  //   RegWrite
  //   half
  //   imm
  //   可计数暂停的时钟源
  //   为方便自动评测，需要输出流水线各段保存的PC值，注意是PC不是PC+4，另外ID段寄存器写入信息，Mem段内存写入信息也要输出
  //   PC+4
  //   JAL
  //   JALR
  //   BEQ/BNE
  //   数据存储器
endmodule

module \中断按键参考电路  (
  input  \同步清零信号 ,
  output \与中断屏蔽位与 
);

  wire \_1号中断_out , and_1_out, clock_1_out, d_ff_1_q, or_1_out, or_2_out;

  Clock #(.highDuration(1), .lowDuration(1)) clock_1 (.out(clock_1_out));
  Button \_1号中断  (.out(\_1号中断_out ));
  LED #(.active("true")) \_1号中断等待指示灯  (.in(or_1_out));
  or or_1 (or_1_out, \与中断屏蔽位与 , d_ff_1_q);
  D_Flip_Flop #(.trigger("rising"), .Pre_Clr_Positions("LEGACY"), .NegatePresetClear("false"), .enable("true"), .NewFFLayout("false")) d_ff_1 (
    .clk(\_1号中断_out ), .D(1'b1), .Q(d_ff_1_q), .reset(\与中断屏蔽位与 ));  // open: Qn, preset, en
  or or_2 (or_2_out, d_ff_1_q, \与中断屏蔽位与 );
  and and_1 (and_1_out, or_2_out, ~\同步清零信号 );  // AND_Gate
  D_Flip_Flop #(.trigger("rising"), .Pre_Clr_Positions("LEGACY"), .NegatePresetClear("false"), .enable("true"), .NewFFLayout("false")) IR1 (
    .clk(clock_1_out), .D(and_1_out), .Q(\与中断屏蔽位与 ));  // open: Qn, preset, en, reset

  // Notes on the sheet:
  //   中断信号采样参考电路
  //   Reset 
endmodule

module \单周期_多级中断  (
  input  IR1,
  input  IR2,
  input  IR3,
  output RegWrite,
  output MemWrite,
  output [31:0] PC,
  output [31:0] IR,
  output [31:0] RDin,
  output [31:0] MDin,
  output [31:0] LedData
);

  wire alu_1_equal, alu_1_out_6, and_1_out, and_2_out, and_3_out, and_4_out, and_10_out, and_11_out,
       and_12_out, auipc, B, blt, CLK, clock_1_out, CLR1, CLR2, CLR3, comparator_1_eq, comparator_2_eq,
       comparator_3_eq, comparator_4_eq, comparator_5_lt, comparator_6_eq, comparator_6_lt, comparator_7_eq,
       CSR, CSRRCI, CSRRSI, d_ff_1_q, d_ff_2_q, d_ff_3_q, d_ff_4_q, d_ff_6_q, ecall, Go, half, halt, IE,
       INTR, INTR1, INTR2, INTR3, IR1_t, IR2_t, IR3_t, IRA, IRB, IRC, J, jal, jalr, led, lui, nand_1_out,
       not_1_out, not_2_out, not_3_out, not_4_out, not_5_out, or_4_out, or_5_out, or_6_out, or_7_out,
       or_8_out, or_11_out, or_13_out, or_14_out, or_15_out, or_16_out, or_18_out, sh, uret, W1, W2, W3,
       \单周期硬布线控制器_1_alu_src , \单周期硬布线控制器_1_beq , \单周期硬布线控制器_1_bne , \单周期硬布线控制器_1_memtoreg ,
       \单周期硬布线控制器_1_s_type ;
  wire [1:0] CUR_INTR, multiplexer_5_out, multiplexer_7_out, multiplexer_11_out, priority_encoder_1_out,
       priority_encoder_2_out, priority_encoder_3_out, priority_encoder_4_out, priority_encoder_5_out,
       register_5_q, register_6_q;
  wire [3:0] ALUOP;
  wire [4:0] multiplexer_8_out, multiplexer_9_out, multiplexer_22_out;
  wire [11:0] multiplexer_10_out;
  wire [12:0] CNT_num;
  wire [15:0] \总周期数 ;
  wire [31:0] adder_1_out, adder_2_out, adder_3_out, adder_4_out, addr, aluresult, and_6_out, and_7_out,
       bit_extender_1_out, bit_extender_2_out, bit_extender_3_out, bit_extender_4_out, bit_extender_5_out,
       IR_PC, MEPC, multiplexer_2_out, multiplexer_3_out, multiplexer_4_out, multiplexer_6_out,
       multiplexer_12_out, multiplexer_13_out, multiplexer_14_out, multiplexer_15_out, multiplexer_18_out,
       multiplexer_19_out, multiplexer_20_out, r2, ram_1_data, regifile_1_r1, register_2_q, register_4_q,
       result, shifter_2_out, shifter_3_out, shifter_4_out, shifter_5_out, U_imm;

  Button \u_继续运行  (.out(Go));
  Button _1 (.out(IRA));
  Button _2 (.out(IRB));
  Button _3 (.out(IRC));
  LED #(.active("true")) led_1 (.in(W1));
  LED #(.active("true")) led_2 (.in(W2));
  LED #(.active("true")) led_3 (.in(W3));
  Hex_Digit_Display hex_digit_display_1 (.value(LedData[31:28]));  // open: dp
  Comparator #(.width(16), .mode("twosComplement")) comparator_1 (
    .a(16'h23b), .b(\总周期数 ), .eq(comparator_1_eq));  // open: gt, lt
  Comparator #(.width(16), .mode("twosComplement")) comparator_2 (
    .a(\总周期数 ), .b(16'h1), .eq(comparator_2_eq));  // open: gt, lt
  Comparator #(.width(16), .mode("twosComplement")) comparator_3 (
    .a(\总周期数 ), .b(16'h4), .eq(comparator_3_eq));  // open: gt, lt
  Comparator #(.width(16), .mode("twosComplement")) comparator_4 (
    .a(\总周期数 ), .b(16'h7), .eq(comparator_4_eq));  // open: gt, lt
  D_Flip_Flop #(.trigger("rising"), .Pre_Clr_Positions("LEGACY"), .NegatePresetClear("false"), .enable("true"), .NewFFLayout("false")) d_ff_1 (
    .clk(IRA), .D(1'b1), .Q(d_ff_1_q), .reset(INTR1));  // open: Qn, preset, en
  or or_1 (W1, INTR1, d_ff_1_q);
  D_Flip_Flop #(.trigger("rising"), .Pre_Clr_Positions("LEGACY"), .NegatePresetClear("false"), .enable("true"), .NewFFLayout("false")) d_ff_2 (
    .clk(IRB), .D(1'b1), .Q(d_ff_2_q), .reset(INTR2));  // open: Qn, preset, en
  or or_2 (W2, INTR2, d_ff_2_q);
  or or_3 (W3, INTR3, d_ff_3_q);
  Demultiplexer #(.select(2), .width(1), .tristate("false"), .disabled("Z"), .enable("false")) demultiplexer_1 (
    .out1(CLR1), .out2(CLR2), .out3(CLR3), .in(uret), .sel(CUR_INTR));  // open: out0
  Hex_Digit_Display hex_digit_display_2 (.value(LedData[23:20]));  // open: dp
  Hex_Digit_Display hex_digit_display_3 (.value(LedData[27:24]));  // open: dp
  or or_4 (or_4_out, comparator_1_eq, comparator_2_eq);
  assign IRA = or_4_out ? ~CLK : 1'bz;  // Controlled_Inverter controlled_inverter_1
  assign IRB = comparator_3_eq ? ~CLK : 1'bz;  // Controlled_Inverter controlled_inverter_2
  assign IRC = comparator_4_eq ? ~CLK : 1'bz;  // Controlled_Inverter controlled_inverter_3
  D_Flip_Flop #(.trigger("rising"), .Pre_Clr_Positions("LEGACY"), .NegatePresetClear("false"), .enable("true"), .NewFFLayout("false")) d_ff_3 (
    .clk(IRC), .D(1'b1), .Q(d_ff_3_q), .reset(INTR3));  // open: Qn, preset, en
  Multiplexer #(.select(2), .width(32), .disabled("Z"), .enable("false")) multiplexer_1 (
    .in0(addr), .in1(32'h30ac), .in2(32'h3158), .in3(32'h3204), .out(IR_PC), .sel(priority_encoder_1_out));
  Priority_Encoder #(.select(2), .disabled("Z")) priority_encoder_1 (
    .in0(1'b1), .in1(INTR1), .in2(INTR2), .in3(INTR3), .out(priority_encoder_1_out));  // open: gs, en_out, en_in
  Hex_Digit_Display hex_digit_display_4 (.value(LedData[19:16]));  // open: dp
  Hex_Digit_Display hex_digit_display_5 (.value(LedData[15:12]));  // open: dp
  Pull_Resistor #(.pull(0)) pull_resistor_1 (.node(IRA));
  Pull_Resistor #(.pull(0)) pull_resistor_2 (.node(IRB));
  Pull_Resistor #(.pull(0)) pull_resistor_3 (.node(IRC));
  or or_5 (or_5_out, d_ff_1_q, INTR1);
  and and_1 (and_1_out, or_5_out, ~CLR1);  // AND_Gate
  or or_6 (or_6_out, d_ff_2_q, INTR2);
  and and_2 (and_2_out, or_6_out, ~CLR2);  // AND_Gate
  or or_7 (or_7_out, d_ff_3_q, INTR3);
  and and_3 (and_3_out, or_7_out, ~CLR3);  // AND_Gate
  Hex_Digit_Display hex_digit_display_6 (.value(LedData[11:8]));  // open: dp
  Hex_Digit_Display hex_digit_display_7 (.value(LedData[7:4]));  // open: dp
  // Probe on \总周期数 
  D_Flip_Flop #(.trigger("rising"), .Pre_Clr_Positions("LEGACY"), .NegatePresetClear("false"), .enable("true"), .NewFFLayout("false")) u_IR1 (
    .clk(CLK), .D(and_1_out), .Q(INTR1));  // open: Qn, preset, en, reset
  D_Flip_Flop #(.trigger("rising"), .Pre_Clr_Positions("LEGACY"), .NegatePresetClear("false"), .enable("true"), .NewFFLayout("false")) IR1_2 (
    .clk(CLK), .D(and_2_out), .Q(INTR2));  // open: Qn, preset, en, reset
  D_Flip_Flop #(.trigger("rising"), .Pre_Clr_Positions("LEGACY"), .NegatePresetClear("false"), .enable("true"), .NewFFLayout("false")) IR1_3 (
    .clk(CLK), .D(and_3_out), .Q(INTR3));  // open: Qn, preset, en, reset
  Hex_Digit_Display hex_digit_display_8 (.value(LedData[3:0]));  // open: dp
  Priority_Encoder #(.select(2), .disabled("Z")) priority_encoder_2 (
    .in0(1'b1), .in1(INTR1), .in2(INTR2), .in3(INTR3), .out(priority_encoder_2_out));  // open: gs, en_out, en_in
  or or_8 (or_8_out, INTR1, INTR2, INTR3);
  or or_9 (IR1_t, IR1, IRA);
  D_Flip_Flop #(.trigger("rising"), .Pre_Clr_Positions("LEGACY"), .NegatePresetClear("false"), .enable("true"), .NewFFLayout("false")) d_ff_4 (
    .clk(CLK), .D(CSRRSI), .Q(d_ff_4_q), .en(CSR));  // open: Qn, preset, reset
  not not_1 (not_1_out, CSRRCI);
  or or_10 (IR2_t, IR2, IRB);
  Comparator #(.width(2), .mode("unsigned")) comparator_5 (
    .a(CUR_INTR), .b(priority_encoder_2_out), .lt(comparator_5_lt));  // open: gt, eq
  or or_11 (or_11_out, ~or_8_out, uret, CSRRSI, and_4_out);  // OR_Gate
  and and_4 (and_4_out, d_ff_4_q, not_1_out);
  D_Flip_Flop #(.trigger("rising"), .Pre_Clr_Positions("LEGACY"), .NegatePresetClear("false"), .enable("true"), .NewFFLayout("true")) d_ff_5 (
    .clk(CLK), .D(or_11_out), .Q(IE));  // open: Qn, preset, en, reset
  or or_12 (IR3_t, IR3, IRC);
  and and_5 (INTR, comparator_5_lt, IE);
  Multiplexer #(.select(2), .width(32), .disabled("Z"), .enable("false")) multiplexer_2 (
    .in0(addr), .in1(IR_PC), .in2(MEPC), .out(multiplexer_2_out), .sel(priority_encoder_3_out));  // open: in3
  // Probe on \总周期数 
  // Probe on \总周期数 
  Counter #(.width(16), .max('hffff), .ongoal("wrap"), .trigger("rising"), .behavior("new")) counter_1 (
    .count(or_13_out), .Q(\总周期数 ), .clk(CLK));  // open: load, D, carry, clr, preset, down
  or or_13 (or_13_out, Go, not_2_out);
  not not_2 (not_2_out, halt);
  or or_14 (or_14_out, Go, not_3_out);
  not not_3 (not_3_out, halt);
  Priority_Encoder #(.select(2), .disabled("Z")) priority_encoder_3 (
    .in0(1'b1), .in1(INTR), .in2(uret), .out(priority_encoder_3_out));  // open: in3, gs, en_out, en_in
  Multiplexer #(.select(1), .width(32), .disabled("Z"), .enable("false")) multiplexer_3 (
    .in0(addr), .in1(register_2_q), .out(multiplexer_3_out), .sel(uret));
  Priority_Encoder #(.select(2), .disabled("Z")) priority_encoder_4 (
    .in0(1'b1), .in1(INTR1), .in2(INTR2), .in3(INTR3), .out(priority_encoder_4_out));  // open: gs, en_out, en_in
  Register #(.width(32), .trigger("rising"), .Select("low")) u_PC (
    .D(multiplexer_2_out), .en(or_14_out), .Q(PC), .clk(CLK));  // open: clr
  Register #(.width(32), .trigger("rising"), .Select("low")) register_1 (
    .D(multiplexer_3_out), .en(or_15_out), .Q(MEPC), .clk(CLK));  // open: clr
  or or_15 (or_15_out, uret, INTR);
  Multiplexer #(.select(1), .width(32), .disabled("Z"), .enable("false")) multiplexer_4 (
    .in0(MEPC), .in1(register_4_q), .out(multiplexer_4_out), .sel(uret));
  Multiplexer #(.select(1), .width(2), .disabled("Z"), .enable("false")) multiplexer_5 (
    .in0(priority_encoder_4_out), .in1(register_5_q), .out(multiplexer_5_out), .sel(uret));
  or or_16 (or_16_out, uret, INTR);
  or or_17 (J, jal, jalr);
  // RiscV_Probe riscv_probe_1: pin names not known; wires that end beside it: IR
  Register #(.width(32), .trigger("rising"), .Select("low")) register_2 (
    .D(multiplexer_4_out), .en(or_15_out), .Q(register_2_q), .clk(CLK));  // open: clr
  Register #(.width(2), .trigger("rising"), .Select("low")) register_3 (
    .D(multiplexer_5_out), .en(or_16_out), .Q(CUR_INTR), .clk(CLK));  // open: clr
  D_Flip_Flop #(.trigger("high"), .Pre_Clr_Positions("LEGACY"), .NegatePresetClear("false"), .enable("true"), .NewFFLayout("false")) d_ff_6 (.Q(d_ff_6_q));  // open: clk, D, Qn, preset, en, reset
  // Probe on 13'hc
  ROM #(.addrWidth(10), .dataWidth(32), .Select("high")) rom_1 (.addr(PC[11:2]), .data(IR));
  Multiplexer #(.select(1), .width(32), .disabled("Z"), .enable("false")) multiplexer_6 (
    .in0(register_2_q), .in1({32{1'b0}}), .out(multiplexer_6_out), .sel(uret));
  Multiplexer #(.select(1), .width(2), .disabled("Z"), .enable("false")) multiplexer_7 (
    .in0(CUR_INTR), .in1(register_6_q), .out(multiplexer_7_out), .sel(uret));
  Comparator #(.width(13), .mode("twosComplement")) comparator_6 (
    .a(CNT_num), .b(13'hc), .eq(comparator_6_eq), .lt(comparator_6_lt));  // open: gt
  Clock #(.highDuration(1), .lowDuration(1)) clock_1 (.out(clock_1_out));
  assign bit_extender_1_out = {{12{IR[31]}}, IR[31:12]};  // Bit_Extender bit_extender_1
  Register #(.width(32), .trigger("rising"), .Select("low")) register_4 (
    .D(multiplexer_6_out), .en(or_15_out), .Q(register_4_q), .clk(CLK));  // open: clr
  Register #(.width(2), .trigger("rising"), .Select("low")) register_5 (
    .D(multiplexer_7_out), .en(or_16_out), .Q(register_5_q), .clk(CLK));  // open: clr
  Counter #(.width(13), .max('h1fff), .ongoal("stay"), .trigger("rising"), .behavior("old")) counter_2 (
    .count(comparator_6_lt), .Q(CNT_num), .clk(clock_1_out));  // open: load, D, carry, clr, preset
  \单周期硬布线控制器  \u_单周期硬布线控制器_1  (
    .Funct({IR[30], IR[25], IR[14:12]}), .OP(IR[6:2]), .ALU_OP(ALUOP), .MemToReg(\单周期硬布线控制器_1_memtoreg ),
    .MemWrite(MemWrite), .ALU_SRC(\单周期硬布线控制器_1_alu_src ), .RegWrite(RegWrite), .ecall(ecall),
    .S_type(\单周期硬布线控制器_1_s_type ), .Jalr(jalr), .Beq(\单周期硬布线控制器_1_beq ), .JAL(jal), .Bne(\单周期硬布线控制器_1_bne ),
    .in_3(IR[21]), .uret(uret), .half(half), .CSR(CSR), .blt(blt), .sh(sh), .auipc(auipc), .lui(lui));
  Multiplexer #(.select(1), .width(5), .disabled("Z"), .enable("false")) multiplexer_8 (
    .in0(IR[19:15]), .in1(5'b10001), .out(multiplexer_8_out), .sel(ecall));
  Multiplexer #(.select(1), .width(5), .disabled("Z"), .enable("false")) multiplexer_9 (
    .in0(IR[24:20]), .in1(5'b01010), .out(multiplexer_9_out), .sel(ecall));
  Multiplexer #(.select(1), .width(12), .disabled("Z"), .enable("false")) multiplexer_10 (
    .in0(IR[31:20]), .in1({IR[31:25], IR[11:7]}), .out(multiplexer_10_out), .sel(\单周期硬布线控制器_1_s_type ));
  Shifter #(.width(32), .shift("ll")) shifter_1 (.in(bit_extender_1_out), .\dist (5'b01100), .out(U_imm));
  assign bit_extender_2_out = {{20{IR[31]}}, {IR[31], IR[7], IR[30:25], IR[11:8]}};  // Bit_Extender bit_extender_2
  assign bit_extender_3_out = {{12{IR[31]}}, {IR[31], IR[19:12], IR[20], IR[30:21]}};  // Bit_Extender bit_extender_3
  Multiplexer #(.select(1), .width(2), .disabled("Z"), .enable("false")) multiplexer_11 (
    .in0(register_5_q), .in1(2'b00), .out(multiplexer_11_out), .sel(uret));
  nand nand_1 (nand_1_out, d_ff_6_q, comparator_6_eq);
  Shifter #(.width(32), .shift("lr")) shifter_2 (.in(result), .\dist (5'b10000), .out(shifter_2_out));
  Shifter #(.width(32), .shift("ll")) shifter_3 (.in(bit_extender_2_out), .\dist (5'b00001), .out(shifter_3_out));
  Shifter #(.width(32), .shift("ll")) shifter_4 (.in(bit_extender_3_out), .\dist (5'b00001), .out(shifter_4_out));
  Register #(.width(2), .trigger("rising"), .Select("low")) register_6 (
    .D(multiplexer_11_out), .en(or_16_out), .Q(register_6_q), .clk(CLK));  // open: clr
  assign CLK = nand_1_out ? clock_1_out : 1'bz;  // Controlled_Buffer controlled_buffer_1
  Pull_Resistor #(.pull(1)) pull_resistor_4 (.node(CLK));
  Regifile regifile_1 (
    .Din(RDin), .Clk(CLK), .R1(regifile_1_r1), .R2(r2), .WE(RegWrite), .W_num(IR[11:7]),
    .R1_num(multiplexer_8_out), .R2_num(multiplexer_9_out));
  assign bit_extender_4_out = {{20{multiplexer_10_out[11]}}, multiplexer_10_out};  // Bit_Extender bit_extender_4
  Multiplexer #(.select(1), .width(32), .disabled("Z"), .enable("false")) multiplexer_12 (
    .in0(result), .in1(shifter_2_out), .out(multiplexer_12_out), .sel(aluresult[1]));
  Adder #(.width(32)) adder_1 (.a(PC), .b(32'h4), .out(adder_1_out));  // open: cin, cout
  Adder #(.width(32)) adder_2 (.a(shifter_3_out), .b(PC), .out(adder_2_out));  // open: cin, cout
  Adder #(.width(32)) adder_3 (.a(shifter_4_out), .b(PC), .out(adder_3_out));  // open: cin, cout
  assign and_6_out = aluresult & 32'hfffffffe;  // AND_Gate and_6, 32 bits wide
  Comparator #(.width(32), .mode("twosComplement")) comparator_7 (
    .a(32'h22), .b(regifile_1_r1), .eq(comparator_7_eq));  // open: gt, lt
  Multiplexer #(.select(1), .width(32), .disabled("Z"), .enable("false")) multiplexer_13 (
    .in0(r2), .in1(bit_extender_4_out), .out(multiplexer_13_out), .sel(\单周期硬布线控制器_1_alu_src ));
  Multiplexer #(.select(1), .width(32), .disabled("Z"), .enable("false")) multiplexer_14 (
    .in0(result), .in1(and_7_out), .out(multiplexer_14_out), .sel(half));
  assign and_7_out = multiplexer_12_out & 32'hffff;  // AND_Gate and_7, 32 bits wide
  and and_8 (CSRRCI, CSR, ~ALUOP[3]);  // AND_Gate
  and and_9 (CSRRSI, CSR, ALUOP[3]);
  and and_10 (and_10_out, alu_1_equal, \单周期硬布线控制器_1_beq );
  not not_4 (not_4_out, alu_1_equal);
  and and_11 (and_11_out, blt, alu_1_out_6);
  ALU alu_1 (
    .X(regifile_1_r1), .Y(multiplexer_13_out), .AluOP(ALUOP), .Equal(alu_1_equal), .Result(aluresult),
    .out_6(alu_1_out_6));  // open: Result_2, out_4
  Multiplexer #(.select(1), .width(32), .disabled("Z"), .enable("false")) multiplexer_15 (
    .in0(multiplexer_14_out), .in1(adder_1_out), .out(multiplexer_15_out), .sel(J));
  Priority_Encoder #(.select(2), .disabled("Z")) priority_encoder_5 (
    .in0(1'b1), .in1(B), .in2(jal), .in3(jalr), .out(priority_encoder_5_out));  // open: gs, en_out, en_in
  Multiplexer #(.select(2), .width(32), .disabled("Z"), .enable("false")) multiplexer_16 (
    .in0(adder_1_out), .in1(adder_2_out), .in2(adder_3_out), .in3(and_6_out), .out(addr),
    .sel(priority_encoder_5_out));
  and and_12 (and_12_out, not_4_out, \单周期硬布线控制器_1_bne );
  or or_18 (or_18_out, and_10_out, and_12_out);
  or or_19 (B, or_18_out, and_11_out);
  and and_13 (led, ecall, comparator_7_eq);
  Multiplexer #(.select(1), .width(32), .disabled("Z"), .enable("false")) multiplexer_17 (
    .in0(multiplexer_15_out), .in1({32{1'b0}}), .out(RDin), .sel(CSR));
  not not_5 (not_5_out, comparator_7_eq);
  and and_14 (halt, ecall, not_5_out);
  RAM #(.addrWidth(10), .dataWidth(32), .bus("separate"), .Select("high")) ram_1 (
    .addr(aluresult[11:2]), .din(MDin), .data(ram_1_data), .str(MemWrite), .clk(CLK), .ld(1'b1));  // open: sel, clr
  Multiplexer #(.select(1), .width(32), .disabled("Z"), .enable("false")) multiplexer_18 (
    .in0({32{1'b0}}), .in1(r2), .out(multiplexer_18_out), .sel(led));
  Multiplexer #(.select(1), .width(32), .disabled("Z"), .enable("false")) multiplexer_19 (
    .in0(aluresult), .in1(ram_1_data), .out(multiplexer_19_out), .sel(\单周期硬布线控制器_1_memtoreg ));
  Adder #(.width(32)) adder_4 (.a(PC), .b(U_imm), .out(adder_4_out));  // open: cin, cout
  Register #(.width(32), .trigger("rising"), .Select("low")) register_7 (
    .D(multiplexer_18_out), .en(led), .Q(LedData), .clk(CLK));  // open: clr
  Multiplexer #(.select(1), .width(32), .disabled("Z"), .enable("false")) multiplexer_20 (
    .in0(multiplexer_19_out), .in1(adder_4_out), .out(multiplexer_20_out), .sel(auipc));
  Multiplexer #(.select(1), .width(32), .disabled("Z"), .enable("false")) multiplexer_21 (
    .in0(multiplexer_20_out), .in1(U_imm), .out(result), .sel(lui));
  assign bit_extender_5_out = {{16{1'b0}}, r2[15:0]};  // Bit_Extender bit_extender_5
  Multiplexer #(.select(1), .width(5), .disabled("Z"), .enable("false")) multiplexer_22 (
    .in0({5{1'b0}}), .in1(5'b10000), .out(multiplexer_22_out), .sel(aluresult[1]));
  Multiplexer #(.select(1), .width(32), .disabled("Z"), .enable("false")) multiplexer_23 (
    .in0(r2), .in1(shifter_5_out), .out(MDin), .sel(sh));
  Shifter #(.width(32), .shift("ll")) shifter_5 (
    .in(bit_extender_5_out), .\dist (multiplexer_22_out), .out(shifter_5_out));

  // Other names for the same wires on the sheet: high = aluresult[1]

  // Notes on the sheet:
  //   中断源
  //   中断等待指示
  //   总复位信号应将除ROM以外所有存储组件全部清零
  //   单级中断测试信号模拟器
  //   清除中断
  //   数码管输出
  //   识别中断类型找地址
  //   数码管输出应该用寄存器锁存，否则显示数据只能一闪而过
  //   Reset 
  //   Reset 
  //   Reset 
  //   中断响应阶段
  //   中断响应
  //   中断使能位(用于开关中断)
  //   为方便自动评测，需要输出PC，IR，寄存器堆写如数据RDin
  //   RAM写使能MemWrite、RAM写入数据MDin等信号
  //   保存断点地址
  //   指令探针
  //   指令存储器
  //   保存中断号
  //   控制位
  //   暂停节拍，不能为0
  //   指令字
  //   contents of rom_1 (hex, n*v repeats v):
  //   7d000113 100413 1f41993 41f9d993 433 c00913 800b13 140413 f47413 800293 100313 499993 89e9b3 1300533
  //   2200893 73 406282b3 fe0294e3 140413 f00f93 1f47433 1c41413 800293 100313 49d993 89e9b3 1300533
  //   2200893 73 406282b3 fe0294e3 1c45413 406b0b33 b0463 f95ff06f 2b3 fff2c293 1029293 fff2e293 500533
  //   2200893 73 f5dff06f 1112023 410113 a12023 410113 812023 410113 1312023 410113 1412023 410113 1512023
  //   410113 1612023 410113 40e073 100b13 300a13 100a93 1600433 441413 14469b3 1300533 2200893 73 fe0416e3
  //   415a0a33 fe0a10e3 40f073 ffc10113 12b03 ffc10113 12a83 ffc10113 12a03 ffc10113 12983 ffc10113 12403
  //   ffc10113 12503 ffc10113 12883 200073 1112023 410113 a12023 410113 812023 410113 1312023 410113
  //   1412023 410113 1512023 410113 1612023 410113 40e073 200b13 300a13 100a93 1600433 441413 14469b3
  //   1300533 2200893 73 fe0416e3 415a0a33 fe0a10e3 40f073 ffc10113 12b03 ffc10113 12a83 ffc10113 12a03
  //   ffc10113 12983 ffc10113 12403 ffc10113 12503 ffc10113 12883 200073 1112023 410113 a12023 410113
  //   812023 410113 1312023 410113 1412023 410113 1512023 410113 1612023 410113 40e073 300b13 300a13
  //   100a93 1600433 441413 14469b3 1300533 2200893 73 fe0416e3 415a0a33 fe0a10e3 40f073 ffc10113 12b03
  //   ffc10113 12a83 ffc10113 12a03 ffc10113 12983 ffc10113 12403 ffc10113 12503 ffc10113 12883 200073
  //   I型指令
  //   s型指令
  //   戳工具置1进入计数暂停模式，ctrl+k时钟自动运行到对应节拍暂停
  //   ctrl+k关闭时钟连续运行，将控制位置零，进入单步调试模式调试
  //   JAL
  //   JALR
  //   URET
  //   B型指令
  //   J型指令
  //   Beq
  //   Bne
  //   MemToReg
  //   MemWrite
  //   AluOP
  //   AluSrcB
  //   RegWrite
  //   half
  //   可计数暂停的时钟源
  //   PC+4
  //   BEQ/BNE
  //   JAL
  //   JALR
  //   数据存储器
endmodule

module \单周期_单级中断  (
  input  IR1,
  input  IR2,
  input  IR3,
  output RegWrite,
  output MemWrite,
  output [31:0] PC,
  output [31:0] IR,
  output [31:0] RDin,
  output [31:0] MDin,
  output [31:0] LedData
);

  wire alu_1_equal, alu_1_out_6, and_1_out, and_2_out, and_3_out, and_6_out, and_7_out, and_8_out, auipc, B,
       blt, CLK, clock_1_out, CLR1, CLR2, CLR3, comparator_1_eq, comparator_2_eq, comparator_3_eq,
       comparator_4_eq, comparator_5_eq, comparator_5_lt, comparator_6_eq, d_ff_1_q, d_ff_2_q, d_ff_3_q,
       d_ff_5_q, ecall, Go, half, halt, IE, INTR, INTR1, INTR2, INTR3, IR1_t, IR2_t, IR3_t, IRA, IRB, IRC,
       IRHAVE, J, jal, jalr, led, lui, nand_1_out, not_1_out, not_2_out, not_3_out, not_4_out, not_5_out,
       or_4_out, or_5_out, or_6_out, or_7_out, or_8_out, or_13_out, or_14_out, or_16_out, sh, uret, W1, W2,
       W3, \单周期硬布线控制器_1_alu_src , \单周期硬布线控制器_1_beq , \单周期硬布线控制器_1_bne , \单周期硬布线控制器_1_memtoreg ,
       \单周期硬布线控制器_1_s_type ;
  wire [1:0] priority_encoder_1_out, priority_encoder_2_out, priority_encoder_3_out, register_1_q;
  wire [3:0] \单周期硬布线控制器_1_alu_op ;
  wire [4:0] multiplexer_3_out, multiplexer_4_out, multiplexer_9_out;
  wire [11:0] multiplexer_5_out;
  wire [12:0] CNT_num;
  wire [15:0] \总周期数 ;
  wire [31:0] adder_1_out, adder_2_out, adder_3_out, adder_4_out, adder_5_out, aluresult, and_5_out,
       and_11_out, and_12_out, bit_extender_1_out, bit_extender_2_out, bit_extender_3_out,
       bit_extender_4_out, bit_extender_5_out, inn, IR_PC, MEPC, multiplexer_2_out, multiplexer_6_out,
       multiplexer_7_out, multiplexer_8_out, multiplexer_10_out, multiplexer_12_out, multiplexer_14_out,
       multiplexer_15_out, multiplexer_16_out, r2, regifile_1_r1, result, shifter_2_out, shifter_3_out,
       shifter_4_out, shifter_5_out, U_imm, \use ;

  Button \u_继续运行  (.out(Go));
  Button _1 (.out(IRA));
  Button _2 (.out(IRB));
  Button _3 (.out(IRC));
  LED #(.active("true")) led_1 (.in(W1));
  LED #(.active("true")) led_2 (.in(W2));
  LED #(.active("true")) led_3 (.in(W3));
  Hex_Digit_Display hex_digit_display_1 (.value(LedData[31:28]));  // open: dp
  Comparator #(.width(16), .mode("twosComplement")) comparator_1 (
    .a(16'h23b), .b(\总周期数 ), .eq(comparator_1_eq));  // open: gt, lt
  Comparator #(.width(16), .mode("twosComplement")) comparator_2 (
    .a(\总周期数 ), .b(16'h1), .eq(comparator_2_eq));  // open: gt, lt
  Comparator #(.width(16), .mode("twosComplement")) comparator_3 (
    .a(\总周期数 ), .b(16'h4), .eq(comparator_3_eq));  // open: gt, lt
  Comparator #(.width(16), .mode("twosComplement")) comparator_4 (
    .a(\总周期数 ), .b(16'h7), .eq(comparator_4_eq));  // open: gt, lt
  D_Flip_Flop #(.trigger("rising"), .Pre_Clr_Positions("LEGACY"), .NegatePresetClear("false"), .enable("true"), .NewFFLayout("false")) d_ff_1 (
    .clk(IRA), .D(1'b1), .Q(d_ff_1_q), .reset(INTR1));  // open: Qn, preset, en
  or or_1 (W1, INTR1, d_ff_1_q);
  D_Flip_Flop #(.trigger("rising"), .Pre_Clr_Positions("LEGACY"), .NegatePresetClear("false"), .enable("true"), .NewFFLayout("false")) d_ff_2 (
    .clk(IRB), .D(1'b1), .Q(d_ff_2_q), .reset(INTR2));  // open: Qn, preset, en
  or or_2 (W2, INTR2, d_ff_2_q);
  D_Flip_Flop #(.trigger("rising"), .Pre_Clr_Positions("LEGACY"), .NegatePresetClear("false"), .enable("true"), .NewFFLayout("false")) d_ff_3 (
    .clk(IRC), .D(1'b1), .Q(d_ff_3_q), .reset(INTR3));  // open: Qn, preset, en
  or or_3 (W3, INTR3, d_ff_3_q);
  Hex_Digit_Display hex_digit_display_2 (.value(LedData[27:24]));  // open: dp
  Hex_Digit_Display hex_digit_display_3 (.value(LedData[23:20]));  // open: dp
  or or_4 (or_4_out, comparator_1_eq, comparator_2_eq);
  assign IRA = or_4_out ? ~CLK : 1'bz;  // Controlled_Inverter controlled_inverter_1
  assign IRB = comparator_3_eq ? ~CLK : 1'bz;  // Controlled_Inverter controlled_inverter_2
  assign IRC = comparator_4_eq ? ~CLK : 1'bz;  // Controlled_Inverter controlled_inverter_3
  or or_5 (or_5_out, d_ff_1_q, INTR1);
  or or_6 (or_6_out, d_ff_2_q, INTR2);
  Multiplexer #(.select(2), .width(32), .disabled("Z"), .enable("false")) multiplexer_1 (
    .in0(32'h30ac), .in1(32'h3150), .in2(32'h31f4), .out(IR_PC), .sel(priority_encoder_1_out));  // open: in3
  Priority_Encoder #(.select(2), .disabled("Z")) priority_encoder_1 (
    .in0(INTR1), .in1(INTR2), .in2(INTR3), .out(priority_encoder_1_out));  // open: in3, gs, en_out, en_in
  Hex_Digit_Display hex_digit_display_4 (.value(LedData[15:12]));  // open: dp
  Hex_Digit_Display hex_digit_display_5 (.value(LedData[19:16]));  // open: dp
  Pull_Resistor #(.pull(0)) pull_resistor_1 (.node(IRA));
  Pull_Resistor #(.pull(0)) pull_resistor_2 (.node(IRB));
  Pull_Resistor #(.pull(0)) pull_resistor_3 (.node(IRC));
  and and_1 (and_1_out, or_5_out, ~CLR1);  // AND_Gate
  and and_2 (and_2_out, or_6_out, ~CLR2);  // AND_Gate
  or or_7 (or_7_out, d_ff_3_q, INTR3);
  and and_3 (and_3_out, or_7_out, ~CLR3);  // AND_Gate
  Hex_Digit_Display hex_digit_display_6 (.value(LedData[7:4]));  // open: dp
  Hex_Digit_Display hex_digit_display_7 (.value(LedData[11:8]));  // open: dp
  // Probe on \总周期数 
  // Probe on \总周期数 
  D_Flip_Flop #(.trigger("rising"), .Pre_Clr_Positions("LEGACY"), .NegatePresetClear("false"), .enable("true"), .NewFFLayout("false")) u_IR1 (
    .clk(CLK), .D(and_1_out), .Q(INTR1));  // open: Qn, preset, en, reset
  D_Flip_Flop #(.trigger("rising"), .Pre_Clr_Positions("LEGACY"), .NegatePresetClear("false"), .enable("true"), .NewFFLayout("false")) IR1_2 (
    .clk(CLK), .D(and_2_out), .Q(INTR2));  // open: Qn, preset, en, reset
  D_Flip_Flop #(.trigger("rising"), .Pre_Clr_Positions("LEGACY"), .NegatePresetClear("false"), .enable("true"), .NewFFLayout("false")) IR1_3 (
    .clk(CLK), .D(and_3_out), .Q(INTR3));  // open: Qn, preset, en, reset
  Hex_Digit_Display hex_digit_display_8 (.value(LedData[3:0]));  // open: dp
  or or_8 (or_8_out, ~IRHAVE, uret);  // OR_Gate
  Register #(.width(2), .trigger("rising"), .Select("low")) register_1 (
    .D(priority_encoder_1_out), .en(INTR), .Q(register_1_q), .clk(CLK));  // open: clr
  // Probe on PC
  or or_9 (IRHAVE, INTR1, INTR2, INTR3);
  or or_10 (IR1_t, IR1, IRA);
  D_Flip_Flop #(.trigger("rising"), .Pre_Clr_Positions("LEGACY"), .NegatePresetClear("false"), .enable("true"), .NewFFLayout("true")) d_ff_4 (
    .clk(CLK), .D(or_8_out), .Q(IE));  // open: Qn, preset, en, reset
  Demultiplexer #(.select(2), .width(1), .tristate("false"), .disabled("Z"), .enable("false")) demultiplexer_1 (
    .out0(CLR1), .out1(CLR2), .out2(CLR3), .in(uret), .sel(register_1_q));  // open: out3
  or or_11 (IR2_t, IR2, IRB);
  and and_4 (INTR, IRHAVE, IE);
  or or_12 (IR3_t, IR3, IRC);
  or or_13 (or_13_out, Go, not_1_out);
  not not_1 (not_1_out, halt);
  Multiplexer #(.select(2), .width(32), .disabled("Z"), .enable("false")) multiplexer_2 (
    .in0(multiplexer_7_out), .in1(IR_PC), .in2(MEPC), .out(multiplexer_2_out), .sel(priority_encoder_2_out));  // open: in3
  Counter #(.width(16), .max('hffff), .ongoal("wrap"), .trigger("rising"), .behavior("new")) counter_1 (
    .count(or_13_out), .Q(\总周期数 ), .clk(CLK));  // open: load, D, carry, clr, preset, down
  Register #(.width(32), .trigger("rising"), .Select("low")) u_PC (
    .D(multiplexer_2_out), .en(or_14_out), .Q(PC), .clk(CLK));  // open: clr
  or or_14 (or_14_out, Go, not_2_out);
  not not_2 (not_2_out, halt);
  Priority_Encoder #(.select(2), .disabled("Z")) priority_encoder_2 (
    .in0(1'b1), .in1(INTR), .in2(uret), .out(priority_encoder_2_out));  // open: in3, gs, en_out, en_in
  Register #(.width(32), .trigger("rising"), .Select("low")) register_2 (
    .D(multiplexer_7_out), .en(INTR), .Q(MEPC), .clk(CLK));  // open: clr
  or or_15 (J, jal, jalr);
  // RiscV_Probe riscv_probe_1: pin names not known; wires that end beside it: IR
  ROM #(.addrWidth(10), .dataWidth(32), .Select("high")) rom_1 (.addr(PC[11:2]), .data(IR));
  D_Flip_Flop #(.trigger("high"), .Pre_Clr_Positions("LEGACY"), .NegatePresetClear("false"), .enable("true"), .NewFFLayout("false")) d_ff_5 (.Q(d_ff_5_q));  // open: clk, D, Qn, preset, en, reset
  // Probe on 13'hc
  \单周期硬布线控制器  \u_单周期硬布线控制器_1  (
    .Funct({IR[30], IR[25], IR[14:12]}), .OP(IR[6:2]), .ALU_OP(\单周期硬布线控制器_1_alu_op ),
    .MemToReg(\单周期硬布线控制器_1_memtoreg ), .MemWrite(MemWrite), .ALU_SRC(\单周期硬布线控制器_1_alu_src ),
    .RegWrite(RegWrite), .ecall(ecall), .S_type(\单周期硬布线控制器_1_s_type ), .Jalr(jalr), .Beq(\单周期硬布线控制器_1_beq ),
    .JAL(jal), .Bne(\单周期硬布线控制器_1_bne ), .in_3(IR[21]), .uret(uret), .half(half), .blt(blt), .sh(sh),
    .auipc(auipc), .lui(lui));  // open: CSR
  Multiplexer #(.select(1), .width(5), .disabled("Z"), .enable("false")) multiplexer_3 (
    .in0(IR[19:15]), .in1(5'b10001), .out(multiplexer_3_out), .sel(ecall));
  assign bit_extender_1_out = {{12{IR[31]}}, IR[31:12]};  // Bit_Extender bit_extender_1
  Comparator #(.width(13), .mode("twosComplement")) comparator_5 (
    .a(CNT_num), .b(13'hc), .eq(comparator_5_eq), .lt(comparator_5_lt));  // open: gt
  Clock #(.highDuration(1), .lowDuration(1)) clock_1 (.out(clock_1_out));
  Multiplexer #(.select(1), .width(5), .disabled("Z"), .enable("false")) multiplexer_4 (
    .in0(IR[24:20]), .in1(5'b01010), .out(multiplexer_4_out), .sel(ecall));
  Multiplexer #(.select(1), .width(12), .disabled("Z"), .enable("false")) multiplexer_5 (
    .in0(IR[31:20]), .in1({IR[31:25], IR[11:7]}), .out(multiplexer_5_out), .sel(\单周期硬布线控制器_1_s_type ));
  Shifter #(.width(32), .shift("ll")) shifter_1 (.in(bit_extender_1_out), .\dist (5'b01100), .out(U_imm));
  assign bit_extender_2_out = {{20{IR[31]}}, {IR[31], IR[7], IR[30:25], IR[11:8]}};  // Bit_Extender bit_extender_2
  assign bit_extender_3_out = {{12{IR[31]}}, {IR[31], IR[19:12], IR[20], IR[30:21]}};  // Bit_Extender bit_extender_3
  Counter #(.width(13), .max('h1fff), .ongoal("stay"), .trigger("rising"), .behavior("old")) counter_2 (
    .count(comparator_5_lt), .Q(CNT_num), .clk(clock_1_out));  // open: load, D, carry, clr, preset
  Shifter #(.width(32), .shift("ll")) shifter_2 (.in(bit_extender_2_out), .\dist (5'b00001), .out(shifter_2_out));
  Shifter #(.width(32), .shift("ll")) shifter_3 (.in(bit_extender_3_out), .\dist (5'b00001), .out(shifter_3_out));
  nand nand_1 (nand_1_out, d_ff_5_q, comparator_5_eq);
  not not_3 (not_3_out, RegWrite);
  Regifile regifile_1 (
    .Din(RDin), .Clk(CLK), .R1(regifile_1_r1), .R2(r2), .WE(RegWrite), .W_num(IR[11:7]),
    .R1_num(multiplexer_3_out), .R2_num(multiplexer_4_out));
  assign bit_extender_4_out = {{20{multiplexer_5_out[11]}}, multiplexer_5_out};  // Bit_Extender bit_extender_4
  Adder #(.width(32)) adder_1 (.a(PC), .b(32'h4), .out(adder_1_out));  // open: cin, cout
  Adder #(.width(32)) adder_2 (.a(shifter_2_out), .b(PC), .out(adder_2_out));  // open: cin, cout
  Adder #(.width(32)) adder_3 (.a(shifter_3_out), .b(PC), .out(adder_3_out));  // open: cin, cout
  assign and_5_out = aluresult & 32'hfffffffe;  // AND_Gate and_5, 32 bits wide
  assign CLK = nand_1_out ? clock_1_out : 1'bz;  // Controlled_Buffer controlled_buffer_1
  Pull_Resistor #(.pull(1)) pull_resistor_4 (.node(CLK));
  Comparator #(.width(32), .mode("twosComplement")) comparator_6 (
    .a(32'h22), .b(regifile_1_r1), .eq(comparator_6_eq));  // open: gt, lt
  Multiplexer #(.select(1), .width(32), .disabled("Z"), .enable("false")) multiplexer_6 (
    .in0(r2), .in1(bit_extender_4_out), .out(multiplexer_6_out), .sel(\单周期硬布线控制器_1_alu_src ));
  and and_6 (and_6_out, alu_1_equal, \单周期硬布线控制器_1_beq );
  not not_4 (not_4_out, alu_1_equal);
  and and_7 (and_7_out, not_4_out, \单周期硬布线控制器_1_bne );
  and and_8 (and_8_out, not_3_out, alu_1_out_6);
  ALU alu_1 (
    .X(regifile_1_r1), .Y(multiplexer_6_out), .AluOP(\单周期硬布线控制器_1_alu_op ), .Equal(alu_1_equal),
    .Result(aluresult), .out_6(alu_1_out_6));  // open: Result_2, out_4
  Priority_Encoder #(.select(2), .disabled("Z")) priority_encoder_3 (
    .in0(1'b1), .in1(B), .in2(jal), .in3(jalr), .out(priority_encoder_3_out));  // open: gs, en_out, en_in
  Multiplexer #(.select(2), .width(32), .disabled("Z"), .enable("false")) multiplexer_7 (
    .in0(adder_1_out), .in1(adder_2_out), .in2(adder_3_out), .in3(and_5_out), .out(multiplexer_7_out),
    .sel(priority_encoder_3_out));
  or or_16 (or_16_out, and_6_out, and_7_out);
  and and_9 (led, ecall, comparator_6_eq);
  or or_17 (B, or_16_out, and_8_out);
  Multiplexer #(.select(1), .width(32), .disabled("Z"), .enable("false")) multiplexer_8 (
    .in0({32{1'b0}}), .in1(r2), .out(multiplexer_8_out), .sel(led));
  not not_5 (not_5_out, comparator_6_eq);
  RAM #(.addrWidth(10), .dataWidth(32), .bus("separate"), .Select("high")) ram_1 (
    .addr(aluresult[11:2]), .din(MDin), .data(\use ), .str(MemWrite), .clk(CLK), .ld(1'b1));  // open: sel, clr
  Register #(.width(32), .trigger("rising"), .Select("low")) register_3 (
    .D(multiplexer_8_out), .en(led), .Q(LedData), .clk(CLK));  // open: clr
  and and_10 (halt, ecall, not_5_out);
  assign bit_extender_5_out = {{16{1'b0}}, r2[15:0]};  // Bit_Extender bit_extender_5
  Multiplexer #(.select(1), .width(5), .disabled("Z"), .enable("false")) multiplexer_9 (
    .in0({5{1'b0}}), .in1(5'b10000), .out(multiplexer_9_out), .sel(aluresult[1]));
  Multiplexer #(.select(1), .width(32), .disabled("Z"), .enable("false")) multiplexer_10 (
    .in0(32'hffff0000), .in1(32'hffff), .out(multiplexer_10_out), .sel(aluresult[1]));
  Multiplexer #(.select(1), .width(32), .disabled("Z"), .enable("false")) multiplexer_11 (
    .in0(aluresult), .in1(\use ), .out(result), .sel(\单周期硬布线控制器_1_memtoreg ));
  Shifter #(.width(32), .shift("lr")) shifter_4 (.in(result), .\dist (5'b10000), .out(shifter_4_out));
  Shifter #(.width(32), .shift("ll")) shifter_5 (
    .in(bit_extender_5_out), .\dist (multiplexer_9_out), .out(shifter_5_out));
  assign and_11_out = \use  & multiplexer_10_out;  // AND_Gate and_11, 32 bits wide
  Multiplexer #(.select(1), .width(32), .disabled("Z"), .enable("false")) multiplexer_12 (
    .in0(result), .in1(shifter_4_out), .out(multiplexer_12_out), .sel(aluresult[1]));
  Adder #(.width(32)) adder_4 (.a(PC), .b(32'h4), .out(adder_4_out));  // open: cin, cout
  assign inn = shifter_5_out | and_11_out;  // OR_Gate or_18, 32 bits wide
  Multiplexer #(.select(1), .width(32), .disabled("Z"), .enable("false")) multiplexer_13 (
    .in0(r2), .in1(inn), .out(MDin), .sel(sh));
  Multiplexer #(.select(1), .width(32), .disabled("Z"), .enable("false")) multiplexer_14 (
    .in0(result), .in1(and_12_out), .out(multiplexer_14_out), .sel(half));
  assign and_12_out = multiplexer_12_out & 32'hffff;  // AND_Gate and_12, 32 bits wide
  Multiplexer #(.select(1), .width(32), .disabled("Z"), .enable("false")) multiplexer_15 (
    .in0(multiplexer_14_out), .in1(adder_4_out), .out(multiplexer_15_out), .sel(J));
  Adder #(.width(32)) adder_5 (.a(PC), .b(U_imm), .out(adder_5_out));  // open: cin, cout
  Multiplexer #(.select(1), .width(32), .disabled("Z"), .enable("false")) multiplexer_16 (
    .in0(multiplexer_15_out), .in1(adder_5_out), .out(multiplexer_16_out), .sel(auipc));
  Multiplexer #(.select(1), .width(32), .disabled("Z"), .enable("false")) multiplexer_17 (
    .in0(multiplexer_16_out), .in1(U_imm), .out(RDin), .sel(lui));

  // Other names for the same wires on the sheet: high = aluresult[1]

  // Notes on the sheet:
  //   中断源
  //   中断等待指示
  //   总复位信号应将除ROM以外所有存储组件全部清零
  //   单级中断测试信号模拟器
  //   识别中断类型找地址
  //   数码管输出
  //   数码管输出应该用寄存器锁存，否则显示数据只能一闪而过
  //   Reset 
  //   Reset 
  //   Reset 
  //   中断响应阶段
  //   中断使能位(用于开关中断)
  //   清除中断
  //   判断中断使能
  //   中断响应
  //   保存断点
  //   为方便自动评测，需要输出PC，IR，寄存器堆写如数据RDin
  //   RAM写使能MemWrite、RAM写入数据MDin等信号
  //   指令探针
  //   指令存储器
  //   指令字
  //   contents of rom_1 (hex, n*v repeats v):
  //   7d000113 100413 1f41993 41f9d993 433 c00913 800b13 140413 f47413 800293 100313 499993 89e9b3 1300533
  //   2200893 73 406282b3 fe0294e3 140413 f00f93 1f47433 1c41413 800293 100313 49d993 89e9b3 1300533
  //   2200893 73 406282b3 fe0294e3 1c45413 406b0b33 b0463 f95ff06f 2b3 fff2c293 1029293 fff2e293 500533
  //   2200893 73 f5dff06f 1112023 410113 a12023 410113 812023 410113 1312023 410113 1412023 410113 1512023
  //   410113 1612023 410113 100b13 300a13 100a93 1600433 441413 14469b3 1300533 2200893 73 fe0416e3
  //   415a0a33 fe0a10e3 ffc10113 12b03 ffc10113 12a83 ffc10113 12a03 ffc10113 12983 ffc10113 12403
  //   ffc10113 12503 ffc10113 12883 200073 1112023 410113 a12023 410113 812023 410113 1312023 410113
  //   1412023 410113 1512023 410113 1612023 410113 200b13 300a13 100a93 1600433 441413 14469b3 1300533
  //   2200893 73 fe0416e3 415a0a33 fe0a10e3 ffc10113 12b03 ffc10113 12a83 ffc10113 12a03 ffc10113 12983
  //   ffc10113 12403 ffc10113 12503 ffc10113 12883 200073 1112023 410113 a12023 410113 812023 410113
  //   1312023 410113 1412023 410113 1512023 410113 1612023 410113 300b13 300a13 100a93 1600433 441413
  //   14469b3 1300533 2200893 73 fe0416e3 415a0a33 fe0a10e3 ffc10113 12b03 ffc10113 12a83 ffc10113 12a03
  //   ffc10113 12983 ffc10113 12403 ffc10113 12503 ffc10113 12883 200073
  //   JAL
  //   JALR
  //   URET
  //   I型指令
  //   s型指令
  //   B型指令
  //   J型指令
  //   控制位
  //   暂停节拍，不能为0
  //   Beq
  //   Bne
  //   AluOP
  //   AluSrcB
  //   RegWrite
  //   half
  //   戳工具置1进入计数暂停模式，ctrl+k时钟自动运行到对应节拍暂停
  //   ctrl+k关闭时钟连续运行，将控制位置零，进入单步调试模式调试
  //   MemToReg
  //   MemWrite
  //   PC+4
  //   BEQ/BNE
  //   JAL
  //   JALR
  //   可计数暂停的时钟源
  //   数据存储器
  //   PC+4
endmodule

module \封装正确性测试  (
);

  wire IR1, IR2, IR3, MemW, RegW;
  wire [31:0] EX_PC, ID_PC, IF_PC, IR, LED, MDin, MDinr, MEM_PC, PC, RDin, RDinr, WB_PC;

  \单周期RISC_V  \u_单周期risc_v_1  (
    .IR1(IR1), .IR2(IR2), .IR3(IR3), .RegWrite(RegW), .MemWrite(MemW), .PC(PC), .IR(IR), .RDin(RDin),
    .MDin(MDin), .LedData(LED));
  \气泡流水线  \u_气泡流水线_1  (
    .RegWrite(RegW), .MemWrite(MemW), .IF_PC(IF_PC), .ID_PC(ID_PC), .EX_PC(EX_PC), .M_PC(MEM_PC),
    .WB_PC(WB_PC), .RDin(RDinr), .MDin(MDinr), .LedData(LED));
  \单周期_单级中断  \u_单周期_单级中断_1  (
    .IR1(IR1), .IR2(IR2), .IR3(IR3), .RegWrite(RegW), .MemWrite(MemW), .PC(PC), .IR(IR), .RDin(RDin),
    .MDin(MDin), .LedData(LED));
  \理想流水线  \u_理想流水线_1  (
    .RegWrite(RegW), .MemWrite(MemW), .IF_PC(IF_PC), .ID_PC(ID_PC), .EX_PC(EX_PC), .M_PC(MEM_PC),
    .WB_PC(WB_PC), .RDin(RDinr), .MDin(MDinr), .LedData(LED));
  \重定向流水线  \u_重定向流水线_1  (
    .RegWrite(RegW), .MemWrite(MemW), .IF_PC(IF_PC), .ID_PC(ID_PC), .EX_PC(EX_PC), .M_PC(MEM_PC),
    .WB_PC(WB_PC), .RDin(RDinr), .MDin(MDinr), .LedData(LED));
  \单周期_多级中断  \u_单周期_多级中断_1  (
    .IR1(IR1), .IR2(IR2), .IR3(IR3), .RegWrite(RegW), .MemWrite(MemW), .PC(PC), .IR(IR), .RDin(RDin),
    .MDin(MDin), .LedData(LED));

  // Notes on the sheet:
  //   单周期封装测试
  //   气泡流水封装测试
  //   单周期+单级中断封装测试
  //   请检查上面封装有无位宽不匹配，引脚标签是否和连接的标签相对应，否则无法在educoder平台上正确测试
  //   理想流水封装测试
  //   重定向流水封装测试
  //   单周期+多级中断封装测试
endmodule

module IF_ID (
  input  CLK,
  input  RST,
  input  [31:0] IR,
  input  [31:0] PC,
  input  PREDICT,
  input  FLUSH,
  input  EN,
  output [31:0] IROUT,
  output [31:0] PCOUT,
  output PREDICTOUT
);

  wire multiplexer_2_out, not_1_out;
  wire [31:0] multiplexer_1_out, multiplexer_3_out;

  Multiplexer #(.select(1), .width(32), .disabled("Z"), .enable("false")) multiplexer_1 (
    .in0(IR), .in1({32{1'b0}}), .out(multiplexer_1_out), .sel(FLUSH));
  Multiplexer #(.select(1), .width(1), .disabled("Z"), .enable("false")) multiplexer_2 (
    .in0(PREDICT), .in1(1'b0), .out(multiplexer_2_out), .sel(FLUSH));
  Multiplexer #(.select(1), .width(32), .disabled("Z"), .enable("false")) multiplexer_3 (
    .in0(PC), .in1({32{1'b0}}), .out(multiplexer_3_out), .sel(FLUSH));
  not not_1 (not_1_out, EN);
  Register #(.width(32), .trigger("rising"), .Select("low")) register_1 (
    .D(multiplexer_1_out), .en(not_1_out), .Q(IROUT), .clk(CLK), .clr(RST));
  Register #(.width(32), .trigger("rising"), .Select("low")) register_2 (
    .D(multiplexer_3_out), .en(not_1_out), .Q(PCOUT), .clk(CLK), .clr(RST));
  Register #(.width(1), .trigger("rising"), .Select("low")) register_3 (
    .D(multiplexer_2_out), .en(not_1_out), .Q(PREDICTOUT), .clk(CLK));  // open: clr
endmodule

module ID_EX (
  input  CLK,
  input  RST,
  input  JAL,
  input  JALR,
  input  URET,
  input  beq,
  input  BNE,
  input  MEMTOREG,
  input  MEMWRITE,
  input  [3:0] ALUOP,
  input  ALUSRC,
  input  REGWRITE,
  input  half,
  input  CSR,
  input  ECALL,
  input  [1:0] R1F,
  input  [31:0] R1,
  input  [31:0] R2,
  input  [1:0] R2F,
  input  [4:0] WRITEREG,
  input  [31:0] PC,
  input  [31:0] IR,
  input  [31:0] IMM1,
  input  [31:0] IMM2,
  input  [31:0] IMM3,
  input  PREDICT,
  input  FLUSH,
  input  EN,
  output JALOUT,
  output JALROUT,
  output URETOUT,
  output BEQOUT,
  output BNEOUT,
  output MEMTOREGOUT,
  output MEMWRITEOUT,
  output [3:0] ALUOPOUT,
  output ALUSRCOUT,
  output REGWRITEOUT,
  output halfOUT,
  output CSROUT,
  output ECALLOUT,
  output [1:0] R1FOUT,
  output [31:0] R1OUT,
  output [31:0] R2OUT_prime,
  output [1:0] R2FOUT,
  output [4:0] WRITEREGOUT_prime,
  output [31:0] PCOUT_prime,
  output [31:0] IROUT_prime,
  output [31:0] IMM1OUT_prime,
  output [31:0] IMM2OUT_prime,
  output [31:0] IMM3OUT_prime,
  output PREDICTOUT
);

  wire multiplexer_1_out, multiplexer_2_out, multiplexer_3_out, multiplexer_4_out, multiplexer_5_out,
       multiplexer_6_out, multiplexer_7_out, multiplexer_9_out, multiplexer_10_out, multiplexer_11_out,
       multiplexer_12_out, multiplexer_13_out, multiplexer_24_out, not_1_out;
  wire [1:0] multiplexer_14_out, multiplexer_17_out;
  wire [3:0] multiplexer_8_out;
  wire [4:0] multiplexer_18_out;
  wire [31:0] multiplexer_15_out, multiplexer_16_out, multiplexer_19_out, multiplexer_20_out,
       multiplexer_21_out, multiplexer_22_out, multiplexer_23_out;

  Multiplexer #(.select(1), .width(1), .disabled("Z"), .enable("false")) multiplexer_1 (
    .in0(JAL), .in1(1'b0), .out(multiplexer_1_out), .sel(FLUSH));
  Multiplexer #(.select(1), .width(1), .disabled("Z"), .enable("false")) multiplexer_2 (
    .in0(JALR), .in1(1'b0), .out(multiplexer_2_out), .sel(FLUSH));
  Multiplexer #(.select(1), .width(1), .disabled("Z"), .enable("false")) multiplexer_3 (
    .in0(URET), .in1(1'b0), .out(multiplexer_3_out), .sel(FLUSH));
  Multiplexer #(.select(1), .width(1), .disabled("Z"), .enable("false")) multiplexer_4 (
    .in0(beq), .in1(1'b0), .out(multiplexer_4_out), .sel(FLUSH));
  Multiplexer #(.select(1), .width(1), .disabled("Z"), .enable("false")) multiplexer_5 (
    .in0(BNE), .in1(1'b0), .out(multiplexer_5_out), .sel(FLUSH));
  Multiplexer #(.select(1), .width(1), .disabled("Z"), .enable("false")) multiplexer_6 (
    .in0(MEMTOREG), .in1(1'b0), .out(multiplexer_6_out), .sel(FLUSH));
  Multiplexer #(.select(1), .width(1), .disabled("Z"), .enable("false")) multiplexer_7 (
    .in0(MEMWRITE), .in1(1'b0), .out(multiplexer_7_out), .sel(FLUSH));
  Multiplexer #(.select(1), .width(4), .disabled("Z"), .enable("false")) multiplexer_8 (
    .in0(ALUOP), .in1(4'b0000), .out(multiplexer_8_out), .sel(FLUSH));
  Multiplexer #(.select(1), .width(1), .disabled("Z"), .enable("false")) multiplexer_9 (
    .in0(ALUSRC), .in1(1'b0), .out(multiplexer_9_out), .sel(FLUSH));
  Multiplexer #(.select(1), .width(1), .disabled("Z"), .enable("false")) multiplexer_10 (
    .in0(REGWRITE), .in1(1'b0), .out(multiplexer_10_out), .sel(FLUSH));
  Multiplexer #(.select(1), .width(1), .disabled("Z"), .enable("false")) multiplexer_11 (
    .in0(half), .in1(1'b0), .out(multiplexer_11_out), .sel(FLUSH));
  Multiplexer #(.select(1), .width(1), .disabled("Z"), .enable("false")) multiplexer_12 (
    .in0(CSR), .in1(1'b0), .out(multiplexer_12_out), .sel(FLUSH));
  Multiplexer #(.select(1), .width(1), .disabled("Z"), .enable("false")) multiplexer_13 (
    .in0(ECALL), .in1(1'b0), .out(multiplexer_13_out), .sel(FLUSH));
  Multiplexer #(.select(1), .width(2), .disabled("Z"), .enable("false")) multiplexer_14 (
    .in0(R1F), .in1(2'b00), .out(multiplexer_14_out), .sel(FLUSH));
  Multiplexer #(.select(1), .width(32), .disabled("Z"), .enable("false")) multiplexer_15 (
    .in0(R1), .in1({32{1'b0}}), .out(multiplexer_15_out), .sel(FLUSH));
  Multiplexer #(.select(1), .width(32), .disabled("Z"), .enable("false")) multiplexer_16 (
    .in0(R2), .in1({32{1'b0}}), .out(multiplexer_16_out), .sel(FLUSH));
  Multiplexer #(.select(1), .width(2), .disabled("Z"), .enable("false")) multiplexer_17 (
    .in0(R2F), .in1(2'b00), .out(multiplexer_17_out), .sel(FLUSH));
  Multiplexer #(.select(1), .width(5), .disabled("Z"), .enable("false")) multiplexer_18 (
    .in0(WRITEREG), .in1({5{1'b0}}), .out(multiplexer_18_out), .sel(FLUSH));
  Multiplexer #(.select(1), .width(32), .disabled("Z"), .enable("false")) multiplexer_19 (
    .in0(PC), .in1({32{1'b0}}), .out(multiplexer_19_out), .sel(FLUSH));
  Multiplexer #(.select(1), .width(32), .disabled("Z"), .enable("false")) multiplexer_20 (
    .in0(IR), .in1({32{1'b0}}), .out(multiplexer_20_out), .sel(FLUSH));
  Multiplexer #(.select(1), .width(32), .disabled("Z"), .enable("false")) multiplexer_21 (
    .in0(IMM1), .in1({32{1'b0}}), .out(multiplexer_21_out), .sel(FLUSH));
  Multiplexer #(.select(1), .width(32), .disabled("Z"), .enable("false")) multiplexer_22 (
    .in0(IMM2), .in1({32{1'b0}}), .out(multiplexer_22_out), .sel(FLUSH));
  Multiplexer #(.select(1), .width(32), .disabled("Z"), .enable("false")) multiplexer_23 (
    .in0(IMM3), .in1({32{1'b0}}), .out(multiplexer_23_out), .sel(FLUSH));
  Multiplexer #(.select(1), .width(1), .disabled("Z"), .enable("false")) multiplexer_24 (
    .in0(PREDICT), .in1(1'b0), .out(multiplexer_24_out), .sel(FLUSH));
  not not_1 (not_1_out, EN);
  Register #(.width(1), .trigger("rising"), .Select("low")) register_1 (
    .D(multiplexer_1_out), .en(not_1_out), .Q(JALOUT), .clk(CLK), .clr(RST));
  Register #(.width(1), .trigger("rising"), .Select("low")) register_2 (
    .D(multiplexer_2_out), .en(not_1_out), .Q(JALROUT), .clk(CLK), .clr(RST));
  Register #(.width(1), .trigger("rising"), .Select("low")) register_3 (
    .D(multiplexer_3_out), .en(not_1_out), .Q(URETOUT), .clk(CLK), .clr(RST));
  Register #(.width(1), .trigger("rising"), .Select("low")) register_4 (
    .D(multiplexer_4_out), .en(not_1_out), .Q(BEQOUT), .clk(CLK), .clr(RST));
  Register #(.width(1), .trigger("rising"), .Select("low")) register_5 (
    .D(multiplexer_5_out), .en(not_1_out), .Q(BNEOUT), .clk(CLK), .clr(RST));
  Register #(.width(1), .trigger("rising"), .Select("low")) register_6 (
    .D(multiplexer_6_out), .en(not_1_out), .Q(MEMTOREGOUT), .clk(CLK), .clr(RST));
  Register #(.width(1), .trigger("rising"), .Select("low")) register_7 (
    .D(multiplexer_7_out), .en(not_1_out), .Q(MEMWRITEOUT), .clk(CLK), .clr(RST));
  Register #(.width(4), .trigger("rising"), .Select("low")) register_8 (
    .D(multiplexer_8_out), .en(not_1_out), .Q(ALUOPOUT), .clk(CLK), .clr(RST));
  Register #(.width(1), .trigger("rising"), .Select("low")) register_9 (
    .D(multiplexer_9_out), .en(not_1_out), .Q(ALUSRCOUT), .clk(CLK), .clr(RST));
  Register #(.width(1), .trigger("rising"), .Select("low")) register_10 (
    .D(multiplexer_10_out), .en(not_1_out), .Q(REGWRITEOUT), .clk(CLK), .clr(RST));
  Register #(.width(1), .trigger("rising"), .Select("low")) register_11 (
    .D(multiplexer_11_out), .en(not_1_out), .Q(halfOUT), .clk(CLK), .clr(RST));
  Register #(.width(1), .trigger("rising"), .Select("low")) register_12 (
    .D(multiplexer_12_out), .en(not_1_out), .Q(CSROUT), .clk(CLK), .clr(RST));
  Register #(.width(1), .trigger("rising"), .Select("low")) register_13 (
    .D(multiplexer_13_out), .en(not_1_out), .Q(ECALLOUT), .clk(CLK), .clr(RST));
  Register #(.width(2), .trigger("rising"), .Select("low")) register_14 (
    .D(multiplexer_14_out), .en(not_1_out), .Q(R1FOUT), .clk(CLK), .clr(RST));
  Register #(.width(32), .trigger("rising"), .Select("low")) register_15 (
    .D(multiplexer_15_out), .en(not_1_out), .Q(R1OUT), .clk(CLK), .clr(RST));
  Register #(.width(32), .trigger("rising"), .Select("low")) register_16 (
    .D(multiplexer_16_out), .en(not_1_out), .Q(R2OUT_prime), .clk(CLK), .clr(RST));
  Register #(.width(2), .trigger("rising"), .Select("low")) register_17 (
    .D(multiplexer_17_out), .en(not_1_out), .Q(R2FOUT), .clk(CLK), .clr(RST));
  Register #(.width(5), .trigger("rising"), .Select("low")) register_18 (
    .D(multiplexer_18_out), .en(not_1_out), .Q(WRITEREGOUT_prime), .clk(CLK), .clr(RST));
  Register #(.width(32), .trigger("rising"), .Select("low")) register_19 (
    .D(multiplexer_19_out), .en(not_1_out), .Q(PCOUT_prime), .clk(CLK), .clr(RST));
  Register #(.width(32), .trigger("rising"), .Select("low")) register_20 (
    .D(multiplexer_20_out), .en(not_1_out), .Q(IROUT_prime), .clk(CLK), .clr(RST));
  Register #(.width(32), .trigger("rising"), .Select("low")) register_21 (
    .D(multiplexer_21_out), .en(not_1_out), .Q(IMM1OUT_prime), .clk(CLK), .clr(RST));
  Register #(.width(32), .trigger("rising"), .Select("low")) register_22 (
    .D(multiplexer_22_out), .en(not_1_out), .Q(IMM2OUT_prime), .clk(CLK), .clr(RST));
  Register #(.width(32), .trigger("rising"), .Select("low")) register_23 (
    .D(multiplexer_23_out), .en(not_1_out), .Q(IMM3OUT_prime), .clk(CLK), .clr(RST));
  Register #(.width(1), .trigger("rising"), .Select("low")) register_24 (
    .D(multiplexer_24_out), .en(not_1_out), .Q(PREDICTOUT), .clk(CLK), .clr(RST));
endmodule

module EX_MEM (
  input  CLK,
  input  RST,
  input  J,
  input  MEMWRITE,
  input  MEMTOREGWRITE,
  input  REGWRITE,
  input  HALF,
  input  HALT,
  input  [31:0] ALURESULT,
  input  [31:0] WRITEDATA,
  input  [4:0] WRITEREG,
  input  [31:0] PC,
  input  [31:0] IR,
  input  [31:0] IMM,
  input  FLUSH,
  input  EN,
  output JOUT,
  output MEMWRITEOUT,
  output MEMTOREGOUT,
  output REGWRITEOUT,
  output HALFOUT,
  output HALTOUT,
  output [31:0] ALURESULTOUT,
  output [31:0] WRITEDATAOUT,
  output [4:0] WRITEREGOUT,
  output [31:0] PCOUT,
  output [31:0] IROUT,
  output [31:0] IMMOUT
);

  wire multiplexer_1_out, multiplexer_2_out, multiplexer_3_out, multiplexer_4_out, multiplexer_5_out,
       multiplexer_6_out, not_1_out;
  wire [4:0] multiplexer_9_out;
  wire [31:0] multiplexer_7_out, multiplexer_8_out, multiplexer_10_out, multiplexer_11_out,
       multiplexer_12_out;

  Multiplexer #(.select(1), .width(1), .disabled("Z"), .enable("false")) multiplexer_1 (
    .in0(J), .in1(1'b0), .out(multiplexer_1_out), .sel(FLUSH));
  Multiplexer #(.select(1), .width(1), .disabled("Z"), .enable("false")) multiplexer_2 (
    .in0(MEMWRITE), .in1(1'b0), .out(multiplexer_2_out), .sel(FLUSH));
  Multiplexer #(.select(1), .width(1), .disabled("Z"), .enable("false")) multiplexer_3 (
    .in0(MEMTOREGWRITE), .in1(1'b0), .out(multiplexer_3_out), .sel(FLUSH));
  Multiplexer #(.select(1), .width(1), .disabled("Z"), .enable("false")) multiplexer_4 (
    .in0(REGWRITE), .in1(1'b0), .out(multiplexer_4_out), .sel(FLUSH));
  Multiplexer #(.select(1), .width(1), .disabled("Z"), .enable("false")) multiplexer_5 (
    .in0(HALF), .in1(1'b0), .out(multiplexer_5_out), .sel(FLUSH));
  Multiplexer #(.select(1), .width(1), .disabled("Z"), .enable("false")) multiplexer_6 (
    .in0(HALT), .in1(1'b0), .out(multiplexer_6_out), .sel(FLUSH));
  Multiplexer #(.select(1), .width(32), .disabled("Z"), .enable("false")) multiplexer_7 (
    .in0(ALURESULT), .in1({32{1'b0}}), .out(multiplexer_7_out), .sel(FLUSH));
  Multiplexer #(.select(1), .width(32), .disabled("Z"), .enable("false")) multiplexer_8 (
    .in0(WRITEDATA), .in1({32{1'b0}}), .out(multiplexer_8_out), .sel(FLUSH));
  Multiplexer #(.select(1), .width(5), .disabled("Z"), .enable("false")) multiplexer_9 (
    .in0(WRITEREG), .in1({5{1'b0}}), .out(multiplexer_9_out), .sel(FLUSH));
  Multiplexer #(.select(1), .width(32), .disabled("Z"), .enable("false")) multiplexer_10 (
    .in0(PC), .in1({32{1'b0}}), .out(multiplexer_10_out), .sel(FLUSH));
  Multiplexer #(.select(1), .width(32), .disabled("Z"), .enable("false")) multiplexer_11 (
    .in0(IR), .in1({32{1'b0}}), .out(multiplexer_11_out), .sel(FLUSH));
  Multiplexer #(.select(1), .width(32), .disabled("Z"), .enable("false")) multiplexer_12 (
    .in0(IMM), .in1({32{1'b0}}), .out(multiplexer_12_out), .sel(FLUSH));
  not not_1 (not_1_out, EN);
  Register #(.width(1), .trigger("rising"), .Select("low")) register_1 (
    .D(multiplexer_1_out), .en(not_1_out), .Q(JOUT), .clk(CLK), .clr(RST));
  Register #(.width(1), .trigger("rising"), .Select("low")) register_2 (
    .D(multiplexer_2_out), .en(not_1_out), .Q(MEMWRITEOUT), .clk(CLK), .clr(RST));
  Register #(.width(1), .trigger("rising"), .Select("low")) register_3 (
    .D(multiplexer_3_out), .en(not_1_out), .Q(MEMTOREGOUT), .clk(CLK), .clr(RST));
  Register #(.width(1), .trigger("rising"), .Select("low")) register_4 (
    .D(multiplexer_4_out), .en(not_1_out), .Q(REGWRITEOUT), .clk(CLK), .clr(RST));
  Register #(.width(1), .trigger("rising"), .Select("low")) register_5 (
    .D(multiplexer_5_out), .en(not_1_out), .Q(HALFOUT), .clk(CLK), .clr(RST));
  Register #(.width(1), .trigger("rising"), .Select("low")) register_6 (
    .D(multiplexer_6_out), .en(not_1_out), .Q(HALTOUT), .clk(CLK), .clr(RST));
  Register #(.width(32), .trigger("rising"), .Select("low")) register_7 (
    .D(multiplexer_7_out), .en(not_1_out), .Q(ALURESULTOUT), .clk(CLK), .clr(RST));
  Register #(.width(32), .trigger("rising"), .Select("low")) register_8 (
    .D(multiplexer_8_out), .en(not_1_out), .Q(WRITEDATAOUT), .clk(CLK), .clr(RST));
  Register #(.width(5), .trigger("rising"), .Select("low")) register_9 (
    .D(multiplexer_9_out), .en(not_1_out), .Q(WRITEREGOUT), .clk(CLK), .clr(RST));
  Register #(.width(32), .trigger("rising"), .Select("low")) register_10 (
    .D(multiplexer_10_out), .en(not_1_out), .Q(PCOUT), .clk(CLK), .clr(RST));
  Register #(.width(32), .trigger("rising"), .Select("low")) register_11 (
    .D(multiplexer_11_out), .en(not_1_out), .Q(IROUT), .clk(CLK), .clr(RST));
  Register #(.width(32), .trigger("rising"), .Select("low")) register_12 (
    .D(multiplexer_12_out), .en(not_1_out), .Q(IMMOUT), .clk(CLK), .clr(RST));
endmodule

// MEM/WB
module MEM_WB (
  input  in_1,
  input  in_2,
  input  J,
  input  MEMTOREG,
  input  REGWRITE,
  input  HALF,
  input  HALT,
  input  [31:0] ALURESULT,
  input  [31:0] MEMDATA,
  input  HIGH,
  input  [4:0] WRITEREG,
  input  [31:0] PC,
  input  [31:0] IR,
  input  [31:0] IMM,
  input  FLUSH,
  input  EN,
  output JOUT,
  output MEMTOREGOUT,
  output REGWRITEOUT,
  output HALFOUT,
  output HALTOUT,
  output [31:0] ALURESULTOUT,
  output [31:0] MEMDATAOUT,
  output HIGHOUT,
  output [4:0] WRITEREGOUT,
  output [31:0] PCOUT,
  output [31:0] IROUT,
  output [31:0] IMMOUT
);

  wire multiplexer_1_out, multiplexer_2_out, multiplexer_3_out, multiplexer_4_out, multiplexer_5_out,
       multiplexer_8_out, not_1_out;
  wire [4:0] multiplexer_9_out;
  wire [31:0] multiplexer_6_out, multiplexer_7_out, multiplexer_10_out, multiplexer_11_out,
       multiplexer_12_out;

  Multiplexer #(.select(1), .width(1), .disabled("Z"), .enable("false")) multiplexer_1 (
    .in0(J), .in1(1'b0), .out(multiplexer_1_out), .sel(FLUSH));
  Multiplexer #(.select(1), .width(1), .disabled("Z"), .enable("false")) multiplexer_2 (
    .in0(MEMTOREG), .in1(1'b0), .out(multiplexer_2_out), .sel(FLUSH));
  Multiplexer #(.select(1), .width(1), .disabled("Z"), .enable("false")) multiplexer_3 (
    .in0(REGWRITE), .in1(1'b0), .out(multiplexer_3_out), .sel(FLUSH));
  Multiplexer #(.select(1), .width(1), .disabled("Z"), .enable("false")) multiplexer_4 (
    .in0(HALF), .in1(1'b0), .out(multiplexer_4_out), .sel(FLUSH));
  Multiplexer #(.select(1), .width(1), .disabled("Z"), .enable("false")) multiplexer_5 (
    .in0(HALT), .in1(1'b0), .out(multiplexer_5_out), .sel(FLUSH));
  Multiplexer #(.select(1), .width(32), .disabled("Z"), .enable("false")) multiplexer_6 (
    .in0(ALURESULT), .in1({32{1'b0}}), .out(multiplexer_6_out), .sel(FLUSH));
  Multiplexer #(.select(1), .width(32), .disabled("Z"), .enable("false")) multiplexer_7 (
    .in0(MEMDATA), .in1({32{1'b0}}), .out(multiplexer_7_out), .sel(FLUSH));
  Multiplexer #(.select(1), .width(1), .disabled("Z"), .enable("false")) multiplexer_8 (
    .in0(HIGH), .in1(1'b0), .out(multiplexer_8_out), .sel(FLUSH));
  Multiplexer #(.select(1), .width(5), .disabled("Z"), .enable("false")) multiplexer_9 (
    .in0(WRITEREG), .in1({5{1'b0}}), .out(multiplexer_9_out), .sel(FLUSH));
  Multiplexer #(.select(1), .width(32), .disabled("Z"), .enable("false")) multiplexer_10 (
    .in0(PC), .in1({32{1'b0}}), .out(multiplexer_10_out), .sel(FLUSH));
  Multiplexer #(.select(1), .width(32), .disabled("Z"), .enable("false")) multiplexer_11 (
    .in0(IR), .in1({32{1'b0}}), .out(multiplexer_11_out), .sel(FLUSH));
  Multiplexer #(.select(1), .width(32), .disabled("Z"), .enable("false")) multiplexer_12 (
    .in0(IMM), .in1({32{1'b0}}), .out(multiplexer_12_out), .sel(FLUSH));
  not not_1 (not_1_out, EN);
  Register #(.width(1), .trigger("rising"), .Select("low")) register_1 (
    .D(multiplexer_1_out), .en(not_1_out), .Q(JOUT), .clk(in_1), .clr(in_2));
  Register #(.width(1), .trigger("rising"), .Select("low")) register_2 (
    .D(multiplexer_2_out), .en(not_1_out), .Q(MEMTOREGOUT), .clk(in_1), .clr(in_2));
  Register #(.width(1), .trigger("rising"), .Select("low")) register_3 (
    .D(multiplexer_4_out), .en(not_1_out), .Q(HALFOUT), .clk(in_1), .clr(in_2));
  Register #(.width(1), .trigger("rising"), .Select("low")) register_4 (
    .D(multiplexer_5_out), .en(not_1_out), .Q(HALTOUT), .clk(in_1), .clr(in_2));
  Register #(.width(32), .trigger("rising"), .Select("low")) register_5 (
    .D(multiplexer_6_out), .en(not_1_out), .Q(ALURESULTOUT), .clk(in_1), .clr(in_2));
  Register #(.width(32), .trigger("rising"), .Select("low")) register_6 (
    .D(multiplexer_7_out), .en(not_1_out), .Q(MEMDATAOUT), .clk(in_1), .clr(in_2));
  Register #(.width(1), .trigger("rising"), .Select("low")) register_7 (
    .D(multiplexer_8_out), .en(not_1_out), .Q(HIGHOUT), .clk(in_1), .clr(in_2));
  Register #(.width(1), .trigger("rising"), .Select("low")) register_8 (
    .D(multiplexer_3_out), .en(not_1_out), .Q(REGWRITEOUT), .clk(in_1), .clr(in_2));
  Register #(.width(5), .trigger("rising"), .Select("low")) register_9 (
    .D(multiplexer_9_out), .en(not_1_out), .Q(WRITEREGOUT), .clk(in_1), .clr(in_2));
  Register #(.width(32), .trigger("rising"), .Select("low")) register_10 (
    .D(multiplexer_10_out), .en(not_1_out), .Q(PCOUT), .clk(in_1), .clr(in_2));
  Register #(.width(32), .trigger("rising"), .Select("low")) register_11 (
    .D(multiplexer_11_out), .en(not_1_out), .Q(IROUT), .clk(in_1), .clr(in_2));
  Register #(.width(32), .trigger("rising"), .Select("low")) register_12 (
    .D(multiplexer_12_out), .en(not_1_out), .Q(IMMOUT), .clk(in_1), .clr(in_2));
endmodule

// 冲突检测逻辑
module \冲突检测逻辑_气泡  (
  input  MEM_REGWRITE,
  input  EX_REGWRITE,
  input  [4:0] EX_WRITEREG,
  input  [4:0] MEM_WRITEREG,
  input  [31:0] ID_IR,
  output STALL
);

  wire ALUSRCB, and_1_out, and_2_out, and_3_out, and_4_out, and_5_out, and_6_out, and_7_out, comparator_1_eq,
       comparator_2_eq, comparator_3_eq, comparator_4_eq, comparator_5_eq, comparator_6_eq, ID_ecall, JAL,
       not_2_out, not_3_out, not_4_out, not_5_out, R1USED, R2USED, STYPE;
  wire [4:0] multiplexer_1_out, multiplexer_2_out;

  not not_1 (R1USED, JAL);
  \单周期硬布线控制器  \u_单周期硬布线控制器_1  (
    .Funct({ID_IR[30], ID_IR[25], ID_IR[14:12]}), .OP(ID_IR[6:2]), .ALU_SRC(ALUSRCB), .ecall(ID_ecall),
    .S_type(STYPE), .JAL(JAL), .in_3(ID_IR[21]));  // open: ALU_OP, MemToReg, MemWrite, RegWrite, Jalr, Beq, Bne, uret, half, CSR, blt, sh, auipc, lui
  Multiplexer #(.select(1), .width(5), .disabled("Z"), .enable("false")) multiplexer_1 (
    .in0(ID_IR[19:15]), .in1(5'b10001), .out(multiplexer_1_out), .sel(ID_ecall));
  not not_2 (not_2_out, JAL);
  not not_3 (not_3_out, ALUSRCB);
  Multiplexer #(.select(1), .width(5), .disabled("Z"), .enable("false")) multiplexer_2 (
    .in0(ID_IR[24:20]), .in1(5'b01010), .out(multiplexer_2_out), .sel(ID_ecall));
  and and_1 (and_1_out, not_2_out, not_3_out);
  or or_1 (R2USED, and_1_out, STYPE);
  Comparator #(.width(5), .mode("twosComplement")) comparator_1 (
    .a(EX_WRITEREG), .b(multiplexer_2_out), .eq(comparator_1_eq));  // open: gt, lt
  Comparator #(.width(5), .mode("twosComplement")) comparator_2 (
    .a(EX_WRITEREG), .b(multiplexer_1_out), .eq(comparator_2_eq));  // open: gt, lt
  Comparator #(.width(5), .mode("twosComplement")) comparator_3 (
    .a(MEM_WRITEREG), .b(multiplexer_2_out), .eq(comparator_3_eq));  // open: gt, lt
  Comparator #(.width(5), .mode("twosComplement")) comparator_4 (
    .a(MEM_WRITEREG), .b(multiplexer_1_out), .eq(comparator_4_eq));  // open: gt, lt
  Comparator #(.width(5), .mode("twosComplement")) comparator_5 (
    .a(multiplexer_2_out), .b({5{1'b0}}), .eq(comparator_5_eq));  // open: gt, lt
  Comparator #(.width(5), .mode("twosComplement")) comparator_6 (
    .a(multiplexer_1_out), .b({5{1'b0}}), .eq(comparator_6_eq));  // open: gt, lt
  not not_4 (not_4_out, comparator_5_eq);
  not not_5 (not_5_out, comparator_6_eq);
  and and_2 (and_2_out, not_4_out, R2USED);
  and and_3 (and_3_out, not_5_out, R1USED);
  and and_4 (and_4_out, EX_REGWRITE, comparator_1_eq, and_2_out);
  and and_5 (and_5_out, EX_REGWRITE, comparator_2_eq, and_3_out);
  and and_6 (and_6_out, MEM_REGWRITE, comparator_3_eq, and_2_out);
  and and_7 (and_7_out, MEM_REGWRITE, comparator_4_eq, and_3_out);
  or or_2 (STALL, and_4_out, and_5_out, and_6_out, and_7_out);

  // Notes on the sheet:
  //   JAL
  //   JALR
  //   URET
  //   R1
  //   R2
  //   Beq
  //   Bne
  //   AluOP
  //   AluSrcB
  //   RegWrite
  //   half
  //   MemToReg
  //   MemWrite
endmodule

// 冲突检测逻辑
module \冲突检测逻辑_重定向  (
  input  EX_REGWRITE,
  input  MEM_REGWRITE,
  input  [4:0] MEM_WRITEREG,
  input  [4:0] EX_WRITEREG,
  input  EX_MEMTOREG,
  input  [31:0] ID_IR,
  output [1:0] R1FOWARD,
  output LOADUSE,
  output [1:0] R2FOWARD
);

  wire ALUSRCB, and_1_out, and_2_out, and_3_out, comparator_1_eq, comparator_2_eq, comparator_3_eq,
       comparator_4_eq, comparator_5_eq, comparator_6_eq, comparator_7_eq, comparator_8_eq, comparator_9_eq,
       comparator_10_eq, ID_ecall, JAL, not_1_out, not_2_out, not_3_out, not_4_out, not_5_out, not_6_out,
       not_7_out, R1USED, R2USED, STYPE, \单周期硬布线控制器_1_auipc , \单周期硬布线控制器_1_lui ;
  wire [4:0] R1, R2;

  or or_1 (R1USED, not_1_out, \单周期硬布线控制器_1_lui , \单周期硬布线控制器_1_auipc );
  not not_1 (not_1_out, JAL);
  \单周期硬布线控制器  \u_单周期硬布线控制器_1  (
    .Funct({ID_IR[30], ID_IR[25], ID_IR[14:12]}), .OP(ID_IR[6:2]), .ALU_SRC(ALUSRCB), .ecall(ID_ecall),
    .S_type(STYPE), .JAL(JAL), .in_3(ID_IR[21]), .auipc(\单周期硬布线控制器_1_auipc ), .lui(\单周期硬布线控制器_1_lui ));  // open: ALU_OP, MemToReg, MemWrite, RegWrite, Jalr, Beq, Bne, uret, half, CSR, blt, sh
  Multiplexer #(.select(1), .width(5), .disabled("Z"), .enable("false")) multiplexer_1 (
    .in0(ID_IR[19:15]), .in1(5'b10001), .out(R1), .sel(ID_ecall));
  not not_2 (not_2_out, JAL);
  not not_3 (not_3_out, ALUSRCB);
  Multiplexer #(.select(1), .width(5), .disabled("Z"), .enable("false")) multiplexer_2 (
    .in0(ID_IR[24:20]), .in1(5'b01010), .out(R2), .sel(ID_ecall));
  and and_1 (and_1_out, not_2_out, not_3_out);
  or or_2 (R2USED, and_1_out, STYPE, ID_ecall);
  Comparator #(.width(5), .mode("twosComplement")) comparator_1 (
    .a(EX_WRITEREG), .b(R1), .eq(comparator_1_eq));  // open: gt, lt
  Comparator #(.width(5), .mode("twosComplement")) comparator_2 (
    .a(EX_WRITEREG), .b(R2), .eq(comparator_2_eq));  // open: gt, lt
  Comparator #(.width(5), .mode("twosComplement")) comparator_3 (
    .a(R1), .b({5{1'b0}}), .eq(comparator_3_eq));  // open: gt, lt
  Comparator #(.width(5), .mode("twosComplement")) comparator_4 (
    .a(R2), .b({5{1'b0}}), .eq(comparator_4_eq));  // open: gt, lt
  not not_4 (not_4_out, comparator_3_eq);
  not not_5 (not_5_out, comparator_4_eq);
  and and_2 (and_2_out, comparator_1_eq, EX_MEMTOREG, R1USED, not_4_out);
  and and_3 (and_3_out, comparator_2_eq, EX_MEMTOREG, not_5_out, R2USED);
  or or_3 (LOADUSE, and_2_out, and_3_out);
  Comparator #(.width(5), .mode("twosComplement")) comparator_5 (
    .a(R1), .b({5{1'b0}}), .eq(comparator_5_eq));  // open: gt, lt
  not not_6 (not_6_out, comparator_5_eq);
  Comparator #(.width(5), .mode("twosComplement")) comparator_6 (
    .a(EX_WRITEREG), .b(R1), .eq(comparator_6_eq));  // open: gt, lt
  Comparator #(.width(5), .mode("twosComplement")) comparator_7 (
    .a(R2), .b({5{1'b0}}), .eq(comparator_7_eq));  // open: gt, lt
  Comparator #(.width(5), .mode("twosComplement")) comparator_8 (
    .a(R1), .b(MEM_WRITEREG), .eq(comparator_8_eq));  // open: gt, lt
  Comparator #(.width(5), .mode("twosComplement")) comparator_9 (
    .a(R2), .b(MEM_WRITEREG), .eq(comparator_9_eq));  // open: gt, lt
  not not_7 (not_7_out, comparator_7_eq);
  Comparator #(.width(5), .mode("twosComplement")) comparator_10 (
    .a(EX_WRITEREG), .b(R2), .eq(comparator_10_eq));  // open: gt, lt
  and and_4 (R1FOWARD[0], comparator_8_eq, MEM_REGWRITE, not_6_out, R1USED);
  and and_5 (R1FOWARD[1], not_6_out, R1USED, EX_REGWRITE, comparator_6_eq);
  and and_6 (R2FOWARD[1], not_7_out, R2USED, EX_REGWRITE, comparator_10_eq);
  and and_7 (R2FOWARD[0], comparator_9_eq, MEM_REGWRITE, not_7_out, R2USED);

  // Notes on the sheet:
  //   R1
  //   R2
  //   JAL
  //   JALR
  //   URET
  //   Beq
  //   Bne
  //   MemToReg
  //   MemWrite
  //   AluOP
  //   AluSrcB
  //   RegWrite
  //   half
endmodule

// REGIFILE
module \regifile_气泡  (
  input  [31:0] Din,
  input  Clk,
  input  WE,
  input  [4:0] R1_num,
  input  [4:0] W_num,
  input  [4:0] R2_num,
  output [31:0] R1,
  output [31:0] R2
);

  // RegisterFile registerfile_1: pin names not known; wires that end beside it: Din, Clk, WE, W_num, R1_num, R2_num, R1, R2
endmodule
module \流水线中断_单级EX  (
  input  IR1,
  input  IR2,
  input  IR3,
  output RegWrite,
  output MemWrite,
  output [31:0] IF_PC,
  output [31:0] ID_PC,
  output [31:0] EX_PC,
  output [31:0] M_PC,
  output [31:0] WB_PC,
  output [31:0] RDin,
  output [31:0] MDin,
  output [31:0] LedData
);

  wire alu_1_equal, alu_1_out_6, and_1_out, and_2_out, and_3_out, and_5_out, and_6_out, and_7_out, and_9_out,
       and_10_out, and_11_out, and_13_out, and_14_out, B, BRANCHTAKEN, CLK, clock_1_out, CLR1, CLR2, CLR3,
       comparator_1_eq, comparator_2_eq, comparator_3_eq, comparator_4_eq, comparator_5_eq, comparator_5_lt,
       comparator_6_eq, d_ff_1_q, d_ff_2_q, d_ff_3_q, d_ff_5_q, d_ff_6_q, ecall, ex_mem_1_halfout,
       ex_mem_1_haltout, ex_mem_1_memtoregout, EX_MEMTOREG, EX_REGWRITE, EX_URET, Go, halt, high,
       id_ex_1_alusrcout, id_ex_1_beqout, id_ex_1_bneout, id_ex_1_ecallout, id_ex_1_halfout,
       id_ex_1_memwriteout, IE, INTR, INTR1, INTR2, INTR3, IR1_t, IR2_t, IR3_t, IRA, IRB, IRC, IRHAVE, jal,
       jalr, JUMP, led, LOADUSE, MEM_J, MEM_REGWRITE, mem_wb_1_halfout, mem_wb_1_highout, mem_wb_1_jout,
       mem_wb_1_memtoregout, nand_1_out, not_1_out, not_2_out, not_3_out, not_4_out, not_5_out, or_4_out,
       or_5_out, or_6_out, or_7_out, or_9_out, or_10_out, or_11_out, or_14_out, or_18_out, or_19_out,
       or_20_out, RST, W1, W2, W3, \单周期硬布线控制器_1_alu_src , \单周期硬布线控制器_1_beq , \单周期硬布线控制器_1_bne ,
       \单周期硬布线控制器_1_half , \单周期硬布线控制器_1_jal , \单周期硬布线控制器_1_jalr , \单周期硬布线控制器_1_memtoreg ,
       \单周期硬布线控制器_1_memwrite , \单周期硬布线控制器_1_regwrite , \单周期硬布线控制器_1_s_type , \单周期硬布线控制器_1_uret ;
  wire [1:0] EX_R1F, EX_R2F, priority_encoder_1_out, priority_encoder_2_out, priority_encoder_3_out,
       R1FOWARD, R2FOWARD, register_1_q;
  wire [3:0] id_ex_1_aluopout, \单周期硬布线控制器_1_alu_op ;
  wire [4:0] EX_WRITEREG, mem_wb_1_writeregout, MEM_WRITEREG, multiplexer_6_out, multiplexer_7_out;
  wire [11:0] multiplexer_8_out;
  wire [12:0] CNT_num;
  wire [15:0] \LoadUse次数 , \总周期数 , \插入气泡数 , \无条件分支数 , \条件分支成功数 ;
  wire [31:0] adder_1_out, adder_2_out, adder_3_out, adder_4_out, aluresult, and_8_out, and_15_out,
       bit_extender_1_out, bit_extender_2_out, bit_extender_3_out, EX_IR, ex_mem_1_aluresultout,
       ex_mem_1_immout, EX_R1, EX_R2, id_ex_1_imm1out_prime, id_ex_1_imm2out_prime, id_ex_1_imm3out_prime,
       ID_IR, IF_IR, IR_PC, MEM_IR, MEM_RESULT, mem_wb_1_aluresultout, mem_wb_1_immout, mem_wb_1_memdataout,
       MEPC, multiplexer_2_out, multiplexer_3_out, multiplexer_4_out, multiplexer_5_out, multiplexer_9_out,
       multiplexer_10_out, multiplexer_14_out, multiplexer_15_out, multiplexer_16_out, R1R, R2R, ram_1_data,
       \regifile_气泡_1_r1 , \regifile_气泡_1_r2 , shifter_1_out, shifter_2_out, shifter_3_out, WB_IR;

  Button \u_总复位  (.out(RST));
  Button _1 (.out(IRA));
  Button _2 (.out(IRB));
  Button _3 (.out(IRC));
  // Probe on \总周期数 
  // Probe on \总周期数 
  Button \u_继续运行  (.out(Go));
  LED #(.active("true")) led_1 (.in(W1));
  LED #(.active("true")) led_2 (.in(W2));
  LED #(.active("true")) led_3 (.in(W3));
  or or_1 (W1, INTR1, d_ff_1_q);
  or or_2 (W2, INTR2, d_ff_2_q);
  or or_3 (W3, INTR3, d_ff_3_q);
  Hex_Digit_Display hex_digit_display_1 (.value(LedData[31:28]));  // open: dp
  // Probe on IF_PC[19:0]
  // RiscV_Probe riscv_probe_1: pin names not known; wires that end beside it: IF_IR
  Comparator #(.width(16), .mode("twosComplement")) comparator_1 (
    .a(16'h23b), .b(\总周期数 ), .eq(comparator_1_eq));  // open: gt, lt
  Comparator #(.width(16), .mode("twosComplement")) comparator_2 (
    .a(\总周期数 ), .b(16'h1), .eq(comparator_2_eq));  // open: gt, lt
  Comparator #(.width(16), .mode("twosComplement")) comparator_3 (
    .a(\总周期数 ), .b(16'h4), .eq(comparator_3_eq));  // open: gt, lt
  Comparator #(.width(16), .mode("twosComplement")) comparator_4 (
    .a(\总周期数 ), .b(16'h7), .eq(comparator_4_eq));  // open: gt, lt
  D_Flip_Flop #(.trigger("rising"), .Pre_Clr_Positions("LEGACY"), .NegatePresetClear("false"), .enable("true"), .NewFFLayout("false")) d_ff_1 (
    .clk(IRA), .D(1'b1), .Q(d_ff_1_q), .reset(INTR1));  // open: Qn, preset, en
  D_Flip_Flop #(.trigger("rising"), .Pre_Clr_Positions("LEGACY"), .NegatePresetClear("false"), .enable("true"), .NewFFLayout("false")) d_ff_2 (
    .clk(IRB), .D(1'b1), .Q(d_ff_2_q), .reset(INTR2));  // open: Qn, preset, en
  D_Flip_Flop #(.trigger("rising"), .Pre_Clr_Positions("LEGACY"), .NegatePresetClear("false"), .enable("true"), .NewFFLayout("false")) d_ff_3 (
    .clk(IRC), .D(1'b1), .Q(d_ff_3_q), .reset(INTR3));  // open: Qn, preset, en
  Priority_Encoder #(.select(2), .disabled("Z")) priority_encoder_1 (
    .in0(INTR1), .in1(INTR2), .in2(INTR3), .out(priority_encoder_1_out));  // open: in3, gs, en_out, en_in
  Hex_Digit_Display hex_digit_display_2 (.value(LedData[27:24]));  // open: dp
  Hex_Digit_Display hex_digit_display_3 (.value(LedData[23:20]));  // open: dp
  // Probe on ID_PC[19:0]
  // RiscV_Probe riscv_probe_2: pin names not known; wires that end beside it: ID_IR
  or or_4 (or_4_out, comparator_1_eq, comparator_2_eq);
  Pull_Resistor #(.pull(0)) pull_resistor_1 (.node(IRA));
  assign IRA = or_4_out ? ~CLK : 1'bz;  // Controlled_Inverter controlled_inverter_1
  Pull_Resistor #(.pull(0)) pull_resistor_2 (.node(IRB));
  assign IRB = comparator_3_eq ? ~CLK : 1'bz;  // Controlled_Inverter controlled_inverter_2
  Pull_Resistor #(.pull(0)) pull_resistor_3 (.node(IRC));
  assign IRC = comparator_4_eq ? ~CLK : 1'bz;  // Controlled_Inverter controlled_inverter_3
  or or_5 (or_5_out, d_ff_1_q, INTR1);
  or or_6 (or_6_out, d_ff_2_q, INTR2);
  or or_7 (or_7_out, d_ff_3_q, INTR3);
  Multiplexer #(.select(2), .width(32), .disabled("Z"), .enable("false")) multiplexer_1 (
    .in0(32'h30ac), .in1(32'h3150), .in2(32'h31f4), .out(IR_PC), .sel(priority_encoder_1_out));  // open: in3
  Hex_Digit_Display hex_digit_display_4 (.value(LedData[19:16]));  // open: dp
  Hex_Digit_Display hex_digit_display_5 (.value(LedData[15:12]));  // open: dp
  and and_1 (and_1_out, or_5_out, ~CLR1);  // AND_Gate
  and and_2 (and_2_out, or_6_out, ~CLR2);  // AND_Gate
  and and_3 (and_3_out, or_7_out, ~CLR3);  // AND_Gate
  Hex_Digit_Display hex_digit_display_6 (.value(LedData[11:8]));  // open: dp
  Hex_Digit_Display hex_digit_display_7 (.value(LedData[7:4]));  // open: dp
  // Probe on EX_PC[19:0]
  // RiscV_Probe riscv_probe_3: pin names not known; wires that end beside it: EX_IR
  D_Flip_Flop #(.trigger("rising"), .Pre_Clr_Positions("LEGACY"), .NegatePresetClear("false"), .enable("true"), .NewFFLayout("false")) u_IR1 (
    .clk(CLK), .D(and_1_out), .Q(INTR1));  // open: Qn, preset, en, reset
  D_Flip_Flop #(.trigger("rising"), .Pre_Clr_Positions("LEGACY"), .NegatePresetClear("false"), .enable("true"), .NewFFLayout("false")) IR1_2 (
    .clk(CLK), .D(and_2_out), .Q(INTR2));  // open: Qn, preset, en, reset
  D_Flip_Flop #(.trigger("rising"), .Pre_Clr_Positions("LEGACY"), .NegatePresetClear("false"), .enable("true"), .NewFFLayout("false")) IR1_3 (
    .clk(CLK), .D(and_3_out), .Q(INTR3));  // open: Qn, preset, en, reset
  Hex_Digit_Display hex_digit_display_8 (.value(LedData[3:0]));  // open: dp
  or or_8 (IRHAVE, INTR1, INTR2, INTR3);
  or or_9 (or_9_out, ~IRHAVE, EX_URET);  // OR_Gate
  Register #(.width(2), .trigger("rising"), .Select("low")) register_1 (
    .D(priority_encoder_1_out), .en(INTR), .Q(register_1_q), .clk(CLK));  // open: clr
  // Probe on \总周期数 
  // Probe on M_PC[19:0]
  // RiscV_Probe riscv_probe_4: pin names not known; wires that end beside it: MEM_IR
  D_Flip_Flop #(.trigger("rising"), .Pre_Clr_Positions("LEGACY"), .NegatePresetClear("false"), .enable("true"), .NewFFLayout("true")) d_ff_4 (
    .clk(CLK), .D(or_9_out), .Q(IE));  // open: Qn, preset, en, reset
  Demultiplexer #(.select(2), .width(1), .tristate("false"), .disabled("Z"), .enable("false")) demultiplexer_1 (
    .out0(CLR1), .out1(CLR2), .out2(CLR3), .in(EX_URET), .sel(register_1_q));  // open: out3
  // Probe on \总周期数 
  // Probe on \无条件分支数 
  // Probe on \条件分支成功数 
  // Probe on \插入气泡数 
  // Probe on \LoadUse次数 
  // Probe on IF_PC[11:0]
  // Probe on WB_PC[19:0]
  // RiscV_Probe riscv_probe_5: pin names not known; wires that end beside it: WB_IR
  and and_4 (INTR, IRHAVE, IE);
  // Probe on ID_PC[11:0]
  // Probe on EX_PC[11:0]
  D_Flip_Flop #(.trigger("rising"), .Pre_Clr_Positions("LEGACY"), .NegatePresetClear("false"), .enable("true"), .NewFFLayout("false")) d_ff_5 (
    .clk(CLK), .D(EX_URET), .Q(d_ff_5_q));  // open: Qn, preset, en, reset
  Multiplexer #(.select(1), .width(32), .disabled("Z"), .enable("false")) multiplexer_2 (
    .in0(multiplexer_3_out), .in1(multiplexer_5_out), .out(multiplexer_2_out), .sel(JUMP));
  Register #(.width(32), .trigger("rising"), .Select("low")) register_2 (
    .D(multiplexer_2_out), .en(INTR), .Q(MEPC), .clk(CLK));  // open: clr
  // Probe on M_PC[11:0]
  D_Flip_Flop #(.trigger("high"), .Pre_Clr_Positions("LEGACY"), .NegatePresetClear("false"), .enable("true"), .NewFFLayout("false")) d_ff_6 (.Q(d_ff_6_q));  // open: clk, D, Qn, preset, en, reset
  // Probe on 13'hc
  Multiplexer #(.select(1), .width(32), .disabled("Z"), .enable("false")) multiplexer_3 (
    .in0(ID_PC), .in1(IF_PC), .out(multiplexer_3_out), .sel(d_ff_5_q));
  // Probe on WB_PC[11:0]
  Comparator #(.width(13), .mode("twosComplement")) comparator_5 (
    .a(CNT_num), .b(13'hc), .eq(comparator_5_eq), .lt(comparator_5_lt));  // open: gt
  Clock #(.highDuration(1), .lowDuration(1)) clock_1 (.out(clock_1_out));
  nand nand_1 (nand_1_out, d_ff_6_q, comparator_5_eq);
  Counter #(.width(13), .max('h1fff), .ongoal("stay"), .trigger("rising"), .behavior("old")) counter_1 (
    .count(comparator_5_lt), .Q(CNT_num), .clk(clock_1_out));  // open: load, D, carry, clr, preset
  Counter #(.width(16), .max('hffff), .ongoal("wrap"), .trigger("rising"), .behavior("new")) counter_2 (
    .count(or_10_out), .Q(\总周期数 ), .clk(CLK));  // open: load, D, carry, clr, preset, down
  or or_10 (or_10_out, Go, not_1_out);
  not not_1 (not_1_out, halt);
  and and_5 (and_5_out, ~LOADUSE, or_11_out);  // AND_Gate
  or or_11 (or_11_out, Go, not_2_out);
  not not_2 (not_2_out, halt);
  Multiplexer #(.select(2), .width(32), .disabled("Z"), .enable("false")) multiplexer_4 (
    .in0(multiplexer_5_out), .in1(IR_PC), .in2(MEPC), .out(multiplexer_4_out), .sel(priority_encoder_2_out));  // open: in3
  Priority_Encoder #(.select(2), .disabled("Z")) priority_encoder_2 (
    .in0(1'b1), .in1(INTR), .in2(EX_URET), .out(priority_encoder_2_out));  // open: in3, gs, en_out, en_in
  assign CLK = nand_1_out ? clock_1_out : 1'bz;  // Controlled_Buffer controlled_buffer_1
  Register #(.width(32), .trigger("rising"), .Select("low")) PC (
    .D(multiplexer_4_out), .en(and_5_out), .Q(IF_PC), .clk(CLK), .clr(RST));
  Pull_Resistor #(.pull(1)) pull_resistor_4 (.node(CLK));
  Adder #(.width(32)) adder_1 (.a(IF_PC), .b(32'h4), .out(adder_1_out));  // open: cin, cout
  Multiplexer #(.select(2), .width(32), .disabled("Z"), .enable("false")) multiplexer_5 (
    .in0(adder_1_out), .in1(adder_3_out), .in2(adder_4_out), .in3(and_8_out), .out(multiplexer_5_out),
    .sel(priority_encoder_3_out));
  Priority_Encoder #(.select(2), .disabled("Z")) priority_encoder_3 (
    .in0(1'b1), .in1(B), .in2(jal), .in3(jalr), .out(priority_encoder_3_out));  // open: gs, en_out, en_in
  ROM #(.addrWidth(10), .dataWidth(32), .Select("high")) rom_1 (.addr(IF_PC[11:2]), .data(IF_IR));
  or or_12 (IR1_t, IR1, IRA);
  IF_ID if_id_1 (
    .IR(IF_IR), .PC(IF_PC), .IROUT(ID_IR), .PCOUT(ID_PC), .CLK(CLK), .RST(RST), .FLUSH(BRANCHTAKEN),
    .EN(or_14_out));  // open: PREDICT, PREDICTOUT
  \冲突检测逻辑_重定向  \u_冲突检测逻辑_重定向_1  (
    .EX_REGWRITE(EX_REGWRITE), .MEM_REGWRITE(MEM_REGWRITE), .MEM_WRITEREG(MEM_WRITEREG),
    .EX_WRITEREG(EX_WRITEREG), .EX_MEMTOREG(EX_MEMTOREG), .ID_IR(ID_IR), .R1FOWARD(R1FOWARD),
    .LOADUSE(LOADUSE), .R2FOWARD(R2FOWARD));
  or or_13 (IR2_t, IR2, IRB);
  // RiscV_Probe riscv_probe_6: pin names not known; wires that end beside it: CLK, RST, ID_IR
  or or_14 (or_14_out, and_6_out, LOADUSE);
  and and_6 (and_6_out, halt, ~Go);  // AND_Gate
  or or_15 (IR3_t, IR3, IRC);
  \单周期硬布线控制器  \u_单周期硬布线控制器_1  (
    .Funct({ID_IR[30], ID_IR[25], ID_IR[14:12]}), .OP(ID_IR[6:2]), .ALU_OP(\单周期硬布线控制器_1_alu_op ),
    .MemToReg(\单周期硬布线控制器_1_memtoreg ), .MemWrite(\单周期硬布线控制器_1_memwrite ), .ALU_SRC(\单周期硬布线控制器_1_alu_src ),
    .RegWrite(\单周期硬布线控制器_1_regwrite ), .ecall(ecall), .S_type(\单周期硬布线控制器_1_s_type ),
    .Jalr(\单周期硬布线控制器_1_jalr ), .Beq(\单周期硬布线控制器_1_beq ), .JAL(\单周期硬布线控制器_1_jal ), .Bne(\单周期硬布线控制器_1_bne ),
    .in_3(ID_IR[21]), .uret(\单周期硬布线控制器_1_uret ), .half(\单周期硬布线控制器_1_half ));  // open: CSR, blt, sh, auipc, lui
  Multiplexer #(.select(1), .width(5), .disabled("Z"), .enable("false")) multiplexer_6 (
    .in0(ID_IR[19:15]), .in1(5'b10001), .out(multiplexer_6_out), .sel(ecall));
  or or_16 (JUMP, B, jal, jalr);
  or or_17 (BRANCHTAKEN, B, jal, jalr, EX_URET, INTR);
  Multiplexer #(.select(1), .width(5), .disabled("Z"), .enable("false")) multiplexer_7 (
    .in0(ID_IR[24:20]), .in1(5'b01010), .out(multiplexer_7_out), .sel(ecall));
  Multiplexer #(.select(1), .width(12), .disabled("Z"), .enable("false")) multiplexer_8 (
    .in0(ID_IR[31:20]), .in1({ID_IR[31:25], ID_IR[11:7]}), .out(multiplexer_8_out), .sel(\单周期硬布线控制器_1_s_type ));
  assign bit_extender_1_out = {{20{ID_IR[31]}}, {ID_IR[31], ID_IR[7], ID_IR[30:25], ID_IR[11:8]}};  // Bit_Extender bit_extender_1
  assign bit_extender_2_out = {{12{ID_IR[31]}}, {ID_IR[31], ID_IR[19:12], ID_IR[20], ID_IR[30:21]}};  // Bit_Extender bit_extender_2
  assign bit_extender_3_out = {{20{multiplexer_8_out[11]}}, multiplexer_8_out};  // Bit_Extender bit_extender_3
  \regifile_气泡  \regifile_气泡_1  (
    .Din(RDin), .Clk(CLK), .R1(\regifile_气泡_1_r1 ), .R2(\regifile_气泡_1_r2 ), .WE(RegWrite),
    .W_num(mem_wb_1_writeregout), .R1_num(multiplexer_6_out), .R2_num(multiplexer_7_out));
  ID_EX id_ex_1 (
    .JAL(\单周期硬布线控制器_1_jal ), .JALR(\单周期硬布线控制器_1_jalr ), .URET(\单周期硬布线控制器_1_uret ), .beq(\单周期硬布线控制器_1_beq ),
    .MEMTOREG(\单周期硬布线控制器_1_memtoreg ), .MEMWRITE(\单周期硬布线控制器_1_memwrite ), .ALUSRC(\单周期硬布线控制器_1_alu_src ),
    .R1(\regifile_气泡_1_r1 ), .R2(\regifile_气泡_1_r2 ), .PC(ID_PC), .IMM1(bit_extender_3_out),
    .IMM2(bit_extender_1_out), .IMM3(bit_extender_2_out), .JALOUT(jal), .JALROUT(jalr), .URETOUT(EX_URET),
    .BEQOUT(id_ex_1_beqout), .MEMTOREGOUT(EX_MEMTOREG), .MEMWRITEOUT(id_ex_1_memwriteout),
    .ALUSRCOUT(id_ex_1_alusrcout), .R1OUT(EX_R1), .R2OUT_prime(EX_R2), .PCOUT_prime(EX_PC),
    .IMM1OUT_prime(id_ex_1_imm1out_prime), .IMM2OUT_prime(id_ex_1_imm2out_prime),
    .IMM3OUT_prime(id_ex_1_imm3out_prime), .CLK(CLK), .RST(RST), .BNE(\单周期硬布线控制器_1_bne ),
    .BNEOUT(id_ex_1_bneout), .ALUOP(\单周期硬布线控制器_1_alu_op ), .ALUOPOUT(id_ex_1_aluopout),
    .REGWRITE(\单周期硬布线控制器_1_regwrite ), .REGWRITEOUT(EX_REGWRITE), .half(\单周期硬布线控制器_1_half ),
    .halfOUT(id_ex_1_halfout), .ECALL(ecall), .ECALLOUT(id_ex_1_ecallout), .WRITEREG(ID_IR[11:7]),
    .WRITEREGOUT_prime(EX_WRITEREG), .IR(ID_IR), .IROUT_prime(EX_IR), .FLUSH(or_18_out), .EN(and_7_out),
    .R1F(R1FOWARD), .R1FOUT(EX_R1F), .R2F(R2FOWARD), .R2FOUT(EX_R2F));  // open: CSR, CSROUT, PREDICT, PREDICTOUT
  and and_7 (and_7_out, halt, ~Go);  // AND_Gate
  or or_18 (or_18_out, BRANCHTAKEN, LOADUSE);
  or or_19 (or_19_out, jal, jalr);
  Comparator #(.width(32), .mode("twosComplement")) comparator_6 (
    .a(32'h22), .b(R1R), .eq(comparator_6_eq));  // open: gt, lt
  Shifter #(.width(32), .shift("ll")) shifter_1 (.in(id_ex_1_imm2out_prime), .\dist (5'b00001), .out(shifter_1_out));
  Shifter #(.width(32), .shift("ll")) shifter_2 (.in(id_ex_1_imm3out_prime), .\dist (5'b00001), .out(shifter_2_out));
  Multiplexer #(.select(1), .width(32), .disabled("Z"), .enable("false")) multiplexer_9 (
    .in0(R2R), .in1(id_ex_1_imm1out_prime), .out(multiplexer_9_out), .sel(id_ex_1_alusrcout));
  Adder #(.width(32)) adder_2 (.a(EX_PC), .b(32'h4), .out(adder_2_out));  // open: cin, cout
  Adder #(.width(32)) adder_3 (.a(shifter_1_out), .b(EX_PC), .out(adder_3_out));  // open: cin, cout
  Adder #(.width(32)) adder_4 (.a(shifter_2_out), .b(EX_PC), .out(adder_4_out));  // open: cin, cout
  assign and_8_out = aluresult & 32'hfffffffe;  // AND_Gate and_8, 32 bits wide
  and and_9 (and_9_out, alu_1_equal, id_ex_1_beqout);
  not not_3 (not_3_out, alu_1_equal);
  and and_10 (and_10_out, not_3_out, id_ex_1_bneout);
  and and_11 (and_11_out, ~EX_REGWRITE, alu_1_out_6);  // AND_Gate
  ALU alu_1 (
    .X(R1R), .Y(multiplexer_9_out), .AluOP(id_ex_1_aluopout), .Equal(alu_1_equal), .Result(aluresult),
    .out_6(alu_1_out_6));  // open: Result_2, out_4
  or or_20 (or_20_out, and_9_out, and_10_out);
  and and_12 (led, id_ex_1_ecallout, comparator_6_eq);
  Multiplexer #(.select(1), .width(32), .disabled("Z"), .enable("false")) multiplexer_10 (
    .in0({32{1'b0}}), .in1(R2R), .out(multiplexer_10_out), .sel(led));
  or or_21 (B, or_20_out, and_11_out);
  not not_4 (not_4_out, comparator_6_eq);
  Register #(.width(32), .trigger("rising"), .Select("low")) register_3 (
    .D(multiplexer_10_out), .en(led), .Q(LedData), .clk(CLK));  // open: clr
  and and_13 (and_13_out, id_ex_1_ecallout, not_4_out);
  EX_MEM ex_mem_1 (
    .MEMTOREGWRITE(EX_MEMTOREG), .HALF(id_ex_1_halfout), .ALURESULT(aluresult), .WRITEDATA(R2R),
    .MEMTOREGOUT(ex_mem_1_memtoregout), .HALFOUT(ex_mem_1_halfout),
    .ALURESULTOUT({ex_mem_1_aluresultout[31:2], high, ex_mem_1_aluresultout[0]}), .WRITEDATAOUT(MDin),
    .CLK(CLK), .RST(RST), .MEMWRITE(id_ex_1_memwriteout), .MEMWRITEOUT(MemWrite), .J(or_19_out),
    .JOUT(MEM_J), .REGWRITEOUT(MEM_REGWRITE), .REGWRITE(EX_REGWRITE), .WRITEREG(EX_WRITEREG),
    .WRITEREGOUT(MEM_WRITEREG), .PC(EX_PC), .PCOUT(M_PC), .IR(EX_IR), .IROUT(MEM_IR), .IMM(adder_2_out),
    .IMMOUT(ex_mem_1_immout), .HALT(and_13_out), .HALTOUT(ex_mem_1_haltout), .FLUSH(1'b0), .EN(and_14_out));
  Multiplexer #(.select(1), .width(32), .disabled("Z"), .enable("false")) multiplexer_11 (
    .in0({ex_mem_1_aluresultout[31:2], high, ex_mem_1_aluresultout[0]}), .in1(ex_mem_1_immout),
    .out(MEM_RESULT), .sel(MEM_J));
  Multiplexer #(.select(2), .width(32), .disabled("Z"), .enable("false")) multiplexer_12 (
    .in0(EX_R1), .in1(RDin), .in2(MEM_RESULT), .in3(MEM_RESULT), .out(R1R), .sel(EX_R1F));
  Multiplexer #(.select(2), .width(32), .disabled("Z"), .enable("false")) multiplexer_13 (
    .in0(EX_R2), .in1(RDin), .in2(MEM_RESULT), .in3(MEM_RESULT), .out(R2R), .sel(EX_R2F));
  RAM #(.addrWidth(10), .dataWidth(32), .bus("separate"), .Select("high")) ram_1 (
    .addr(ex_mem_1_aluresultout[11:2]), .din(MDin), .data(ram_1_data), .str(MemWrite), .clk(CLK),
    .ld(not_5_out));  // open: sel, clr
  not not_5 (not_5_out, MemWrite);
  MEM_WB mem_wb_1 (
    .MEMTOREG(ex_mem_1_memtoregout),
    .ALURESULT({ex_mem_1_aluresultout[31:2], high, ex_mem_1_aluresultout[0]}), .MEMDATA(ram_1_data),
    .MEMTOREGOUT(mem_wb_1_memtoregout), .ALURESULTOUT(mem_wb_1_aluresultout),
    .MEMDATAOUT(mem_wb_1_memdataout), .in_1(CLK), .in_2(RST), .HALF(ex_mem_1_halfout),
    .HALFOUT(mem_wb_1_halfout), .J(MEM_J), .JOUT(mem_wb_1_jout), .WRITEREG(MEM_WRITEREG),
    .WRITEREGOUT(mem_wb_1_writeregout), .REGWRITE(MEM_REGWRITE), .REGWRITEOUT(RegWrite), .PC(M_PC),
    .PCOUT(WB_PC), .IR(MEM_IR), .IROUT(WB_IR), .IMM(ex_mem_1_immout), .IMMOUT(mem_wb_1_immout),
    .HALT(ex_mem_1_haltout), .HALTOUT(halt), .HIGH(high), .HIGHOUT(mem_wb_1_highout), .FLUSH(1'b0),
    .EN(and_14_out));
  and and_14 (and_14_out, halt, ~Go);  // AND_Gate
  Multiplexer #(.select(1), .width(32), .disabled("Z"), .enable("false")) multiplexer_14 (
    .in0(mem_wb_1_aluresultout), .in1(mem_wb_1_memdataout), .out(multiplexer_14_out),
    .sel(mem_wb_1_memtoregout));
  Shifter #(.width(32), .shift("lr")) shifter_3 (.in(multiplexer_14_out), .\dist (5'b10000), .out(shifter_3_out));
  Multiplexer #(.select(1), .width(32), .disabled("Z"), .enable("false")) multiplexer_15 (
    .in0(multiplexer_14_out), .in1(shifter_3_out), .out(multiplexer_15_out), .sel(mem_wb_1_highout));
  Multiplexer #(.select(1), .width(32), .disabled("Z"), .enable("false")) multiplexer_16 (
    .in0(multiplexer_14_out), .in1(and_15_out), .out(multiplexer_16_out), .sel(mem_wb_1_halfout));
  assign and_15_out = multiplexer_15_out & 32'hffff;  // AND_Gate and_15, 32 bits wide
  Multiplexer #(.select(1), .width(32), .disabled("Z"), .enable("false")) multiplexer_17 (
    .in0(multiplexer_16_out), .in1(mem_wb_1_immout), .out(RDin), .sel(mem_wb_1_jout));

  // Other names for the same wires on the sheet: WRITEREG[4:0] = ID_IR[11:7]; MEM_PC[31:0] = M_PC

  // Notes on the sheet:
  //   中断源
  //   时空图监测，可删除
  //   中断等待指示
  //   单级中断测试信号模拟器
  //   识别中断类型找地址
  //   数码管输出
  //   Reset 
  //   Reset 
  //   Reset 
  //   中断响应阶段
  //   中断使能位(用于开关中断)
  //   清除中断
  //   判断中断使能
  //   中断响应
  //   保存断点
  //   控制位
  //   流水调试日志用
  //   暂停节拍，不能为0
  //   戳工具置1进入计数暂停模式，ctrl+k时钟自动运行到对应节拍暂停
  //   ctrl+k关闭时钟连续运行，将控制位置零，进入单步调试模式调试
  //   可计数暂停的时钟源
  //   指令存储器
  //   contents of rom_1 (hex, n*v repeats v):
  //   7d000113 100413 1f41993 41f9d993 433 c00913 800b13 140413 f47413 800293 100313 499993 89e9b3 1300533
  //   2200893 73 406282b3 fe0294e3 140413 f00f93 1f47433 1c41413 800293 100313 49d993 89e9b3 1300533
  //   2200893 73 406282b3 fe0294e3 1c45413 406b0b33 b0463 f95ff06f 2b3 fff2c293 1029293 fff2e293 500533
  //   2200893 73 f5dff06f 1112023 410113 a12023 410113 812023 410113 1312023 410113 1412023 410113 1512023
  //   410113 1612023 410113 100b13 300a13 100a93 1600433 441413 14469b3 1300533 2200893 73 fe0416e3
  //   415a0a33 fe0a10e3 ffc10113 12b03 ffc10113 12a83 ffc10113 12a03 ffc10113 12983 ffc10113 12403
  //   ffc10113 12503 ffc10113 12883 200073 1112023 410113 a12023 410113 812023 410113 1312023 410113
  //   1412023 410113 1512023 410113 1612023 410113 200b13 300a13 100a93 1600433 441413 14469b3 1300533
  //   2200893 73 fe0416e3 415a0a33 fe0a10e3 ffc10113 12b03 ffc10113 12a83 ffc10113 12a03 ffc10113 12983
  //   ffc10113 12403 ffc10113 12503 ffc10113 12883 200073 1112023 410113 a12023 410113 812023 410113
  //   1312023 410113 1412023 410113 1512023 410113 1612023 410113 300b13 300a13 100a93 1600433 441413
  //   14469b3 1300533 2200893 73 fe0416e3 415a0a33 fe0a10e3 ffc10113 12b03 ffc10113 12a83 ffc10113 12a03
  //   ffc10113 12983 ffc10113 12403 ffc10113 12503 ffc10113 12883 200073
  //   PC+4
  //   为方便自动评测，需要输出流水线各段保存的PC值，注意是PC不是PC+4，另外ID段寄存器写入信息，Mem段内存写入信息也要输出
  //   指令探针
  //   指令字
  //   I型指令
  //   s型指令
  //   B型指令
  //   J型指令
  //   JAL
  //   JALR
  //   URET
  //   Beq
  //   Bne
  //   MemToReg
  //   MemWrite
  //   AluOP
  //   AluSrcB
  //   RegWrite
  //   half
  //   PC+4
  //   BEQ/BNE
  //   JAL
  //   JALR
  //   数据存储器
endmodule

module \流水线中断_多级EX  (
  input  IR1,
  input  IR2,
  input  IR3,
  output RegWrite,
  output MemWrite,
  output [31:0] IF_PC,
  output [31:0] ID_PC,
  output [31:0] EX_PC,
  output [31:0] M_PC,
  output [31:0] WB_PC,
  output [31:0] RDin,
  output [31:0] MDin,
  output [31:0] LedData
);

  wire alu_1_equal, alu_1_out_6, and_1_out, and_2_out, and_3_out, and_4_out, and_6_out, and_7_out, and_8_out,
       and_9_out, and_13_out, and_14_out, and_16_out, and_17_out, B, BRANCHTAKEN, CLK, clock_1_out, CLR1,
       CLR2, CLR3, comparator_1_eq, comparator_2_eq, comparator_3_eq, comparator_4_eq, comparator_5_eq,
       comparator_6_gt, comparator_7_gt, comparator_8_gt, comparator_9_lt, comparator_10_eq,
       comparator_10_lt, comparator_11_eq, CSR, CSRRCI, CSRRSI, d_ff_1_q, d_ff_2_q, d_ff_3_q, d_ff_4_q,
       d_ff_6_q, d_ff_7_q, demultiplexer_1_out1, demultiplexer_1_out2, demultiplexer_1_out3, ecall,
       ex_mem_1_halfout, ex_mem_1_haltout, ex_mem_1_memtoregout, EX_MEMTOREG, EX_REGWRITE, Go, halt, high,
       id_ex_1_alusrcout, id_ex_1_beqout, id_ex_1_bneout, id_ex_1_ecallout, id_ex_1_halfout,
       id_ex_1_memwriteout, ID_URET, IE, INTR, INTR1, INTR2, INTR3, IR1_t, IR2_t, IR3_t, IRA, IRB, IRC, jal,
       jalr, JUMP, led, LOADUSE, MEM_J, MEM_REGWRITE, mem_wb_1_halfout, mem_wb_1_highout, mem_wb_1_jout,
       mem_wb_1_memtoregout, nand_1_out, not_1_out, not_2_out, not_3_out, not_4_out, not_5_out, not_6_out,
       or_1_out, or_2_out, or_5_out, or_7_out, or_8_out, or_9_out, or_10_out, or_11_out, or_12_out,
       or_13_out, or_14_out, or_15_out, or_16_out, or_17_out, or_18_out, or_19_out, or_20_out, or_23_out,
       or_27_out, or_28_out, or_29_out, RST, uret, W1, W2, W3, \单周期硬布线控制器_1_alu_src , \单周期硬布线控制器_1_beq ,
       \单周期硬布线控制器_1_bne , \单周期硬布线控制器_1_csr , \单周期硬布线控制器_1_half , \单周期硬布线控制器_1_jal , \单周期硬布线控制器_1_jalr ,
       \单周期硬布线控制器_1_memtoreg , \单周期硬布线控制器_1_memwrite , \单周期硬布线控制器_1_regwrite , \单周期硬布线控制器_1_s_type ;
  wire [1:0] CUR_INTR, EX_R1F, EX_R2F, multiplexer_7_out, multiplexer_9_out, multiplexer_11_out,
       priority_encoder_1_out, priority_encoder_2_out, priority_encoder_3_out, priority_encoder_4_out,
       priority_encoder_5_out, R1FOWARD, R2FOWARD, register_5_q, register_6_q;
  wire [3:0] ALUOP, \单周期硬布线控制器_1_alu_op ;
  wire [4:0] EX_WRITEREG, mem_wb_1_writeregout, MEM_WRITEREG, multiplexer_12_out, multiplexer_13_out;
  wire [7:0] counter_1_q, counter_2_q, counter_3_q;
  wire [11:0] multiplexer_14_out;
  wire [12:0] CNT_num;
  wire [15:0] \LoadUse次数 , \总周期数 , \插入气泡数 , \无条件分支数 , \条件分支成功数 ;
  wire [31:0] adder_1_out, adder_2_out, adder_3_out, adder_4_out, aluresult, and_10_out, and_18_out,
       bit_extender_1_out, bit_extender_2_out, bit_extender_3_out, EX_IR, ex_mem_1_aluresultout,
       ex_mem_1_immout, EX_R1, EX_R2, id_ex_1_imm1out_prime, id_ex_1_imm2out_prime, id_ex_1_imm3out_prime,
       ID_IR, IF_IR, IR_PC, MEM_IR, MEM_RESULT, mem_wb_1_aluresultout, mem_wb_1_immout, mem_wb_1_memdataout,
       MEPC, multiplexer_2_out, multiplexer_3_out, multiplexer_4_out, multiplexer_5_out, multiplexer_6_out,
       multiplexer_8_out, multiplexer_10_out, multiplexer_15_out, multiplexer_16_out, multiplexer_20_out,
       multiplexer_21_out, multiplexer_22_out, R1R, R2R, ram_1_data, \regifile_气泡_1_r1 , \regifile_气泡_1_r2 ,
       register_2_q, register_4_q, shifter_1_out, shifter_2_out, shifter_3_out, WB_IR;

  Demultiplexer #(.select(2), .width(1), .tristate("false"), .disabled("Z"), .enable("false")) demultiplexer_1 (
    .out1(demultiplexer_1_out1), .out2(demultiplexer_1_out2), .out3(demultiplexer_1_out3), .in(ID_URET),
    .sel(CUR_INTR));  // open: out0
  Comparator #(.width(16), .mode("twosComplement")) comparator_1 (
    .a(16'h258), .b(\总周期数 ), .eq(comparator_1_eq));  // open: gt, lt
  Comparator #(.width(16), .mode("twosComplement")) comparator_2 (
    .a(\总周期数 ), .b(16'h1), .eq(comparator_2_eq));  // open: gt, lt
  Comparator #(.width(16), .mode("twosComplement")) comparator_3 (
    .a(\总周期数 ), .b(16'h4), .eq(comparator_3_eq));  // open: gt, lt
  Comparator #(.width(16), .mode("twosComplement")) comparator_4 (
    .a(\总周期数 ), .b(16'h7), .eq(comparator_4_eq));  // open: gt, lt
  or or_1 (or_1_out, comparator_4_eq, comparator_5_eq);
  Comparator #(.width(16), .mode("twosComplement")) comparator_5 (
    .a(\总周期数 ), .b(16'h241), .eq(comparator_5_eq));  // open: gt, lt
  Priority_Encoder #(.select(2), .disabled("Z")) priority_encoder_1 (
    .in0(1'b1), .in1(INTR1), .in2(INTR2), .in3(INTR3), .out(priority_encoder_1_out));  // open: gs, en_out, en_in
  Button \u_总复位  (.out(RST));
  Button _1 (.out(IRA));
  Button _2 (.out(IRB));
  Button _3 (.out(IRC));
  // Probe on \总周期数 
  // Probe on \总周期数 
  or or_2 (or_2_out, comparator_1_eq, comparator_2_eq);
  Pull_Resistor #(.pull(0)) pull_resistor_1 (.node(IRA));
  assign IRA = or_2_out ? ~CLK : 1'bz;  // Controlled_Inverter controlled_inverter_1
  Pull_Resistor #(.pull(0)) pull_resistor_2 (.node(IRB));
  assign IRB = comparator_3_eq ? ~CLK : 1'bz;  // Controlled_Inverter controlled_inverter_2
  Pull_Resistor #(.pull(0)) pull_resistor_3 (.node(IRC));
  assign IRC = or_1_out ? ~CLK : 1'bz;  // Controlled_Inverter controlled_inverter_3
  Multiplexer #(.select(2), .width(32), .disabled("Z"), .enable("false")) multiplexer_1 (
    .in1(32'h30ac), .in2(32'h3158), .in3(32'h3204), .out(IR_PC), .sel(priority_encoder_1_out));  // open: in0
  Button \u_继续运行  (.out(Go));
  LED #(.active("true")) led_1 (.in(W1));
  LED #(.active("true")) led_2 (.in(W2));
  LED #(.active("true")) led_3 (.in(W3));
  // Probe on IF_PC[19:0]
  // RiscV_Probe riscv_probe_1: pin names not known; wires that end beside it: IF_IR
  D_Flip_Flop #(.trigger("rising"), .Pre_Clr_Positions("LEGACY"), .NegatePresetClear("false"), .enable("true"), .NewFFLayout("false")) d_ff_1 (
    .clk(IRA), .D(1'b1), .Q(d_ff_1_q), .reset(INTR1));  // open: Qn, preset, en
  or or_3 (W1, INTR1, d_ff_1_q);
  or or_4 (W2, INTR2, d_ff_2_q);
  or or_5 (or_5_out, demultiplexer_1_out2, IRB);
  or or_6 (W3, INTR3, d_ff_3_q);
  or or_7 (or_7_out, demultiplexer_1_out3, IRC);
  Hex_Digit_Display hex_digit_display_1 (.value(LedData[27:24]));  // open: dp
  Hex_Digit_Display hex_digit_display_2 (.value(LedData[31:28]));  // open: dp
  or or_8 (or_8_out, d_ff_1_q, INTR1);
  or or_9 (or_9_out, demultiplexer_1_out1, IRA);
  Counter #(.width(8), .max('hff), .ongoal("wrap"), .trigger("rising"), .behavior("new")) counter_1 (
    .count(or_9_out), .Q(counter_1_q), .clk(CLK), .down(demultiplexer_1_out1));  // open: load, D, carry, clr, preset
  D_Flip_Flop #(.trigger("rising"), .Pre_Clr_Positions("LEGACY"), .NegatePresetClear("false"), .enable("true"), .NewFFLayout("false")) d_ff_2 (
    .clk(IRB), .D(1'b1), .Q(d_ff_2_q), .reset(INTR2));  // open: Qn, preset, en
  Counter #(.width(8), .max('hff), .ongoal("wrap"), .trigger("rising"), .behavior("new")) counter_2 (
    .count(or_5_out), .Q(counter_2_q), .clk(CLK), .down(demultiplexer_1_out2));  // open: load, D, carry, clr, preset
  D_Flip_Flop #(.trigger("rising"), .Pre_Clr_Positions("LEGACY"), .NegatePresetClear("false"), .enable("true"), .NewFFLayout("false")) d_ff_3 (
    .clk(IRC), .D(1'b1), .Q(d_ff_3_q), .reset(INTR3));  // open: Qn, preset, en
  Counter #(.width(8), .max('hff), .ongoal("wrap"), .trigger("rising"), .behavior("new")) counter_3 (
    .count(or_7_out), .Q(counter_3_q), .clk(CLK), .down(demultiplexer_1_out3));  // open: load, D, carry, clr, preset
  Hex_Digit_Display hex_digit_display_3 (.value(LedData[23:20]));  // open: dp
  Hex_Digit_Display hex_digit_display_4 (.value(LedData[19:16]));  // open: dp
  // Probe on ID_PC[19:0]
  // RiscV_Probe riscv_probe_2: pin names not known; wires that end beside it: ID_IR
  and and_1 (and_1_out, or_8_out, ~CLR1);  // AND_Gate
  Comparator #(.width(8), .mode("unsigned")) comparator_6 (
    .a(counter_1_q), .b({8{1'b0}}), .gt(comparator_6_gt));  // open: eq, lt
  or or_10 (or_10_out, d_ff_2_q, INTR2);
  Comparator #(.width(8), .mode("unsigned")) comparator_7 (
    .a(counter_2_q), .b({8{1'b0}}), .gt(comparator_7_gt));  // open: eq, lt
  or or_11 (or_11_out, d_ff_3_q, INTR3);
  Comparator #(.width(8), .mode("unsigned")) comparator_8 (
    .a(counter_3_q), .b({8{1'b0}}), .gt(comparator_8_gt));  // open: eq, lt
  Hex_Digit_Display hex_digit_display_5 (.value(LedData[15:12]));  // open: dp
  Hex_Digit_Display hex_digit_display_6 (.value(LedData[11:8]));  // open: dp
  or or_12 (or_12_out, and_1_out, comparator_6_gt);
  and and_2 (and_2_out, or_10_out, ~CLR2);  // AND_Gate
  or or_13 (or_13_out, and_2_out, comparator_7_gt);
  and and_3 (and_3_out, or_11_out, ~CLR3);  // AND_Gate
  or or_14 (or_14_out, and_3_out, comparator_8_gt);
  Demultiplexer #(.select(2), .width(1), .tristate("false"), .disabled("Z"), .enable("false")) demultiplexer_2 (
    .out1(CLR1), .out2(CLR2), .out3(CLR3), .in(uret), .sel(CUR_INTR));  // open: out0
  Hex_Digit_Display hex_digit_display_7 (.value(LedData[3:0]));  // open: dp
  Hex_Digit_Display hex_digit_display_8 (.value(LedData[7:4]));  // open: dp
  // Probe on EX_PC[19:0]
  // RiscV_Probe riscv_probe_3: pin names not known; wires that end beside it: EX_IR
  Priority_Encoder #(.select(2), .disabled("Z")) priority_encoder_2 (
    .in0(1'b1), .in1(INTR1), .in2(INTR2), .in3(INTR3), .out(priority_encoder_2_out));  // open: gs, en_out, en_in
  or or_15 (or_15_out, INTR1, INTR2, INTR3);
  D_Flip_Flop #(.trigger("rising"), .Pre_Clr_Positions("LEGACY"), .NegatePresetClear("false"), .enable("true"), .NewFFLayout("false")) d_ff_4 (
    .D(CSRRSI), .Q(d_ff_4_q), .en(CSR));  // open: clk, Qn, preset, reset
  not not_1 (not_1_out, CSRRCI);
  D_Flip_Flop #(.trigger("rising"), .Pre_Clr_Positions("LEGACY"), .NegatePresetClear("false"), .enable("true"), .NewFFLayout("false")) u_IR1 (
    .clk(CLK), .D(or_12_out), .Q(INTR1));  // open: Qn, preset, en, reset
  D_Flip_Flop #(.trigger("rising"), .Pre_Clr_Positions("LEGACY"), .NegatePresetClear("false"), .enable("true"), .NewFFLayout("false")) IR1_2 (
    .clk(CLK), .D(or_13_out), .Q(INTR2));  // open: Qn, preset, en, reset
  or or_16 (or_16_out, ~or_15_out, uret, CSRRSI, and_4_out);  // OR_Gate
  and and_4 (and_4_out, d_ff_4_q, not_1_out);
  D_Flip_Flop #(.trigger("rising"), .Pre_Clr_Positions("LEGACY"), .NegatePresetClear("false"), .enable("true"), .NewFFLayout("false")) IR1_3 (
    .clk(CLK), .D(or_14_out), .Q(INTR3));  // open: Qn, preset, en, reset
  // Probe on \总周期数 
  // Probe on M_PC[19:0]
  // RiscV_Probe riscv_probe_4: pin names not known; wires that end beside it: MEM_IR
  Comparator #(.width(2), .mode("unsigned")) comparator_9 (
    .a(CUR_INTR), .b(priority_encoder_2_out), .lt(comparator_9_lt));  // open: gt, eq
  D_Flip_Flop #(.trigger("rising"), .Pre_Clr_Positions("LEGACY"), .NegatePresetClear("false"), .enable("true"), .NewFFLayout("true")) d_ff_5 (
    .clk(CLK), .D(or_16_out), .Q(IE));  // open: Qn, preset, en, reset
  // Probe on \总周期数 
  // Probe on \无条件分支数 
  // Probe on \条件分支成功数 
  // Probe on \插入气泡数 
  // Probe on \LoadUse次数 
  // Probe on WB_PC[19:0]
  // RiscV_Probe riscv_probe_5: pin names not known; wires that end beside it: WB_IR
  and and_5 (INTR, comparator_9_lt, IE);
  // Probe on IF_PC[11:0]
  // Probe on EX_PC[11:0]
  // Probe on ID_PC[11:0]
  D_Flip_Flop #(.trigger("high"), .Pre_Clr_Positions("LEGACY"), .NegatePresetClear("false"), .enable("true"), .NewFFLayout("false")) d_ff_6 (.Q(d_ff_6_q));  // open: clk, D, Qn, preset, en, reset
  // Probe on M_PC[11:0]
  // Probe on WB_PC[11:0]
  // Probe on 13'hc
  Multiplexer #(.select(1), .width(32), .disabled("Z"), .enable("false")) multiplexer_2 (
    .in0(ID_PC), .in1(IF_PC), .out(multiplexer_2_out), .sel(d_ff_7_q));
  D_Flip_Flop #(.trigger("rising"), .Pre_Clr_Positions("LEGACY"), .NegatePresetClear("false"), .enable("true"), .NewFFLayout("false")) d_ff_7 (
    .clk(CLK), .D(uret), .Q(d_ff_7_q));  // open: Qn, preset, en, reset
  Multiplexer #(.select(1), .width(32), .disabled("Z"), .enable("false")) multiplexer_3 (
    .in0(multiplexer_5_out), .in1(register_2_q), .out(multiplexer_3_out), .sel(uret));
  Priority_Encoder #(.select(2), .disabled("Z")) priority_encoder_3 (
    .in0(1'b1), .in1(INTR1), .in2(INTR2), .in3(INTR3), .out(priority_encoder_3_out));  // open: gs, en_out, en_in
  Comparator #(.width(13), .mode("twosComplement")) comparator_10 (
    .a(CNT_num), .b(13'hc), .eq(comparator_10_eq), .lt(comparator_10_lt));  // open: gt
  Clock #(.highDuration(1), .lowDuration(1)) clock_1 (.out(clock_1_out));
  or or_17 (or_17_out, Go, not_2_out);
  Multiplexer #(.select(2), .width(32), .disabled("Z"), .enable("false")) multiplexer_4 (
    .in0(multiplexer_8_out), .in1(IR_PC), .in2(MEPC), .out(multiplexer_4_out), .sel(priority_encoder_4_out));  // open: in3
  Multiplexer #(.select(1), .width(32), .disabled("Z"), .enable("false")) multiplexer_5 (
    .in0(multiplexer_2_out), .in1(multiplexer_8_out), .out(multiplexer_5_out), .sel(JUMP));
  Register #(.width(32), .trigger("rising"), .Select("low")) register_1 (
    .D(multiplexer_3_out), .en(or_18_out), .Q(MEPC), .clk(CLK));  // open: clr
  or or_18 (or_18_out, uret, INTR);
  nand nand_1 (nand_1_out, d_ff_6_q, comparator_10_eq);
  Counter #(.width(13), .max('h1fff), .ongoal("stay"), .trigger("rising"), .behavior("old")) counter_4 (
    .count(comparator_10_lt), .Q(CNT_num), .clk(clock_1_out));  // open: load, D, carry, clr, preset
  Counter #(.width(16), .max('hffff), .ongoal("wrap"), .trigger("rising"), .behavior("new")) counter_5 (
    .count(or_17_out), .Q(\总周期数 ), .clk(CLK));  // open: load, D, carry, clr, preset, down
  not not_2 (not_2_out, halt);
  Register #(.width(32), .trigger("rising"), .Select("low")) PC (
    .D(multiplexer_4_out), .en(and_6_out), .Q(IF_PC), .clk(CLK), .clr(RST));
  and and_6 (and_6_out, ~LOADUSE, or_19_out);  // AND_Gate
  or or_19 (or_19_out, Go, not_3_out);
  not not_3 (not_3_out, halt);
  Priority_Encoder #(.select(2), .disabled("Z")) priority_encoder_4 (
    .in0(1'b1), .in1(INTR), .in2(uret), .out(priority_encoder_4_out));  // open: in3, gs, en_out, en_in
  Multiplexer #(.select(1), .width(32), .disabled("Z"), .enable("false")) multiplexer_6 (
    .in0(MEPC), .in1(register_4_q), .out(multiplexer_6_out), .sel(uret));
  Multiplexer #(.select(1), .width(2), .disabled("Z"), .enable("false")) multiplexer_7 (
    .in0(priority_encoder_3_out), .in1(register_5_q), .out(multiplexer_7_out), .sel(uret));
  assign CLK = nand_1_out ? clock_1_out : 1'bz;  // Controlled_Buffer controlled_buffer_1
  Pull_Resistor #(.pull(1)) pull_resistor_4 (.node(CLK));
  Multiplexer #(.select(2), .width(32), .disabled("Z"), .enable("false")) multiplexer_8 (
    .in0(adder_1_out), .in1(adder_3_out), .in2(adder_4_out), .in3(and_10_out), .out(multiplexer_8_out),
    .sel(priority_encoder_5_out));
  Register #(.width(32), .trigger("rising"), .Select("low")) register_2 (
    .D(multiplexer_6_out), .en(or_18_out), .Q(register_2_q), .clk(CLK));  // open: clr
  Register #(.width(2), .trigger("rising"), .Select("low")) register_3 (
    .D(multiplexer_7_out), .en(or_20_out), .Q(CUR_INTR), .clk(CLK));  // open: clr
  or or_20 (or_20_out, uret, INTR);
  Adder #(.width(32)) adder_1 (.a(IF_PC), .b(32'h4), .out(adder_1_out));  // open: cin, cout
  Priority_Encoder #(.select(2), .disabled("Z")) priority_encoder_5 (
    .in0(1'b1), .in1(B), .in2(jal), .in3(jalr), .out(priority_encoder_5_out));  // open: gs, en_out, en_in
  Multiplexer #(.select(1), .width(2), .disabled("Z"), .enable("false")) multiplexer_9 (
    .in0(CUR_INTR), .in1(register_6_q), .out(multiplexer_9_out), .sel(uret));
  ROM #(.addrWidth(10), .dataWidth(32), .Select("high")) rom_1 (.addr(IF_PC[11:2]), .data(IF_IR));
  Register #(.width(32), .trigger("rising"), .Select("low")) register_4 (
    .D(multiplexer_10_out), .en(or_18_out), .Q(register_4_q), .clk(CLK));  // open: clr
  Multiplexer #(.select(1), .width(32), .disabled("Z"), .enable("false")) multiplexer_10 (
    .in0(register_2_q), .in1({32{1'b0}}), .out(multiplexer_10_out), .sel(uret));
  Register #(.width(2), .trigger("rising"), .Select("low")) register_5 (
    .D(multiplexer_9_out), .en(or_20_out), .Q(register_5_q), .clk(CLK));  // open: clr
  or or_21 (IR1_t, IR1, IRA);
  Multiplexer #(.select(1), .width(2), .disabled("Z"), .enable("false")) multiplexer_11 (
    .in0(register_5_q), .in1(2'b00), .out(multiplexer_11_out), .sel(uret));
  IF_ID if_id_1 (
    .IR(IF_IR), .PC(IF_PC), .IROUT(ID_IR), .PCOUT(ID_PC), .CLK(CLK), .RST(RST), .FLUSH(BRANCHTAKEN),
    .EN(or_23_out));  // open: PREDICT, PREDICTOUT
  and and_7 (and_7_out, halt, ~Go);  // AND_Gate
  \冲突检测逻辑_重定向  \u_冲突检测逻辑_重定向_1  (
    .EX_REGWRITE(EX_REGWRITE), .MEM_REGWRITE(MEM_REGWRITE), .MEM_WRITEREG(MEM_WRITEREG),
    .EX_WRITEREG(EX_WRITEREG), .EX_MEMTOREG(EX_MEMTOREG), .ID_IR(ID_IR), .R1FOWARD(R1FOWARD),
    .LOADUSE(LOADUSE), .R2FOWARD(R2FOWARD));
  Register #(.width(2), .trigger("rising"), .Select("low")) register_6 (
    .D(multiplexer_11_out), .en(or_20_out), .Q(register_6_q), .clk(CLK));  // open: clr
  or or_22 (IR2_t, IR2, IRB);
  // RiscV_Probe riscv_probe_6: pin names not known; wires that end beside it: CLK, RST, ID_IR
  or or_23 (or_23_out, and_7_out, LOADUSE);
  or or_24 (IR3_t, IR3, IRC);
  or or_25 (JUMP, B, jal, jalr);
  or or_26 (BRANCHTAKEN, B, jal, jalr, uret, INTR);
  \单周期硬布线控制器  \u_单周期硬布线控制器_1  (
    .Funct({ID_IR[30], ID_IR[25], ID_IR[14:12]}), .OP(ID_IR[6:2]), .ALU_OP(\单周期硬布线控制器_1_alu_op ),
    .MemToReg(\单周期硬布线控制器_1_memtoreg ), .MemWrite(\单周期硬布线控制器_1_memwrite ), .ALU_SRC(\单周期硬布线控制器_1_alu_src ),
    .RegWrite(\单周期硬布线控制器_1_regwrite ), .ecall(ecall), .S_type(\单周期硬布线控制器_1_s_type ),
    .Jalr(\单周期硬布线控制器_1_jalr ), .Beq(\单周期硬布线控制器_1_beq ), .JAL(\单周期硬布线控制器_1_jal ), .Bne(\单周期硬布线控制器_1_bne ),
    .in_3(ID_IR[21]), .uret(ID_URET), .half(\单周期硬布线控制器_1_half ), .CSR(\单周期硬布线控制器_1_csr ));  // open: blt, sh, auipc, lui
  Multiplexer #(.select(1), .width(5), .disabled("Z"), .enable("false")) multiplexer_12 (
    .in0(ID_IR[19:15]), .in1(5'b10001), .out(multiplexer_12_out), .sel(ecall));
  Multiplexer #(.select(1), .width(5), .disabled("Z"), .enable("false")) multiplexer_13 (
    .in0(ID_IR[24:20]), .in1(5'b01010), .out(multiplexer_13_out), .sel(ecall));
  Multiplexer #(.select(1), .width(12), .disabled("Z"), .enable("false")) multiplexer_14 (
    .in0(ID_IR[31:20]), .in1({ID_IR[31:25], ID_IR[11:7]}), .out(multiplexer_14_out),
    .sel(\单周期硬布线控制器_1_s_type ));
  assign bit_extender_1_out = {{20{ID_IR[31]}}, {ID_IR[31], ID_IR[7], ID_IR[30:25], ID_IR[11:8]}};  // Bit_Extender bit_extender_1
  assign bit_extender_2_out = {{12{ID_IR[31]}}, {ID_IR[31], ID_IR[19:12], ID_IR[20], ID_IR[30:21]}};  // Bit_Extender bit_extender_2
  \regifile_气泡  \regifile_气泡_1  (
    .Din(RDin), .Clk(CLK), .R1(\regifile_气泡_1_r1 ), .R2(\regifile_气泡_1_r2 ), .WE(RegWrite),
    .W_num(mem_wb_1_writeregout), .R1_num(multiplexer_12_out), .R2_num(multiplexer_13_out));
  assign bit_extender_3_out = {{20{multiplexer_14_out[11]}}, multiplexer_14_out};  // Bit_Extender bit_extender_3
  or or_27 (or_27_out, BRANCHTAKEN, LOADUSE);
  ID_EX id_ex_1 (
    .JAL(\单周期硬布线控制器_1_jal ), .JALR(\单周期硬布线控制器_1_jalr ), .URET(ID_URET), .beq(\单周期硬布线控制器_1_beq ),
    .MEMTOREG(\单周期硬布线控制器_1_memtoreg ), .MEMWRITE(\单周期硬布线控制器_1_memwrite ), .ALUSRC(\单周期硬布线控制器_1_alu_src ),
    .R1(\regifile_气泡_1_r1 ), .R2(\regifile_气泡_1_r2 ), .PC(ID_PC), .IMM1(bit_extender_3_out),
    .IMM2(bit_extender_1_out), .IMM3(bit_extender_2_out), .JALOUT(jal), .JALROUT(jalr), .URETOUT(uret),
    .BEQOUT(id_ex_1_beqout), .MEMTOREGOUT(EX_MEMTOREG), .MEMWRITEOUT(id_ex_1_memwriteout),
    .ALUSRCOUT(id_ex_1_alusrcout), .R1OUT(EX_R1), .R2OUT_prime(EX_R2), .PCOUT_prime(EX_PC),
    .IMM1OUT_prime(id_ex_1_imm1out_prime), .IMM2OUT_prime(id_ex_1_imm2out_prime),
    .IMM3OUT_prime(id_ex_1_imm3out_prime), .CLK(CLK), .RST(RST), .BNE(\单周期硬布线控制器_1_bne ),
    .BNEOUT(id_ex_1_bneout), .ALUOP(\单周期硬布线控制器_1_alu_op ), .ALUOPOUT(ALUOP),
    .REGWRITE(\单周期硬布线控制器_1_regwrite ), .REGWRITEOUT(EX_REGWRITE), .half(\单周期硬布线控制器_1_half ),
    .halfOUT(id_ex_1_halfout), .ECALL(ecall), .ECALLOUT(id_ex_1_ecallout), .WRITEREG(ID_IR[11:7]),
    .WRITEREGOUT_prime(EX_WRITEREG), .IR(ID_IR), .IROUT_prime(EX_IR), .FLUSH(or_27_out), .EN(and_8_out),
    .R1F(R1FOWARD), .R1FOUT(EX_R1F), .R2F(R2FOWARD), .R2FOUT(EX_R2F), .CSR(\单周期硬布线控制器_1_csr ), .CSROUT(CSR));  // open: PREDICT, PREDICTOUT
  and and_8 (and_8_out, halt, ~Go);  // AND_Gate
  or or_28 (or_28_out, jal, jalr);
  Comparator #(.width(32), .mode("twosComplement")) comparator_11 (
    .a(32'h22), .b(R1R), .eq(comparator_11_eq));  // open: gt, lt
  Multiplexer #(.select(1), .width(32), .disabled("Z"), .enable("false")) multiplexer_15 (
    .in0(R2R), .in1(id_ex_1_imm1out_prime), .out(multiplexer_15_out), .sel(id_ex_1_alusrcout));
  Shifter #(.width(32), .shift("ll")) shifter_1 (.in(id_ex_1_imm2out_prime), .\dist (5'b00001), .out(shifter_1_out));
  Shifter #(.width(32), .shift("ll")) shifter_2 (.in(id_ex_1_imm3out_prime), .\dist (5'b00001), .out(shifter_2_out));
  not not_4 (not_4_out, alu_1_equal);
  and and_9 (and_9_out, ~EX_REGWRITE, alu_1_out_6);  // AND_Gate
  ALU alu_1 (
    .X(R1R), .Y(multiplexer_15_out), .AluOP(ALUOP), .Equal(alu_1_equal), .Result(aluresult),
    .out_6(alu_1_out_6));  // open: Result_2, out_4
  Adder #(.width(32)) adder_2 (.a(EX_PC), .b(32'h4), .out(adder_2_out));  // open: cin, cout
  Adder #(.width(32)) adder_3 (.a(shifter_1_out), .b(EX_PC), .out(adder_3_out));  // open: cin, cout
  Adder #(.width(32)) adder_4 (.a(shifter_2_out), .b(EX_PC), .out(adder_4_out));  // open: cin, cout
  assign and_10_out = aluresult & 32'hfffffffe;  // AND_Gate and_10, 32 bits wide
  and and_11 (CSRRCI, CSR, ~ALUOP[3]);  // AND_Gate
  and and_12 (CSRRSI, CSR, ALUOP[3]);
  and and_13 (and_13_out, alu_1_equal, id_ex_1_beqout);
  and and_14 (and_14_out, not_4_out, id_ex_1_bneout);
  or or_29 (or_29_out, and_13_out, and_14_out);
  and and_15 (led, id_ex_1_ecallout, comparator_11_eq);
  Multiplexer #(.select(1), .width(32), .disabled("Z"), .enable("false")) multiplexer_16 (
    .in0({32{1'b0}}), .in1(R2R), .out(multiplexer_16_out), .sel(led));
  or or_30 (B, or_29_out, and_9_out);
  and and_16 (and_16_out, id_ex_1_ecallout, not_5_out);
  not not_5 (not_5_out, comparator_11_eq);
  Register #(.width(32), .trigger("rising"), .Select("low")) register_7 (
    .D(multiplexer_16_out), .en(led), .Q(LedData), .clk(CLK));  // open: clr
  EX_MEM ex_mem_1 (
    .MEMTOREGWRITE(EX_MEMTOREG), .HALF(id_ex_1_halfout), .ALURESULT(aluresult), .WRITEDATA(R2R),
    .MEMTOREGOUT(ex_mem_1_memtoregout), .HALFOUT(ex_mem_1_halfout),
    .ALURESULTOUT({ex_mem_1_aluresultout[31:2], high, ex_mem_1_aluresultout[0]}), .WRITEDATAOUT(MDin),
    .CLK(CLK), .RST(RST), .MEMWRITE(id_ex_1_memwriteout), .MEMWRITEOUT(MemWrite), .J(or_28_out),
    .JOUT(MEM_J), .REGWRITEOUT(MEM_REGWRITE), .REGWRITE(EX_REGWRITE), .WRITEREG(EX_WRITEREG),
    .WRITEREGOUT(MEM_WRITEREG), .PC(EX_PC), .PCOUT(M_PC), .IR(EX_IR), .IROUT(MEM_IR), .IMM(adder_2_out),
    .IMMOUT(ex_mem_1_immout), .HALT(and_16_out), .HALTOUT(ex_mem_1_haltout), .FLUSH(1'b0), .EN(and_17_out));
  Multiplexer #(.select(1), .width(32), .disabled("Z"), .enable("false")) multiplexer_17 (
    .in0({ex_mem_1_aluresultout[31:2], high, ex_mem_1_aluresultout[0]}), .in1(ex_mem_1_immout),
    .out(MEM_RESULT), .sel(MEM_J));
  not not_6 (not_6_out, MemWrite);
  Multiplexer #(.select(2), .width(32), .disabled("Z"), .enable("false")) multiplexer_18 (
    .in0(EX_R1), .in1(RDin), .in2(MEM_RESULT), .in3(MEM_RESULT), .out(R1R), .sel(EX_R1F));
  Multiplexer #(.select(2), .width(32), .disabled("Z"), .enable("false")) multiplexer_19 (
    .in0(EX_R2), .in1(RDin), .in2(MEM_RESULT), .in3(MEM_RESULT), .out(R2R), .sel(EX_R2F));
  RAM #(.addrWidth(10), .dataWidth(32), .bus("separate"), .Select("high")) ram_1 (
    .addr(ex_mem_1_aluresultout[11:2]), .din(MDin), .data(ram_1_data), .str(MemWrite), .clk(CLK),
    .ld(not_6_out));  // open: sel, clr
  MEM_WB mem_wb_1 (
    .MEMTOREG(ex_mem_1_memtoregout),
    .ALURESULT({ex_mem_1_aluresultout[31:2], high, ex_mem_1_aluresultout[0]}), .MEMDATA(ram_1_data),
    .MEMTOREGOUT(mem_wb_1_memtoregout), .ALURESULTOUT(mem_wb_1_aluresultout),
    .MEMDATAOUT(mem_wb_1_memdataout), .in_1(CLK), .in_2(RST), .HALF(ex_mem_1_halfout),
    .HALFOUT(mem_wb_1_halfout), .J(MEM_J), .JOUT(mem_wb_1_jout), .WRITEREG(MEM_WRITEREG),
    .WRITEREGOUT(mem_wb_1_writeregout), .REGWRITE(MEM_REGWRITE), .REGWRITEOUT(RegWrite), .PC(M_PC),
    .PCOUT(WB_PC), .IR(MEM_IR), .IROUT(WB_IR), .IMM(ex_mem_1_immout), .IMMOUT(mem_wb_1_immout),
    .HALT(ex_mem_1_haltout), .HALTOUT(halt), .HIGH(high), .HIGHOUT(mem_wb_1_highout), .FLUSH(1'b0),
    .EN(and_17_out));
  and and_17 (and_17_out, halt, ~Go);  // AND_Gate
  Multiplexer #(.select(1), .width(32), .disabled("Z"), .enable("false")) multiplexer_20 (
    .in0(mem_wb_1_aluresultout), .in1(mem_wb_1_memdataout), .out(multiplexer_20_out),
    .sel(mem_wb_1_memtoregout));
  Shifter #(.width(32), .shift("lr")) shifter_3 (.in(multiplexer_20_out), .\dist (5'b10000), .out(shifter_3_out));
  Multiplexer #(.select(1), .width(32), .disabled("Z"), .enable("false")) multiplexer_21 (
    .in0(multiplexer_20_out), .in1(shifter_3_out), .out(multiplexer_21_out), .sel(mem_wb_1_highout));
  Multiplexer #(.select(1), .width(32), .disabled("Z"), .enable("false")) multiplexer_22 (
    .in0(multiplexer_20_out), .in1(and_18_out), .out(multiplexer_22_out), .sel(mem_wb_1_halfout));
  assign and_18_out = multiplexer_21_out & 32'hffff;  // AND_Gate and_18, 32 bits wide
  Multiplexer #(.select(1), .width(32), .disabled("Z"), .enable("false")) multiplexer_23 (
    .in0(multiplexer_22_out), .in1(mem_wb_1_immout), .out(RDin), .sel(mem_wb_1_jout));

  // Other names for the same wires on the sheet: WRITEREG[4:0] = ID_IR[11:7]; MEM_PC[31:0] = M_PC

  // Notes on the sheet:
  //   多级中断测试信号模拟器
  //   清除中断
  //   中断源
  //   时空图监测，可删除
  //   中断等待指示
  //   识别中断类型找地址
  //   数码管输出
  //   中断响应阶段
  //   中断使能位(用于开关中断)
  //   中断响应
  //   控制位
  //   流水调试日志用
  //   暂停节拍，不能为0
  //   戳工具置1进入计数暂停模式，ctrl+k时钟自动运行到对应节拍暂停
  //   ctrl+k关闭时钟连续运行，将控制位置零，进入单步调试模式调试
  //   保存断点地址
  //   可计数暂停的时钟源
  //   保存中断号
  //   指令存储器
  //   PC+4
  //   contents of rom_1 (hex, n*v repeats v):
  //   7d000113 100413 1f41993 41f9d993 433 c00913 800b13 140413 f47413 800293 100313 499993 89e9b3 1300533
  //   2200893 73 406282b3 fe0294e3 140413 f00f93 1f47433 1c41413 800293 100313 49d993 89e9b3 1300533
  //   2200893 73 406282b3 fe0294e3 1c45413 406b0b33 b0463 f95ff06f 2b3 fff2c293 1029293 fff2e293 500533
  //   2200893 73 f5dff06f 1112023 410113 a12023 410113 812023 410113 1312023 410113 1412023 410113 1512023
  //   410113 1612023 410113 40e073 100b13 300a13 100a93 1600433 441413 14469b3 1300533 2200893 73 fe0416e3
  //   415a0a33 fe0a10e3 40f073 ffc10113 12b03 ffc10113 12a83 ffc10113 12a03 ffc10113 12983 ffc10113 12403
  //   ffc10113 12503 ffc10113 12883 200073 1112023 410113 a12023 410113 812023 410113 1312023 410113
  //   1412023 410113 1512023 410113 1612023 410113 40e073 200b13 300a13 100a93 1600433 441413 14469b3
  //   1300533 2200893 73 fe0416e3 415a0a33 fe0a10e3 40f073 ffc10113 12b03 ffc10113 12a83 ffc10113 12a03
  //   ffc10113 12983 ffc10113 12403 ffc10113 12503 ffc10113 12883 200073 1112023 410113 a12023 410113
  //   812023 410113 1312023 410113 1412023 410113 1512023 410113 1612023 410113 40e073 300b13 300a13
  //   100a93 1600433 441413 14469b3 1300533 2200893 73 fe0416e3 415a0a33 fe0a10e3 40f073 ffc10113 12b03
  //   ffc10113 12a83 ffc10113 12a03 ffc10113 12983 ffc10113 12403 ffc10113 12503 ffc10113 12883 200073
  //   为方便自动评测，需要输出流水线各段保存的PC值，注意是PC不是PC+4，另外ID段寄存器写入信息，Mem段内存写入信息也要输出
  //   指令探针
  //   指令字
  //   JAL
  //   JALR
  //   URET
  //   I型指令
  //   s型指令
  //   B型指令
  //   J型指令
  //   Beq
  //   Bne
  //   AluOP
  //   AluSrcB
  //   RegWrite
  //   half
  //   MemToReg
  //   MemWrite
  //   PC+4
  //   BEQ/BNE
  //   JAL
  //   JALR
  //   数据存储器
endmodule

module \动态分支预测  (
  output RegWrite,
  output MemWrite,
  output [31:0] IF_PC,
  output [31:0] ID_PC,
  output [31:0] EX_PC,
  output [31:0] M_PC,
  output [31:0] WB_PC,
  output [31:0] RDin,
  output [31:0] MDin,
  output [31:0] LedData
);

  wire alu_1_equal, alu_1_out_6, and_1_out, and_2_out, and_3_out, and_5_out, and_6_out, and_7_out, and_9_out,
       and_10_out, auipc, auipc1, auipc2, auipc3, B, blt, blt1, BRANCHTAKEN, btb_1_predictjump, CLK,
       clock_1_out, comparator_1_eq, comparator_1_lt, comparator_2_eq, d_ff_1_q, ecall, EX_BEQ, EX_BNE,
       EX_BRANCH, ex_mem_1_halfout, ex_mem_1_haltout, ex_mem_1_memtoregout, EX_MEMTOREG, EX_REGWRITE, Go,
       halt, high, id_ex_1_alusrcout, id_ex_1_ecallout, id_ex_1_halfout, id_ex_1_memwriteout,
       if_id_1_predictout, IR1, IR2, IR3, jal, jalr, led, LOADUSE, lui, lui1, lui2, lui3, MEM_J,
       MEM_REGWRITE, mem_wb_1_halfout, mem_wb_1_highout, mem_wb_1_jout, mem_wb_1_memtoregout, nand_1_out,
       not_1_out, not_2_out, not_3_out, not_4_out, not_5_out, not_6_out, not_7_out, not_8_out, or_1_out,
       or_2_out, or_3_out, or_4_out, or_7_out, or_8_out, PERROR, PREDICT, RST, sh, sh1, sh2, W1, W2, W3,
       \单周期硬布线控制器_1_alu_src , \单周期硬布线控制器_1_beq , \单周期硬布线控制器_1_bne , \单周期硬布线控制器_1_half , \单周期硬布线控制器_1_jal ,
       \单周期硬布线控制器_1_jalr , \单周期硬布线控制器_1_memtoreg , \单周期硬布线控制器_1_memwrite , \单周期硬布线控制器_1_regwrite ,
       \单周期硬布线控制器_1_s_type , \单周期硬布线控制器_1_uret ;
  wire [1:0] EX_R1F, EX_R2F, R1FOWARD, R2FOWARD;
  wire [3:0] id_ex_1_aluopout, \单周期硬布线控制器_1_alu_op ;
  wire [4:0] EX_WRITEREG, mem_wb_1_writeregout, MEM_WRITEREG, multiplexer_4_out, multiplexer_5_out,
       multiplexer_18_out;
  wire [11:0] multiplexer_6_out;
  wire [12:0] CNT_num;
  wire [15:0] \LoadUse次数 , \PERROR次数 , \总周期数 , \插入气泡数 , \无条件分支数 , \条件分支成功数 ;
  wire [31:0] adder_1_out, adder_2_out, adder_3_out, adder_4_out, adder_5_out, adder_6_out, adder_7_out,
       aluresult, and_4_out, and_11_out, and_12_out, bit_extender_1_out, bit_extender_2_out,
       bit_extender_3_out, bit_extender_4_out, bit_extender_5_out, BRANCHADDR, btb_1_predictaddr, EX_IR,
       ex_mem_1_aluresultout, ex_mem_1_immout, EX_R1, EX_R2, id_ex_1_imm1out_prime, id_ex_1_imm2out_prime,
       id_ex_1_imm3out_prime, ID_IR, IF_IR, inn, MEM_IR, MEM_RESULT, mem_wb_1_aluresultout, mem_wb_1_immout,
       mem_wb_1_memdataout, multiplexer_1_out, multiplexer_2_out, multiplexer_3_out, multiplexer_7_out,
       multiplexer_8_out, multiplexer_9_out, multiplexer_10_out, multiplexer_12_out, multiplexer_15_out,
       multiplexer_17_out, multiplexer_19_out, multiplexer_20_out, multiplexer_21_out, multiplexer_22_out,
       multiplexer_24_out, R1R, R2R, \regifile_气泡_1_r1 , \regifile_气泡_1_r2 , Res, shifter_2_out,
       shifter_3_out, shifter_4_out, shifter_5_out, u_imm, u_imm1, u_imm2, u_imm3, \use , WB_IR;

  Button \u_总复位  (.out(RST));
  Button _1 (.out(IR1));
  Button _2 (.out(IR2));
  Button _3 (.out(IR3));
  // Probe on \总周期数 
  // Probe on \总周期数 
  Button \u_继续运行  (.out(Go));
  LED #(.active("true")) led_1 (.in(W1));
  LED #(.active("true")) led_2 (.in(W2));
  LED #(.active("true")) led_3 (.in(W3));
  // Probe on IF_PC[19:0]
  // RiscV_Probe riscv_probe_1: pin names not known; wires that end beside it: IF_IR
  Hex_Digit_Display hex_digit_display_1 (.value(LedData[31:28]));  // open: dp
  Hex_Digit_Display hex_digit_display_2 (.value(LedData[27:24]));  // open: dp
  Hex_Digit_Display hex_digit_display_3 (.value(LedData[23:20]));  // open: dp
  Hex_Digit_Display hex_digit_display_4 (.value(LedData[19:16]));  // open: dp
  // Probe on ID_PC[19:0]
  // RiscV_Probe riscv_probe_2: pin names not known; wires that end beside it: ID_IR
  or or_1 (or_1_out, Go, not_1_out);
  not not_1 (not_1_out, halt);
  and and_1 (and_1_out, ~LOADUSE, or_2_out);  // AND_Gate
  or or_2 (or_2_out, Go, not_2_out);
  not not_2 (not_2_out, halt);
  Multiplexer #(.select(1), .width(32), .disabled("Z"), .enable("false")) multiplexer_1 (
    .in0(multiplexer_3_out), .in1(multiplexer_2_out), .out(multiplexer_1_out), .sel(PERROR));
  Multiplexer #(.select(1), .width(32), .disabled("Z"), .enable("false")) multiplexer_2 (
    .in0(adder_1_out), .in1(BRANCHADDR), .out(multiplexer_2_out), .sel(BRANCHTAKEN));
  Adder #(.width(32)) adder_1 (.a(EX_PC), .b(32'h4), .out(adder_1_out));  // open: cin, cout
  Hex_Digit_Display hex_digit_display_5 (.value(LedData[11:8]));  // open: dp
  Hex_Digit_Display hex_digit_display_6 (.value(LedData[15:12]));  // open: dp
  Counter #(.width(16), .max('hffff), .ongoal("wrap"), .trigger("rising"), .behavior("new")) counter_1 (
    .count(or_1_out), .Q(\总周期数 ), .clk(CLK));  // open: load, D, carry, clr, preset, down
  Register #(.width(32), .trigger("rising"), .Select("low")) PC (
    .D(multiplexer_1_out), .en(and_1_out), .Q(IF_PC), .clk(CLK), .clr(RST));
  Multiplexer #(.select(1), .width(32), .disabled("Z"), .enable("false")) multiplexer_3 (
    .in0(adder_2_out), .in1(btb_1_predictaddr), .out(multiplexer_3_out), .sel(btb_1_predictjump));
  Hex_Digit_Display hex_digit_display_7 (.value(LedData[3:0]));  // open: dp
  Hex_Digit_Display hex_digit_display_8 (.value(LedData[7:4]));  // open: dp
  // Probe on EX_PC[19:0]
  // RiscV_Probe riscv_probe_3: pin names not known; wires that end beside it: EX_IR
  BTB btb_1 (
    .EX_BRANCHTAKEN(BRANCHTAKEN), .EX_BRANCH(EX_BRANCH), .CLK(CLK), .EX_PC(EX_PC), .PC(IF_PC),
    .EX_BRANCHADDR(BRANCHADDR), .PREDICTJUMP(btb_1_predictjump), .PREDICTADDR(btb_1_predictaddr));
  Adder #(.width(32)) adder_2 (.a(IF_PC), .b(32'h4), .out(adder_2_out));  // open: cin, cout
  // Probe on \总周期数 
  // Probe on M_PC[19:0]
  // RiscV_Probe riscv_probe_4: pin names not known; wires that end beside it: MEM_IR
  Counter #(.width(16), .max('hffff), .ongoal("wrap"), .trigger("rising"), .behavior("new")) counter_2 (
    .count(LOADUSE), .Q(\LoadUse次数 ), .clk(CLK));  // open: load, D, carry, clr, preset, down
  ROM #(.addrWidth(10), .dataWidth(32), .Select("high")) rom_1 (.addr(IF_PC[11:2]), .data(IF_IR));
  // Probe on \总周期数 
  // Probe on \无条件分支数 
  // Probe on \条件分支成功数 
  // Probe on \插入气泡数 
  // Probe on \LoadUse次数 
  // RiscV_Probe riscv_probe_5: pin names not known; wires that end beside it: WB_IR
  IF_ID if_id_1 (
    .IR(IF_IR), .PC(IF_PC), .IROUT(ID_IR), .PCOUT(ID_PC), .CLK(CLK), .RST(RST), .FLUSH(PERROR),
    .EN(or_3_out), .PREDICT(btb_1_predictjump), .PREDICTOUT(if_id_1_predictout));
  \冲突检测逻辑_重定向  \u_冲突检测逻辑_重定向_1  (
    .EX_REGWRITE(EX_REGWRITE), .MEM_REGWRITE(MEM_REGWRITE), .MEM_WRITEREG(MEM_WRITEREG),
    .EX_WRITEREG(EX_WRITEREG), .EX_MEMTOREG(EX_MEMTOREG), .ID_IR(ID_IR), .R1FOWARD(R1FOWARD),
    .LOADUSE(LOADUSE), .R2FOWARD(R2FOWARD));
  // Probe on IF_PC[11:0]
  // Probe on WB_PC[19:0]
  // RiscV_Probe riscv_probe_6: pin names not known; wires that end beside it: CLK, RST, ID_IR
  or or_3 (or_3_out, and_2_out, LOADUSE);
  and and_2 (and_2_out, halt, ~Go);  // AND_Gate
  // Probe on EX_PC[11:0]
  // Probe on ID_PC[11:0]
  // Probe on \PERROR次数 
  Counter #(.width(16), .max('hffff), .ongoal("wrap"), .trigger("rising"), .behavior("new")) counter_3 (
    .count(PERROR), .Q(\PERROR次数 ), .clk(CLK));  // open: load, D, carry, clr, preset, down
  xor xor_1 (PERROR, BRANCHTAKEN, PREDICT);
  // Probe on M_PC[11:0]
  D_Flip_Flop #(.trigger("high"), .Pre_Clr_Positions("LEGACY"), .NegatePresetClear("false"), .enable("true"), .NewFFLayout("false")) d_ff_1 (.Q(d_ff_1_q));  // open: clk, D, Qn, preset, en, reset
  // Probe on 13'hc
  assign bit_extender_1_out = {{12{ID_IR[31]}}, ID_IR[31:12]};  // Bit_Extender bit_extender_1
  // Probe on WB_PC[11:0]
  Comparator #(.width(13), .mode("twosComplement")) comparator_1 (
    .a(CNT_num), .b(13'hc), .eq(comparator_1_eq), .lt(comparator_1_lt));  // open: gt
  Clock #(.highDuration(1), .lowDuration(1)) clock_1 (.out(clock_1_out));
  \单周期硬布线控制器  \u_单周期硬布线控制器_1  (
    .Funct({ID_IR[30], ID_IR[25], ID_IR[14:12]}), .OP(ID_IR[6:2]), .ALU_OP(\单周期硬布线控制器_1_alu_op ),
    .MemToReg(\单周期硬布线控制器_1_memtoreg ), .MemWrite(\单周期硬布线控制器_1_memwrite ), .ALU_SRC(\单周期硬布线控制器_1_alu_src ),
    .RegWrite(\单周期硬布线控制器_1_regwrite ), .ecall(ecall), .S_type(\单周期硬布线控制器_1_s_type ),
    .Jalr(\单周期硬布线控制器_1_jalr ), .Beq(\单周期硬布线控制器_1_beq ), .JAL(\单周期硬布线控制器_1_jal ), .Bne(\单周期硬布线控制器_1_bne ),
    .in_3(ID_IR[21]), .uret(\单周期硬布线控制器_1_uret ), .half(\单周期硬布线控制器_1_half ), .blt(blt1), .sh(sh1),
    .auipc(auipc1), .lui(lui1));  // open: CSR
  Multiplexer #(.select(1), .width(5), .disabled("Z"), .enable("false")) multiplexer_4 (
    .in0(ID_IR[19:15]), .in1(5'b10001), .out(multiplexer_4_out), .sel(ecall));
  Multiplexer #(.select(1), .width(5), .disabled("Z"), .enable("false")) multiplexer_5 (
    .in0(ID_IR[24:20]), .in1(5'b01010), .out(multiplexer_5_out), .sel(ecall));
  Multiplexer #(.select(1), .width(12), .disabled("Z"), .enable("false")) multiplexer_6 (
    .in0(ID_IR[31:20]), .in1({ID_IR[31:25], ID_IR[11:7]}), .out(multiplexer_6_out), .sel(\单周期硬布线控制器_1_s_type ));
  assign bit_extender_2_out = {{20{ID_IR[31]}}, {ID_IR[31], ID_IR[7], ID_IR[30:25], ID_IR[11:8]}};  // Bit_Extender bit_extender_2
  assign bit_extender_3_out = {{12{ID_IR[31]}}, {ID_IR[31], ID_IR[19:12], ID_IR[20], ID_IR[30:21]}};  // Bit_Extender bit_extender_3
  nand nand_1 (nand_1_out, d_ff_1_q, comparator_1_eq);
  Counter #(.width(13), .max('h1fff), .ongoal("stay"), .trigger("rising"), .behavior("old")) counter_4 (
    .count(comparator_1_lt), .Q(CNT_num), .clk(clock_1_out));  // open: load, D, carry, clr, preset
  Shifter #(.width(32), .shift("ll")) shifter_1 (.in(bit_extender_1_out), .\dist (5'b01100), .out(u_imm1));
  assign CLK = nand_1_out ? clock_1_out : 1'bz;  // Controlled_Buffer controlled_buffer_1
  assign bit_extender_4_out = {{20{multiplexer_6_out[11]}}, multiplexer_6_out};  // Bit_Extender bit_extender_4
  Pull_Resistor #(.pull(1)) pull_resistor_1 (.node(CLK));
  \regifile_气泡  \regifile_气泡_1  (
    .Din(RDin), .Clk(CLK), .R1(\regifile_气泡_1_r1 ), .R2(\regifile_气泡_1_r2 ), .WE(RegWrite),
    .W_num(mem_wb_1_writeregout), .R1_num(multiplexer_4_out), .R2_num(multiplexer_5_out));
  or or_4 (or_4_out, PERROR, LOADUSE);
  not not_3 (not_3_out, and_3_out);
  Multiplexer #(.select(1), .width(32), .disabled("Z"), .enable("false")) multiplexer_7 (
    .in0(u_imm1), .in1({32{1'b0}}), .out(multiplexer_7_out), .sel(or_4_out));
  or or_5 (BRANCHTAKEN, B, jal, jalr);
  ID_EX id_ex_1 (
    .JAL(\单周期硬布线控制器_1_jal ), .JALR(\单周期硬布线控制器_1_jalr ), .URET(\单周期硬布线控制器_1_uret ), .beq(\单周期硬布线控制器_1_beq ),
    .MEMTOREG(\单周期硬布线控制器_1_memtoreg ), .MEMWRITE(\单周期硬布线控制器_1_memwrite ), .ALUSRC(\单周期硬布线控制器_1_alu_src ),
    .R1(\regifile_气泡_1_r1 ), .R2(\regifile_气泡_1_r2 ), .PC(ID_PC), .IMM1(bit_extender_4_out),
    .IMM2(bit_extender_2_out), .IMM3(bit_extender_3_out), .JALOUT(jal), .JALROUT(jalr), .BEQOUT(EX_BEQ),
    .MEMTOREGOUT(EX_MEMTOREG), .MEMWRITEOUT(id_ex_1_memwriteout), .ALUSRCOUT(id_ex_1_alusrcout),
    .R1OUT(EX_R1), .R2OUT_prime(EX_R2), .PCOUT_prime(EX_PC), .IMM1OUT_prime(id_ex_1_imm1out_prime),
    .IMM2OUT_prime(id_ex_1_imm2out_prime), .IMM3OUT_prime(id_ex_1_imm3out_prime), .CLK(CLK), .RST(RST),
    .BNE(\单周期硬布线控制器_1_bne ), .BNEOUT(EX_BNE), .ALUOP(\单周期硬布线控制器_1_alu_op ), .ALUOPOUT(id_ex_1_aluopout),
    .REGWRITE(\单周期硬布线控制器_1_regwrite ), .REGWRITEOUT(EX_REGWRITE), .half(\单周期硬布线控制器_1_half ),
    .halfOUT(id_ex_1_halfout), .ECALL(ecall), .ECALLOUT(id_ex_1_ecallout), .WRITEREG(ID_IR[11:7]),
    .WRITEREGOUT_prime(EX_WRITEREG), .IR(ID_IR), .IROUT_prime(EX_IR), .FLUSH(or_4_out), .EN(and_3_out),
    .R1F(R1FOWARD), .R1FOUT(EX_R1F), .R2F(R2FOWARD), .R2FOUT(EX_R2F), .PREDICT(if_id_1_predictout),
    .PREDICTOUT(PREDICT));  // open: URETOUT, CSR, CSROUT
  and and_3 (and_3_out, halt, ~Go);  // AND_Gate
  ID_EX_ccab id_ex_ccab_1 (
    .c1(sh1), .c2(blt1), .b1(auipc1), .a1(lui1), .c1out(sh2), .c2out(blt), .b1out(auipc2), .a1out(lui2),
    .CLK(CLK), .RST(RST), .flush(or_4_out), .en(and_3_out));
  Register #(.width(32), .trigger("rising"), .Select("low")) register_1 (
    .D(multiplexer_7_out), .en(not_3_out), .Q(u_imm2), .clk(CLK), .clr(RST));
  or or_6 (EX_BRANCH, EX_BEQ, EX_BNE, jal, jalr);
  Counter #(.width(16), .max('hffff), .ongoal("wrap"), .trigger("rising"), .behavior("new")) counter_5 (
    .count(or_7_out), .Q(\无条件分支数 ), .clk(CLK));  // open: load, D, carry, clr, preset, down
  or or_7 (or_7_out, jal, jalr);
  Comparator #(.width(32), .mode("twosComplement")) comparator_2 (
    .a(32'h22), .b(R1R), .eq(comparator_2_eq));  // open: gt, lt
  Shifter #(.width(32), .shift("ll")) shifter_2 (.in(id_ex_1_imm2out_prime), .\dist (5'b00001), .out(shifter_2_out));
  Shifter #(.width(32), .shift("ll")) shifter_3 (.in(id_ex_1_imm3out_prime), .\dist (5'b00001), .out(shifter_3_out));
  Multiplexer #(.select(1), .width(32), .disabled("Z"), .enable("false")) multiplexer_8 (
    .in0(R2R), .in1(id_ex_1_imm1out_prime), .out(multiplexer_8_out), .sel(id_ex_1_alusrcout));
  Adder #(.width(32)) adder_3 (.a(EX_PC), .b(32'h4), .out(adder_3_out));  // open: cin, cout
  Adder #(.width(32)) adder_4 (.a(shifter_2_out), .b(EX_PC), .out(adder_4_out));  // open: cin, cout
  Adder #(.width(32)) adder_5 (.a(shifter_3_out), .b(EX_PC), .out(adder_5_out));  // open: cin, cout
  assign and_4_out = aluresult & 32'hfffffffe;  // AND_Gate and_4, 32 bits wide
  and and_5 (and_5_out, alu_1_equal, EX_BEQ);
  not not_4 (not_4_out, alu_1_equal);
  and and_6 (and_6_out, not_4_out, EX_BNE);
  and and_7 (and_7_out, blt, alu_1_out_6);
  ALU alu_1 (
    .X(R1R), .Y(multiplexer_8_out), .AluOP(id_ex_1_aluopout), .Equal(alu_1_equal), .Result(aluresult),
    .out_6(alu_1_out_6));  // open: Result_2, out_4
  or or_8 (or_8_out, and_5_out, and_6_out);
  Multiplexer #(.select(1), .width(32), .disabled("Z"), .enable("false")) multiplexer_9 (
    .in0({32{1'b0}}), .in1(R2R), .out(multiplexer_9_out), .sel(led));
  or or_9 (B, or_8_out, and_7_out);
  and and_8 (led, id_ex_1_ecallout, comparator_2_eq);
  not not_5 (not_5_out, comparator_2_eq);
  Register #(.width(32), .trigger("rising"), .Select("low")) register_2 (
    .D(multiplexer_9_out), .en(led), .Q(LedData), .clk(CLK));  // open: clr
  not not_6 (not_6_out, B);
  Multiplexer #(.select(1), .width(32), .disabled("Z"), .enable("false")) multiplexer_10 (
    .in0(adder_5_out), .in1(and_4_out), .out(multiplexer_10_out), .sel(jalr));
  Counter #(.width(16), .max('hffff), .ongoal("wrap"), .trigger("rising"), .behavior("new")) counter_6 (
    .count(B), .Q(\条件分支成功数 ), .clk(CLK));  // open: load, D, carry, clr, preset, down
  and and_9 (and_9_out, id_ex_1_ecallout, not_5_out);
  Multiplexer #(.select(1), .width(32), .disabled("Z"), .enable("false")) multiplexer_11 (
    .in0(adder_4_out), .in1(multiplexer_10_out), .out(BRANCHADDR), .sel(not_6_out));
  not not_7 (not_7_out, and_10_out);
  ID_EX_ccab id_ex_ccab_2 (
    .c1(sh2), .b1(auipc2), .a1(lui2), .c1out(sh), .b1out(auipc3), .a1out(lui3), .CLK(CLK), .RST(RST),
    .flush(1'b0), .en(and_10_out));  // open: c2, c2out
  Register #(.width(32), .trigger("rising"), .Select("low")) register_3 (
    .D(u_imm2), .en(not_7_out), .Q(u_imm3), .clk(CLK), .clr(RST));
  EX_MEM ex_mem_1 (
    .MEMTOREGWRITE(EX_MEMTOREG), .HALF(id_ex_1_halfout), .ALURESULT(aluresult), .WRITEDATA(R2R),
    .MEMTOREGOUT(ex_mem_1_memtoregout), .HALFOUT(ex_mem_1_halfout),
    .ALURESULTOUT({ex_mem_1_aluresultout[31:2], high, ex_mem_1_aluresultout[0]}), .WRITEDATAOUT(Res),
    .CLK(CLK), .RST(RST), .MEMWRITE(id_ex_1_memwriteout), .MEMWRITEOUT(MemWrite), .J(or_7_out), .JOUT(MEM_J),
    .REGWRITEOUT(MEM_REGWRITE), .REGWRITE(EX_REGWRITE), .WRITEREG(EX_WRITEREG), .WRITEREGOUT(MEM_WRITEREG),
    .PC(EX_PC), .PCOUT(M_PC), .IR(EX_IR), .IROUT(MEM_IR), .IMM(adder_3_out), .IMMOUT(ex_mem_1_immout),
    .HALT(and_9_out), .HALTOUT(ex_mem_1_haltout), .FLUSH(1'b0), .EN(and_10_out));
  Multiplexer #(.select(1), .width(32), .disabled("Z"), .enable("false")) multiplexer_12 (
    .in0({ex_mem_1_aluresultout[31:2], high, ex_mem_1_aluresultout[0]}), .in1(ex_mem_1_immout),
    .out(multiplexer_12_out), .sel(MEM_J));
  Multiplexer #(.select(2), .width(32), .disabled("Z"), .enable("false")) multiplexer_13 (
    .in0(EX_R1), .in1(RDin), .in2(MEM_RESULT), .in3(MEM_RESULT), .out(R1R), .sel(EX_R1F));
  Multiplexer #(.select(2), .width(32), .disabled("Z"), .enable("false")) multiplexer_14 (
    .in0(EX_R2), .in1(RDin), .in2(MEM_RESULT), .in3(MEM_RESULT), .out(R2R), .sel(EX_R2F));
  RAM #(.addrWidth(10), .dataWidth(32), .bus("separate"), .Select("high")) ram_1 (
    .addr(ex_mem_1_aluresultout[11:2]), .din(MDin), .data(\use ), .str(MemWrite), .clk(CLK), .ld(1'b1));  // open: sel, clr
  Multiplexer #(.select(1), .width(32), .disabled("Z"), .enable("false")) multiplexer_15 (
    .in0(multiplexer_12_out), .in1(u_imm3), .out(multiplexer_15_out), .sel(lui3));
  Adder #(.width(32)) adder_6 (.a(M_PC), .b(u_imm3), .out(adder_6_out));  // open: cin, cout
  ID_EX_ccab id_ex_ccab_3 (
    .b1(auipc3), .a1(lui3), .b1out(auipc), .a1out(lui), .CLK(CLK), .RST(RST), .flush(1'b0), .en(and_10_out));  // open: c1, c2, c1out, c2out
  not not_8 (not_8_out, and_10_out);
  Multiplexer #(.select(1), .width(32), .disabled("Z"), .enable("false")) multiplexer_16 (
    .in0(multiplexer_15_out), .in1(adder_6_out), .out(MEM_RESULT), .sel(auipc3));
  Register #(.width(32), .trigger("rising"), .Select("low")) register_4 (
    .D(u_imm3), .en(not_8_out), .Q(u_imm), .clk(CLK), .clr(RST));
  MEM_WB mem_wb_1 (
    .MEMTOREG(ex_mem_1_memtoregout),
    .ALURESULT({ex_mem_1_aluresultout[31:2], high, ex_mem_1_aluresultout[0]}), .MEMDATA(\use ),
    .MEMTOREGOUT(mem_wb_1_memtoregout), .ALURESULTOUT(mem_wb_1_aluresultout),
    .MEMDATAOUT(mem_wb_1_memdataout), .in_1(CLK), .in_2(RST), .HALF(ex_mem_1_halfout),
    .HALFOUT(mem_wb_1_halfout), .J(MEM_J), .JOUT(mem_wb_1_jout), .WRITEREG(MEM_WRITEREG),
    .WRITEREGOUT(mem_wb_1_writeregout), .REGWRITE(MEM_REGWRITE), .REGWRITEOUT(RegWrite), .PC(M_PC),
    .PCOUT(WB_PC), .IR(MEM_IR), .IROUT(WB_IR), .IMM(ex_mem_1_immout), .IMMOUT(mem_wb_1_immout),
    .HALT(ex_mem_1_haltout), .HALTOUT(halt), .HIGH(high), .HIGHOUT(mem_wb_1_highout), .FLUSH(1'b0),
    .EN(and_10_out));
  and and_10 (and_10_out, halt, ~Go);  // AND_Gate
  Multiplexer #(.select(1), .width(32), .disabled("Z"), .enable("false")) multiplexer_17 (
    .in0(mem_wb_1_aluresultout), .in1(mem_wb_1_memdataout), .out(multiplexer_17_out),
    .sel(mem_wb_1_memtoregout));
  Shifter #(.width(32), .shift("lr")) shifter_4 (.in(multiplexer_17_out), .\dist (5'b10000), .out(shifter_4_out));
  assign bit_extender_5_out = {{16{1'b0}}, Res[15:0]};  // Bit_Extender bit_extender_5
  Multiplexer #(.select(1), .width(5), .disabled("Z"), .enable("false")) multiplexer_18 (
    .in0({5{1'b0}}), .in1(5'b10000), .out(multiplexer_18_out), .sel(high));
  Multiplexer #(.select(1), .width(32), .disabled("Z"), .enable("false")) multiplexer_19 (
    .in0(32'hffff0000), .in1(32'hffff), .out(multiplexer_19_out), .sel(high));
  Multiplexer #(.select(1), .width(32), .disabled("Z"), .enable("false")) multiplexer_20 (
    .in0(multiplexer_17_out), .in1(shifter_4_out), .out(multiplexer_20_out), .sel(mem_wb_1_highout));
  Shifter #(.width(32), .shift("ll")) shifter_5 (
    .in(bit_extender_5_out), .\dist (multiplexer_18_out), .out(shifter_5_out));
  assign and_11_out = \use  & multiplexer_19_out;  // AND_Gate and_11, 32 bits wide
  assign and_12_out = multiplexer_20_out & 32'hffff;  // AND_Gate and_12, 32 bits wide
  assign inn = shifter_5_out | and_11_out;  // OR_Gate or_10, 32 bits wide
  Multiplexer #(.select(1), .width(32), .disabled("Z"), .enable("false")) multiplexer_21 (
    .in0(multiplexer_17_out), .in1(and_12_out), .out(multiplexer_21_out), .sel(mem_wb_1_halfout));
  Multiplexer #(.select(1), .width(32), .disabled("Z"), .enable("false")) multiplexer_22 (
    .in0(multiplexer_21_out), .in1(mem_wb_1_immout), .out(multiplexer_22_out), .sel(mem_wb_1_jout));
  Adder #(.width(32)) adder_7 (.a(WB_PC), .b(u_imm), .out(adder_7_out));  // open: cin, cout
  Multiplexer #(.select(1), .width(32), .disabled("Z"), .enable("false")) multiplexer_23 (
    .in0(Res), .in1(inn), .out(MDin), .sel(sh));
  Multiplexer #(.select(1), .width(32), .disabled("Z"), .enable("false")) multiplexer_24 (
    .in0(multiplexer_22_out), .in1(adder_7_out), .out(multiplexer_24_out), .sel(auipc));
  Multiplexer #(.select(1), .width(32), .disabled("Z"), .enable("false")) multiplexer_25 (
    .in0(multiplexer_24_out), .in1(u_imm), .out(RDin), .sel(lui));

  // Other names for the same wires on the sheet: WRITEREG[4:0] = ID_IR[11:7]; MEM_PC[31:0] = M_PC

  // Notes on the sheet:
  //   中断源
  //   时空图监测，可删除
  //   中断等待指示
  //   数码管输出
  //   指令存储器
  //   PC+4
  //   contents of rom_1 (hex, n*v repeats v):
  //   100493 100006f 100493 200913 300993 100006f 100493 200913 300993 100006f 100493 200913 300993
  //   100006f 100493 200913 300993 3f8000ef 100413 100493 1f49493 900533 2200893 73 24d493 48463 fedff06f
  //   900533 2200893 73 100493 249493 900533 2200893 73 48463 fedff06f 100493 1f49493 900533 2200893 73
  //   4034d493 900533 2200893 73 4044d493 900533 2200893 73 4044d493 900533 2200893 73 4044d493 900533
  //   2200893 73 4044d493 900533 2200893 73 4044d493 900533 2200893 73 4044d493 900533 2200893 73 4044d493
  //   900533 2200893 73 100413 1f41993 41f9d993 433 c00913 300b13 140413 f47413 800293 100313 499993
  //   89e9b3 1300533 2200893 73 406282b3 fe0294e3 140413 f00f93 1f47433 1c41413 800293 100313 49d993
  //   89e9b3 1300533 2200893 73 406282b3 fe0294e3 1c45413 406b0b33 b0463 f95ff06f 2b3 fff2c293 829293
  //   ff2e293 500533 2200893 73 fff00413 493 84a023 140413 448493 84a023 140413 448493 84a023 140413
  //   448493 84a023 140413 448493 84a023 140413 448493 84a023 140413 448493 84a023 140413 448493 84a023
  //   140413 448493 84a023 140413 448493 84a023 140413 448493 84a023 140413 448493 84a023 140413 448493
  //   84a023 140413 448493 84a023 140413 448493 84a023 140413 448493 84a023 140413 448493 140413 433
  //   3c00493 42983 4aa03 149a2b3 28663 134a023 1442023 ffc48493 fe9412e3 800533 2200893 73 440413 3c00493
  //   fc9416e3 a00893 73 13 430497 900533 2200893 73 430497 900533 2200893 73 430497 900533 2200893 73
  //   430497 900533 2200893 73 430497 900533 2200893 73 430497 900533 2200893 73 430497 900533 2200893 73
  //   430497 900533 2200893 73 a00893 73 800e13 fedc04b7 fff00413 1045413 84e4b3 900533 2200893 73 ba984b7
  //   900533 73 76544b7 900533 73 32104b7 900533 73 fffe0e13 fa0e1ee3 a00893 73 313 2000e13 100493 100913
  //   931023 900533 2200893 73 12484b3 230313 fffe0e13 fe0e12e3 1000e13 313 32483 900533 2200893 73 430313
  //   fffe0e13 fe0e14e3 a00893 73 ff100493 900533 2200893 73 148493 fe04c8e3 a00893 73 413 140413 800533
  //   2200893 73 240413 800533 2200893 73 340413 800533 2200893 73 440413 800533 2200893 73 540413 800533
  //   2200893 73 640413 800533 2200893 73 740413 800533 2200893 73 840413 800533 2200893 2200893 73 8067
  //   指令探针
  //   控制位
  //   指令字
  //   I型指令
  //   s型指令
  //   流水调试日志用
  //   暂停节拍，不能为0
  //   JAL
  //   JALR
  //   URET
  //   B型指令
  //   J型指令
  //   戳工具置1进入计数暂停模式，ctrl+k时钟自动运行到对应节拍暂停
  //   ctrl+k关闭时钟连续运行，将控制位置零，进入单步调试模式调试
  //   Beq
  //   Bne
  //   MemToReg
  //   MemWrite
  //   AluOP
  //   AluSrcB
  //   RegWrite
  //   half
  //   imm
  //   可计数暂停的时钟源
  //   为方便自动评测，需要输出流水线各段保存的PC值，注意是PC不是PC+4，另外ID段寄存器写入信息，Mem段内存写入信息也要输出
  //   PC+4
  //   BEQ/BNE
  //   JAL
  //   JALR
  //   数据存储器
endmodule

module BTB (
  input  CLK,
  input  [31:0] PC,
  input  [31:0] EX_PC,
  input  EX_BRANCHTAKEN,
  input  EX_BRANCH,
  input  [31:0] EX_BRANCHADDR,
  output PREDICTJUMP,
  output [31:0] PREDICTADDR
);

  wire and_1_out, and_2_out, and_3_out, and_4_out, and_5_out, and_6_out, and_7_out, and_8_out,
       comparator_1_eq, comparator_2_eq, comparator_3_eq, comparator_4_eq, comparator_5_eq, comparator_6_eq,
       comparator_7_eq, comparator_8_eq, comparator_9_eq, comparator_10_eq, comparator_11_eq,
       comparator_12_eq, comparator_13_eq, comparator_14_eq, comparator_15_eq, comparator_16_eq, d_ff_1_q,
       d_ff_2_q, d_ff_3_q, d_ff_4_q, d_ff_5_q, d_ff_6_q, d_ff_7_q, d_ff_8_q, demultiplexer_1_out0,
       demultiplexer_1_out1, demultiplexer_1_out2, demultiplexer_1_out3, demultiplexer_1_out4,
       demultiplexer_1_out5, demultiplexer_1_out6, demultiplexer_1_out7, demultiplexer_2_out0,
       demultiplexer_2_out1, demultiplexer_2_out2, demultiplexer_2_out3, demultiplexer_2_out4,
       demultiplexer_2_out5, demultiplexer_2_out6, demultiplexer_2_out7, EX_HIT, EX_MISS, H0, H1, H2, H3, H4,
       H5, H6, H7, L0, L1, L2, L3, L4, L5, L6, L7, not_1_out, not_2_out, not_3_out, not_4_out, not_5_out,
       not_6_out, not_7_out, not_8_out, not_10_out, or_1_out, or_2_out, or_3_out, or_4_out, or_5_out,
       or_6_out, or_7_out, or_8_out, or_10_out, or_11_out, or_12_out, or_13_out, or_14_out, or_15_out,
       or_16_out, or_17_out, priority_encoder_1_gs, V0, V1, V2, V3, V4, V5, V6, V7, W0, W1, W2, W3, W4, W5,
       W6, W7;
  wire [0:0] controlled_buffer_1_out;
  wire [1:0] multiplexer_1_out, multiplexer_2_out, multiplexer_3_out, multiplexer_4_out, multiplexer_5_out,
       multiplexer_6_out, multiplexer_7_out, multiplexer_8_out, multiplexer_9_out, multiplexer_11_out, P0,
       P1, P2, P3, P4, P5, P6, P7, PNEXT;
  wire [2:0] comparision_1_max_place, comparision_2_max_place, comparision_3_max_place,
       comparision_4_max_place, comparision_5_max_place, comparision_6_max_place, comparision_7_max_place,
       multiplexer_10_out, priority_encoder_1_out, priority_encoder_2_out;
  wire [31:0] comparision_1_max, comparision_2_max, comparision_3_max, comparision_4_max, comparision_5_max,
       comparision_6_max, COUNT0, COUNT1, COUNT2, COUNT3, COUNT4, COUNT5, COUNT6, COUNT7, CUR0, CUR1, CUR2,
       CUR3, CUR4, CUR5, CUR6, CUR7, NEXT0, NEXT1, NEXT2, NEXT3, NEXT4, NEXT5, NEXT6, NEXT7;

  Register #(.width(1), .trigger("rising"), .Select("low")) register_1 (
    .D(1'b1), .en(W0), .Q(V0), .clk(CLK));  // open: clr
  Register #(.width(1), .trigger("rising"), .Select("low")) register_2 (
    .D(1'b1), .en(W1), .Q(V1), .clk(CLK));  // open: clr
  Register #(.width(1), .trigger("rising"), .Select("low")) register_3 (
    .D(1'b1), .en(W2), .Q(V2), .clk(CLK));  // open: clr
  Register #(.width(1), .trigger("rising"), .Select("low")) register_4 (
    .D(1'b1), .en(W3), .Q(V3), .clk(CLK));  // open: clr
  Register #(.width(1), .trigger("rising"), .Select("low")) register_5 (
    .D(1'b1), .en(W4), .Q(V4), .clk(CLK));  // open: clr
  Register #(.width(1), .trigger("rising"), .Select("low")) register_6 (
    .D(1'b1), .en(W5), .Q(V5), .clk(CLK));  // open: clr
  Register #(.width(1), .trigger("rising"), .Select("low")) register_7 (
    .D(1'b1), .en(W6), .Q(V6), .clk(CLK));  // open: clr
  Register #(.width(1), .trigger("rising"), .Select("low")) register_8 (
    .D(1'b1), .en(W7), .Q(V7), .clk(CLK));  // open: clr
  Register #(.width(32), .trigger("rising"), .Select("low")) register_9 (
    .D(EX_PC), .en(W0), .Q(CUR0), .clk(CLK));  // open: clr
  Register #(.width(32), .trigger("rising"), .Select("low")) register_10 (
    .D(EX_PC), .en(W1), .Q(CUR1), .clk(CLK));  // open: clr
  Register #(.width(32), .trigger("rising"), .Select("low")) register_11 (
    .D(EX_PC), .en(W2), .Q(CUR2), .clk(CLK));  // open: clr
  Register #(.width(32), .trigger("rising"), .Select("low")) register_12 (
    .D(EX_PC), .en(W3), .Q(CUR3), .clk(CLK));  // open: clr
  Register #(.width(32), .trigger("rising"), .Select("low")) register_13 (
    .D(EX_PC), .en(W4), .Q(CUR4), .clk(CLK));  // open: clr
  Register #(.width(32), .trigger("rising"), .Select("low")) register_14 (
    .D(EX_PC), .en(W5), .Q(CUR5), .clk(CLK));  // open: clr
  Register #(.width(32), .trigger("rising"), .Select("low")) register_15 (
    .D(EX_PC), .en(W6), .Q(CUR6), .clk(CLK));  // open: clr
  Register #(.width(32), .trigger("rising"), .Select("low")) register_16 (
    .D(EX_PC), .en(W7), .Q(CUR7), .clk(CLK));  // open: clr
  Register #(.width(32), .trigger("rising"), .Select("low")) register_17 (
    .D(EX_BRANCHADDR), .en(W0), .Q(NEXT0), .clk(CLK));  // open: clr
  Register #(.width(32), .trigger("rising"), .Select("low")) register_18 (
    .D(EX_BRANCHADDR), .en(W1), .Q(NEXT1), .clk(CLK));  // open: clr
  Register #(.width(32), .trigger("rising"), .Select("low")) register_19 (
    .D(EX_BRANCHADDR), .en(W2), .Q(NEXT2), .clk(CLK));  // open: clr
  Register #(.width(32), .trigger("rising"), .Select("low")) register_20 (
    .D(EX_BRANCHADDR), .en(W3), .Q(NEXT3), .clk(CLK));  // open: clr
  Register #(.width(32), .trigger("rising"), .Select("low")) register_21 (
    .D(EX_BRANCHADDR), .en(W4), .Q(NEXT4), .clk(CLK));  // open: clr
  Register #(.width(32), .trigger("rising"), .Select("low")) register_22 (
    .D(EX_BRANCHADDR), .en(W5), .Q(NEXT5), .clk(CLK));  // open: clr
  Register #(.width(32), .trigger("rising"), .Select("low")) register_23 (
    .D(EX_BRANCHADDR), .en(W6), .Q(NEXT6), .clk(CLK));  // open: clr
  Register #(.width(32), .trigger("rising"), .Select("low")) register_24 (
    .D(EX_BRANCHADDR), .en(W7), .Q(NEXT7), .clk(CLK));  // open: clr
  Multiplexer #(.select(1), .width(2), .disabled("Z"), .enable("false")) multiplexer_1 (
    .in0(2'b00), .in1(2'b11), .out(multiplexer_1_out), .sel(EX_BRANCHTAKEN));
  and and_1 (and_1_out, H0, EX_BRANCH);
  and and_2 (and_2_out, H1, EX_BRANCH);
  and and_3 (and_3_out, H2, EX_BRANCH);
  and and_4 (and_4_out, H3, EX_BRANCH);
  and and_5 (and_5_out, H4, EX_BRANCH);
  and and_6 (and_6_out, H5, EX_BRANCH);
  and and_7 (and_7_out, H6, EX_BRANCH);
  and and_8 (and_8_out, H7, EX_BRANCH);
  Multiplexer #(.select(1), .width(2), .disabled("Z"), .enable("false")) multiplexer_2 (
    .in0(PNEXT), .in1(multiplexer_1_out), .out(multiplexer_2_out), .sel(W0));
  Multiplexer #(.select(1), .width(2), .disabled("Z"), .enable("false")) multiplexer_3 (
    .in0(PNEXT), .in1(multiplexer_1_out), .out(multiplexer_3_out), .sel(W1));
  Multiplexer #(.select(1), .width(2), .disabled("Z"), .enable("false")) multiplexer_4 (
    .in0(PNEXT), .in1(multiplexer_1_out), .out(multiplexer_4_out), .sel(W2));
  Multiplexer #(.select(1), .width(2), .disabled("Z"), .enable("false")) multiplexer_5 (
    .in0(PNEXT), .in1(multiplexer_1_out), .out(multiplexer_5_out), .sel(W3));
  Multiplexer #(.select(1), .width(2), .disabled("Z"), .enable("false")) multiplexer_6 (
    .in0(PNEXT), .in1(multiplexer_1_out), .out(multiplexer_6_out), .sel(W4));
  Multiplexer #(.select(1), .width(2), .disabled("Z"), .enable("false")) multiplexer_7 (
    .in0(PNEXT), .in1(multiplexer_1_out), .out(multiplexer_7_out), .sel(W5));
  Multiplexer #(.select(1), .width(2), .disabled("Z"), .enable("false")) multiplexer_8 (
    .in0(PNEXT), .in1(multiplexer_1_out), .out(multiplexer_8_out), .sel(W6));
  Multiplexer #(.select(1), .width(2), .disabled("Z"), .enable("false")) multiplexer_9 (
    .in0(PNEXT), .in1(multiplexer_1_out), .out(multiplexer_9_out), .sel(W7));
  Register #(.width(2), .trigger("rising"), .Select("low")) register_25 (
    .D(multiplexer_2_out), .en(and_1_out), .Q(P0), .clk(CLK));  // open: clr
  Register #(.width(2), .trigger("rising"), .Select("low")) register_26 (
    .D(multiplexer_3_out), .en(and_2_out), .Q(P1), .clk(CLK));  // open: clr
  Register #(.width(2), .trigger("rising"), .Select("low")) register_27 (
    .D(multiplexer_4_out), .en(and_3_out), .Q(P2), .clk(CLK));  // open: clr
  Register #(.width(2), .trigger("rising"), .Select("low")) register_28 (
    .D(multiplexer_5_out), .en(and_4_out), .Q(P3), .clk(CLK));  // open: clr
  Register #(.width(2), .trigger("rising"), .Select("low")) register_29 (
    .D(multiplexer_6_out), .en(and_5_out), .Q(P4), .clk(CLK));  // open: clr
  Register #(.width(2), .trigger("rising"), .Select("low")) register_30 (
    .D(multiplexer_7_out), .en(and_6_out), .Q(P5), .clk(CLK));  // open: clr
  Register #(.width(2), .trigger("rising"), .Select("low")) register_31 (
    .D(multiplexer_8_out), .en(and_7_out), .Q(P6), .clk(CLK));  // open: clr
  Register #(.width(2), .trigger("rising"), .Select("low")) register_32 (
    .D(multiplexer_9_out), .en(and_8_out), .Q(P7), .clk(CLK));  // open: clr
  or or_1 (or_1_out, W0, L0);
  or or_2 (or_2_out, W1, L1);
  or or_3 (or_3_out, W2, L2);
  or or_4 (or_4_out, W3, L3);
  or or_5 (or_5_out, W4, L4);
  or or_6 (or_6_out, W5, L5);
  or or_7 (or_7_out, W6, L6);
  or or_8 (or_8_out, W7, L7);
  Counter #(.width(32), .max('hffffffff), .ongoal("wrap"), .trigger("rising"), .behavior("new")) counter_1 (
    .Q(COUNT0), .clk(CLK), .clr(d_ff_1_q));  // open: load, D, count, carry, preset, down
  D_Flip_Flop #(.trigger("rising"), .Pre_Clr_Positions("LEGACY"), .NegatePresetClear("false"), .enable("true"), .NewFFLayout("false")) d_ff_1 (
    .clk(CLK), .D(or_1_out), .Q(d_ff_1_q));  // open: Qn, preset, en, reset
  Counter #(.width(32), .max('hffffffff), .ongoal("wrap"), .trigger("rising"), .behavior("new")) counter_2 (
    .Q(COUNT1), .clk(CLK), .clr(d_ff_2_q));  // open: load, D, count, carry, preset, down
  D_Flip_Flop #(.trigger("rising"), .Pre_Clr_Positions("LEGACY"), .NegatePresetClear("false"), .enable("true"), .NewFFLayout("false")) d_ff_2 (
    .clk(CLK), .D(or_2_out), .Q(d_ff_2_q));  // open: Qn, preset, en, reset
  Counter #(.width(32), .max('hffffffff), .ongoal("wrap"), .trigger("rising"), .behavior("new")) counter_3 (
    .Q(COUNT2), .clk(CLK), .clr(d_ff_3_q));  // open: load, D, count, carry, preset, down
  D_Flip_Flop #(.trigger("rising"), .Pre_Clr_Positions("LEGACY"), .NegatePresetClear("false"), .enable("true"), .NewFFLayout("false")) d_ff_3 (
    .clk(CLK), .D(or_3_out), .Q(d_ff_3_q));  // open: Qn, preset, en, reset
  Counter #(.width(32), .max('hffffffff), .ongoal("wrap"), .trigger("rising"), .behavior("new")) counter_4 (
    .Q(COUNT3), .clk(CLK), .clr(d_ff_4_q));  // open: load, D, count, carry, preset, down
  D_Flip_Flop #(.trigger("rising"), .Pre_Clr_Positions("LEGACY"), .NegatePresetClear("false"), .enable("true"), .NewFFLayout("false")) d_ff_4 (
    .clk(CLK), .D(or_4_out), .Q(d_ff_4_q));  // open: Qn, preset, en, reset
  Counter #(.width(32), .max('hffffffff), .ongoal("wrap"), .trigger("rising"), .behavior("new")) counter_5 (
    .Q(COUNT4), .clk(CLK), .clr(d_ff_5_q));  // open: load, D, count, carry, preset, down
  D_Flip_Flop #(.trigger("rising"), .Pre_Clr_Positions("LEGACY"), .NegatePresetClear("false"), .enable("true"), .NewFFLayout("false")) d_ff_5 (
    .clk(CLK), .D(or_5_out), .Q(d_ff_5_q));  // open: Qn, preset, en, reset
  Counter #(.width(32), .max('hffffffff), .ongoal("wrap"), .trigger("rising"), .behavior("new")) counter_6 (
    .Q(COUNT5), .clk(CLK), .clr(d_ff_6_q));  // open: load, D, count, carry, preset, down
  D_Flip_Flop #(.trigger("rising"), .Pre_Clr_Positions("LEGACY"), .NegatePresetClear("false"), .enable("true"), .NewFFLayout("false")) d_ff_6 (
    .clk(CLK), .D(or_6_out), .Q(d_ff_6_q));  // open: Qn, preset, en, reset
  Counter #(.width(32), .max('hffffffff), .ongoal("wrap"), .trigger("rising"), .behavior("new")) counter_7 (
    .Q(COUNT6), .clk(CLK), .clr(d_ff_7_q));  // open: load, D, count, carry, preset, down
  D_Flip_Flop #(.trigger("rising"), .Pre_Clr_Positions("LEGACY"), .NegatePresetClear("false"), .enable("true"), .NewFFLayout("false")) d_ff_7 (
    .clk(CLK), .D(or_7_out), .Q(d_ff_7_q));  // open: Qn, preset, en, reset
  Counter #(.width(32), .max('hffffffff), .ongoal("wrap"), .trigger("rising"), .behavior("new")) counter_8 (
    .Q(COUNT7), .clk(CLK), .clr(d_ff_8_q));  // open: load, D, count, carry, preset, down
  D_Flip_Flop #(.trigger("rising"), .Pre_Clr_Positions("LEGACY"), .NegatePresetClear("false"), .enable("true"), .NewFFLayout("false")) d_ff_8 (
    .clk(CLK), .D(or_8_out), .Q(d_ff_8_q));  // open: Qn, preset, en, reset
  Comparator #(.width(32), .mode("twosComplement")) comparator_1 (
    .a(CUR0), .b(EX_PC), .eq(comparator_1_eq));  // open: gt, lt
  Comparator #(.width(32), .mode("twosComplement")) comparator_2 (
    .a(CUR1), .b(EX_PC), .eq(comparator_2_eq));  // open: gt, lt
  Comparator #(.width(32), .mode("twosComplement")) comparator_3 (
    .a(CUR2), .b(EX_PC), .eq(comparator_3_eq));  // open: gt, lt
  Comparator #(.width(32), .mode("twosComplement")) comparator_4 (
    .a(CUR3), .b(EX_PC), .eq(comparator_4_eq));  // open: gt, lt
  Comparator #(.width(32), .mode("twosComplement")) comparator_5 (
    .a(CUR4), .b(EX_PC), .eq(comparator_5_eq));  // open: gt, lt
  Comparator #(.width(32), .mode("twosComplement")) comparator_6 (
    .a(CUR5), .b(EX_PC), .eq(comparator_6_eq));  // open: gt, lt
  Comparator #(.width(32), .mode("twosComplement")) comparator_7 (
    .a(CUR6), .b(EX_PC), .eq(comparator_7_eq));  // open: gt, lt
  Comparator #(.width(32), .mode("twosComplement")) comparator_8 (
    .a(CUR7), .b(EX_PC), .eq(comparator_8_eq));  // open: gt, lt
  and and_9 (H0, comparator_1_eq, V0);
  and and_10 (H1, comparator_2_eq, V1);
  and and_11 (H2, comparator_3_eq, V2);
  and and_12 (H3, comparator_4_eq, V3);
  and and_13 (H5, comparator_6_eq, V5);
  and and_14 (H4, comparator_5_eq, V4);
  and and_15 (H6, comparator_7_eq, V6);
  and and_16 (H7, comparator_8_eq, V7);
  not not_1 (not_1_out, V0);
  not not_2 (not_2_out, V1);
  not not_3 (not_3_out, V2);
  not not_4 (not_4_out, V3);
  not not_5 (not_5_out, V4);
  not not_6 (not_6_out, V5);
  not not_7 (not_7_out, V6);
  not not_8 (not_8_out, V7);
  or or_9 (EX_HIT, H0, H1, H2, H3, H4, H5, H6, H7);
  COMPARISION comparision_1 (
    .X(COUNT0), .Y(COUNT1), .X_PLACE(3'b000), .Y_PLACE(3'b001), .MAX(comparision_1_max),
    .MAX_PLACE(comparision_1_max_place));
  COMPARISION comparision_2 (
    .X(COUNT2), .Y(COUNT3), .X_PLACE(3'b010), .Y_PLACE(3'b011), .MAX(comparision_2_max),
    .MAX_PLACE(comparision_2_max_place));
  COMPARISION comparision_3 (
    .X(COUNT4), .Y(COUNT5), .X_PLACE(3'b100), .Y_PLACE(3'b101), .MAX(comparision_3_max),
    .MAX_PLACE(comparision_3_max_place));
  COMPARISION comparision_4 (
    .X(COUNT6), .Y(COUNT7), .X_PLACE(3'b110), .Y_PLACE(3'b111), .MAX(comparision_4_max),
    .MAX_PLACE(comparision_4_max_place));
  not not_9 (EX_MISS, EX_HIT);
  Priority_Encoder #(.select(3), .disabled("Z")) priority_encoder_1 (
    .in0(not_1_out), .in1(not_2_out), .in2(not_3_out), .in3(not_4_out), .in4(not_5_out), .in5(not_6_out),
    .in6(not_7_out), .in7(not_8_out), .out(priority_encoder_1_out), .gs(priority_encoder_1_gs));  // open: en_out, en_in
  not not_10 (not_10_out, priority_encoder_1_gs);
  COMPARISION comparision_5 (
    .X(comparision_1_max), .Y(comparision_2_max), .X_PLACE(comparision_1_max_place),
    .Y_PLACE(comparision_2_max_place), .MAX(comparision_5_max), .MAX_PLACE(comparision_5_max_place));
  Multiplexer #(.select(1), .width(3), .disabled("Z"), .enable("false")) multiplexer_10 (
    .in0(3'b000), .in1(priority_encoder_1_out), .out(multiplexer_10_out), .sel(priority_encoder_1_gs));
  COMPARISION comparision_6 (
    .X(comparision_3_max), .Y(comparision_4_max), .X_PLACE(comparision_3_max_place),
    .Y_PLACE(comparision_4_max_place), .MAX(comparision_6_max), .MAX_PLACE(comparision_6_max_place));
  Demultiplexer #(.select(3), .width(1), .tristate("false"), .disabled("Z"), .enable("true")) demultiplexer_1 (
    .out0(demultiplexer_1_out0), .out1(demultiplexer_1_out1), .out2(demultiplexer_1_out2),
    .out3(demultiplexer_1_out3), .out4(demultiplexer_1_out4), .out5(demultiplexer_1_out5),
    .out6(demultiplexer_1_out6), .out7(demultiplexer_1_out7), .in(priority_encoder_1_gs),
    .sel(multiplexer_10_out));  // open: en
  Demultiplexer #(.select(3), .width(1), .tristate("false"), .disabled("Z"), .enable("false")) demultiplexer_2 (
    .out0(demultiplexer_2_out0), .out1(demultiplexer_2_out1), .out2(demultiplexer_2_out2),
    .out3(demultiplexer_2_out3), .out4(demultiplexer_2_out4), .out5(demultiplexer_2_out5),
    .out6(demultiplexer_2_out6), .out7(demultiplexer_2_out7), .in(not_10_out), .sel(comparision_7_max_place));
  COMPARISION comparision_7 (
    .X(comparision_5_max), .Y(comparision_6_max), .X_PLACE(comparision_5_max_place),
    .Y_PLACE(comparision_6_max_place), .MAX_PLACE(comparision_7_max_place));  // open: MAX
  Priority_Encoder #(.select(3), .disabled("Z")) priority_encoder_2 (
    .in0(H0), .in1(H1), .in2(H2), .in3(H3), .in4(H4), .in5(H5), .in6(H6), .in7(H7),
    .out(priority_encoder_2_out));  // open: gs, en_out, en_in
  Multiplexer #(.select(3), .width(2), .disabled("Z"), .enable("false")) multiplexer_11 (
    .in0(P0), .in1(P1), .in2(P2), .in3(P3), .in4(P4), .in5(P5), .in6(P6), .in7(P7), .out(multiplexer_11_out),
    .sel(priority_encoder_2_out));
  or or_10 (or_10_out, demultiplexer_1_out0, demultiplexer_2_out0);
  or or_11 (or_11_out, demultiplexer_1_out1, demultiplexer_2_out1);
  or or_12 (or_12_out, demultiplexer_1_out2, demultiplexer_2_out2);
  or or_13 (or_13_out, demultiplexer_1_out3, demultiplexer_2_out3);
  or or_14 (or_14_out, demultiplexer_1_out4, demultiplexer_2_out4);
  or or_15 (or_15_out, demultiplexer_1_out5, demultiplexer_2_out5);
  or or_16 (or_16_out, demultiplexer_1_out6, demultiplexer_2_out6);
  or or_17 (or_17_out, demultiplexer_1_out7, demultiplexer_2_out7);
  FSM fsm_1 (.NEXT(PNEXT), .JUMP(EX_BRANCHTAKEN), .CUR(multiplexer_11_out));
  and and_17 (W0, or_10_out, EX_MISS, EX_BRANCH);
  and and_18 (W1, or_11_out, EX_MISS, EX_BRANCH);
  and and_19 (W2, or_12_out, EX_MISS, EX_BRANCH);
  and and_20 (W3, or_13_out, EX_MISS, EX_BRANCH);
  and and_21 (W4, or_14_out, EX_MISS, EX_BRANCH);
  and and_22 (W5, or_15_out, EX_MISS, EX_BRANCH);
  and and_23 (W6, or_16_out, EX_MISS, EX_BRANCH);
  and and_24 (W7, or_17_out, EX_MISS, EX_BRANCH);
  Comparator #(.width(32), .mode("twosComplement")) comparator_9 (
    .a(CUR0), .b(PC), .eq(comparator_9_eq));  // open: gt, lt
  Comparator #(.width(32), .mode("twosComplement")) comparator_10 (
    .a(CUR1), .b(PC), .eq(comparator_10_eq));  // open: gt, lt
  Comparator #(.width(32), .mode("twosComplement")) comparator_11 (
    .a(CUR2), .b(PC), .eq(comparator_11_eq));  // open: gt, lt
  Comparator #(.width(32), .mode("twosComplement")) comparator_12 (
    .a(CUR3), .b(PC), .eq(comparator_12_eq));  // open: gt, lt
  Comparator #(.width(32), .mode("twosComplement")) comparator_13 (
    .a(CUR4), .b(PC), .eq(comparator_13_eq));  // open: gt, lt
  Comparator #(.width(32), .mode("twosComplement")) comparator_14 (
    .a(CUR5), .b(PC), .eq(comparator_14_eq));  // open: gt, lt
  Comparator #(.width(32), .mode("twosComplement")) comparator_15 (
    .a(CUR6), .b(PC), .eq(comparator_15_eq));  // open: gt, lt
  Comparator #(.width(32), .mode("twosComplement")) comparator_16 (
    .a(CUR7), .b(PC), .eq(comparator_16_eq));  // open: gt, lt
  and and_25 (L0, comparator_9_eq, V0);
  and and_26 (L1, comparator_10_eq, V1);
  and and_27 (L2, comparator_11_eq, V2);
  and and_28 (L3, comparator_12_eq, V3);
  and and_29 (L4, comparator_13_eq, V4);
  and and_30 (L5, comparator_14_eq, V5);
  and and_31 (L6, comparator_15_eq, V6);
  and and_32 (L7, comparator_16_eq, V7);
  assign {PREDICTJUMP, controlled_buffer_1_out[0]} = L0 ? P0 : 2'bz;  // Controlled_Buffer controlled_buffer_1
  assign {PREDICTJUMP, controlled_buffer_1_out[0]} = L1 ? P1 : 2'bz;  // Controlled_Buffer controlled_buffer_2
  assign {PREDICTJUMP, controlled_buffer_1_out[0]} = L2 ? P2 : 2'bz;  // Controlled_Buffer controlled_buffer_3
  assign {PREDICTJUMP, controlled_buffer_1_out[0]} = L3 ? P3 : 2'bz;  // Controlled_Buffer controlled_buffer_4
  assign {PREDICTJUMP, controlled_buffer_1_out[0]} = L4 ? P4 : 2'bz;  // Controlled_Buffer controlled_buffer_5
  assign {PREDICTJUMP, controlled_buffer_1_out[0]} = L5 ? P5 : 2'bz;  // Controlled_Buffer controlled_buffer_6
  assign {PREDICTJUMP, controlled_buffer_1_out[0]} = L6 ? P6 : 2'bz;  // Controlled_Buffer controlled_buffer_7
  assign {PREDICTJUMP, controlled_buffer_1_out[0]} = L7 ? P7 : 2'bz;  // Controlled_Buffer controlled_buffer_8
  Pull_Resistor #(.pull(0)) pull_resistor_1 (.node({PREDICTJUMP, controlled_buffer_1_out[0]}));
  assign PREDICTADDR = L0 ? NEXT0 : 32'bz;  // Controlled_Buffer controlled_buffer_9
  assign PREDICTADDR = L1 ? NEXT1 : 32'bz;  // Controlled_Buffer controlled_buffer_10
  assign PREDICTADDR = L2 ? NEXT2 : 32'bz;  // Controlled_Buffer controlled_buffer_11
  assign PREDICTADDR = L3 ? NEXT3 : 32'bz;  // Controlled_Buffer controlled_buffer_12
  assign PREDICTADDR = L4 ? NEXT4 : 32'bz;  // Controlled_Buffer controlled_buffer_13
  assign PREDICTADDR = L5 ? NEXT5 : 32'bz;  // Controlled_Buffer controlled_buffer_14
  assign PREDICTADDR = L6 ? NEXT6 : 32'bz;  // Controlled_Buffer controlled_buffer_15
  assign PREDICTADDR = L7 ? NEXT7 : 32'bz;  // Controlled_Buffer controlled_buffer_16
  Pull_Resistor #(.pull(0)) pull_resistor_2 (.node(PREDICTADDR));

  // Other names for the same wires on the sheet: PREDICTADDRl[31:0] = PREDICTADDR

  // Notes on the sheet:
  //   VALID
  //   分支指令地址
  //   分支目标地址
  //   分支预测历史位
  //   置换标记
  //   EX分支写入逻辑
  //   选择一个位置写入该分支信息
  //   更新历史预测位
  //   IF段预测逻辑
  //   预测结果
endmodule

// 比较器
module COMPARISION (
  input  [31:0] X,
  input  [31:0] Y,
  input  [2:0] X_PLACE,
  input  [2:0] Y_PLACE,
  output [31:0] MAX,
  output [2:0] MAX_PLACE
);

  wire comparator_1_lt;

  Comparator #(.width(32), .mode("twosComplement")) comparator_1 (.a(X), .b(Y), .lt(comparator_1_lt));  // open: gt, eq
  Multiplexer #(.select(1), .width(32), .disabled("Z"), .enable("false")) multiplexer_1 (
    .in0(X), .in1(Y), .out(MAX), .sel(comparator_1_lt));
  Multiplexer #(.select(1), .width(3), .disabled("Z"), .enable("false")) multiplexer_2 (
    .in0(X_PLACE), .in1(Y_PLACE), .out(MAX_PLACE), .sel(comparator_1_lt));
endmodule

module FSM (
  input  [1:0] CUR,
  input  JUMP,
  output [1:0] NEXT
);

  Multiplexer #(.select(3), .width(2), .disabled("Z"), .enable("false")) multiplexer_1 (
    .in0(2'b00), .in1(2'b00), .in2(2'b11), .in3(2'b00), .in4(2'b01), .in5(2'b10), .in6(2'b10), .in7(2'b10),
    .out(NEXT), .sel({JUMP, CUR}));
endmodule

module ID_EX_ccab (
  input  CLK,
  input  RST,
  input  c1,
  input  c2,
  input  b1,
  input  a1,
  input  flush,
  input  en,
  output c1out,
  output c2out,
  output b1out,
  output a1out
);

  wire multiplexer_1_out, multiplexer_2_out, multiplexer_3_out, multiplexer_4_out, not_1_out;

  Multiplexer #(.select(1), .width(1), .disabled("Z"), .enable("false")) multiplexer_1 (
    .in0(c1), .in1(1'b0), .out(multiplexer_1_out), .sel(flush));
  Multiplexer #(.select(1), .width(1), .disabled("Z"), .enable("false")) multiplexer_2 (
    .in0(c2), .in1(1'b0), .out(multiplexer_2_out), .sel(flush));
  Multiplexer #(.select(1), .width(1), .disabled("Z"), .enable("false")) multiplexer_3 (
    .in0(b1), .in1(1'b0), .out(multiplexer_3_out), .sel(flush));
  Multiplexer #(.select(1), .width(1), .disabled("Z"), .enable("false")) multiplexer_4 (
    .in0(a1), .in1(1'b0), .out(multiplexer_4_out), .sel(flush));
  not not_1 (not_1_out, en);
  Register #(.width(1), .trigger("rising"), .Select("low")) register_1 (
    .D(multiplexer_1_out), .en(not_1_out), .Q(c1out), .clk(CLK), .clr(RST));
  Register #(.width(1), .trigger("rising"), .Select("low")) register_2 (
    .D(multiplexer_2_out), .en(not_1_out), .Q(c2out), .clk(CLK), .clr(RST));
  Register #(.width(1), .trigger("rising"), .Select("low")) register_3 (
    .D(multiplexer_3_out), .en(not_1_out), .Q(b1out), .clk(CLK), .clr(RST));
  Register #(.width(1), .trigger("rising"), .Select("low")) register_4 (
    .D(multiplexer_4_out), .en(not_1_out), .Q(a1out), .clk(CLK), .clr(RST));
endmodule
